// Logisim project 2A03_APU.circ as structural Verilog: 42 circuits, main circuit 2A03_APU
module _2A03_APU (
  input  DBG__EXT,
  input  CLK,
  input  nNMI_PIN,
  input  nIRQ_PIN,
  input  nRES_PIN,
  input  [7:0] DB_in,
  input  PHI1_FromCore,
  input  PHI2_FromCore,
  input  R_W__CPU,
  input  [15:0] CPU_Ax,
  input  [7:0] Data_from_CPU,
  output [7:0] AUX_A,
  output OUT0,
  output OUT1,
  output OUT2,
  output nIN0,
  output nIN1,
  output R_W__EXT,
  output M2__EXT,
  output [15:0] AB,
  output [7:0] DB_out,
  output PHI0__CPU,
  output nIRQ_CPU,
  output [14:0] AUX_B,
  output nNMI_CPU,
  output RDY__CPU,
  output [7:0] Data_to_CPU
);

  wire ACLK1, clk_divider_1_nm2, dpcm_channel_1_dmca0, dpcm_channel_1_dmca1, dpcm_channel_1_dmca2,
       dpcm_channel_1_dmca3, dpcm_channel_1_dmca4, dpcm_channel_1_dmca5, dpcm_channel_1_dmca6,
       dpcm_channel_1_dmca7, dpcm_channel_1_dmca8, dpcm_channel_1_dmca9, dpcm_channel_1_dmca10,
       dpcm_channel_1_dmca11, dpcm_channel_1_dmca12, dpcm_channel_1_dmca13, dpcm_channel_1_dmca14,
       dpcm_channel_1_dmcint, dpcm_channel_1_dmcrdy, dpcm_channel_1_ndmc_ab, dpcm_channel_1_rundmc,
       io_control_1_nclk_int, length_down_counter_1_noxxx, length_down_counter_2_noxxx,
       length_down_counter_3_noxxx, length_down_counter_4_noxxx, length_table_1_lc0, length_table_1_lc1,
       length_table_1_lc2, length_table_1_lc3, length_table_1_lc4, length_table_1_lc5, length_table_1_lc6,
       length_table_1_lc7, lfo_1_int, LOCK, nACLK2, nDBGRD, nLFO1, nLFO2, noise_channel_1_nrnd_lc, not_1_out,
       not_2_out, nR401A, nR4015, nR4016, nR4017, nR4018, nR4019, PHI1, PHI2, RES,
       sprite_dma_1_r_w__to_r_w_ic_pin, sprite_dma_1_wr, square_channel_0_1_nsqa_lc,
       square_channel_1_1_nsqb_lc, triangle_channel_1_tri_lc, W400A, W400B, W400C, W400E, W400F, W401A,
       W4000, W4001, W4002, W4003, W4004, W4005, W4006, W4007, W4008, W4010, W4011, W4012, W4013, W4014,
       W4015, W4016, W4017;
  wire [15:0] sprite_dma_1_a0;

  SQUARE_CHANNEL_1 square_channel_1_1 (
    .nACLK2(nACLK2), .ACLK1(ACLK1), .W4004(W4004), .W4005(W4005), .W4006(W4006), .W4007(W4007),
    .D0(Data_from_CPU[0]), .D1(Data_from_CPU[1]), .D2(Data_from_CPU[2]), .D3(Data_from_CPU[3]),
    .D4(Data_from_CPU[4]), .D5(Data_from_CPU[5]), .D6(Data_from_CPU[6]), .D7(Data_from_CPU[7]),
    .NOSQB(length_down_counter_3_noxxx), .RES(RES), .nLFO1(nLFO1), .nLFO2(nLFO2), .SQB0(AUX_A[4]),
    .SQB1(AUX_A[5]), .SQB2(AUX_A[6]), .SQB3(AUX_A[7]), .nSQB_LC(square_channel_1_1_nsqb_lc), .LOCK(LOCK));
  TRIANGLE_CHANNEL triangle_channel_1 (
    .PHI1(PHI1), .ACLK1(ACLK1), .W4008(W4008), .W400A(W400A), .W400B(W400B), .D0(Data_from_CPU[0]),
    .D1(Data_from_CPU[1]), .D2(Data_from_CPU[2]), .D3(Data_from_CPU[3]), .D4(Data_from_CPU[4]),
    .D5(Data_from_CPU[5]), .D6(Data_from_CPU[6]), .D7(Data_from_CPU[7]), .RES(RES), .nLFO1(nLFO1),
    .NOTRI(length_down_counter_2_noxxx), .TRI0(AUX_B[0]), .TRI1(AUX_B[1]), .TRI2(AUX_B[2]), .TRI3(AUX_B[3]),
    .TRI_LC(triangle_channel_1_tri_lc), .LOCk(LOCK), .W401A(W401A));
  NOISE_CHANNEL noise_channel_1 (
    .nACLK2(nACLK2), .ACLK1(ACLK1), .D7(Data_from_CPU[7]), .D5(Data_from_CPU[5]), .D4(Data_from_CPU[4]),
    .D3(Data_from_CPU[3]), .D2(Data_from_CPU[2]), .D1(Data_from_CPU[1]), .D0(Data_from_CPU[0]),
    .W400E(W400E), .W400F(W400F), .Res(RES), .NORND(length_down_counter_1_noxxx), .nLFO1(nLFO1),
    .W400C(W400C), .RND0(AUX_B[4]), .RND1(AUX_B[5]), .RND2(AUX_B[6]), .RND3(AUX_B[7]),
    .nRND_LC(noise_channel_1_nrnd_lc), .LOCK(LOCK));
  LENGTH_TABLE length_table_1 (
    .D3(Data_from_CPU[3]), .D4(Data_from_CPU[4]), .D5(Data_from_CPU[5]), .D6(Data_from_CPU[6]),
    .D7(Data_from_CPU[7]), .LC7(length_table_1_lc7), .LC6(length_table_1_lc6), .LC5(length_table_1_lc5),
    .LC4(length_table_1_lc4), .LC3(length_table_1_lc3), .LC2(length_table_1_lc2), .LC1(length_table_1_lc1),
    .LC0(length_table_1_lc0));
  not not_1 (not_1_out, nACLK2);
  LENGTH_DOWN_COUNTER length_down_counter_1 (
    .ACLK1(ACLK1), .W400x(W400F), .LC7(length_table_1_lc7), .LC6(length_table_1_lc6),
    .LC5(length_table_1_lc5), .LC4(length_table_1_lc4), .LC3(length_table_1_lc3), .LC2(length_table_1_lc2),
    .LC1(length_table_1_lc1), .LC0(length_table_1_lc0), .HALT(noise_channel_1_nrnd_lc),
    .NOxxx(length_down_counter_1_noxxx), .W4015(W4015), .Dx_2(Data_to_CPU[3]), .Dx(Data_from_CPU[3]),
    .RES(RES), .nLFO2(nLFO2), .nR4015(nR4015), .ACLK4(not_1_out));
  LENGTH_DOWN_COUNTER length_down_counter_2 (
    .ACLK1(ACLK1), .W400x(W400B), .LC7(length_table_1_lc7), .LC6(length_table_1_lc6),
    .LC5(length_table_1_lc5), .LC4(length_table_1_lc4), .LC3(length_table_1_lc3), .LC2(length_table_1_lc2),
    .LC1(length_table_1_lc1), .LC0(length_table_1_lc0), .HALT(triangle_channel_1_tri_lc),
    .NOxxx(length_down_counter_2_noxxx), .W4015(W4015), .Dx_2(Data_to_CPU[2]), .Dx(Data_from_CPU[2]),
    .RES(RES), .nLFO2(nLFO2), .nR4015(nR4015), .ACLK4(not_1_out));
  SQUARE_CHANNEL_0 square_channel_0_1 (
    .nACLK2(nACLK2), .ACLK1(ACLK1), .W4000(W4000), .W4001(W4001), .W4002(W4002), .W4003(W4003),
    .D0(Data_from_CPU[0]), .D1(Data_from_CPU[1]), .D2(Data_from_CPU[2]), .D3(Data_from_CPU[3]),
    .D4(Data_from_CPU[4]), .D5(Data_from_CPU[5]), .D6(Data_from_CPU[6]), .D7(Data_from_CPU[7]),
    .NOSQA(length_down_counter_4_noxxx), .RES(RES), .nLFO1(nLFO1), .nLFO2(nLFO2), .SQA0(AUX_A[0]),
    .SQA1(AUX_A[1]), .SQ2(AUX_A[2]), .SQA3(AUX_A[3]), .nSQA_LC(square_channel_0_1_nsqa_lc), .LOCK(LOCK));
  SPRITE_DMA sprite_dma_1 (
    .PHI1(PHI1), .PHI2(PHI2_FromCore), .nACLK2(nACLK2), .ACLK1(ACLK1), .nR4015(nR4015), .W4014(W4014),
    .D0(Data_from_CPU[0]), .D1(Data_from_CPU[1]), .D2(Data_from_CPU[2]), .D3(Data_from_CPU[3]),
    .D4(Data_from_CPU[4]), .D5(Data_from_CPU[5]), .D6(Data_from_CPU[6]), .D7(Data_from_CPU[7]),
    .RUNDMC(dpcm_channel_1_rundmc), .DMC_RDY(dpcm_channel_1_dmcrdy), .nDMC_AB(dpcm_channel_1_ndmc_ab),
    .R_W__CPU(R_W__CPU), .RES(RES), .CPUA0(CPU_Ax[0]), .CPUA1(CPU_Ax[1]), .CPUA2(CPU_Ax[2]),
    .CPUA3(CPU_Ax[3]), .CPUA4(CPU_Ax[4]), .CPUA5(CPU_Ax[5]), .CPUA6(CPU_Ax[6]), .CPUA7(CPU_Ax[7]),
    .CPUA8(CPU_Ax[8]), .CPUA9(CPU_Ax[9]), .CPUA10(CPU_Ax[10]), .CPUA11(CPU_Ax[11]), .CPUA12(CPU_Ax[12]),
    .CPUA13(CPU_Ax[13]), .CPUA14(CPU_Ax[14]), .CPUA15(CPU_Ax[15]), .DMC0(dpcm_channel_1_dmca0),
    .DMC1(dpcm_channel_1_dmca1), .DMC2(dpcm_channel_1_dmca2), .DMC3(dpcm_channel_1_dmca3),
    .DMC4(dpcm_channel_1_dmca4), .DMC5(dpcm_channel_1_dmca5), .DMC6(dpcm_channel_1_dmca6),
    .DMC7(dpcm_channel_1_dmca7), .DMC8(dpcm_channel_1_dmca8), .DMC9(dpcm_channel_1_dmca9),
    .DMC10(dpcm_channel_1_dmca10), .DMC11(dpcm_channel_1_dmca11), .DMC12(dpcm_channel_1_dmca12),
    .DMC13(dpcm_channel_1_dmca13), .DMC14(dpcm_channel_1_dmca14),
    .R_W__to_R_W_ic_pin(sprite_dma_1_r_w__to_r_w_ic_pin), .WR(sprite_dma_1_wr), .RDY(RDY__CPU),
    .A0(sprite_dma_1_a0[0]), .A1(sprite_dma_1_a0[1]), .A2(sprite_dma_1_a0[2]), .A3(sprite_dma_1_a0[3]),
    .A4(sprite_dma_1_a0[4]), .A5(sprite_dma_1_a0[5]), .A6(sprite_dma_1_a0[6]), .A7(sprite_dma_1_a0[7]),
    .A8(sprite_dma_1_a0[8]), .A9(sprite_dma_1_a0[9]), .A10(sprite_dma_1_a0[10]), .A11(sprite_dma_1_a0[11]),
    .A12(sprite_dma_1_a0[12]), .A13(sprite_dma_1_a0[13]), .A14(sprite_dma_1_a0[14]),
    .A15(sprite_dma_1_a0[15]), .D0_3(Data_to_CPU[0]), .D0_2(Data_from_CPU[0]), .D1_3(Data_to_CPU[1]),
    .D1_2(Data_from_CPU[1]), .D2_3(Data_to_CPU[2]), .D2_2(Data_from_CPU[2]), .D3_3(Data_to_CPU[3]),
    .D3_2(Data_from_CPU[3]), .D4_3(Data_to_CPU[4]), .D4_2(Data_from_CPU[4]), .D5_3(Data_to_CPU[5]),
    .D5_2(Data_from_CPU[5]), .D6_3(Data_to_CPU[6]), .D6_2(Data_from_CPU[6]), .D7_3(Data_to_CPU[7]),
    .D7_2(Data_from_CPU[7]), .nDBGRD(nDBGRD));
  DPCM_CHANNEL dpcm_channel_1 (
    .PHI1(PHI1), .nACLK2(nACLK2), .ACLK1(ACLK1), .W4010(W4010), .W4011(W4011), .W4012(W4012), .W4013(W4013),
    .W4015(W4015), .nR4015(nR4015), .D0(Data_from_CPU[0]), .D1(Data_from_CPU[1]), .D2(Data_from_CPU[2]),
    .D3(Data_from_CPU[3]), .D4(Data_from_CPU[4]), .D5(Data_from_CPU[5]), .D6(Data_from_CPU[6]),
    .D7(Data_from_CPU[7]), .R_W(R_W__CPU), .Res(RES), .D4_2(Data_to_CPU[4]), .DMCINT(dpcm_channel_1_dmcint),
    .D7_2(Data_to_CPU[7]), .RUNDMC(dpcm_channel_1_rundmc), .DMCRDY(dpcm_channel_1_dmcrdy),
    .nDMC_AB(dpcm_channel_1_ndmc_ab), .DMC0(AUX_B[8]), .DMC1(AUX_B[9]), .DMC2(AUX_B[10]), .DMC3(AUX_B[11]),
    .DMC4(AUX_B[12]), .DMC5(AUX_B[13]), .DMC6(AUX_B[14]), .DMCA0(dpcm_channel_1_dmca0),
    .DMCA1(dpcm_channel_1_dmca1), .DMCA2(dpcm_channel_1_dmca2), .DMCA3(dpcm_channel_1_dmca3),
    .DMCA4(dpcm_channel_1_dmca4), .DMCA5(dpcm_channel_1_dmca5), .DMCA6(dpcm_channel_1_dmca6),
    .DMCA7(dpcm_channel_1_dmca7), .DMCA8(dpcm_channel_1_dmca8), .DMCA9(dpcm_channel_1_dmca9),
    .DMCA10(dpcm_channel_1_dmca10), .DMCA11(dpcm_channel_1_dmca11), .DMCA12(dpcm_channel_1_dmca12),
    .DMCA13(dpcm_channel_1_dmca13), .DMCA14(dpcm_channel_1_dmca14), .LOCK(LOCK));
  LENGTH_DOWN_COUNTER length_down_counter_3 (
    .ACLK1(ACLK1), .W400x(W4007), .LC7(length_table_1_lc7), .LC6(length_table_1_lc6),
    .LC5(length_table_1_lc5), .LC4(length_table_1_lc4), .LC3(length_table_1_lc3), .LC2(length_table_1_lc2),
    .LC1(length_table_1_lc1), .LC0(length_table_1_lc0), .HALT(square_channel_1_1_nsqb_lc),
    .NOxxx(length_down_counter_3_noxxx), .W4015(W4015), .Dx_2(Data_to_CPU[1]), .Dx(Data_from_CPU[1]),
    .RES(RES), .nLFO2(nLFO2), .nR4015(nR4015), .ACLK4(not_1_out));
  LENGTH_DOWN_COUNTER length_down_counter_4 (
    .ACLK1(ACLK1), .W400x(W4003), .LC7(length_table_1_lc7), .LC6(length_table_1_lc6),
    .LC5(length_table_1_lc5), .LC4(length_table_1_lc4), .LC3(length_table_1_lc3), .LC2(length_table_1_lc2),
    .LC1(length_table_1_lc1), .LC0(length_table_1_lc0), .HALT(square_channel_0_1_nsqa_lc),
    .NOxxx(length_down_counter_4_noxxx), .W4015(W4015), .Dx_2(Data_to_CPU[0]), .Dx(Data_from_CPU[0]),
    .RES(RES), .nLFO2(nLFO2), .nR4015(nR4015), .ACLK4(not_1_out));
  not not_2 (not_2_out, ACLK1);
  D_Flip_Flop #(.trigger("low")) d_ff_1 (
    .clk(not_2_out), .D(Data_from_CPU[7]), .Q(LOCK), .en(W401A), .reset(RES));  // open: Qn, preset
  REGISTER_SELECT register_select_1 (
    .PHI1(PHI1), .R_W(R_W__CPU), .A15(CPU_Ax[15]), .A14(CPU_Ax[14]), .A13(CPU_Ax[13]), .A12(CPU_Ax[12]),
    .A11(CPU_Ax[11]), .A10(CPU_Ax[10]), .A9(CPU_Ax[9]), .A8(CPU_Ax[8]), .A7(CPU_Ax[7]), .A6(CPU_Ax[6]),
    .A5(CPU_Ax[5]), .A4(sprite_dma_1_a0[4]), .A3(sprite_dma_1_a0[3]), .A2(sprite_dma_1_a0[2]),
    .A1(sprite_dma_1_a0[1]), .A0(sprite_dma_1_a0[0]), .W4000(W4000), .W4001(W4001), .W4002(W4002),
    .W4003(W4003), .W4004(W4004), .W4005(W4005), .W4006(W4006), .W4007(W4007), .W4008(W4008), .W400A(W400A),
    .W400B(W400B), .W400C(W400C), .W400E(W400E), .W400F(W400F), .W4010(W4010), .W4011(W4011), .W4012(W4012),
    .W4013(W4013), .W4014(W4014), .W4015(W4015), .W4016(W4016), .W4017(W4017), .nR4015(nR4015),
    .nR4016(nR4016), .nR4017(nR4017), .nR4018(nR4018), .nR4019(nR4019), .nR401A(nR401A), .W401A(W401A),
    .DBG(DBG__EXT), .nDBGRD(nDBGRD));
  LFO lfo_1 (
    .W4017(W4017), .D7(Data_from_CPU[7]), .D6(Data_from_CPU[6]), .Res(RES), .nR4015(nR4015),
    .DMCINT(dpcm_channel_1_dmcint), .nLFO1(nLFO1), .nLFO2(nLFO2), .INT(lfo_1_int), .D6_State(Data_to_CPU[6]),
    .PHI1(PHI1), .ACLK1(ACLK1), .nACLK2(nACLK2));
  ACLK aclk_1 (.PHI0(PHI0__CPU), .RES(RES), .PHI1(PHI1), .PHI2(PHI2), .nACLK2(nACLK2), .ACLK1(ACLK1));
  CLK_DIVIDER clk_divider_1 (
    .nCLK(io_control_1_nclk_int), .PHI2_CPU(PHI2_FromCore), .PHI0_CPU(PHI0__CPU), .nM2(clk_divider_1_nm2));
  IO_CONTROL io_control_1 (
    .nACLK2(nACLK2), .W4016(W4016), .D0(Data_from_CPU[0]), .D1(Data_from_CPU[1]), .D2(Data_from_CPU[2]),
    .nRES_PIN(nRES_PIN), .R_W_int(sprite_dma_1_r_w__to_r_w_ic_pin), .nR4016(nR4016), .nR4017(nR4017),
    .nNMI_INT(nNMI_CPU), .nIRQ_INT(nIRQ_CPU), .INT_from_apu(lfo_1_int), .nCLK_INT(io_control_1_nclk_int),
    .OUT0_PIN(OUT0), .OUT1_PIN(OUT1), .OUT2_PIN(OUT2), .MASTER_RESET(RES), .R_W_PIN(R_W__EXT),
    .IN0_PIN(nIN0), .IN1_PIN(nIN1), .nNMI_PIN(nNMI_PIN), .nIRQ_PIN(nIRQ_PIN), .CLK_PIN(CLK),
    .nM2(clk_divider_1_nm2), .M2(M2__EXT), .DBG(DBG__EXT), .Ax(AB), .APU_Ax(sprite_dma_1_a0),
    .DB_OUT(Data_to_CPU), .DB_OUT_EXT(DB_out), .WR(sprite_dma_1_wr), .DB_IN(Data_from_CPU),
    .DB_IN_EXT(DB_in), .ACLK1(ACLK1));

  // Other names for the same wires on the sheet: PHI2_CPU = PHI2_FromCore

  // Notes on the sheet:
  //   2A03 APU
  //   DMC[6:0]
  //   LENGTH COUNTER NOISE
  //   LENGTH COUNTER TRIANGLE
  //   LENGTH COUNTER SQUARE 1
  //   LENGTH COUNTER SQUARE 0
  //   LOCK FF
  //   CPU ADDRESS  BUS
  //   CLOCK 6502
  //   EXTERNAL DATA BUS
  //   EXTERNAL ADDRESS BUS
endmodule

module D_latch (
  input  EN,
  input  D,
  output Q,
  output NOT_Q
);

  D_Flip_Flop #(.trigger("high")) d_ff_1 (.clk(EN), .D(D), .Q(Q), .Qn(NOT_Q));  // open: preset, en, reset
endmodule

module LFO (
  input  nACLK2,
  input  ACLK1,
  input  W4017,
  input  D7,
  input  D6,
  input  Res,
  input  PHI1,
  input  nR4015,
  input  DMCINT,
  output nLFO1,
  output nLFO2,
  output D6_State,
  output INT
);

  wire _0, _0_t, _1, _1_t, _2, _2_t, _3, _3_t, _4, _4_t, _5, _5_t, _6, _6_t, _7, _7_t, _8, _8_t, _9, _9_t,
       _10, _10_t, _11, _11_t, _12, _12_t, _13, _13_t, _14, _14_t, and_1_out, and_2_out, d_ff_1_qn, d_ff_2_q,
       d_ff_3_qn, d_ff_4_qn, d_ff_5_qn, d_ff_6_qn, d_ff_7_qn, d_ff_8_qn, d_ff_9_qn, d_ff_10_qn, d_ff_11_qn,
       d_ff_12_qn, d_ff_13_qn, d_ff_14_qn, d_ff_15_qn, d_ff_16_qn, d_ff_17_qn, d_latch_1_not_q, d_latch_1_q,
       d_latch_2_not_q, d_latch_2_q, d_latch_3_q, Nor0_out, Nor1_out, Nor2_out, Nor3_out, Nor4_out, Nor5_out,
       nor_1_out, nor_2_out, nor_3_out, nor_4_out, nor_5_out, nor_6_out, nor_7_out, nor_8_out, nor_9_out,
       nor_10_out, nor_11_out, nor_12_out, nor_13_out, nor_14_out, nor_15_out, not_1_out, not_2_out,
       not_3_out;

  nor nor_1 (nor_1_out, nACLK2, d_latch_1_q);
  nor nor_2 (nor_2_out, nor_1_out, nor_3_out);
  nor nor_3 (nor_3_out, nor_2_out, W4017, Res);
  nor nor_4 (nor_4_out, Nor5_out, _14_t, _13_t);
  and and_1 (and_1_out, _14_t, _13_t);
  nor Nor5 (Nor5_out, _0_t, _1_t, _2_t, _3_t, _4_t, _5_t, _6_t, _7_t, _8_t, _9_t, _10_t, _11_t, _12_t, _13_t, _14_t);
  D_latch d_latch_1 (.EN(ACLK1), .D(nor_3_out), .Q(d_latch_1_q), .NOT_Q(d_latch_1_not_q));
  D_latch d_latch_2 (.EN(ACLK1), .D(d_ff_1_qn), .Q(d_latch_2_q), .NOT_Q(d_latch_2_not_q));
  not not_1 (not_1_out, ACLK1);
  D_Flip_Flop #(.trigger("high")) d_ff_1 (
    .clk(not_1_out), .D(D7), .Qn(d_ff_1_qn), .en(W4017));  // open: Q, preset, reset
  D_Flip_Flop #(.trigger("high")) d_ff_2 (
    .clk(not_1_out), .D(D6), .Q(d_ff_2_q), .en(W4017));  // open: Qn, preset, reset
  nor nor_5 (nor_5_out, nor_4_out, and_1_out);
  nor nor_6 (nor_6_out, not_2_out, nACLK2);
  nor nor_7 (nor_7_out, d_latch_1_q, d_latch_2_q);
  nor nor_8 (nor_8_out, nACLK2, nor_9_out);
  not not_2 (not_2_out, nor_9_out);
  nor nor_9 (nor_9_out, d_latch_1_not_q, Nor4_out, Nor3_out);
  D_Flip_Flop #(.trigger("high")) d_ff_3 (
    .clk(nor_6_out), .D(nor_5_out), .Qn(d_ff_3_qn), .preset(nor_8_out));  // open: Q, en, reset
  D_Flip_Flop #(.trigger("high")) d_ff_4 (
    .clk(nor_6_out), .D(_0_t), .Qn(d_ff_4_qn), .preset(nor_8_out));  // open: Q, en, reset
  D_Flip_Flop #(.trigger("high")) d_ff_5 (
    .clk(nor_6_out), .D(_1_t), .Qn(d_ff_5_qn), .preset(nor_8_out));  // open: Q, en, reset
  D_Flip_Flop #(.trigger("high")) d_ff_6 (
    .clk(nor_6_out), .D(_2_t), .Qn(d_ff_6_qn), .preset(nor_8_out));  // open: Q, en, reset
  D_Flip_Flop #(.trigger("high")) d_ff_7 (
    .clk(nor_6_out), .D(_3_t), .Qn(d_ff_7_qn), .preset(nor_8_out));  // open: Q, en, reset
  D_Flip_Flop #(.trigger("high")) d_ff_8 (
    .clk(nor_6_out), .D(_4_t), .Qn(d_ff_8_qn), .preset(nor_8_out));  // open: Q, en, reset
  D_Flip_Flop #(.trigger("high")) d_ff_9 (
    .clk(nor_6_out), .D(_5_t), .Qn(d_ff_9_qn), .preset(nor_8_out));  // open: Q, en, reset
  D_Flip_Flop #(.trigger("high")) d_ff_10 (
    .clk(nor_6_out), .D(_6_t), .Qn(d_ff_10_qn), .preset(nor_8_out));  // open: Q, en, reset
  D_Flip_Flop #(.trigger("high")) d_ff_11 (
    .clk(nor_6_out), .D(_7_t), .Qn(d_ff_11_qn), .preset(nor_8_out));  // open: Q, en, reset
  D_Flip_Flop #(.trigger("high")) d_ff_12 (
    .clk(nor_6_out), .D(_8_t), .Qn(d_ff_12_qn), .preset(nor_8_out));  // open: Q, en, reset
  D_Flip_Flop #(.trigger("high")) d_ff_13 (
    .clk(nor_6_out), .D(_9_t), .Qn(d_ff_13_qn), .preset(nor_8_out));  // open: Q, en, reset
  D_Flip_Flop #(.trigger("high")) d_ff_14 (
    .clk(nor_6_out), .D(_10_t), .Qn(d_ff_14_qn), .preset(nor_8_out));  // open: Q, en, reset
  D_Flip_Flop #(.trigger("high")) d_ff_15 (
    .clk(nor_6_out), .D(_11_t), .Qn(d_ff_15_qn), .preset(nor_8_out));  // open: Q, en, reset
  D_Flip_Flop #(.trigger("high")) d_ff_16 (
    .clk(nor_6_out), .D(_12_t), .Qn(d_ff_16_qn), .preset(nor_8_out));  // open: Q, en, reset
  D_Flip_Flop #(.trigger("high")) d_ff_17 (
    .clk(nor_6_out), .D(_13_t), .Qn(d_ff_17_qn), .preset(nor_8_out));  // open: Q, en, reset
  D_Flip_Flop #(.trigger("high")) d_ff_18 (.clk(ACLK1), .D(d_ff_3_qn), .Q(_0), .Qn(_0_t));  // open: preset, en, reset
  D_Flip_Flop #(.trigger("high")) d_ff_19 (.clk(ACLK1), .D(d_ff_4_qn), .Q(_1), .Qn(_1_t));  // open: preset, en, reset
  D_Flip_Flop #(.trigger("high")) d_ff_20 (.clk(ACLK1), .D(d_ff_5_qn), .Q(_2), .Qn(_2_t));  // open: preset, en, reset
  D_Flip_Flop #(.trigger("high")) d_ff_21 (.clk(ACLK1), .D(d_ff_6_qn), .Q(_3), .Qn(_3_t));  // open: preset, en, reset
  D_Flip_Flop #(.trigger("high")) d_ff_22 (.clk(ACLK1), .D(d_ff_7_qn), .Q(_4), .Qn(_4_t));  // open: preset, en, reset
  D_Flip_Flop #(.trigger("high")) d_ff_23 (.clk(ACLK1), .D(d_ff_8_qn), .Q(_5), .Qn(_5_t));  // open: preset, en, reset
  D_Flip_Flop #(.trigger("high")) d_ff_24 (.clk(ACLK1), .D(d_ff_9_qn), .Q(_6), .Qn(_6_t));  // open: preset, en, reset
  D_Flip_Flop #(.trigger("high")) d_ff_25 (.clk(ACLK1), .D(d_ff_10_qn), .Q(_7), .Qn(_7_t));  // open: preset, en, reset
  D_Flip_Flop #(.trigger("high")) d_ff_26 (.clk(ACLK1), .D(d_ff_11_qn), .Q(_8), .Qn(_8_t));  // open: preset, en, reset
  D_Flip_Flop #(.trigger("high")) d_ff_27 (.clk(ACLK1), .D(d_ff_12_qn), .Q(_9), .Qn(_9_t));  // open: preset, en, reset
  D_Flip_Flop #(.trigger("high")) d_ff_28 (
    .clk(ACLK1), .D(d_ff_13_qn), .Q(_10), .Qn(_10_t));  // open: preset, en, reset
  D_Flip_Flop #(.trigger("high")) d_ff_29 (
    .clk(ACLK1), .D(d_ff_14_qn), .Q(_11), .Qn(_11_t));  // open: preset, en, reset
  D_Flip_Flop #(.trigger("high")) d_ff_30 (
    .clk(ACLK1), .D(d_ff_15_qn), .Q(_12), .Qn(_12_t));  // open: preset, en, reset
  D_Flip_Flop #(.trigger("high")) d_ff_31 (
    .clk(ACLK1), .D(d_ff_16_qn), .Q(_13), .Qn(_13_t));  // open: preset, en, reset
  D_Flip_Flop #(.trigger("high")) d_ff_32 (
    .clk(ACLK1), .D(d_ff_17_qn), .Q(_14), .Qn(_14_t));  // open: preset, en, reset
  and and_2 (and_2_out, Nor3_out, d_ff_1_qn);
  nor nor_10 (nor_10_out, PHI1, nR4015);
  nor nor_11 (nor_11_out, and_2_out, nor_12_out);
  nor nor_12 (nor_12_out, nor_11_out, d_ff_2_q, Res, nor_10_out);
  D_latch d_latch_3 (.EN(ACLK1), .D(nor_11_out), .Q(d_latch_3_q));  // open: NOT_Q
  nor Nor0 (Nor0_out, _0, _1_t, _2_t, _3_t, _4_t, _5, _6, _7_t, _8_t, _9_t, _10_t, _11_t, _12, _13_t, _14_t);
  nor Nor1 (Nor1_out, _0, _1, _2_t, _3_t, _4_t, _5_t, _6_t, _7_t, _8_t, _9, _10, _11_t, _12, _13, _14_t);
  nor Nor2 (Nor2_out, _0, _1, _2_t, _3_t, _4, _5_t, _6, _7, _8_t, _9_t, _10, _11, _12_t, _13, _14_t);
  nor Nor3 (Nor3_out, _0, _1, _2, _3, _4, _5_t, _6_t, _7_t, _8_t, _9, _10_t, _11, _12_t, _13_t, _14_t, d_latch_2_not_q);
  nor Nor4 (Nor4_out, _0, _1_t, _2, _3_t, _4_t, _5_t, _6_t, _7, _8, _9_t, _10_t, _11_t, _12, _13, _14);
  assign D6_State = not_3_out ? ~d_latch_3_q : 1'bz;  // Controlled_Inverter controlled_inverter_1
  not not_3 (not_3_out, nR4015);
  nor nor_13 (nor_13_out, Nor0_out, Nor2_out, Nor1_out, Nor3_out, Nor4_out, nor_7_out);
  nor nor_14 (nor_14_out, Nor1_out, Nor3_out, Nor4_out, nor_7_out);
  nor nor_15 (nor_15_out, nor_12_out, DMCINT);
  not not_4 (INT, nor_15_out);
  or or_1 (nLFO1, nACLK2, nor_13_out);
  or or_2 (nLFO2, nACLK2, nor_14_out);

  // Notes on the sheet:
  //   Nor5=3728  X1
  //   Nor4=7456  X2
  //   Nor3=11184  X3
  //   Nor2=14914  X4
  //   Nor1=18640  X5
  //   R
  //   RS2
  //   S
  //   Nor0=16384  CARRY COUNT
  //   NOR6
  //   Q
  //   NORFF1
  //   CLEAR LFO
  //   NORFF2
  //   /Q
  //   NOR 5 NTSC = NOR5 PAL
  //   DL3
  //   DL6
  //   MD_Latch
  //   MODE  FLAG
  //   RESET INT FLAG
  //   Z1
  //   Z2
  //   4 OR 5 STEP
  //   IRQ DISABLE
  //   0
  //   1
  //   2
  //   3
  //   4
  //   5
  //   6
  //   7
  //   8
  //   9
  //   10
  //   11
  //   12
  //   13
  //   14
  //   S
  //   R
  //   INT FLAG
  //   NORFF2
  //   RS1
  //   NORFF1
  //   /Q
  //   Q
  //   INT STATUS
  //   0
  //   1
  //   NTSC   NOR  CONFIGURATION
  //   2
  //   3
  //   4
  //   NOR 5 NTSC = NOR5 PAL
  //   0
  //   1
  //   PAL   NOR  CONFIGURATION
  //   2
  //   3
  //   4
endmodule

module ACLK (
  input  PHI0,
  input  RES,
  output PHI1,
  output PHI2,
  output nACLK2,
  output ACLK1
);

  wire d_ff_1_qn, d_ff_2_qn, nor_1_out, nor_2_out, not_2_out;

  not not_1 (PHI1, PHI0);
  D_Flip_Flop #(.trigger("high")) d_ff_1 (.clk(PHI1), .D(nor_1_out), .Qn(d_ff_1_qn));  // open: Q, preset, en, reset
  not not_2 (not_2_out, PHI1);
  D_Flip_Flop #(.trigger("high")) d_ff_2 (.clk(PHI0), .D(d_ff_1_qn), .Qn(d_ff_2_qn));  // open: Q, preset, en, reset
  nor nor_1 (nor_1_out, RES, d_ff_2_qn);
  nor nor_2 (nor_2_out, nor_1_out, not_2_out);
  not not_3 (nACLK2, nor_2_out);
  nor nor_3 (ACLK1, not_2_out, d_ff_2_qn);

  assign PHI2 = PHI0;

  // Notes on the sheet:
  //   /ACLK2
  //   ACLK2
  //   PHI1
  //   PHI2
  //   ACLK1
  //   DL1
  //   INV1
  //   DL2
  //   NOR1
  //   NOR2
  //   NOR3
endmodule

// CLK DIVIDER
module CLK_DIVIDER (
  input  nCLK,
  input  PHI2_CPU,
  output PHI0_CPU,
  output nM2
);

  wire d_latch_1_not_q, d_latch_2_not_q, d_latch_3_not_q, d_latch_4_not_q, d_latch_5_not_q, d_latch_6_not_q,
       d_latch_7_not_q, d_latch_8_not_q, d_latch_10_not_q, d_latch_11_q, d_latch_12_q, d_latch_13_q,
       d_latch_14_q, d_latch_15_q, d_latch_16_q, demultiplexer_1_out0, demultiplexer_1_out1, nor_1_out,
       nor_2_out, nor_3_out, nor_5_out, nor_6_out, nor_7_out, nor_8_out, nor_9_out, nor_10_out, not_1_out,
       not_2_out, or_1_out;

  not not_1 (not_1_out, nCLK);
  not not_2 (not_2_out, not_1_out);
  nor nor_1 (nor_1_out, not_1_out, nor_2_out);
  nor nor_2 (nor_2_out, nor_1_out, not_2_out);
  D_latch d_latch_1 (.EN(nor_2_out), .D(d_latch_10_not_q), .NOT_Q(d_latch_1_not_q));  // open: Q
  D_latch d_latch_2 (.EN(nor_2_out), .D(nor_5_out), .NOT_Q(d_latch_2_not_q));  // open: Q
  D_latch d_latch_3 (.EN(nor_2_out), .D(nor_6_out), .NOT_Q(d_latch_3_not_q));  // open: Q
  D_latch d_latch_4 (.EN(nor_2_out), .D(nor_7_out), .NOT_Q(d_latch_4_not_q));  // open: Q
  D_latch d_latch_5 (.EN(nor_2_out), .D(nor_8_out), .NOT_Q(d_latch_5_not_q));  // open: Q
  D_latch d_latch_6 (.EN(nor_2_out), .D(or_1_out), .NOT_Q(d_latch_6_not_q));  // open: Q
  D_latch d_latch_7 (.EN(nor_2_out), .D(nor_10_out), .NOT_Q(d_latch_7_not_q));  // open: Q
  D_latch d_latch_8 (.EN(nor_2_out), .D(demultiplexer_1_out1), .NOT_Q(d_latch_8_not_q));  // open: Q
  D_latch d_latch_9 (.EN(nor_1_out), .D(d_latch_1_not_q), .Q(PHI0_CPU));  // open: NOT_Q
  D_latch d_latch_10 (.EN(nor_1_out), .D(d_latch_2_not_q), .NOT_Q(d_latch_10_not_q));  // open: Q
  D_latch d_latch_11 (.EN(nor_1_out), .D(d_latch_3_not_q), .Q(d_latch_11_q));  // open: NOT_Q
  D_latch d_latch_12 (.EN(nor_1_out), .D(d_latch_4_not_q), .Q(d_latch_12_q));  // open: NOT_Q
  D_latch d_latch_13 (.EN(nor_1_out), .D(d_latch_5_not_q), .Q(d_latch_13_q));  // open: NOT_Q
  D_latch d_latch_14 (.EN(nor_1_out), .D(d_latch_6_not_q), .Q(d_latch_14_q));  // open: NOT_Q
  D_latch d_latch_15 (.EN(nor_1_out), .D(d_latch_7_not_q), .Q(d_latch_15_q));  // open: NOT_Q
  D_latch d_latch_16 (.EN(nor_1_out), .D(d_latch_8_not_q), .Q(d_latch_16_q));  // open: NOT_Q
  nor nor_3 (nor_3_out, PHI0_CPU, d_latch_10_not_q);
  nor nor_4 (nM2, d_latch_2_not_q, PHI2_CPU);
  nor nor_5 (nor_5_out, nor_3_out, d_latch_11_q);
  nor nor_6 (nor_6_out, nor_3_out, d_latch_12_q);
  nor nor_7 (nor_7_out, nor_3_out, d_latch_13_q);
  nor nor_8 (nor_8_out, nor_3_out, d_latch_14_q);
  nor nor_9 (nor_9_out, nor_3_out, d_latch_15_q);
  nor nor_10 (nor_10_out, nor_3_out, d_latch_16_q);
  or or_1 (or_1_out, demultiplexer_1_out0, nor_9_out);
  Demultiplexer #(.disabled(0), .enable("false")) demultiplexer_1 (
    .out0(demultiplexer_1_out0), .out1(demultiplexer_1_out1), .in(PHI0_CPU), .sel(1'b0));

  // Notes on the sheet:
  //   INV2
  //   NOR1
  //   NOR2
  //   0 NTSC
  //   1 PAL
  //   #CLK
  //   PHI0 NTSC
  //   PHI0 PAL
endmodule

// REGISTER SELECT
module REGISTER_SELECT (
  input  PHI1,
  input  R_W,
  input  A15,
  input  A14,
  input  A13,
  input  A12,
  input  A11,
  input  A10,
  input  A9,
  input  A8,
  input  A7,
  input  A6,
  input  A5,
  input  A4,
  input  A3,
  input  A2,
  input  A1,
  input  A0,
  input  DBG,
  output W4000,
  output W4001,
  output W4002,
  output W4003,
  output W4004,
  output W4005,
  output W4006,
  output W4007,
  output W4008,
  output W400A,
  output W400B,
  output W400C,
  output W400E,
  output W400F,
  output W4010,
  output W4011,
  output W4012,
  output W4013,
  output W4014,
  output W4015,
  output W4016,
  output W4017,
  output W401A,
  output nR4015,
  output nR4016,
  output nR4017,
  output nR4018,
  output nR4019,
  output nR401A,
  output nDBGRD
);

  wire decoder_1_out21, decoder_1_out22, decoder_1_out23, decoder_1_out24, decoder_1_out25, decoder_1_out26,
       demultiplexer_1_out0, demultiplexer_1_out1, demultiplexer_2_out26, nor_1_out, not_1_out, not_2_out,
       not_3_out;

  not not_1 (not_1_out, A14);
  nor nor_1 (nor_1_out, A15, not_1_out, A13, A12, A11, A10, A9, A8, A7, A6, A5);
  Demultiplexer #(.enable("false")) demultiplexer_1 (
    .out0(demultiplexer_1_out0), .out1(demultiplexer_1_out1), .in(nor_1_out), .sel(R_W));
  not not_2 (not_2_out, PHI1);
  Demultiplexer #(.select(5), .disabled(0)) demultiplexer_2 (
    .out0(W4000), .out1(W4001), .out2(W4002), .out3(W4003), .out4(W4004), .out5(W4005), .out6(W4006),
    .out7(W4007), .out8(W4008), .out10(W400A), .out11(W400B), .out12(W400C), .out14(W400E), .out15(W400F),
    .out16(W4010), .out17(W4011), .out18(W4012), .out19(W4013), .out20(W4014), .out21(W4015), .out22(W4016),
    .out23(W4017), .out26(demultiplexer_2_out26), .in(not_2_out), .sel({A4, A3, A2, A1, A0}),
    .en(demultiplexer_1_out0));  // open: out9, out13, out24, out25, out27, out28, out29, out30, out31
  Decoder #(.select(5), .disabled(0)) decoder_1 (
    .out21(decoder_1_out21), .out22(decoder_1_out22), .out23(decoder_1_out23), .out24(decoder_1_out24),
    .out25(decoder_1_out25), .out26(decoder_1_out26), .sel({A4, A3, A2, A1, A0}), .en(demultiplexer_1_out1));  // open: out0, out1, out2, out3, out4, out5, out6, out7, out8, out9, out10, out11, out12, out13, out14, out15, out16, out17, out18, out19, out20, out27, out28, out29, out30, out31
  not not_3 (not_3_out, demultiplexer_1_out1);
  and and_1 (W401A, demultiplexer_2_out26, DBG);
  not not_4 (nR4015, decoder_1_out21);
  not not_5 (nR4016, decoder_1_out22);
  not not_6 (nR4017, decoder_1_out23);
  nand nand_1 (nR4018, decoder_1_out24, DBG);
  nand nand_2 (nR4019, decoder_1_out25, DBG);
  nand nand_3 (nR401A, decoder_1_out26, DBG);
  nand nand_4 (nDBGRD, DBG, not_3_out);

  // Notes on the sheet:
  //   REGWR
  //   Enable write ports
  //   REGRD
  //   Enable read ports
endmodule

// ENVELOPE GENERATOR
module ENVELOPE_GENERATOR (
  input  ACLK1,
  input  RES,
  input  W400_0__4__C,
  input  D0,
  input  D1,
  input  D2,
  input  D3,
  input  D4,
  input  D5,
  input  W400_3__7__F,
  input  nLFO1,
  input  CH_IN,
  output V0,
  output V1,
  output V2,
  output V3,
  output nCH_LC
);

  wire _7_out, _8_out, _11_out, _12_out, _13_out, _14_out, _15_out, _16_out, _18_out, _19_out, d_ff_1_q,
       d_ff_2_q, d_ff_3_q, d_ff_4_q, d_ff_5_q, d_ff_7_q, d_ff_7_qn, d_ff_8_q, d_ff_8_qn, d_ff_9_q, d_ff_9_qn,
       d_ff_10_q, d_ff_10_qn, d_ff_11_q, d_ff_11_qn, d_ff_12_q, d_ff_12_qn, d_ff_13_q, d_ff_13_qn, d_ff_14_q,
       d_ff_14_qn, d_ff_15_qn, d_ff_16_qn, d_ff_17_qn, d_ff_18_qn, d_ff_19_qn, d_ff_20_qn, d_ff_21_qn,
       d_ff_22_qn, d_latch_1_q, d_latch_2_not_q, d_latch_2_q, d_latch_3_q, d_latch_4_q, demultiplexer_1_out0,
       demultiplexer_1_out1, demultiplexer_2_out0, demultiplexer_2_out1, demultiplexer_3_out0,
       demultiplexer_3_out1, demultiplexer_4_out0, demultiplexer_4_out1, demultiplexer_5_out0,
       demultiplexer_5_out1, demultiplexer_6_out0, demultiplexer_6_out1, demultiplexer_7_out0,
       demultiplexer_7_out1, demultiplexer_8_out0, demultiplexer_8_out1, multiplexer_1_out,
       multiplexer_2_out, multiplexer_3_out, multiplexer_4_out, nor_1_out, nor_2_out, nor_3_out, nor_4_out,
       nor_5_out, nor_6_out, nor_7_out, nor_8_out, not_1_out, not_2_out, not_3_out, not_4_out, not_5_out,
       not_6_out, not_7_out, not_8_out, not_9_out, not_10_out, not_11_out, not_12_out, not_13_out,
       not_14_out, not_15_out, or_1_out, or_2_out, or_3_out, or_4_out, or_5_out, or_6_out, or_7_out,
       or_8_out, xor_1_out, xor_2_out, xor_3_out, xor_4_out, xor_5_out, xor_6_out, xor_7_out, xor_8_out;

  not not_1 (not_1_out, ACLK1);
  D_Flip_Flop #(.trigger("high")) d_ff_1 (
    .clk(not_1_out), .D(D0), .Q(d_ff_1_q), .en(W400_0__4__C));  // open: Qn, preset, reset
  D_Flip_Flop #(.trigger("high")) d_ff_2 (
    .clk(not_1_out), .D(D1), .Q(d_ff_2_q), .en(W400_0__4__C));  // open: Qn, preset, reset
  D_Flip_Flop #(.trigger("high")) d_ff_3 (
    .clk(not_1_out), .D(D2), .Q(d_ff_3_q), .en(W400_0__4__C));  // open: Qn, preset, reset
  D_Flip_Flop #(.trigger("high")) d_ff_4 (
    .clk(not_1_out), .D(D3), .Q(d_ff_4_q), .en(W400_0__4__C));  // open: Qn, preset, reset
  D_Flip_Flop #(.trigger("high")) d_ff_5 (
    .clk(not_1_out), .D(D4), .Q(d_ff_5_q), .en(W400_0__4__C));  // open: Qn, preset, reset
  D_Flip_Flop #(.trigger("high")) d_ff_6 (
    .clk(not_1_out), .D(D5), .Qn(nCH_LC), .en(W400_0__4__C));  // open: Q, preset, reset
  Demultiplexer #(.enable("false")) demultiplexer_1 (
    .out0(demultiplexer_1_out0), .out1(demultiplexer_1_out1), .in(_16_out), .sel(d_ff_1_q));
  Demultiplexer #(.enable("false")) demultiplexer_2 (
    .out0(demultiplexer_2_out0), .out1(demultiplexer_2_out1), .in(_16_out), .sel(d_ff_2_q));
  Demultiplexer #(.enable("false")) demultiplexer_3 (
    .out0(demultiplexer_3_out0), .out1(demultiplexer_3_out1), .in(_16_out), .sel(d_ff_3_q));
  Demultiplexer #(.enable("false")) demultiplexer_4 (
    .out0(demultiplexer_4_out0), .out1(demultiplexer_4_out1), .in(_16_out), .sel(d_ff_4_q));
  Demultiplexer #(.enable("false")) demultiplexer_5 (
    .out0(demultiplexer_5_out0), .out1(demultiplexer_5_out1), .in(_8_out), .sel(_12_out));
  Demultiplexer #(.enable("false")) demultiplexer_6 (
    .out0(demultiplexer_6_out0), .out1(demultiplexer_6_out1), .in(_8_out), .sel(_12_out));
  Demultiplexer #(.enable("false")) demultiplexer_7 (
    .out0(demultiplexer_7_out0), .out1(demultiplexer_7_out1), .in(_8_out), .sel(_12_out));
  Demultiplexer #(.enable("false")) demultiplexer_8 (
    .out0(demultiplexer_8_out0), .out1(demultiplexer_8_out1), .in(_8_out), .sel(_12_out));
  or or_1 (or_1_out, RES, demultiplexer_1_out0);
  or or_2 (or_2_out, RES, demultiplexer_2_out0);
  or or_3 (or_3_out, RES, demultiplexer_3_out0);
  or or_4 (or_4_out, RES, demultiplexer_4_out0);
  or or_5 (or_5_out, RES, demultiplexer_5_out0);
  or or_6 (or_6_out, RES, demultiplexer_6_out0);
  or or_7 (or_7_out, RES, demultiplexer_7_out0);
  or or_8 (or_8_out, RES, demultiplexer_8_out0);
  D_Flip_Flop #(.trigger("high")) d_ff_7 (
    .clk(_18_out), .D(d_ff_15_qn), .Q(d_ff_7_q), .Qn(d_ff_7_qn), .preset(demultiplexer_1_out1),
    .reset(or_1_out));  // open: en
  D_Flip_Flop #(.trigger("high")) d_ff_8 (
    .clk(_18_out), .D(d_ff_16_qn), .Q(d_ff_8_q), .Qn(d_ff_8_qn), .preset(demultiplexer_2_out1),
    .reset(or_2_out));  // open: en
  D_Flip_Flop #(.trigger("high")) d_ff_9 (
    .clk(_18_out), .D(d_ff_17_qn), .Q(d_ff_9_q), .Qn(d_ff_9_qn), .preset(demultiplexer_3_out1),
    .reset(or_3_out));  // open: en
  D_Flip_Flop #(.trigger("high")) d_ff_10 (
    .clk(_18_out), .D(d_ff_18_qn), .Q(d_ff_10_q), .Qn(d_ff_10_qn), .preset(demultiplexer_4_out1),
    .reset(or_4_out));  // open: en
  D_Flip_Flop #(.trigger("high")) d_ff_11 (
    .clk(_7_out), .D(d_ff_19_qn), .Q(d_ff_11_q), .Qn(d_ff_11_qn), .preset(demultiplexer_5_out1),
    .reset(or_5_out));  // open: en
  D_Flip_Flop #(.trigger("high")) d_ff_12 (
    .clk(_7_out), .D(d_ff_20_qn), .Q(d_ff_12_q), .Qn(d_ff_12_qn), .preset(demultiplexer_6_out1),
    .reset(or_6_out));  // open: en
  D_Flip_Flop #(.trigger("high")) d_ff_13 (
    .clk(_7_out), .D(d_ff_21_qn), .Q(d_ff_13_q), .Qn(d_ff_13_qn), .preset(demultiplexer_7_out1),
    .reset(or_7_out));  // open: en
  D_Flip_Flop #(.trigger("high")) d_ff_14 (
    .clk(_7_out), .D(d_ff_22_qn), .Q(d_ff_14_q), .Qn(d_ff_14_qn), .preset(demultiplexer_8_out1),
    .reset(or_8_out));  // open: en
  not not_2 (not_2_out, 1'b1);
  not not_3 (not_3_out, nor_1_out);
  not not_4 (not_4_out, nor_2_out);
  not not_5 (not_5_out, nor_3_out);
  nor _15 (_15_out, _19_out, _14_out);
  nor _14 (_14_out, _15_out, W400_3__7__F);
  nor _13 (_13_out, nor_4_out, _15_out);
  not not_6 (not_6_out, 1'b1);
  not not_7 (not_7_out, nor_5_out);
  not not_8 (not_8_out, nor_6_out);
  not not_9 (not_9_out, nor_7_out);
  xor xor_1 (xor_1_out, 1'b1, d_ff_7_qn);
  nor nor_1 (nor_1_out, not_2_out, d_ff_7_q);
  xor xor_2 (xor_2_out, nor_1_out, d_ff_8_qn);
  nor nor_2 (nor_2_out, not_3_out, d_ff_8_q);
  xor xor_3 (xor_3_out, nor_2_out, d_ff_9_qn);
  nor nor_3 (nor_3_out, not_4_out, d_ff_9_q);
  xor xor_4 (xor_4_out, nor_3_out, d_ff_10_qn);
  nor nor_4 (nor_4_out, not_5_out, d_ff_10_q);
  D_latch d_latch_1 (.EN(ACLK1), .D(_14_out), .Q(d_latch_1_q));  // open: NOT_Q
  D_latch d_latch_2 (.EN(ACLK1), .D(_13_out), .Q(d_latch_2_q), .NOT_Q(d_latch_2_not_q));
  xor xor_5 (xor_5_out, 1'b1, d_ff_11_qn);
  nor nor_5 (nor_5_out, not_6_out, d_ff_11_q);
  xor xor_6 (xor_6_out, nor_5_out, d_ff_12_qn);
  nor nor_6 (nor_6_out, not_7_out, d_ff_12_q);
  xor xor_7 (xor_7_out, nor_6_out, d_ff_13_qn);
  nor nor_7 (nor_7_out, not_8_out, d_ff_13_q);
  xor xor_8 (xor_8_out, nor_7_out, d_ff_14_qn);
  nor nor_8 (nor_8_out, not_9_out, _15_out, d_ff_14_q);
  D_Flip_Flop #(.trigger("high")) d_ff_15 (.clk(ACLK1), .D(xor_1_out), .Qn(d_ff_15_qn));  // open: Q, preset, en, reset
  D_Flip_Flop #(.trigger("high")) d_ff_16 (.clk(ACLK1), .D(xor_2_out), .Qn(d_ff_16_qn));  // open: Q, preset, en, reset
  D_Flip_Flop #(.trigger("high")) d_ff_17 (.clk(ACLK1), .D(xor_3_out), .Qn(d_ff_17_qn));  // open: Q, preset, en, reset
  D_Flip_Flop #(.trigger("high")) d_ff_18 (.clk(ACLK1), .D(xor_4_out), .Qn(d_ff_18_qn));  // open: Q, preset, en, reset
  nor _19 (_19_out, d_latch_1_q, nLFO1);
  nor _16 (_16_out, nLFO1, d_latch_2_q);
  nor _18 (_18_out, d_latch_2_not_q, nLFO1);
  D_Flip_Flop #(.trigger("high")) d_ff_19 (.clk(ACLK1), .D(xor_5_out), .Qn(d_ff_19_qn));  // open: Q, preset, en, reset
  D_Flip_Flop #(.trigger("high")) d_ff_20 (.clk(ACLK1), .D(xor_6_out), .Qn(d_ff_20_qn));  // open: Q, preset, en, reset
  D_Flip_Flop #(.trigger("high")) d_ff_21 (.clk(ACLK1), .D(xor_7_out), .Qn(d_ff_21_qn));  // open: Q, preset, en, reset
  D_Flip_Flop #(.trigger("high")) d_ff_22 (.clk(ACLK1), .D(xor_8_out), .Qn(d_ff_22_qn));  // open: Q, preset, en, reset
  D_latch d_latch_3 (.EN(ACLK1), .D(nor_8_out), .Q(d_latch_3_q));  // open: NOT_Q
  D_latch d_latch_4 (.EN(ACLK1), .D(_15_out), .Q(d_latch_4_q));  // open: NOT_Q
  nand _12 (_12_out, d_latch_3_q, nCH_LC);
  nor _11 (_11_out, d_latch_3_q, d_latch_4_q);
  not not_10 (not_10_out, _11_out);
  not not_11 (not_11_out, _16_out);
  nor _7 (_7_out, not_10_out, not_11_out);
  nor _8 (_8_out, _11_out, not_11_out);
  Multiplexer #(.enable("false")) multiplexer_1 (
    .in0(d_ff_11_q), .in1(d_ff_1_q), .out(multiplexer_1_out), .sel(d_ff_5_q));
  not not_12 (not_12_out, multiplexer_1_out);
  Multiplexer #(.enable("false")) multiplexer_2 (
    .in0(d_ff_12_q), .in1(d_ff_2_q), .out(multiplexer_2_out), .sel(d_ff_5_q));
  not not_13 (not_13_out, multiplexer_2_out);
  Multiplexer #(.enable("false")) multiplexer_3 (
    .in0(d_ff_13_q), .in1(d_ff_3_q), .out(multiplexer_3_out), .sel(d_ff_5_q));
  not not_14 (not_14_out, multiplexer_3_out);
  Multiplexer #(.enable("false")) multiplexer_4 (
    .in0(d_ff_14_q), .in1(d_ff_4_q), .out(multiplexer_4_out), .sel(d_ff_5_q));
  not not_15 (not_15_out, multiplexer_4_out);
  nor nor_9 (V0, not_12_out, CH_IN);
  nor nor_10 (V1, not_13_out, CH_IN);
  nor nor_11 (V2, not_14_out, CH_IN);
  nor nor_12 (V3, not_15_out, CH_IN);

  // Notes on the sheet:
  //   W4000(SQR A)
  //   W4004 (SQR B)
  //   W400C (NOISE)
  //   W4003 (SQR A)
  //   W4007 (SQR B)
  //   W400F (NOISE)
  //   ENVDIS
  //   #SQA(B)(NOISE)/LC
  //   RELOAD
  //   ENVELOPE DECAY DOWN COUNTER
  //   R
  //   RS1
  //   S
  //   ENVELOPE DOWN COUNTER
  //   Q
  //   /Q
  //   DL6
  //   DL10
  //   The signal names are shown for the noise channel. For square channels A and B, the designation changes instead of N to A or B, respectively
  //   RLOAD
  //   RSTEP
  //   DL7
  //   DL9
  //   VOL0
  //   VOL1
  //   VOL2
  //   VOL3
  //   ENV0
  //   ENV1
  //   ENV2
  //   ENV3
  //   RLOAD
  //   EIN
  //   10
  //   9
  //   ENVDIS
  //   ESTEP
  //   ERES
endmodule

// SQUARE CHANNEL 0
module SQUARE_CHANNEL_0 (
  input  nACLK2,
  input  ACLK1,
  input  W4003,
  input  W4000,
  input  W4002,
  input  D0,
  input  D1,
  input  D2,
  input  D3,
  input  D4,
  input  D5,
  input  D6,
  input  D7,
  input  LOCK,
  input  W4001,
  input  nLFO2,
  input  RES,
  input  NOSQA,
  input  nLFO1,
  output SQA0,
  output SQA1,
  output SQ2,
  output SQA3,
  output nSQA_LC
);

  wire d_latch_1_q, nor_1_out, nor_2_out, nor_3_out, not_1_out, not_2_out, not_3_out, square_adder_1_ncout,
       square_barrel_shifter_1_s0, square_barrel_shifter_1_s1, square_barrel_shifter_1_s2,
       square_barrel_shifter_1_s3, square_barrel_shifter_1_s4, square_barrel_shifter_1_s5,
       square_barrel_shifter_1_s6, square_barrel_shifter_1_s7, square_barrel_shifter_1_s8,
       square_barrel_shifter_1_s9, square_barrel_shifter_1_s10, square_duty_down_counter_1_sqout,
       square_frequency_down_counter_1_fload, square_frequency_down_counter_1_fqout, square_register_1_mu0,
       square_register_1_mu1, square_register_1_mu2, square_register_1_mu3, square_register_1_mu4,
       square_register_1_mu5, square_register_1_mu6, square_register_1_mu7, square_register_1_mu8,
       square_register_1_mu9, square_register_1_mu10, square_sweep_control_1_d_i,
       square_sweep_control_1_do_sweep, square_sweep_control_1_sw_ovf;
  wire [2:0] square_sweep_control_1_sr0;
  wire [10:0] square_adder_1_nsum0, square_register_1_f0;

  not not_1 (not_1_out, nACLK2);
  SQUARE_SWEEP_CONTROL square_sweep_control_1 (
    .ACLK1(ACLK1), .W400x(W4001), .D0(D0), .D1(D1), .D2(D2), .D3(D3), .D4(D4), .D5(D5), .D6(D6), .D7(D7),
    .nLFO2(nLFO2), .NOSQA(NOSQA), .nCOUT(square_adder_1_ncout), .SW_UVF(nor_3_out), .RES(RES),
    .SR0(square_sweep_control_1_sr0[0]), .SR1(square_sweep_control_1_sr0[1]),
    .SR2(square_sweep_control_1_sr0[2]), .D_I(square_sweep_control_1_d_i),
    .DO_SWEEP(square_sweep_control_1_do_sweep), .SW_OVF(square_sweep_control_1_sw_ovf));
  not not_2 (not_2_out, square_sweep_control_1_d_i);
  SQUARE_REGISTER square_register_1 (
    .ACLK1(ACLK1), .ACLK3(not_1_out), .W4002(W4002), .W4003(W4003), .D0(D0), .D1(D1), .D2(D2), .D3(D3),
    .D4(D4), .D5(D5), .D6(D6), .D7(D7), .D_I(square_sweep_control_1_d_i), .F0(square_register_1_f0[0]),
    .MU0(square_register_1_mu0), .nSum0(square_adder_1_nsum0[0]), .F1(square_register_1_f0[1]),
    .MU1(square_register_1_mu1), .nSum1(square_adder_1_nsum0[1]), .F2(square_register_1_f0[2]),
    .MU2(square_register_1_mu2), .nSum2(square_adder_1_nsum0[2]), .F3(square_register_1_f0[3]),
    .MU3(square_register_1_mu3), .nSum3(square_adder_1_nsum0[3]), .F4(square_register_1_f0[4]),
    .MU4(square_register_1_mu4), .nSum4(square_adder_1_nsum0[4]), .F5(square_register_1_f0[5]),
    .MU5(square_register_1_mu5), .nSum5(square_adder_1_nsum0[5]), .F6(square_register_1_f0[6]),
    .MU6(square_register_1_mu6), .nSum6(square_adder_1_nsum0[6]), .F7(square_register_1_f0[7]),
    .MU7(square_register_1_mu7), .nSum7(square_adder_1_nsum0[7]), .F8(square_register_1_f0[8]),
    .MU8(square_register_1_mu8), .nSum8(square_adder_1_nsum0[8]), .F9(square_register_1_f0[9]),
    .MU9(square_register_1_mu9), .nSum9(square_adder_1_nsum0[9]), .F10(square_register_1_f0[10]),
    .MU10(square_register_1_mu10), .DO_SWEEP(square_sweep_control_1_do_sweep),
    .nSum10(square_adder_1_nsum0[10]));
  SQUARE_BARREL_SHIFTER square_barrel_shifter_1 (
    .MUI0(square_register_1_mu0), .MUI1(square_register_1_mu1), .MUI2(square_register_1_mu2),
    .MUI3(square_register_1_mu3), .MUI4(square_register_1_mu4), .MUI5(square_register_1_mu5),
    .MUI6(square_register_1_mu6), .MUI7(square_register_1_mu7), .MUI8(square_register_1_mu8),
    .MUI9(square_register_1_mu9), .MUI10(square_register_1_mu10), .Dec_Inc(square_sweep_control_1_d_i),
    .SR0(square_sweep_control_1_sr0[0]), .SR1(square_sweep_control_1_sr0[1]),
    .SR2(square_sweep_control_1_sr0[2]), .S0(square_barrel_shifter_1_s0), .S1(square_barrel_shifter_1_s1),
    .S2(square_barrel_shifter_1_s2), .S3(square_barrel_shifter_1_s3), .S4(square_barrel_shifter_1_s4),
    .S5(square_barrel_shifter_1_s5), .S6(square_barrel_shifter_1_s6), .S7(square_barrel_shifter_1_s7),
    .S8(square_barrel_shifter_1_s8), .S9(square_barrel_shifter_1_s9), .S10(square_barrel_shifter_1_s10));
  not not_3 (not_3_out, square_duty_down_counter_1_sqout);
  SQUARE_ADDER square_adder_1 (
    .nCIN(1'b1), .FX0(square_register_1_f0[0]), .nSum0(square_adder_1_nsum0[0]),
    .SX0(square_barrel_shifter_1_s0), .FX1(square_register_1_f0[1]), .nSum1(square_adder_1_nsum0[1]),
    .SX1(square_barrel_shifter_1_s1), .FX2(square_register_1_f0[2]), .nSum2(square_adder_1_nsum0[2]),
    .SX2(square_barrel_shifter_1_s2), .FX3(square_register_1_f0[3]), .nSum3(square_adder_1_nsum0[3]),
    .SX3(square_barrel_shifter_1_s3), .FX4(square_register_1_f0[4]), .nSum4(square_adder_1_nsum0[4]),
    .SX4(square_barrel_shifter_1_s4), .FX5(square_register_1_f0[5]), .nSum5(square_adder_1_nsum0[5]),
    .SX5(square_barrel_shifter_1_s5), .FX6(square_register_1_f0[6]), .nSum6(square_adder_1_nsum0[6]),
    .SX6(square_barrel_shifter_1_s6), .FX7(square_register_1_f0[7]), .nSum7(square_adder_1_nsum0[7]),
    .SX7(square_barrel_shifter_1_s7), .FX8(square_register_1_f0[8]), .nSum8(square_adder_1_nsum0[8]),
    .SX8(square_barrel_shifter_1_s8), .FX9(square_register_1_f0[9]), .nSum9(square_adder_1_nsum0[9]),
    .SX9(square_barrel_shifter_1_s9), .nCOUT(square_adder_1_ncout), .FX10(square_register_1_f0[10]),
    .SX10(square_barrel_shifter_1_s10), .nSum10(square_adder_1_nsum0[10]));
  nor nor_1 (nor_1_out, nor_3_out, not_3_out, square_sweep_control_1_sw_ovf, NOSQA);
  D_latch d_latch_1 (.EN(ACLK1), .D(nor_1_out), .Q(d_latch_1_q));  // open: NOT_Q
  nor nor_2 (nor_2_out, d_latch_1_q, LOCK);
  nor nor_3 (nor_3_out, square_register_1_f0[2], square_register_1_f0[3], square_register_1_f0[4], square_register_1_f0[5], square_register_1_f0[6], square_register_1_f0[7], square_register_1_f0[8], square_register_1_f0[9], square_register_1_f0[10]);
  SQUARE_FREQUENCY_DOWN_COUNTER square_frequency_down_counter_1 (
    .ACLK1(ACLK1), .nACLK2(nACLK2), .RES(RES), .PL0(square_register_1_f0[0]), .PL1(square_register_1_f0[1]),
    .PL2(square_register_1_f0[2]), .PL3(square_register_1_f0[3]), .PL4(square_register_1_f0[4]),
    .PL5(square_register_1_f0[5]), .PL6(square_register_1_f0[6]), .PL7(square_register_1_f0[7]),
    .PL8(square_register_1_f0[8]), .PL9(square_register_1_f0[9]), .PL10(square_register_1_f0[10]),
    .FQOUT(square_frequency_down_counter_1_fqout), .FLOAD(square_frequency_down_counter_1_fload));
  SQUARE_DUTY_DOWN_COUNTER square_duty_down_counter_1 (
    .ACLK1(ACLK1), .FQOUT(square_frequency_down_counter_1_fqout), .RES(RES), .W4003(W4003),
    .FLOAD(square_frequency_down_counter_1_fload), .W4000(W4000), .D6(D6), .D7(D7),
    .SQOUT(square_duty_down_counter_1_sqout));
  ENVELOPE_GENERATOR envelope_generator_1 (
    .ACLK1(ACLK1), .W400_0__4__C(W4000), .W400_3__7__F(W4003), .D0(D0), .D1(D1), .D2(D2), .D3(D3), .D4(D4),
    .D5(D5), .nLFO1(nLFO1), .RES(RES), .V0(SQA0), .V1(SQA1), .V2(SQ2), .V3(SQA3), .nCH_LC(nSQA_LC),
    .CH_IN(nor_2_out));

  // Notes on the sheet:
  //   Connect to VCC for square0, connect to inverter for square1
  //   !!!
  //   INV5
  //   SW_UVF
endmodule

// SQUARE CHANNEL 1
module SQUARE_CHANNEL_1 (
  input  nACLK2,
  input  ACLK1,
  input  W4004,
  input  W4007,
  input  W4006,
  input  D0,
  input  D1,
  input  D2,
  input  D3,
  input  D4,
  input  D5,
  input  D6,
  input  D7,
  input  LOCK,
  input  W4005,
  input  nLFO2,
  input  RES,
  input  NOSQB,
  input  nLFO1,
  output SQB0,
  output SQB1,
  output SQB2,
  output SQB3,
  output nSQB_LC
);

  wire d_latch_1_q, nor_1_out, nor_2_out, nor_3_out, not_1_out, not_2_out, not_3_out, square_adder_1_ncout,
       square_barrel_shifter_1_s0, square_barrel_shifter_1_s1, square_barrel_shifter_1_s2,
       square_barrel_shifter_1_s3, square_barrel_shifter_1_s4, square_barrel_shifter_1_s5,
       square_barrel_shifter_1_s6, square_barrel_shifter_1_s7, square_barrel_shifter_1_s8,
       square_barrel_shifter_1_s9, square_barrel_shifter_1_s10, square_duty_down_counter_1_sqout,
       square_frequency_down_counter_1_fload, square_frequency_down_counter_1_fqout, square_register_1_mu0,
       square_register_1_mu1, square_register_1_mu2, square_register_1_mu3, square_register_1_mu4,
       square_register_1_mu5, square_register_1_mu6, square_register_1_mu7, square_register_1_mu8,
       square_register_1_mu9, square_register_1_mu10, square_sweep_control_1_d_i,
       square_sweep_control_1_do_sweep, square_sweep_control_1_sw_ovf;
  wire [2:0] square_sweep_control_1_sr0;
  wire [10:0] square_adder_1_nsum0, square_register_1_f0;

  not not_1 (not_1_out, square_sweep_control_1_d_i);
  not not_2 (not_2_out, nACLK2);
  SQUARE_SWEEP_CONTROL square_sweep_control_1 (
    .ACLK1(ACLK1), .W400x(W4005), .D0(D0), .D1(D1), .D2(D2), .D3(D3), .D4(D4), .D5(D5), .D6(D6), .D7(D7),
    .nLFO2(nLFO2), .NOSQA(NOSQB), .nCOUT(square_adder_1_ncout), .SW_UVF(nor_3_out), .RES(RES),
    .SR0(square_sweep_control_1_sr0[0]), .SR1(square_sweep_control_1_sr0[1]),
    .SR2(square_sweep_control_1_sr0[2]), .D_I(square_sweep_control_1_d_i),
    .DO_SWEEP(square_sweep_control_1_do_sweep), .SW_OVF(square_sweep_control_1_sw_ovf));
  SQUARE_REGISTER square_register_1 (
    .ACLK1(ACLK1), .ACLK3(not_2_out), .W4002(W4006), .W4003(W4007), .D0(D0), .D1(D1), .D2(D2), .D3(D3),
    .D4(D4), .D5(D5), .D6(D6), .D7(D7), .D_I(square_sweep_control_1_d_i), .F0(square_register_1_f0[0]),
    .MU0(square_register_1_mu0), .nSum0(square_adder_1_nsum0[0]), .F1(square_register_1_f0[1]),
    .MU1(square_register_1_mu1), .nSum1(square_adder_1_nsum0[1]), .F2(square_register_1_f0[2]),
    .MU2(square_register_1_mu2), .nSum2(square_adder_1_nsum0[2]), .F3(square_register_1_f0[3]),
    .MU3(square_register_1_mu3), .nSum3(square_adder_1_nsum0[3]), .F4(square_register_1_f0[4]),
    .MU4(square_register_1_mu4), .nSum4(square_adder_1_nsum0[4]), .F5(square_register_1_f0[5]),
    .MU5(square_register_1_mu5), .nSum5(square_adder_1_nsum0[5]), .F6(square_register_1_f0[6]),
    .MU6(square_register_1_mu6), .nSum6(square_adder_1_nsum0[6]), .F7(square_register_1_f0[7]),
    .MU7(square_register_1_mu7), .nSum7(square_adder_1_nsum0[7]), .F8(square_register_1_f0[8]),
    .MU8(square_register_1_mu8), .nSum8(square_adder_1_nsum0[8]), .F9(square_register_1_f0[9]),
    .MU9(square_register_1_mu9), .nSum9(square_adder_1_nsum0[9]), .F10(square_register_1_f0[10]),
    .MU10(square_register_1_mu10), .DO_SWEEP(square_sweep_control_1_do_sweep),
    .nSum10(square_adder_1_nsum0[10]));
  SQUARE_BARREL_SHIFTER square_barrel_shifter_1 (
    .MUI0(square_register_1_mu0), .MUI1(square_register_1_mu1), .MUI2(square_register_1_mu2),
    .MUI3(square_register_1_mu3), .MUI4(square_register_1_mu4), .MUI5(square_register_1_mu5),
    .MUI6(square_register_1_mu6), .MUI7(square_register_1_mu7), .MUI8(square_register_1_mu8),
    .MUI9(square_register_1_mu9), .MUI10(square_register_1_mu10), .Dec_Inc(square_sweep_control_1_d_i),
    .SR0(square_sweep_control_1_sr0[0]), .SR1(square_sweep_control_1_sr0[1]),
    .SR2(square_sweep_control_1_sr0[2]), .S0(square_barrel_shifter_1_s0), .S1(square_barrel_shifter_1_s1),
    .S2(square_barrel_shifter_1_s2), .S3(square_barrel_shifter_1_s3), .S4(square_barrel_shifter_1_s4),
    .S5(square_barrel_shifter_1_s5), .S6(square_barrel_shifter_1_s6), .S7(square_barrel_shifter_1_s7),
    .S8(square_barrel_shifter_1_s8), .S9(square_barrel_shifter_1_s9), .S10(square_barrel_shifter_1_s10));
  not not_3 (not_3_out, square_duty_down_counter_1_sqout);
  SQUARE_ADDER square_adder_1 (
    .nCIN(not_1_out), .FX0(square_register_1_f0[0]), .nSum0(square_adder_1_nsum0[0]),
    .SX0(square_barrel_shifter_1_s0), .FX1(square_register_1_f0[1]), .nSum1(square_adder_1_nsum0[1]),
    .SX1(square_barrel_shifter_1_s1), .FX2(square_register_1_f0[2]), .nSum2(square_adder_1_nsum0[2]),
    .SX2(square_barrel_shifter_1_s2), .FX3(square_register_1_f0[3]), .nSum3(square_adder_1_nsum0[3]),
    .SX3(square_barrel_shifter_1_s3), .FX4(square_register_1_f0[4]), .nSum4(square_adder_1_nsum0[4]),
    .SX4(square_barrel_shifter_1_s4), .FX5(square_register_1_f0[5]), .nSum5(square_adder_1_nsum0[5]),
    .SX5(square_barrel_shifter_1_s5), .FX6(square_register_1_f0[6]), .nSum6(square_adder_1_nsum0[6]),
    .SX6(square_barrel_shifter_1_s6), .FX7(square_register_1_f0[7]), .nSum7(square_adder_1_nsum0[7]),
    .SX7(square_barrel_shifter_1_s7), .FX8(square_register_1_f0[8]), .nSum8(square_adder_1_nsum0[8]),
    .SX8(square_barrel_shifter_1_s8), .FX9(square_register_1_f0[9]), .nSum9(square_adder_1_nsum0[9]),
    .SX9(square_barrel_shifter_1_s9), .nCOUT(square_adder_1_ncout), .FX10(square_register_1_f0[10]),
    .SX10(square_barrel_shifter_1_s10), .nSum10(square_adder_1_nsum0[10]));
  nor nor_1 (nor_1_out, nor_3_out, not_3_out, square_sweep_control_1_sw_ovf, NOSQB);
  D_latch d_latch_1 (.EN(ACLK1), .D(nor_1_out), .Q(d_latch_1_q));  // open: NOT_Q
  nor nor_2 (nor_2_out, d_latch_1_q, LOCK);
  nor nor_3 (nor_3_out, square_register_1_f0[2], square_register_1_f0[3], square_register_1_f0[4], square_register_1_f0[5], square_register_1_f0[6], square_register_1_f0[7], square_register_1_f0[8], square_register_1_f0[9], square_register_1_f0[10]);
  SQUARE_FREQUENCY_DOWN_COUNTER square_frequency_down_counter_1 (
    .ACLK1(ACLK1), .nACLK2(nACLK2), .RES(RES), .PL0(square_register_1_f0[0]), .PL1(square_register_1_f0[1]),
    .PL2(square_register_1_f0[2]), .PL3(square_register_1_f0[3]), .PL4(square_register_1_f0[4]),
    .PL5(square_register_1_f0[5]), .PL6(square_register_1_f0[6]), .PL7(square_register_1_f0[7]),
    .PL8(square_register_1_f0[8]), .PL9(square_register_1_f0[9]), .PL10(square_register_1_f0[10]),
    .FQOUT(square_frequency_down_counter_1_fqout), .FLOAD(square_frequency_down_counter_1_fload));
  SQUARE_DUTY_DOWN_COUNTER square_duty_down_counter_1 (
    .ACLK1(ACLK1), .FQOUT(square_frequency_down_counter_1_fqout), .RES(RES), .W4003(W4007),
    .FLOAD(square_frequency_down_counter_1_fload), .W4000(W4004), .D6(D6), .D7(D7),
    .SQOUT(square_duty_down_counter_1_sqout));
  ENVELOPE_GENERATOR envelope_generator_1 (
    .ACLK1(ACLK1), .W400_0__4__C(W4004), .W400_3__7__F(W4007), .D0(D0), .D1(D1), .D2(D2), .D3(D3), .D4(D4),
    .D5(D5), .nLFO1(nLFO1), .RES(RES), .V0(SQB0), .V1(SQB1), .V2(SQB2), .V3(SQB3), .nCH_LC(nSQB_LC),
    .CH_IN(nor_2_out));

  // Notes on the sheet:
  //   Connect to VCC for square0, connect to inverter for square1
  //   !!!
  //   INV5
  //   SW_UVF
endmodule

// SQUARE REGISTER
module SQUARE_REGISTER (
  input  ACLK3,
  input  ACLK1,
  input  W4002,
  input  D0,
  input  nSum0,
  input  D1,
  input  nSum1,
  input  D2,
  input  nSum2,
  input  D3,
  input  nSum3,
  input  D4,
  input  nSum4,
  input  D5,
  input  nSum5,
  input  D6,
  input  nSum6,
  input  D7,
  input  nSum7,
  input  nSum8,
  input  nSum9,
  input  nSum10,
  input  DO_SWEEP,
  input  W4003,
  input  D_I,
  output F0,
  output MU0,
  output F1,
  output MU1,
  output F2,
  output MU2,
  output F3,
  output MU3,
  output F4,
  output MU4,
  output F5,
  output MU5,
  output F6,
  output MU6,
  output F7,
  output MU7,
  output F8,
  output MU8,
  output F9,
  output MU9,
  output F10,
  output MU10
);

  wire d_ff_1_q, d_ff_2_q, d_ff_3_q, d_ff_4_q, d_ff_5_q, d_ff_6_q, d_ff_7_q, d_ff_8_q, d_ff_9_q, d_ff_10_q,
       d_ff_11_q, demultiplexer_1_out0, demultiplexer_1_out1, demultiplexer_2_out0, demultiplexer_2_out1,
       demultiplexer_3_out0, demultiplexer_3_out1, demultiplexer_4_out0, demultiplexer_4_out1,
       demultiplexer_5_out0, demultiplexer_5_out1, demultiplexer_6_out0, demultiplexer_6_out1,
       demultiplexer_7_out0, demultiplexer_7_out1, demultiplexer_8_out0, demultiplexer_8_out1,
       demultiplexer_9_out0, demultiplexer_9_out1, demultiplexer_10_out0, demultiplexer_10_out1,
       demultiplexer_11_out0, demultiplexer_11_out1, not_1_out;

  not not_1 (not_1_out, ACLK3);
  D_Flip_Flop #(.trigger("high")) d_ff_1 (.clk(ACLK1), .D(nSum0), .Q(d_ff_1_q));  // open: Qn, preset, en, reset
  Demultiplexer #(.enable("false")) demultiplexer_1 (
    .out0(demultiplexer_1_out0), .out1(demultiplexer_1_out1), .in(DO_SWEEP), .sel(d_ff_1_q));
  D_Flip_Flop #(.trigger("high")) d_ff_2 (.clk(ACLK1), .D(nSum1), .Q(d_ff_2_q));  // open: Qn, preset, en, reset
  Demultiplexer #(.enable("false")) demultiplexer_2 (
    .out0(demultiplexer_2_out0), .out1(demultiplexer_2_out1), .in(DO_SWEEP), .sel(d_ff_2_q));
  D_Flip_Flop #(.trigger("high")) d_ff_3 (.clk(ACLK1), .D(nSum2), .Q(d_ff_3_q));  // open: Qn, preset, en, reset
  Demultiplexer #(.enable("false")) demultiplexer_3 (
    .out0(demultiplexer_3_out0), .out1(demultiplexer_3_out1), .in(DO_SWEEP), .sel(d_ff_3_q));
  D_Flip_Flop #(.trigger("high")) d_ff_4 (.clk(ACLK1), .D(nSum3), .Q(d_ff_4_q));  // open: Qn, preset, en, reset
  Demultiplexer #(.enable("false")) demultiplexer_4 (
    .out0(demultiplexer_4_out0), .out1(demultiplexer_4_out1), .in(DO_SWEEP), .sel(d_ff_4_q));
  D_Flip_Flop #(.trigger("high")) d_ff_5 (.clk(ACLK1), .D(nSum4), .Q(d_ff_5_q));  // open: Qn, preset, en, reset
  Demultiplexer #(.enable("false")) demultiplexer_5 (
    .out0(demultiplexer_5_out0), .out1(demultiplexer_5_out1), .in(DO_SWEEP), .sel(d_ff_5_q));
  D_Flip_Flop #(.trigger("high")) d_ff_6 (.clk(ACLK1), .D(nSum5), .Q(d_ff_6_q));  // open: Qn, preset, en, reset
  Demultiplexer #(.enable("false")) demultiplexer_6 (
    .out0(demultiplexer_6_out0), .out1(demultiplexer_6_out1), .in(DO_SWEEP), .sel(d_ff_6_q));
  D_Flip_Flop #(.trigger("high")) d_ff_7 (.clk(ACLK1), .D(nSum6), .Q(d_ff_7_q));  // open: Qn, preset, en, reset
  Demultiplexer #(.enable("false")) demultiplexer_7 (
    .out0(demultiplexer_7_out0), .out1(demultiplexer_7_out1), .in(DO_SWEEP), .sel(d_ff_7_q));
  D_Flip_Flop #(.trigger("high")) d_ff_8 (.clk(ACLK1), .D(nSum7), .Q(d_ff_8_q));  // open: Qn, preset, en, reset
  Demultiplexer #(.enable("false")) demultiplexer_8 (
    .out0(demultiplexer_8_out0), .out1(demultiplexer_8_out1), .in(DO_SWEEP), .sel(d_ff_8_q));
  D_Flip_Flop #(.trigger("high")) d_ff_9 (.clk(ACLK1), .D(nSum8), .Q(d_ff_9_q));  // open: Qn, preset, en, reset
  Demultiplexer #(.enable("false")) demultiplexer_9 (
    .out0(demultiplexer_9_out0), .out1(demultiplexer_9_out1), .in(DO_SWEEP), .sel(d_ff_9_q));
  D_Flip_Flop #(.trigger("high")) d_ff_10 (.clk(ACLK1), .D(nSum9), .Q(d_ff_10_q));  // open: Qn, preset, en, reset
  Demultiplexer #(.enable("false")) demultiplexer_10 (
    .out0(demultiplexer_10_out0), .out1(demultiplexer_10_out1), .in(DO_SWEEP), .sel(d_ff_10_q));
  D_Flip_Flop #(.trigger("high")) d_ff_11 (.clk(ACLK1), .D(nSum10), .Q(d_ff_11_q));  // open: Qn, preset, en, reset
  Demultiplexer #(.enable("false")) demultiplexer_11 (
    .out0(demultiplexer_11_out0), .out1(demultiplexer_11_out1), .in(DO_SWEEP), .sel(d_ff_11_q));
  D_Flip_Flop #(.trigger("high")) d_ff_12 (
    .clk(not_1_out), .D(D0), .Q(F0), .preset(demultiplexer_1_out0), .en(W4002), .reset(demultiplexer_1_out1));  // open: Qn
  D_Flip_Flop #(.trigger("high")) d_ff_13 (
    .clk(not_1_out), .D(D1), .Q(F1), .preset(demultiplexer_2_out0), .en(W4002), .reset(demultiplexer_2_out1));  // open: Qn
  D_Flip_Flop #(.trigger("high")) d_ff_14 (
    .clk(not_1_out), .D(D2), .Q(F2), .preset(demultiplexer_3_out0), .en(W4002), .reset(demultiplexer_3_out1));  // open: Qn
  D_Flip_Flop #(.trigger("high")) d_ff_15 (
    .clk(not_1_out), .D(D3), .Q(F3), .preset(demultiplexer_4_out0), .en(W4002), .reset(demultiplexer_4_out1));  // open: Qn
  D_Flip_Flop #(.trigger("high")) d_ff_16 (
    .clk(not_1_out), .D(D4), .Q(F4), .preset(demultiplexer_5_out0), .en(W4002), .reset(demultiplexer_5_out1));  // open: Qn
  D_Flip_Flop #(.trigger("high")) d_ff_17 (
    .clk(not_1_out), .D(D5), .Q(F5), .preset(demultiplexer_6_out0), .en(W4002), .reset(demultiplexer_6_out1));  // open: Qn
  D_Flip_Flop #(.trigger("high")) d_ff_18 (
    .clk(not_1_out), .D(D6), .Q(F6), .preset(demultiplexer_7_out0), .en(W4002), .reset(demultiplexer_7_out1));  // open: Qn
  D_Flip_Flop #(.trigger("high")) d_ff_19 (
    .clk(not_1_out), .D(D7), .Q(F7), .preset(demultiplexer_8_out0), .en(W4002), .reset(demultiplexer_8_out1));  // open: Qn
  D_Flip_Flop #(.trigger("high")) d_ff_20 (
    .clk(not_1_out), .D(D0), .Q(F8), .preset(demultiplexer_9_out0), .en(W4003), .reset(demultiplexer_9_out1));  // open: Qn
  D_Flip_Flop #(.trigger("high")) d_ff_21 (
    .clk(not_1_out), .D(D1), .Q(F9), .preset(demultiplexer_10_out0), .en(W4003), .reset(demultiplexer_10_out1));  // open: Qn
  D_Flip_Flop #(.trigger("high")) d_ff_22 (
    .clk(not_1_out), .D(D2), .Q(F10), .preset(demultiplexer_11_out0), .en(W4003),
    .reset(demultiplexer_11_out1));  // open: Qn
  xor xor_1 (MU0, F0, D_I);
  xor xor_2 (MU1, F1, D_I);
  xor xor_3 (MU2, F2, D_I);
  xor xor_4 (MU3, F3, D_I);
  xor xor_5 (MU4, F4, D_I);
  xor xor_6 (MU5, F5, D_I);
  xor xor_7 (MU6, F6, D_I);
  xor xor_8 (MU7, F7, D_I);
  xor xor_9 (MU8, F8, D_I);
  xor xor_10 (MU9, F9, D_I);
  xor xor_11 (MU10, F10, D_I);

  // Notes on the sheet:
  //   !
  //   W4002 SQUARE0
  //   W4006 SQUARE1
  //   W4003 SQUARE0
  //   W4007 SQUARE1
  //   if /sum 1 reset latch
  //   if /sum 0 preset latch
endmodule

// BARREL SHIFTER
module SQUARE_BARREL_SHIFTER (
  input  MUI0,
  input  MUI1,
  input  MUI2,
  input  MUI3,
  input  MUI4,
  input  MUI5,
  input  MUI6,
  input  MUI7,
  input  MUI8,
  input  MUI9,
  input  MUI10,
  input  Dec_Inc,
  input  SR0,
  input  SR1,
  input  SR2,
  output S0,
  output S1,
  output S2,
  output S3,
  output S4,
  output S5,
  output S6,
  output S7,
  output S8,
  output S9,
  output S10
);

  wire multiplexer_1_out, multiplexer_2_out, multiplexer_3_out, multiplexer_4_out, multiplexer_5_out,
       multiplexer_6_out, multiplexer_7_out, multiplexer_8_out, multiplexer_9_out, multiplexer_10_out,
       multiplexer_11_out, multiplexer_12_out, multiplexer_13_out, multiplexer_14_out, multiplexer_15_out,
       multiplexer_16_out, multiplexer_17_out, multiplexer_18_out, multiplexer_19_out, multiplexer_20_out,
       multiplexer_21_out, multiplexer_22_out;

  Multiplexer #(.enable("false")) multiplexer_1 (.in0(MUI0), .in1(MUI1), .out(multiplexer_1_out), .sel(SR0));
  Multiplexer #(.enable("false")) multiplexer_2 (.in0(MUI1), .in1(MUI2), .out(multiplexer_2_out), .sel(SR0));
  Multiplexer #(.enable("false")) multiplexer_3 (.in0(MUI2), .in1(MUI3), .out(multiplexer_3_out), .sel(SR0));
  Multiplexer #(.enable("false")) multiplexer_4 (.in0(MUI3), .in1(MUI4), .out(multiplexer_4_out), .sel(SR0));
  Multiplexer #(.enable("false")) multiplexer_5 (.in0(MUI4), .in1(MUI5), .out(multiplexer_5_out), .sel(SR0));
  Multiplexer #(.enable("false")) multiplexer_6 (.in0(MUI5), .in1(MUI6), .out(multiplexer_6_out), .sel(SR0));
  Multiplexer #(.enable("false")) multiplexer_7 (.in0(MUI6), .in1(MUI7), .out(multiplexer_7_out), .sel(SR0));
  Multiplexer #(.enable("false")) multiplexer_8 (.in0(MUI7), .in1(MUI8), .out(multiplexer_8_out), .sel(SR0));
  Multiplexer #(.enable("false")) multiplexer_9 (.in0(MUI8), .in1(MUI9), .out(multiplexer_9_out), .sel(SR0));
  Multiplexer #(.enable("false")) multiplexer_10 (.in0(MUI9), .in1(MUI10), .out(multiplexer_10_out), .sel(SR0));
  Multiplexer #(.enable("false")) multiplexer_11 (.in0(MUI10), .in1(Dec_Inc), .out(multiplexer_11_out), .sel(SR0));
  Multiplexer #(.enable("false")) multiplexer_12 (
    .in0(multiplexer_1_out), .in1(multiplexer_3_out), .out(multiplexer_12_out), .sel(SR1));
  Multiplexer #(.enable("false")) multiplexer_13 (
    .in0(multiplexer_2_out), .in1(multiplexer_4_out), .out(multiplexer_13_out), .sel(SR1));
  Multiplexer #(.enable("false")) multiplexer_14 (
    .in0(multiplexer_3_out), .in1(multiplexer_5_out), .out(multiplexer_14_out), .sel(SR1));
  Multiplexer #(.enable("false")) multiplexer_15 (
    .in0(multiplexer_4_out), .in1(multiplexer_6_out), .out(multiplexer_15_out), .sel(SR1));
  Multiplexer #(.enable("false")) multiplexer_16 (
    .in0(multiplexer_5_out), .in1(multiplexer_7_out), .out(multiplexer_16_out), .sel(SR1));
  Multiplexer #(.enable("false")) multiplexer_17 (
    .in0(multiplexer_6_out), .in1(multiplexer_8_out), .out(multiplexer_17_out), .sel(SR1));
  Multiplexer #(.enable("false")) multiplexer_18 (
    .in0(multiplexer_7_out), .in1(multiplexer_9_out), .out(multiplexer_18_out), .sel(SR1));
  Multiplexer #(.enable("false")) multiplexer_19 (
    .in0(multiplexer_8_out), .in1(multiplexer_10_out), .out(multiplexer_19_out), .sel(SR1));
  Multiplexer #(.enable("false")) multiplexer_20 (
    .in0(multiplexer_9_out), .in1(multiplexer_11_out), .out(multiplexer_20_out), .sel(SR1));
  Multiplexer #(.enable("false")) multiplexer_21 (
    .in0(multiplexer_10_out), .in1(Dec_Inc), .out(multiplexer_21_out), .sel(SR1));
  Multiplexer #(.enable("false")) multiplexer_22 (
    .in0(multiplexer_11_out), .in1(Dec_Inc), .out(multiplexer_22_out), .sel(SR1));
  Multiplexer #(.enable("false")) multiplexer_23 (
    .in0(multiplexer_12_out), .in1(multiplexer_16_out), .out(S0), .sel(SR2));
  Multiplexer #(.enable("false")) multiplexer_24 (
    .in0(multiplexer_13_out), .in1(multiplexer_17_out), .out(S1), .sel(SR2));
  Multiplexer #(.enable("false")) multiplexer_25 (
    .in0(multiplexer_14_out), .in1(multiplexer_18_out), .out(S2), .sel(SR2));
  Multiplexer #(.enable("false")) multiplexer_26 (
    .in0(multiplexer_15_out), .in1(multiplexer_19_out), .out(S3), .sel(SR2));
  Multiplexer #(.enable("false")) multiplexer_27 (
    .in0(multiplexer_16_out), .in1(multiplexer_20_out), .out(S4), .sel(SR2));
  Multiplexer #(.enable("false")) multiplexer_28 (
    .in0(multiplexer_17_out), .in1(multiplexer_21_out), .out(S5), .sel(SR2));
  Multiplexer #(.enable("false")) multiplexer_29 (
    .in0(multiplexer_18_out), .in1(multiplexer_22_out), .out(S6), .sel(SR2));
  Multiplexer #(.enable("false")) multiplexer_30 (.in0(multiplexer_19_out), .in1(Dec_Inc), .out(S7), .sel(SR2));
  Multiplexer #(.enable("false")) multiplexer_31 (.in0(multiplexer_20_out), .in1(Dec_Inc), .out(S8), .sel(SR2));
  Multiplexer #(.enable("false")) multiplexer_32 (.in0(multiplexer_21_out), .in1(Dec_Inc), .out(S9), .sel(SR2));
  Multiplexer #(.enable("false")) multiplexer_33 (.in0(multiplexer_22_out), .in1(Dec_Inc), .out(S10), .sel(SR2));
endmodule

// SQUARE ADDER
module SQUARE_ADDER (
  input  nCIN,
  input  FX0,
  input  SX0,
  input  FX1,
  input  SX1,
  input  FX2,
  input  SX2,
  input  FX3,
  input  SX3,
  input  FX4,
  input  SX4,
  input  FX5,
  input  SX5,
  input  FX6,
  input  SX6,
  input  FX7,
  input  SX7,
  input  FX8,
  input  SX8,
  input  FX9,
  input  SX9,
  input  FX10,
  input  SX10,
  output nSum0,
  output nSum1,
  output nSum2,
  output nSum3,
  output nSum4,
  output nSum5,
  output nSum6,
  output nSum7,
  output nSum8,
  output nSum9,
  output nSum10,
  output nCOUT
);

  wire and_1_out, and_2_out, and_3_out, and_4_out, and_5_out, and_6_out, and_7_out, and_8_out, and_9_out,
       and_10_out, and_11_out, and_12_out, and_13_out, and_14_out, and_15_out, and_16_out, and_17_out,
       and_18_out, and_19_out, and_20_out, and_21_out, and_22_out, nor_1_out, nor_2_out, nor_3_out,
       nor_4_out, nor_5_out, nor_6_out, nor_7_out, nor_8_out, nor_9_out, nor_10_out, not_1_out, xor_1_out,
       xor_2_out, xor_3_out, xor_4_out, xor_5_out, xor_6_out, xor_7_out, xor_8_out, xor_9_out, xor_10_out,
       xor_11_out;

  not not_1 (not_1_out, nCIN);
  xor xor_1 (xor_1_out, FX0, SX0);
  xor xor_2 (xor_2_out, FX1, SX1);
  xor xor_3 (xor_3_out, FX2, SX2);
  xor xor_4 (xor_4_out, FX3, SX3);
  xor xor_5 (xor_5_out, FX4, SX4);
  xor xor_6 (xor_6_out, FX5, SX5);
  xor xor_7 (xor_7_out, FX6, SX6);
  xor xor_8 (xor_8_out, FX7, SX7);
  xor xor_9 (xor_9_out, FX8, SX8);
  xor xor_10 (xor_10_out, FX9, SX9);
  xor xor_11 (xor_11_out, FX10, SX10);
  xnor xnor_1 (nSum0, not_1_out, xor_1_out);
  and and_1 (and_1_out, xor_1_out, not_1_out);
  and and_2 (and_2_out, SX0, FX0);
  xnor xnor_2 (nSum1, nor_1_out, xor_2_out);
  and and_3 (and_3_out, xor_2_out, nor_1_out);
  and and_4 (and_4_out, SX1, FX1);
  xnor xnor_3 (nSum2, nor_2_out, xor_3_out);
  and and_5 (and_5_out, xor_3_out, nor_2_out);
  and and_6 (and_6_out, SX2, FX2);
  xnor xnor_4 (nSum3, nor_3_out, xor_4_out);
  and and_7 (and_7_out, xor_4_out, nor_3_out);
  and and_8 (and_8_out, SX3, FX3);
  xnor xnor_5 (nSum4, nor_4_out, xor_5_out);
  and and_9 (and_9_out, xor_5_out, nor_4_out);
  and and_10 (and_10_out, SX4, FX4);
  xnor xnor_6 (nSum5, nor_5_out, xor_6_out);
  and and_11 (and_11_out, xor_6_out, nor_5_out);
  and and_12 (and_12_out, SX5, FX5);
  xnor xnor_7 (nSum6, nor_6_out, xor_7_out);
  and and_13 (and_13_out, xor_7_out, nor_6_out);
  and and_14 (and_14_out, SX6, FX6);
  xnor xnor_8 (nSum7, nor_7_out, xor_8_out);
  and and_15 (and_15_out, xor_8_out, nor_7_out);
  and and_16 (and_16_out, SX7, FX7);
  xnor xnor_9 (nSum8, nor_8_out, xor_9_out);
  and and_17 (and_17_out, xor_9_out, nor_8_out);
  and and_18 (and_18_out, SX8, FX8);
  xnor xnor_10 (nSum9, nor_9_out, xor_10_out);
  and and_19 (and_19_out, xor_10_out, nor_9_out);
  and and_20 (and_20_out, SX9, FX9);
  xnor xnor_11 (nSum10, nor_10_out, xor_11_out);
  and and_21 (and_21_out, xor_11_out, nor_10_out);
  and and_22 (and_22_out, SX10, FX10);
  nor nor_1 (nor_1_out, and_1_out, and_2_out);
  nor nor_2 (nor_2_out, and_3_out, and_4_out);
  nor nor_3 (nor_3_out, and_5_out, and_6_out);
  nor nor_4 (nor_4_out, and_7_out, and_8_out);
  nor nor_5 (nor_5_out, and_9_out, and_10_out);
  nor nor_6 (nor_6_out, and_11_out, and_12_out);
  nor nor_7 (nor_7_out, and_13_out, and_14_out);
  nor nor_8 (nor_8_out, and_15_out, and_16_out);
  nor nor_9 (nor_9_out, and_17_out, and_18_out);
  nor nor_10 (nor_10_out, and_19_out, and_20_out);
  nor nor_11 (nCOUT, and_21_out, and_22_out);
endmodule

// SWEEP CONTROL
module SQUARE_SWEEP_CONTROL (
  input  ACLK1,
  input  nCOUT,
  input  D0,
  input  D1,
  input  D2,
  input  D3,
  input  D7,
  input  SW_UVF,
  input  NOSQA,
  input  nLFO2,
  input  RES,
  input  D4,
  input  D5,
  input  D6,
  input  W400x,
  output SW_OVF,
  output SR0,
  output SR1,
  output SR2,
  output D_I,
  output DO_SWEEP
);

  wire d_ff_5_qn, d_ff_6_q, d_ff_7_q, d_ff_8_q, d_ff_9_q, d_ff_9_qn, d_ff_10_q, d_ff_10_qn, d_ff_11_q,
       d_ff_11_qn, d_ff_12_qn, d_ff_13_qn, d_ff_14_qn, d_latch_1_not_q, d_latch_1_q, d_latch_2_not_q,
       d_latch_2_q, demultiplexer_1_out0, demultiplexer_1_out1, demultiplexer_2_out0, demultiplexer_2_out1,
       demultiplexer_3_out0, demultiplexer_3_out1, nor_1_out, nor_2_out, nor_3_out, nor_4_out, nor_5_out,
       nor_6_out, nor_7_out, nor_8_out, nor_10_out, nor_11_out, not_1_out, not_2_out, not_3_out, not_4_out,
       not_5_out, or_1_out, or_2_out, or_3_out, xor_1_out, xor_2_out, xor_3_out;

  not not_1 (not_1_out, ACLK1);
  D_Flip_Flop #(.trigger("high")) d_ff_1 (.clk(not_1_out), .D(D0), .Q(SR0), .en(W400x));  // open: Qn, preset, reset
  D_Flip_Flop #(.trigger("high")) d_ff_2 (.clk(not_1_out), .D(D1), .Q(SR1), .en(W400x));  // open: Qn, preset, reset
  D_Flip_Flop #(.trigger("high")) d_ff_3 (.clk(not_1_out), .D(D2), .Q(SR2), .en(W400x));  // open: Qn, preset, reset
  D_Flip_Flop #(.trigger("high")) d_ff_4 (.clk(not_1_out), .D(D3), .Q(D_I), .en(W400x));  // open: Qn, preset, reset
  D_Flip_Flop #(.trigger("high")) d_ff_5 (
    .clk(not_1_out), .D(D7), .Qn(d_ff_5_qn), .en(W400x));  // open: Q, preset, reset
  D_Flip_Flop #(.trigger("high")) d_ff_6 (
    .clk(not_1_out), .D(D4), .Q(d_ff_6_q), .en(W400x));  // open: Qn, preset, reset
  D_Flip_Flop #(.trigger("high")) d_ff_7 (
    .clk(not_1_out), .D(D5), .Q(d_ff_7_q), .en(W400x));  // open: Qn, preset, reset
  D_Flip_Flop #(.trigger("high")) d_ff_8 (
    .clk(not_1_out), .D(D6), .Q(d_ff_8_q), .en(W400x));  // open: Qn, preset, reset
  Demultiplexer #(.enable("false")) demultiplexer_1 (
    .out0(demultiplexer_1_out0), .out1(demultiplexer_1_out1), .in(nor_8_out), .sel(d_ff_6_q));
  Demultiplexer #(.enable("false")) demultiplexer_2 (
    .out0(demultiplexer_2_out0), .out1(demultiplexer_2_out1), .in(nor_8_out), .sel(d_ff_7_q));
  Demultiplexer #(.enable("false")) demultiplexer_3 (
    .out0(demultiplexer_3_out0), .out1(demultiplexer_3_out1), .in(nor_8_out), .sel(d_ff_8_q));
  or or_1 (or_1_out, RES, demultiplexer_1_out0);
  or or_2 (or_2_out, RES, demultiplexer_2_out0);
  or or_3 (or_3_out, RES, demultiplexer_3_out0);
  nor nor_1 (nor_1_out, d_latch_1_q, nLFO2);
  D_Flip_Flop #(.trigger("high")) d_ff_9 (
    .clk(nor_7_out), .D(d_ff_12_qn), .Q(d_ff_9_q), .Qn(d_ff_9_qn), .preset(demultiplexer_1_out1),
    .reset(or_1_out));  // open: en
  D_Flip_Flop #(.trigger("high")) d_ff_10 (
    .clk(nor_7_out), .D(d_ff_13_qn), .Q(d_ff_10_q), .Qn(d_ff_10_qn), .preset(demultiplexer_2_out1),
    .reset(or_2_out));  // open: en
  D_Flip_Flop #(.trigger("high")) d_ff_11 (
    .clk(nor_7_out), .D(d_ff_14_qn), .Q(d_ff_11_q), .Qn(d_ff_11_qn), .preset(demultiplexer_3_out1),
    .reset(or_3_out));  // open: en
  nor nor_2 (nor_2_out, nor_1_out, nor_3_out);
  nor nor_3 (nor_3_out, nor_2_out, W400x);
  xor xor_1 (xor_1_out, 1'b1, d_ff_9_qn);
  not not_2 (not_2_out, 1'b1);
  nor nor_4 (nor_4_out, not_2_out, d_ff_9_q);
  xor xor_2 (xor_2_out, nor_4_out, d_ff_10_qn);
  not not_3 (not_3_out, nor_4_out);
  nor nor_5 (nor_5_out, not_3_out, d_ff_10_q);
  xor xor_3 (xor_3_out, nor_5_out, d_ff_11_qn);
  not not_4 (not_4_out, nor_5_out);
  nor nor_6 (nor_6_out, not_4_out, d_ff_11_q);
  nor nor_7 (nor_7_out, not_5_out, nLFO2);
  nor nor_8 (nor_8_out, nLFO2, nor_11_out);
  nor nor_9 (SW_OVF, nCOUT, D_I);
  not not_5 (not_5_out, nor_11_out);
  D_Flip_Flop #(.trigger("high")) d_ff_12 (.clk(ACLK1), .D(xor_1_out), .Qn(d_ff_12_qn));  // open: Q, preset, en, reset
  D_Flip_Flop #(.trigger("high")) d_ff_13 (.clk(ACLK1), .D(xor_2_out), .Qn(d_ff_13_qn));  // open: Q, preset, en, reset
  D_Flip_Flop #(.trigger("high")) d_ff_14 (.clk(ACLK1), .D(xor_3_out), .Qn(d_ff_14_qn));  // open: Q, preset, en, reset
  D_latch d_latch_1 (.EN(ACLK1), .D(nor_3_out), .Q(d_latch_1_q), .NOT_Q(d_latch_1_not_q));
  nor nor_10 (nor_10_out, SR2, SR1, SR0);
  D_latch d_latch_2 (.EN(ACLK1), .D(nor_6_out), .Q(d_latch_2_q), .NOT_Q(d_latch_2_not_q));
  nor nor_11 (nor_11_out, d_latch_2_q, d_latch_1_not_q);
  nor nor_12 (DO_SWEEP, nor_10_out, SW_OVF, d_ff_5_qn, SW_UVF, NOSQA, nLFO2, d_latch_2_not_q);

  // Notes on the sheet:
  //   W4001 SQUARE0
  //   W4005 SQUARE1
  //   SR0
  //   SR1
  //   SR2
  //   DEC/INC
  //   SWDIS
  //   P0
  //   P1
  //   P2
  //   R
  //   NOR2
  //   S
  //   SWEEP DOWN COUNTER
  //   SSTEP
  //   SLOAD
  //   Q
  //   NORFF1
  //   RS1
  //   NORFF2
  //   /Q
  //   NOR1
  //   DL1
  //   SRZ
  //   /SCO
  //   DL3
  //   NOR7
  //   SWEEPRELOAD
  //   NOR3
  //   NOR4
endmodule

// SQUARE FREQUENCY COUNTER
module SQUARE_FREQUENCY_DOWN_COUNTER (
  input  ACLK1,
  input  RES,
  input  PL0,
  input  PL1,
  input  PL2,
  input  PL3,
  input  PL4,
  input  PL5,
  input  PL6,
  input  PL7,
  input  PL8,
  input  PL9,
  input  PL10,
  input  nACLK2,
  output FQOUT,
  output FLOAD
);

  wire d_ff_1_q, d_ff_1_qn, d_ff_2_q, d_ff_2_qn, d_ff_3_q, d_ff_3_qn, d_ff_4_q, d_ff_4_qn, d_ff_5_q,
       d_ff_5_qn, d_ff_6_q, d_ff_6_qn, d_ff_7_q, d_ff_7_qn, d_ff_8_q, d_ff_8_qn, d_ff_9_q, d_ff_9_qn,
       d_ff_10_q, d_ff_10_qn, d_ff_11_q, d_ff_11_qn, d_ff_12_qn, d_ff_13_qn, d_ff_14_qn, d_ff_15_qn,
       d_ff_16_qn, d_ff_17_qn, d_ff_18_qn, d_ff_19_qn, d_ff_20_qn, d_ff_21_qn, d_ff_22_qn, d_latch_1_not_q,
       demultiplexer_1_out0, demultiplexer_1_out1, demultiplexer_2_out0, demultiplexer_2_out1,
       demultiplexer_3_out0, demultiplexer_3_out1, demultiplexer_4_out0, demultiplexer_4_out1,
       demultiplexer_5_out0, demultiplexer_5_out1, demultiplexer_6_out0, demultiplexer_6_out1,
       demultiplexer_7_out0, demultiplexer_7_out1, demultiplexer_8_out0, demultiplexer_8_out1,
       demultiplexer_9_out0, demultiplexer_9_out1, demultiplexer_10_out0, demultiplexer_10_out1,
       demultiplexer_11_out0, demultiplexer_11_out1, nor_1_out, nor_3_out, nor_4_out, nor_5_out, nor_6_out,
       nor_7_out, nor_8_out, nor_9_out, nor_10_out, nor_11_out, nor_12_out, not_1_out, not_2_out, not_3_out,
       not_4_out, not_5_out, not_6_out, not_7_out, not_8_out, not_9_out, not_10_out, not_11_out, not_12_out,
       or_1_out, or_2_out, or_3_out, or_4_out, or_5_out, or_6_out, or_7_out, or_8_out, or_9_out, or_10_out,
       or_11_out, xor_1_out, xor_2_out, xor_3_out, xor_4_out, xor_5_out, xor_6_out, xor_7_out, xor_8_out,
       xor_9_out, xor_10_out, xor_11_out;

  Demultiplexer #(.enable("false")) demultiplexer_1 (
    .out0(demultiplexer_1_out0), .out1(demultiplexer_1_out1), .in(FLOAD), .sel(PL0));
  Demultiplexer #(.enable("false")) demultiplexer_2 (
    .out0(demultiplexer_2_out0), .out1(demultiplexer_2_out1), .in(FLOAD), .sel(PL1));
  Demultiplexer #(.enable("false")) demultiplexer_3 (
    .out0(demultiplexer_3_out0), .out1(demultiplexer_3_out1), .in(FLOAD), .sel(PL2));
  Demultiplexer #(.enable("false")) demultiplexer_4 (
    .out0(demultiplexer_4_out0), .out1(demultiplexer_4_out1), .in(FLOAD), .sel(PL3));
  Demultiplexer #(.enable("false")) demultiplexer_5 (
    .out0(demultiplexer_5_out0), .out1(demultiplexer_5_out1), .in(FLOAD), .sel(PL4));
  Demultiplexer #(.enable("false")) demultiplexer_6 (
    .out0(demultiplexer_6_out0), .out1(demultiplexer_6_out1), .in(FLOAD), .sel(PL5));
  Demultiplexer #(.enable("false")) demultiplexer_7 (
    .out0(demultiplexer_7_out0), .out1(demultiplexer_7_out1), .in(FLOAD), .sel(PL6));
  Demultiplexer #(.enable("false")) demultiplexer_8 (
    .out0(demultiplexer_8_out0), .out1(demultiplexer_8_out1), .in(FLOAD), .sel(PL7));
  Demultiplexer #(.enable("false")) demultiplexer_9 (
    .out0(demultiplexer_9_out0), .out1(demultiplexer_9_out1), .in(FLOAD), .sel(PL8));
  Demultiplexer #(.enable("false")) demultiplexer_10 (
    .out0(demultiplexer_10_out0), .out1(demultiplexer_10_out1), .in(FLOAD), .sel(PL9));
  Demultiplexer #(.enable("false")) demultiplexer_11 (
    .out0(demultiplexer_11_out0), .out1(demultiplexer_11_out1), .in(FLOAD), .sel(PL10));
  or or_1 (or_1_out, RES, demultiplexer_1_out0);
  or or_2 (or_2_out, RES, demultiplexer_2_out0);
  or or_3 (or_3_out, RES, demultiplexer_3_out0);
  or or_4 (or_4_out, RES, demultiplexer_4_out0);
  or or_5 (or_5_out, RES, demultiplexer_5_out0);
  or or_6 (or_6_out, RES, demultiplexer_6_out0);
  or or_7 (or_7_out, RES, demultiplexer_7_out0);
  or or_8 (or_8_out, RES, demultiplexer_8_out0);
  or or_9 (or_9_out, RES, demultiplexer_9_out0);
  or or_10 (or_10_out, RES, demultiplexer_10_out0);
  or or_11 (or_11_out, RES, demultiplexer_11_out0);
  D_Flip_Flop #(.trigger("high")) d_ff_1 (
    .clk(nor_1_out), .D(d_ff_12_qn), .Q(d_ff_1_q), .Qn(d_ff_1_qn), .preset(demultiplexer_1_out1),
    .reset(or_1_out));  // open: en
  D_Flip_Flop #(.trigger("high")) d_ff_2 (
    .clk(nor_1_out), .D(d_ff_13_qn), .Q(d_ff_2_q), .Qn(d_ff_2_qn), .preset(demultiplexer_2_out1),
    .reset(or_2_out));  // open: en
  D_Flip_Flop #(.trigger("high")) d_ff_3 (
    .clk(nor_1_out), .D(d_ff_14_qn), .Q(d_ff_3_q), .Qn(d_ff_3_qn), .preset(demultiplexer_3_out1),
    .reset(or_3_out));  // open: en
  D_Flip_Flop #(.trigger("high")) d_ff_4 (
    .clk(nor_1_out), .D(d_ff_15_qn), .Q(d_ff_4_q), .Qn(d_ff_4_qn), .preset(demultiplexer_4_out1),
    .reset(or_4_out));  // open: en
  D_Flip_Flop #(.trigger("high")) d_ff_5 (
    .clk(nor_1_out), .D(d_ff_16_qn), .Q(d_ff_5_q), .Qn(d_ff_5_qn), .preset(demultiplexer_5_out1),
    .reset(or_5_out));  // open: en
  D_Flip_Flop #(.trigger("high")) d_ff_6 (
    .clk(nor_1_out), .D(d_ff_17_qn), .Q(d_ff_6_q), .Qn(d_ff_6_qn), .preset(demultiplexer_6_out1),
    .reset(or_6_out));  // open: en
  D_Flip_Flop #(.trigger("high")) d_ff_7 (
    .clk(nor_1_out), .D(d_ff_18_qn), .Q(d_ff_7_q), .Qn(d_ff_7_qn), .preset(demultiplexer_7_out1),
    .reset(or_7_out));  // open: en
  D_Flip_Flop #(.trigger("high")) d_ff_8 (
    .clk(nor_1_out), .D(d_ff_19_qn), .Q(d_ff_8_q), .Qn(d_ff_8_qn), .preset(demultiplexer_8_out1),
    .reset(or_8_out));  // open: en
  D_Flip_Flop #(.trigger("high")) d_ff_9 (
    .clk(nor_1_out), .D(d_ff_20_qn), .Q(d_ff_9_q), .Qn(d_ff_9_qn), .preset(demultiplexer_9_out1),
    .reset(or_9_out));  // open: en
  D_Flip_Flop #(.trigger("high")) d_ff_10 (
    .clk(nor_1_out), .D(d_ff_21_qn), .Q(d_ff_10_q), .Qn(d_ff_10_qn), .preset(demultiplexer_10_out1),
    .reset(or_10_out));  // open: en
  D_Flip_Flop #(.trigger("high")) d_ff_11 (
    .clk(nor_1_out), .D(d_ff_22_qn), .Q(d_ff_11_q), .Qn(d_ff_11_qn), .preset(demultiplexer_11_out1),
    .reset(or_11_out));  // open: en
  not not_1 (not_1_out, d_latch_1_not_q);
  nor nor_1 (nor_1_out, not_1_out, nACLK2);
  nor nor_2 (FLOAD, nACLK2, d_latch_1_not_q);
  xor xor_1 (xor_1_out, 1'b1, d_ff_1_qn);
  not not_2 (not_2_out, 1'b1);
  nor nor_3 (nor_3_out, not_2_out, d_ff_1_q);
  xor xor_2 (xor_2_out, nor_3_out, d_ff_2_qn);
  not not_3 (not_3_out, nor_3_out);
  nor nor_4 (nor_4_out, not_3_out, d_ff_2_q);
  xor xor_3 (xor_3_out, nor_4_out, d_ff_3_qn);
  not not_4 (not_4_out, nor_4_out);
  nor nor_5 (nor_5_out, not_4_out, d_ff_3_q);
  xor xor_4 (xor_4_out, nor_5_out, d_ff_4_qn);
  not not_5 (not_5_out, nor_5_out);
  nor nor_6 (nor_6_out, not_5_out, d_ff_4_q);
  xor xor_5 (xor_5_out, nor_6_out, d_ff_5_qn);
  not not_6 (not_6_out, nor_6_out);
  nor nor_7 (nor_7_out, not_6_out, d_ff_5_q);
  xor xor_6 (xor_6_out, nor_7_out, d_ff_6_qn);
  not not_7 (not_7_out, nor_7_out);
  nor nor_8 (nor_8_out, not_7_out, d_ff_6_q);
  xor xor_7 (xor_7_out, nor_8_out, d_ff_7_qn);
  not not_8 (not_8_out, nor_8_out);
  nor nor_9 (nor_9_out, not_8_out, d_ff_7_q);
  xor xor_8 (xor_8_out, nor_9_out, d_ff_8_qn);
  not not_9 (not_9_out, nor_9_out);
  nor nor_10 (nor_10_out, not_9_out, d_ff_8_q);
  xor xor_9 (xor_9_out, nor_10_out, d_ff_9_qn);
  not not_10 (not_10_out, nor_10_out);
  nor nor_11 (nor_11_out, not_10_out, d_ff_9_q);
  xor xor_10 (xor_10_out, nor_11_out, d_ff_10_qn);
  not not_11 (not_11_out, nor_11_out);
  nor nor_12 (nor_12_out, not_11_out, d_ff_10_q);
  xor xor_11 (xor_11_out, nor_12_out, d_ff_11_qn);
  not not_12 (not_12_out, nor_12_out);
  nor nor_13 (FQOUT, not_12_out, d_ff_11_q);
  D_Flip_Flop #(.trigger("high")) d_ff_12 (.clk(ACLK1), .D(xor_1_out), .Qn(d_ff_12_qn));  // open: Q, preset, en, reset
  D_Flip_Flop #(.trigger("high")) d_ff_13 (.clk(ACLK1), .D(xor_2_out), .Qn(d_ff_13_qn));  // open: Q, preset, en, reset
  D_Flip_Flop #(.trigger("high")) d_ff_14 (.clk(ACLK1), .D(xor_3_out), .Qn(d_ff_14_qn));  // open: Q, preset, en, reset
  D_Flip_Flop #(.trigger("high")) d_ff_15 (.clk(ACLK1), .D(xor_4_out), .Qn(d_ff_15_qn));  // open: Q, preset, en, reset
  D_Flip_Flop #(.trigger("high")) d_ff_16 (.clk(ACLK1), .D(xor_5_out), .Qn(d_ff_16_qn));  // open: Q, preset, en, reset
  D_Flip_Flop #(.trigger("high")) d_ff_17 (.clk(ACLK1), .D(xor_6_out), .Qn(d_ff_17_qn));  // open: Q, preset, en, reset
  D_Flip_Flop #(.trigger("high")) d_ff_18 (.clk(ACLK1), .D(xor_7_out), .Qn(d_ff_18_qn));  // open: Q, preset, en, reset
  D_Flip_Flop #(.trigger("high")) d_ff_19 (.clk(ACLK1), .D(xor_8_out), .Qn(d_ff_19_qn));  // open: Q, preset, en, reset
  D_Flip_Flop #(.trigger("high")) d_ff_20 (.clk(ACLK1), .D(xor_9_out), .Qn(d_ff_20_qn));  // open: Q, preset, en, reset
  D_Flip_Flop #(.trigger("high")) d_ff_21 (.clk(ACLK1), .D(xor_10_out), .Qn(d_ff_21_qn));  // open: Q, preset, en, reset
  D_Flip_Flop #(.trigger("high")) d_ff_22 (.clk(ACLK1), .D(xor_11_out), .Qn(d_ff_22_qn));  // open: Q, preset, en, reset
  D_latch d_latch_1 (.EN(ACLK1), .D(FQOUT), .NOT_Q(d_latch_1_not_q));  // open: Q

  // Notes on the sheet:
  //   FSTEP
  //   FLOAD
  //   DL4
endmodule

// DUTY DOWN COUNTER
module SQUARE_DUTY_DOWN_COUNTER (
  input  ACLK1,
  input  FQOUT,
  input  RES,
  input  W4003,
  input  FLOAD,
  input  D6,
  input  D7,
  input  W4000,
  output SQOUT
);

  wire d_ff_1_q, d_ff_1_qn, d_ff_2_q, d_ff_2_qn, d_ff_3_q, d_ff_3_qn, d_ff_6_qn, d_ff_7_qn, d_ff_8_qn,
       nand_1_out, nor_1_out, nor_2_out, nor_3_out, nor_4_out, not_1_out, not_2_out, not_3_out, not_4_out,
       not_5_out, not_6_out, or_1_out, xor_1_out, xor_2_out, xor_3_out;
  wire [1:0] d_ff_4_q;

  or or_1 (or_1_out, RES, W4003);
  D_Flip_Flop #(.trigger("high")) d_ff_1 (
    .clk(FLOAD), .D(d_ff_6_qn), .Q(d_ff_1_q), .Qn(d_ff_1_qn), .reset(or_1_out));  // open: preset, en
  D_Flip_Flop #(.trigger("high")) d_ff_2 (
    .clk(FLOAD), .D(d_ff_7_qn), .Q(d_ff_2_q), .Qn(d_ff_2_qn), .reset(or_1_out));  // open: preset, en
  D_Flip_Flop #(.trigger("high")) d_ff_3 (
    .clk(FLOAD), .D(d_ff_8_qn), .Q(d_ff_3_q), .Qn(d_ff_3_qn), .reset(or_1_out));  // open: preset, en
  not not_1 (not_1_out, ACLK1);
  D_Flip_Flop #(.trigger("high")) d_ff_4 (
    .clk(not_1_out), .D(D6), .Q(d_ff_4_q[0]), .en(W4000));  // open: Qn, preset, reset
  D_Flip_Flop #(.trigger("high")) d_ff_5 (
    .clk(not_1_out), .D(D7), .Q(d_ff_4_q[1]), .en(W4000));  // open: Qn, preset, reset
  not not_2 (not_2_out, FQOUT);
  not not_3 (not_3_out, nor_1_out);
  not not_4 (not_4_out, nor_2_out);
  xor xor_1 (xor_1_out, FQOUT, d_ff_1_qn);
  nor nor_1 (nor_1_out, not_2_out, d_ff_1_q);
  xor xor_2 (xor_2_out, nor_1_out, d_ff_2_qn);
  nor nor_2 (nor_2_out, not_3_out, d_ff_2_q);
  xor xor_3 (xor_3_out, nor_2_out, d_ff_3_qn);
  nor nor_3 (nor_3_out, not_4_out, d_ff_3_q);
  D_Flip_Flop #(.trigger("high")) d_ff_6 (.clk(ACLK1), .D(xor_1_out), .Qn(d_ff_6_qn));  // open: Q, preset, en, reset
  D_Flip_Flop #(.trigger("high")) d_ff_7 (.clk(ACLK1), .D(xor_2_out), .Qn(d_ff_7_qn));  // open: Q, preset, en, reset
  D_Flip_Flop #(.trigger("high")) d_ff_8 (.clk(ACLK1), .D(xor_3_out), .Qn(d_ff_8_qn));  // open: Q, preset, en, reset
  not not_5 (not_5_out, d_ff_1_q);
  nand nand_1 (nand_1_out, d_ff_2_q, d_ff_3_q);
  nor nor_4 (nor_4_out, not_5_out, nand_1_out);
  not not_6 (not_6_out, nand_1_out);
  Multiplexer #(.select(2), .enable("false")) multiplexer_1 (
    .in0(nor_4_out), .in1(not_6_out), .in2(d_ff_3_q), .in3(nand_1_out), .out(SQOUT), .sel(d_ff_4_q));

  // Notes on the sheet:
  //   W4003  SQUARE 0
  //   W4007  SQUARE 1
  //   W4000 SQUARE 0
  //   W4004 SQUARE 1
  //   not used
  //   INV3
  //   NAND1
  //   NOR10
  //   12.5%
  //   25%
  //   INV4
  //   75%
  //   50%
endmodule

// TRIANGLE CHANNEL
module TRIANGLE_CHANNEL (
  input  PHI1,
  input  ACLK1,
  input  W400A,
  input  D0,
  input  D1,
  input  D2,
  input  D3,
  input  D4,
  input  D5,
  input  D6,
  input  D7,
  input  W4008,
  input  W400B,
  input  W401A,
  input  nLFO1,
  input  RES,
  input  NOTRI,
  input  LOCk,
  output TRI0,
  output TRI1,
  output TRI2,
  output TRI3,
  output TRI_LC
);

  wire _5_out, triangle_frequency_down_counter_1_nfout, triangle_linear_down_counter_1_tco;

  TRIANGLE_FREQUENCY_DOWN_COUNTER triangle_frequency_down_counter_1 (
    .PHI1(PHI1), .W400A(W400A), .W400B(W400B), .RES(RES), .D0(D0), .D1(D1), .D2(D2), .D3(D3), .D4(D4),
    .D5(D5), .D6(D6), .D7(D7), .nFOUT(triangle_frequency_down_counter_1_nfout));
  TRIANGLE_LINEAR_DOWN_COUNTER triangle_linear_down_counter_1 (
    .ACLK1(ACLK1), .W4008(W4008), .W400B(W400B), .nLFO1(nLFO1), .RES(RES), .D0(D0), .D1(D1), .D2(D2),
    .D3(D3), .D4(D4), .D5(D5), .TCO(triangle_linear_down_counter_1_tco), .D6(D6), .D7(D7), .TRI_LC(TRI_LC));
  nor _5 (_5_out, PHI1, triangle_frequency_down_counter_1_nfout, triangle_linear_down_counter_1_tco, NOTRI, LOCk);
  TRIANGLE_OUTPUT_COUNTER triangle_output_counter_1 (
    .PHI1(PHI1), .TTSTEP(_5_out), .RES(RES), .TRI0(TRI0), .TRI1(TRI1), .TRI2(TRI2), .TRI3(TRI3),
    .W401A(W401A), .D0(D0), .D1(D1), .D2(D2), .D3(D3), .D4(D4));
endmodule

// TRIANGLE FREQUENCY DOWN COUNTER
module TRIANGLE_FREQUENCY_DOWN_COUNTER (
  input  PHI1,
  input  RES,
  input  W400A,
  input  D0,
  input  D1,
  input  D2,
  input  D3,
  input  D4,
  input  D5,
  input  D6,
  input  D7,
  input  W400B,
  output nFOUT
);

  wire _1_out, _2_out, d_ff_1_q, d_ff_2_q, d_ff_3_q, d_ff_4_q, d_ff_5_q, d_ff_6_q, d_ff_7_q, d_ff_8_q,
       d_ff_9_q, d_ff_10_q, d_ff_11_q, d_ff_12_q, d_ff_12_qn, d_ff_13_q, d_ff_13_qn, d_ff_14_q, d_ff_14_qn,
       d_ff_15_q, d_ff_15_qn, d_ff_16_q, d_ff_16_qn, d_ff_17_q, d_ff_17_qn, d_ff_18_q, d_ff_18_qn, d_ff_19_q,
       d_ff_19_qn, d_ff_20_q, d_ff_20_qn, d_ff_21_q, d_ff_21_qn, d_ff_22_q, d_ff_22_qn, d_ff_23_qn,
       d_ff_24_qn, d_ff_25_qn, d_ff_26_qn, d_ff_27_qn, d_ff_28_qn, d_ff_29_qn, d_ff_30_qn, d_ff_31_qn,
       d_ff_32_qn, d_ff_33_qn, demultiplexer_1_out0, demultiplexer_1_out1, demultiplexer_2_out0,
       demultiplexer_2_out1, demultiplexer_3_out0, demultiplexer_3_out1, demultiplexer_4_out0,
       demultiplexer_4_out1, demultiplexer_5_out0, demultiplexer_5_out1, demultiplexer_6_out0,
       demultiplexer_6_out1, demultiplexer_7_out0, demultiplexer_7_out1, demultiplexer_8_out0,
       demultiplexer_8_out1, demultiplexer_9_out0, demultiplexer_9_out1, demultiplexer_10_out0,
       demultiplexer_10_out1, demultiplexer_11_out0, demultiplexer_11_out1, nor_1_out, nor_2_out, nor_3_out,
       nor_4_out, nor_5_out, nor_6_out, nor_7_out, nor_8_out, nor_9_out, nor_10_out, nor_11_out, not_1_out,
       not_2_out, not_3_out, not_4_out, not_5_out, not_6_out, not_7_out, not_8_out, not_9_out, not_10_out,
       not_11_out, not_12_out, not_13_out, or_1_out, or_2_out, or_3_out, or_4_out, or_5_out, or_6_out,
       or_7_out, or_8_out, or_9_out, or_10_out, or_11_out, xor_1_out, xor_2_out, xor_3_out, xor_4_out,
       xor_5_out, xor_6_out, xor_7_out, xor_8_out, xor_9_out, xor_10_out, xor_11_out;

  not not_1 (not_1_out, PHI1);
  D_Flip_Flop #(.trigger("high")) d_ff_1 (
    .clk(not_1_out), .D(D0), .Q(d_ff_1_q), .en(W400A));  // open: Qn, preset, reset
  Demultiplexer #(.enable("false")) demultiplexer_1 (
    .out0(demultiplexer_1_out0), .out1(demultiplexer_1_out1), .in(_2_out), .sel(d_ff_1_q));
  D_Flip_Flop #(.trigger("high")) d_ff_2 (
    .clk(not_1_out), .D(D1), .Q(d_ff_2_q), .en(W400A));  // open: Qn, preset, reset
  Demultiplexer #(.enable("false")) demultiplexer_2 (
    .out0(demultiplexer_2_out0), .out1(demultiplexer_2_out1), .in(_2_out), .sel(d_ff_2_q));
  D_Flip_Flop #(.trigger("high")) d_ff_3 (
    .clk(not_1_out), .D(D2), .Q(d_ff_3_q), .en(W400A));  // open: Qn, preset, reset
  Demultiplexer #(.enable("false")) demultiplexer_3 (
    .out0(demultiplexer_3_out0), .out1(demultiplexer_3_out1), .in(_2_out), .sel(d_ff_3_q));
  D_Flip_Flop #(.trigger("high")) d_ff_4 (
    .clk(not_1_out), .D(D3), .Q(d_ff_4_q), .en(W400A));  // open: Qn, preset, reset
  Demultiplexer #(.enable("false")) demultiplexer_4 (
    .out0(demultiplexer_4_out0), .out1(demultiplexer_4_out1), .in(_2_out), .sel(d_ff_4_q));
  D_Flip_Flop #(.trigger("high")) d_ff_5 (
    .clk(not_1_out), .D(D4), .Q(d_ff_5_q), .en(W400A));  // open: Qn, preset, reset
  Demultiplexer #(.enable("false")) demultiplexer_5 (
    .out0(demultiplexer_5_out0), .out1(demultiplexer_5_out1), .in(_2_out), .sel(d_ff_5_q));
  D_Flip_Flop #(.trigger("high")) d_ff_6 (
    .clk(not_1_out), .D(D5), .Q(d_ff_6_q), .en(W400A));  // open: Qn, preset, reset
  Demultiplexer #(.enable("false")) demultiplexer_6 (
    .out0(demultiplexer_6_out0), .out1(demultiplexer_6_out1), .in(_2_out), .sel(d_ff_6_q));
  D_Flip_Flop #(.trigger("high")) d_ff_7 (
    .clk(not_1_out), .D(D6), .Q(d_ff_7_q), .en(W400A));  // open: Qn, preset, reset
  Demultiplexer #(.enable("false")) demultiplexer_7 (
    .out0(demultiplexer_7_out0), .out1(demultiplexer_7_out1), .in(_2_out), .sel(d_ff_7_q));
  D_Flip_Flop #(.trigger("high")) d_ff_8 (
    .clk(not_1_out), .D(D7), .Q(d_ff_8_q), .en(W400A));  // open: Qn, preset, reset
  Demultiplexer #(.enable("false")) demultiplexer_8 (
    .out0(demultiplexer_8_out0), .out1(demultiplexer_8_out1), .in(_2_out), .sel(d_ff_8_q));
  D_Flip_Flop #(.trigger("high")) d_ff_9 (
    .clk(not_1_out), .D(D0), .Q(d_ff_9_q), .en(W400B));  // open: Qn, preset, reset
  Demultiplexer #(.enable("false")) demultiplexer_9 (
    .out0(demultiplexer_9_out0), .out1(demultiplexer_9_out1), .in(_2_out), .sel(d_ff_9_q));
  D_Flip_Flop #(.trigger("high")) d_ff_10 (
    .clk(not_1_out), .D(D1), .Q(d_ff_10_q), .en(W400B));  // open: Qn, preset, reset
  Demultiplexer #(.enable("false")) demultiplexer_10 (
    .out0(demultiplexer_10_out0), .out1(demultiplexer_10_out1), .in(_2_out), .sel(d_ff_10_q));
  D_Flip_Flop #(.trigger("high")) d_ff_11 (
    .clk(not_1_out), .D(D2), .Q(d_ff_11_q), .en(W400B));  // open: Qn, preset, reset
  Demultiplexer #(.enable("false")) demultiplexer_11 (
    .out0(demultiplexer_11_out0), .out1(demultiplexer_11_out1), .in(_2_out), .sel(d_ff_11_q));
  or or_1 (or_1_out, RES, demultiplexer_1_out0);
  or or_2 (or_2_out, RES, demultiplexer_2_out0);
  or or_3 (or_3_out, RES, demultiplexer_3_out0);
  or or_4 (or_4_out, RES, demultiplexer_4_out0);
  or or_5 (or_5_out, RES, demultiplexer_5_out0);
  or or_6 (or_6_out, RES, demultiplexer_6_out0);
  or or_7 (or_7_out, RES, demultiplexer_7_out0);
  or or_8 (or_8_out, RES, demultiplexer_8_out0);
  or or_9 (or_9_out, RES, demultiplexer_9_out0);
  or or_10 (or_10_out, RES, demultiplexer_10_out0);
  or or_11 (or_11_out, RES, demultiplexer_11_out0);
  D_Flip_Flop #(.trigger("high")) d_ff_12 (
    .clk(_1_out), .D(d_ff_23_qn), .Q(d_ff_12_q), .Qn(d_ff_12_qn), .preset(demultiplexer_1_out1),
    .reset(or_1_out));  // open: en
  D_Flip_Flop #(.trigger("high")) d_ff_13 (
    .clk(_1_out), .D(d_ff_24_qn), .Q(d_ff_13_q), .Qn(d_ff_13_qn), .preset(demultiplexer_2_out1),
    .reset(or_2_out));  // open: en
  D_Flip_Flop #(.trigger("high")) d_ff_14 (
    .clk(_1_out), .D(d_ff_25_qn), .Q(d_ff_14_q), .Qn(d_ff_14_qn), .preset(demultiplexer_3_out1),
    .reset(or_3_out));  // open: en
  D_Flip_Flop #(.trigger("high")) d_ff_15 (
    .clk(_1_out), .D(d_ff_26_qn), .Q(d_ff_15_q), .Qn(d_ff_15_qn), .preset(demultiplexer_4_out1),
    .reset(or_4_out));  // open: en
  D_Flip_Flop #(.trigger("high")) d_ff_16 (
    .clk(_1_out), .D(d_ff_27_qn), .Q(d_ff_16_q), .Qn(d_ff_16_qn), .preset(demultiplexer_5_out1),
    .reset(or_5_out));  // open: en
  D_Flip_Flop #(.trigger("high")) d_ff_17 (
    .clk(_1_out), .D(d_ff_28_qn), .Q(d_ff_17_q), .Qn(d_ff_17_qn), .preset(demultiplexer_6_out1),
    .reset(or_6_out));  // open: en
  D_Flip_Flop #(.trigger("high")) d_ff_18 (
    .clk(_1_out), .D(d_ff_29_qn), .Q(d_ff_18_q), .Qn(d_ff_18_qn), .preset(demultiplexer_7_out1),
    .reset(or_7_out));  // open: en
  D_Flip_Flop #(.trigger("high")) d_ff_19 (
    .clk(_1_out), .D(d_ff_30_qn), .Q(d_ff_19_q), .Qn(d_ff_19_qn), .preset(demultiplexer_8_out1),
    .reset(or_8_out));  // open: en
  D_Flip_Flop #(.trigger("high")) d_ff_20 (
    .clk(_1_out), .D(d_ff_31_qn), .Q(d_ff_20_q), .Qn(d_ff_20_qn), .preset(demultiplexer_9_out1),
    .reset(or_9_out));  // open: en
  D_Flip_Flop #(.trigger("high")) d_ff_21 (
    .clk(_1_out), .D(d_ff_32_qn), .Q(d_ff_21_q), .Qn(d_ff_21_qn), .preset(demultiplexer_10_out1),
    .reset(or_10_out));  // open: en
  D_Flip_Flop #(.trigger("high")) d_ff_22 (
    .clk(_1_out), .D(d_ff_33_qn), .Q(d_ff_22_q), .Qn(d_ff_22_qn), .preset(demultiplexer_11_out1),
    .reset(or_11_out));  // open: en
  xor xor_1 (xor_1_out, 1'b1, d_ff_12_qn);
  not not_2 (not_2_out, 1'b1);
  nor nor_1 (nor_1_out, not_2_out, d_ff_12_q);
  xor xor_2 (xor_2_out, nor_1_out, d_ff_13_qn);
  not not_3 (not_3_out, nor_1_out);
  nor nor_2 (nor_2_out, not_3_out, d_ff_13_q);
  xor xor_3 (xor_3_out, nor_2_out, d_ff_14_qn);
  not not_4 (not_4_out, nor_2_out);
  nor nor_3 (nor_3_out, not_4_out, d_ff_14_q);
  xor xor_4 (xor_4_out, nor_3_out, d_ff_15_qn);
  not not_5 (not_5_out, nor_3_out);
  nor nor_4 (nor_4_out, not_5_out, d_ff_15_q);
  xor xor_5 (xor_5_out, nor_4_out, d_ff_16_qn);
  not not_6 (not_6_out, nor_4_out);
  nor nor_5 (nor_5_out, not_6_out, d_ff_16_q);
  xor xor_6 (xor_6_out, nor_5_out, d_ff_17_qn);
  not not_7 (not_7_out, nor_5_out);
  nor nor_6 (nor_6_out, not_7_out, d_ff_17_q);
  xor xor_7 (xor_7_out, nor_6_out, d_ff_18_qn);
  not not_8 (not_8_out, nor_6_out);
  nor nor_7 (nor_7_out, not_8_out, d_ff_18_q);
  xor xor_8 (xor_8_out, nor_7_out, d_ff_19_qn);
  not not_9 (not_9_out, nor_7_out);
  nor nor_8 (nor_8_out, not_9_out, d_ff_19_q);
  xor xor_9 (xor_9_out, nor_8_out, d_ff_20_qn);
  not not_10 (not_10_out, nor_8_out);
  nor nor_9 (nor_9_out, not_10_out, d_ff_20_q);
  xor xor_10 (xor_10_out, nor_9_out, d_ff_21_qn);
  not not_11 (not_11_out, nor_9_out);
  nor nor_10 (nor_10_out, not_11_out, d_ff_21_q);
  xor xor_11 (xor_11_out, nor_10_out, d_ff_22_qn);
  not not_12 (not_12_out, nor_10_out);
  nor nor_11 (nor_11_out, not_12_out, d_ff_22_q);
  nor _1 (_1_out, PHI1, not_13_out);
  nor _2 (_2_out, PHI1, nFOUT);
  D_Flip_Flop #(.trigger("high")) d_ff_23 (.clk(PHI1), .D(xor_1_out), .Qn(d_ff_23_qn));  // open: Q, preset, en, reset
  D_Flip_Flop #(.trigger("high")) d_ff_24 (.clk(PHI1), .D(xor_2_out), .Qn(d_ff_24_qn));  // open: Q, preset, en, reset
  D_Flip_Flop #(.trigger("high")) d_ff_25 (.clk(PHI1), .D(xor_3_out), .Qn(d_ff_25_qn));  // open: Q, preset, en, reset
  D_Flip_Flop #(.trigger("high")) d_ff_26 (.clk(PHI1), .D(xor_4_out), .Qn(d_ff_26_qn));  // open: Q, preset, en, reset
  D_Flip_Flop #(.trigger("high")) d_ff_27 (.clk(PHI1), .D(xor_5_out), .Qn(d_ff_27_qn));  // open: Q, preset, en, reset
  D_Flip_Flop #(.trigger("high")) d_ff_28 (.clk(PHI1), .D(xor_6_out), .Qn(d_ff_28_qn));  // open: Q, preset, en, reset
  D_Flip_Flop #(.trigger("high")) d_ff_29 (.clk(PHI1), .D(xor_7_out), .Qn(d_ff_29_qn));  // open: Q, preset, en, reset
  D_Flip_Flop #(.trigger("high")) d_ff_30 (.clk(PHI1), .D(xor_8_out), .Qn(d_ff_30_qn));  // open: Q, preset, en, reset
  D_Flip_Flop #(.trigger("high")) d_ff_31 (.clk(PHI1), .D(xor_9_out), .Qn(d_ff_31_qn));  // open: Q, preset, en, reset
  D_Flip_Flop #(.trigger("high")) d_ff_32 (.clk(PHI1), .D(xor_10_out), .Qn(d_ff_32_qn));  // open: Q, preset, en, reset
  D_Flip_Flop #(.trigger("high")) d_ff_33 (.clk(PHI1), .D(xor_11_out), .Qn(d_ff_33_qn));  // open: Q, preset, en, reset
  D_latch d_latch_1 (.EN(PHI1), .D(nor_11_out), .NOT_Q(nFOUT));  // open: Q
  not not_13 (not_13_out, nFOUT);

  // Notes on the sheet:
  //   TFSTEP
  //   TFLOAD
  //   4
  //   3
endmodule
// TRIANGLE LINEAR DOWN COUNTER
module TRIANGLE_LINEAR_DOWN_COUNTER (
  input  ACLK1,
  input  RES,
  input  W4008,
  input  D0,
  input  D1,
  input  D2,
  input  D3,
  input  D4,
  input  D5,
  input  D6,
  input  D7,
  input  W400B,
  input  nLFO1,
  output TCO,
  output TRI_LC
);

  wire _8_out, _9_out, _11_out, _12_out, _13_out, d_ff_1_q, d_ff_2_q, d_ff_3_q, d_ff_4_q, d_ff_5_q, d_ff_6_q,
       d_ff_7_q, d_ff_8_q, d_ff_9_q, d_ff_9_qn, d_ff_10_q, d_ff_10_qn, d_ff_11_q, d_ff_11_qn, d_ff_12_q,
       d_ff_12_qn, d_ff_13_q, d_ff_13_qn, d_ff_14_q, d_ff_14_qn, d_ff_15_q, d_ff_15_qn, d_ff_16_qn,
       d_ff_17_qn, d_ff_18_qn, d_ff_19_qn, d_ff_20_qn, d_ff_21_qn, d_ff_22_qn, d_latch_1_q, d_latch_2_q,
       d_latch_3_not_q, demultiplexer_1_out0, demultiplexer_1_out1, demultiplexer_2_out0,
       demultiplexer_2_out1, demultiplexer_3_out0, demultiplexer_3_out1, demultiplexer_4_out0,
       demultiplexer_4_out1, demultiplexer_5_out0, demultiplexer_5_out1, demultiplexer_6_out0,
       demultiplexer_6_out1, demultiplexer_7_out0, demultiplexer_7_out1, nor_1_out, nor_2_out, nor_3_out,
       nor_4_out, nor_5_out, nor_6_out, not_1_out, not_2_out, not_3_out, not_4_out, not_5_out, not_6_out,
       not_7_out, not_8_out, not_9_out, or_1_out, or_2_out, or_3_out, or_4_out, or_5_out, or_6_out, or_7_out,
       xor_1_out, xor_2_out, xor_3_out, xor_4_out, xor_5_out, xor_6_out, xor_7_out;

  not not_1 (not_1_out, ACLK1);
  D_Flip_Flop #(.trigger("high")) d_ff_1 (
    .clk(not_1_out), .D(D0), .Q(d_ff_1_q), .en(W4008));  // open: Qn, preset, reset
  D_Flip_Flop #(.trigger("high")) d_ff_2 (
    .clk(not_1_out), .D(D1), .Q(d_ff_2_q), .en(W4008));  // open: Qn, preset, reset
  D_Flip_Flop #(.trigger("high")) d_ff_3 (
    .clk(not_1_out), .D(D2), .Q(d_ff_3_q), .en(W4008));  // open: Qn, preset, reset
  D_Flip_Flop #(.trigger("high")) d_ff_4 (
    .clk(not_1_out), .D(D3), .Q(d_ff_4_q), .en(W4008));  // open: Qn, preset, reset
  D_Flip_Flop #(.trigger("high")) d_ff_5 (
    .clk(not_1_out), .D(D4), .Q(d_ff_5_q), .en(W4008));  // open: Qn, preset, reset
  D_Flip_Flop #(.trigger("high")) d_ff_6 (
    .clk(not_1_out), .D(D5), .Q(d_ff_6_q), .en(W4008));  // open: Qn, preset, reset
  D_Flip_Flop #(.trigger("high")) d_ff_7 (
    .clk(not_1_out), .D(D6), .Q(d_ff_7_q), .en(W4008));  // open: Qn, preset, reset
  D_Flip_Flop #(.trigger("high")) d_ff_8 (
    .clk(not_1_out), .D(D7), .Q(d_ff_8_q), .Qn(TRI_LC), .en(W4008));  // open: preset, reset
  Demultiplexer #(.enable("false")) demultiplexer_1 (
    .out0(demultiplexer_1_out0), .out1(demultiplexer_1_out1), .in(_8_out), .sel(d_ff_1_q));
  Demultiplexer #(.enable("false")) demultiplexer_2 (
    .out0(demultiplexer_2_out0), .out1(demultiplexer_2_out1), .in(_8_out), .sel(d_ff_2_q));
  Demultiplexer #(.enable("false")) demultiplexer_3 (
    .out0(demultiplexer_3_out0), .out1(demultiplexer_3_out1), .in(_8_out), .sel(d_ff_3_q));
  Demultiplexer #(.enable("false")) demultiplexer_4 (
    .out0(demultiplexer_4_out0), .out1(demultiplexer_4_out1), .in(_8_out), .sel(d_ff_4_q));
  Demultiplexer #(.enable("false")) demultiplexer_5 (
    .out0(demultiplexer_5_out0), .out1(demultiplexer_5_out1), .in(_8_out), .sel(d_ff_5_q));
  Demultiplexer #(.enable("false")) demultiplexer_6 (
    .out0(demultiplexer_6_out0), .out1(demultiplexer_6_out1), .in(_8_out), .sel(d_ff_6_q));
  Demultiplexer #(.enable("false")) demultiplexer_7 (
    .out0(demultiplexer_7_out0), .out1(demultiplexer_7_out1), .in(_8_out), .sel(d_ff_7_q));
  or or_1 (or_1_out, RES, demultiplexer_1_out0);
  or or_2 (or_2_out, RES, demultiplexer_2_out0);
  or or_3 (or_3_out, RES, demultiplexer_3_out0);
  or or_4 (or_4_out, RES, demultiplexer_4_out0);
  or or_5 (or_5_out, RES, demultiplexer_5_out0);
  or or_6 (or_6_out, RES, demultiplexer_6_out0);
  or or_7 (or_7_out, RES, demultiplexer_7_out0);
  nor _11 (_11_out, d_latch_1_q, d_ff_8_q, nLFO1);
  D_Flip_Flop #(.trigger("high")) d_ff_9 (
    .clk(_9_out), .D(d_ff_16_qn), .Q(d_ff_9_q), .Qn(d_ff_9_qn), .preset(demultiplexer_1_out1),
    .reset(or_1_out));  // open: en
  D_Flip_Flop #(.trigger("high")) d_ff_10 (
    .clk(_9_out), .D(d_ff_17_qn), .Q(d_ff_10_q), .Qn(d_ff_10_qn), .preset(demultiplexer_2_out1),
    .reset(or_2_out));  // open: en
  D_Flip_Flop #(.trigger("high")) d_ff_11 (
    .clk(_9_out), .D(d_ff_18_qn), .Q(d_ff_11_q), .Qn(d_ff_11_qn), .preset(demultiplexer_3_out1),
    .reset(or_3_out));  // open: en
  D_Flip_Flop #(.trigger("high")) d_ff_12 (
    .clk(_9_out), .D(d_ff_19_qn), .Q(d_ff_12_q), .Qn(d_ff_12_qn), .preset(demultiplexer_4_out1),
    .reset(or_4_out));  // open: en
  D_Flip_Flop #(.trigger("high")) d_ff_13 (
    .clk(_9_out), .D(d_ff_20_qn), .Q(d_ff_13_q), .Qn(d_ff_13_qn), .preset(demultiplexer_5_out1),
    .reset(or_5_out));  // open: en
  D_Flip_Flop #(.trigger("high")) d_ff_14 (
    .clk(_9_out), .D(d_ff_21_qn), .Q(d_ff_14_q), .Qn(d_ff_14_qn), .preset(demultiplexer_6_out1),
    .reset(or_6_out));  // open: en
  D_Flip_Flop #(.trigger("high")) d_ff_15 (
    .clk(_9_out), .D(d_ff_22_qn), .Q(d_ff_15_q), .Qn(d_ff_15_qn), .preset(demultiplexer_7_out1),
    .reset(or_7_out));  // open: en
  nor _12 (_12_out, _11_out, _13_out);
  nor _13 (_13_out, _12_out, W400B);
  xor xor_1 (xor_1_out, 1'b1, d_ff_9_qn);
  not not_2 (not_2_out, 1'b1);
  nor nor_1 (nor_1_out, not_2_out, d_ff_9_q);
  xor xor_2 (xor_2_out, nor_1_out, d_ff_10_qn);
  not not_3 (not_3_out, nor_1_out);
  nor nor_2 (nor_2_out, not_3_out, d_ff_10_q);
  xor xor_3 (xor_3_out, nor_2_out, d_ff_11_qn);
  not not_4 (not_4_out, nor_2_out);
  nor nor_3 (nor_3_out, not_4_out, d_ff_11_q);
  xor xor_4 (xor_4_out, nor_3_out, d_ff_12_qn);
  not not_5 (not_5_out, nor_3_out);
  nor nor_4 (nor_4_out, not_5_out, d_ff_12_q);
  xor xor_5 (xor_5_out, nor_4_out, d_ff_13_qn);
  not not_6 (not_6_out, nor_4_out);
  nor nor_5 (nor_5_out, not_6_out, d_ff_13_q);
  xor xor_6 (xor_6_out, nor_5_out, d_ff_14_qn);
  not not_7 (not_7_out, nor_5_out);
  nor nor_6 (nor_6_out, not_7_out, d_ff_14_q);
  xor xor_7 (xor_7_out, nor_6_out, d_ff_15_qn);
  not not_8 (not_8_out, nor_6_out);
  nor nor_7 (TCO, not_8_out, d_ff_15_q);
  D_Flip_Flop #(.trigger("high")) d_ff_16 (.clk(ACLK1), .D(xor_1_out), .Qn(d_ff_16_qn));  // open: Q, preset, en, reset
  D_Flip_Flop #(.trigger("high")) d_ff_17 (.clk(ACLK1), .D(xor_2_out), .Qn(d_ff_17_qn));  // open: Q, preset, en, reset
  D_Flip_Flop #(.trigger("high")) d_ff_18 (.clk(ACLK1), .D(xor_3_out), .Qn(d_ff_18_qn));  // open: Q, preset, en, reset
  D_Flip_Flop #(.trigger("high")) d_ff_19 (.clk(ACLK1), .D(xor_4_out), .Qn(d_ff_19_qn));  // open: Q, preset, en, reset
  D_Flip_Flop #(.trigger("high")) d_ff_20 (.clk(ACLK1), .D(xor_5_out), .Qn(d_ff_20_qn));  // open: Q, preset, en, reset
  D_Flip_Flop #(.trigger("high")) d_ff_21 (.clk(ACLK1), .D(xor_6_out), .Qn(d_ff_21_qn));  // open: Q, preset, en, reset
  D_Flip_Flop #(.trigger("high")) d_ff_22 (.clk(ACLK1), .D(xor_7_out), .Qn(d_ff_22_qn));  // open: Q, preset, en, reset
  D_latch d_latch_1 (.EN(ACLK1), .D(_13_out), .Q(d_latch_1_q));  // open: NOT_Q
  D_latch d_latch_2 (.EN(ACLK1), .D(TCO), .Q(d_latch_2_q));  // open: NOT_Q
  not not_9 (not_9_out, d_latch_3_not_q);
  D_latch d_latch_3 (.EN(ACLK1), .D(_12_out), .NOT_Q(d_latch_3_not_q));  // open: Q
  nor _9 (_9_out, d_latch_2_q, not_9_out, nLFO1);
  nor _8 (_8_out, nLFO1, d_latch_3_not_q);

  // Notes on the sheet:
  //   10
  //   R
  //   S
  //   TRELOAD
  //   Q
  //   RELOAD  FF
  //   /Q
  //   TCO
  //   TCO
  //   11
  //   RELOAD LATCH 1
  //   14
  //   TCO LATCH
  //   6,7
  //   RELOAD LATCH 2
  //   TSTEP
  //   TLOAD
endmodule

// TRIANGLE OUTPUT COUNTER
module TRIANGLE_OUTPUT_COUNTER (
  input  PHI1,
  input  TTSTEP,
  input  RES,
  input  D0,
  input  W401A,
  input  D1,
  input  D2,
  input  D3,
  input  D4,
  output TRI0,
  output TRI1,
  output TRI2,
  output TRI3
);

  wire d_ff_1_q, d_ff_1_qn, d_ff_2_q, d_ff_2_qn, d_ff_3_q, d_ff_3_qn, d_ff_4_q, d_ff_4_qn, d_ff_5_q,
       d_ff_5_qn, d_ff_6_qn, d_ff_7_qn, d_ff_8_qn, d_ff_9_qn, d_ff_10_qn, demultiplexer_1_out0,
       demultiplexer_1_out1, demultiplexer_2_out0, demultiplexer_2_out1, demultiplexer_3_out0,
       demultiplexer_3_out1, demultiplexer_4_out0, demultiplexer_4_out1, demultiplexer_5_out0,
       demultiplexer_5_out1, nor_1_out, nor_2_out, nor_3_out, nor_4_out, nor_5_out, not_1_out, not_2_out,
       not_3_out, not_4_out, not_5_out, or_1_out, or_2_out, or_3_out, or_4_out, or_5_out, xor_1_out,
       xor_2_out, xor_3_out, xor_4_out, xor_5_out;

  Demultiplexer #(.enable("false")) demultiplexer_1 (
    .out0(demultiplexer_1_out0), .out1(demultiplexer_1_out1), .in(W401A), .sel(D0));
  Demultiplexer #(.enable("false")) demultiplexer_2 (
    .out0(demultiplexer_2_out0), .out1(demultiplexer_2_out1), .in(W401A), .sel(D1));
  Demultiplexer #(.enable("false")) demultiplexer_3 (
    .out0(demultiplexer_3_out0), .out1(demultiplexer_3_out1), .in(W401A), .sel(D2));
  Demultiplexer #(.enable("false")) demultiplexer_4 (
    .out0(demultiplexer_4_out0), .out1(demultiplexer_4_out1), .in(W401A), .sel(D3));
  Demultiplexer #(.enable("false")) demultiplexer_5 (
    .out0(demultiplexer_5_out0), .out1(demultiplexer_5_out1), .in(W401A), .sel(D4));
  or or_1 (or_1_out, RES, demultiplexer_1_out0);
  or or_2 (or_2_out, RES, demultiplexer_2_out0);
  or or_3 (or_3_out, RES, demultiplexer_3_out0);
  or or_4 (or_4_out, RES, demultiplexer_4_out0);
  or or_5 (or_5_out, RES, demultiplexer_5_out0);
  D_Flip_Flop #(.trigger("high")) d_ff_1 (
    .clk(TTSTEP), .D(d_ff_6_qn), .Q(d_ff_1_q), .Qn(d_ff_1_qn), .preset(demultiplexer_1_out1), .reset(or_1_out));  // open: en
  D_Flip_Flop #(.trigger("high")) d_ff_2 (
    .clk(TTSTEP), .D(d_ff_7_qn), .Q(d_ff_2_q), .Qn(d_ff_2_qn), .preset(demultiplexer_2_out1), .reset(or_2_out));  // open: en
  D_Flip_Flop #(.trigger("high")) d_ff_3 (
    .clk(TTSTEP), .D(d_ff_8_qn), .Q(d_ff_3_q), .Qn(d_ff_3_qn), .preset(demultiplexer_3_out1), .reset(or_3_out));  // open: en
  D_Flip_Flop #(.trigger("high")) d_ff_4 (
    .clk(TTSTEP), .D(d_ff_9_qn), .Q(d_ff_4_q), .Qn(d_ff_4_qn), .preset(demultiplexer_4_out1), .reset(or_4_out));  // open: en
  D_Flip_Flop #(.trigger("high")) d_ff_5 (
    .clk(TTSTEP), .D(d_ff_10_qn), .Q(d_ff_5_q), .Qn(d_ff_5_qn), .preset(demultiplexer_5_out1),
    .reset(or_5_out));  // open: en
  not not_1 (not_1_out, 1'b1);
  not not_2 (not_2_out, nor_1_out);
  not not_3 (not_3_out, nor_2_out);
  not not_4 (not_4_out, nor_3_out);
  not not_5 (not_5_out, nor_4_out);
  xor xor_1 (xor_1_out, 1'b1, d_ff_1_qn);
  nor nor_1 (nor_1_out, not_1_out, d_ff_1_qn);
  xor xor_2 (xor_2_out, nor_1_out, d_ff_2_qn);
  nor nor_2 (nor_2_out, not_2_out, d_ff_2_qn);
  xor xor_3 (xor_3_out, nor_2_out, d_ff_3_qn);
  nor nor_3 (nor_3_out, not_3_out, d_ff_3_qn);
  xor xor_4 (xor_4_out, nor_3_out, d_ff_4_qn);
  nor nor_4 (nor_4_out, not_4_out, d_ff_4_qn);
  xor xor_5 (xor_5_out, nor_4_out, d_ff_5_qn);
  nor nor_5 (nor_5_out, not_5_out, d_ff_5_qn);
  D_Flip_Flop #(.trigger("high")) d_ff_6 (.clk(PHI1), .D(xor_1_out), .Qn(d_ff_6_qn));  // open: Q, preset, en, reset
  D_Flip_Flop #(.trigger("high")) d_ff_7 (.clk(PHI1), .D(xor_2_out), .Qn(d_ff_7_qn));  // open: Q, preset, en, reset
  D_Flip_Flop #(.trigger("high")) d_ff_8 (.clk(PHI1), .D(xor_3_out), .Qn(d_ff_8_qn));  // open: Q, preset, en, reset
  D_Flip_Flop #(.trigger("high")) d_ff_9 (.clk(PHI1), .D(xor_4_out), .Qn(d_ff_9_qn));  // open: Q, preset, en, reset
  D_Flip_Flop #(.trigger("high")) d_ff_10 (.clk(PHI1), .D(xor_5_out), .Qn(d_ff_10_qn));  // open: Q, preset, en, reset
  xnor xnor_1 (TRI0, d_ff_1_q, d_ff_5_q);
  xnor xnor_2 (TRI1, d_ff_2_q, d_ff_5_q);
  xnor xnor_3 (TRI2, d_ff_3_q, d_ff_5_q);
  xnor xnor_4 (TRI3, d_ff_4_q, d_ff_5_q);

  // Notes on the sheet:
  //   not used
endmodule

// NOISE CHANNEL
module NOISE_CHANNEL (
  input  nACLK2,
  input  ACLK1,
  input  D0,
  input  D1,
  input  D2,
  input  D3,
  input  D4,
  input  D5,
  input  D7,
  input  NORND,
  input  LOCK,
  input  W400E,
  input  W400C,
  input  W400F,
  input  Res,
  input  nLFO1,
  output RND0,
  output RND1,
  output RND2,
  output RND3,
  output nRND_LC
);

  wire noise_frequency_lfsr_1_rstep, random_lfsr_1_rndout;

  NOISE_FREQUENCY_LFSR noise_frequency_lfsr_1 (
    .ACLK1(ACLK1), .nACLK2(nACLK2), .RES(Res), .D0(D0), .D1(D1), .D2(D2), .D3(D3),
    .RSTEP(noise_frequency_lfsr_1_rstep), .W400E(W400E));
  RANDOM_LFSR random_lfsr_1 (
    .RSTEP(noise_frequency_lfsr_1_rstep), .W400E(W400E), .D7(D7), .NORND(NORND),
    .RNDOUT(random_lfsr_1_rndout), .LOCK(LOCK), .ACLK1(ACLK1));
  ENVELOPE_GENERATOR envelope_generator_1 (
    .ACLK1(ACLK1), .W400_0__4__C(W400C), .W400_3__7__F(W400F), .D0(D0), .D1(D1), .D2(D2), .D3(D3), .D4(D4),
    .D5(D5), .nLFO1(nLFO1), .RES(Res), .V0(RND0), .V1(RND1), .V2(RND2), .V3(RND3), .nCH_LC(nRND_LC),
    .CH_IN(random_lfsr_1_rndout));
endmodule

// NOISE FREQUENCY LFSR
module NOISE_FREQUENCY_LFSR (
  input  ACLK1,
  input  D0,
  input  D1,
  input  D2,
  input  D3,
  input  W400E,
  input  nACLK2,
  input  RES,
  output RSTEP
);

  wire _9_out, _11_out, _14_out, _15_2_out, _15_out, _16_out, d_ff_1_q, d_ff_2_q, d_ff_3_q, d_ff_4_q,
       d_ff_5_qn, d_ff_6_qn, d_ff_7_qn, d_ff_8_qn, d_ff_9_qn, d_ff_10_qn, d_ff_11_qn, d_ff_12_qn, d_ff_13_qn,
       d_ff_14_qn, d_ff_15_qn, d_ff_16_qn, d_ff_17_qn, d_ff_18_qn, d_ff_19_qn, d_ff_20_qn, d_ff_21_qn,
       d_ff_22_qn, d_ff_23_qn, d_ff_24_qn, d_ff_25_qn, d_ff_26_qn, demultiplexer_1_out0,
       demultiplexer_1_out1, demultiplexer_2_out0, demultiplexer_2_out1, demultiplexer_3_out0,
       demultiplexer_3_out1, demultiplexer_4_out0, demultiplexer_4_out1, demultiplexer_5_out0,
       demultiplexer_5_out1, demultiplexer_6_out0, demultiplexer_6_out1, demultiplexer_7_out0,
       demultiplexer_7_out1, demultiplexer_8_out0, demultiplexer_8_out1, demultiplexer_9_out0,
       demultiplexer_9_out1, demultiplexer_10_out0, demultiplexer_10_out1, demultiplexer_11_out0,
       demultiplexer_11_out1, demultiplexer_12_out0, demultiplexer_12_out1, noise_table_1_nnf0,
       noise_table_1_nnf1, noise_table_1_nnf2, noise_table_1_nnf3, noise_table_1_nnf4, noise_table_1_nnf5,
       noise_table_1_nnf6, noise_table_1_nnf7, noise_table_1_nnf8, noise_table_1_nnf9, noise_table_1_nnf10,
       not_1_out, not_2_out, not_3_out, not_4_out, not_5_out;

  not not_1 (not_1_out, ACLK1);
  D_Flip_Flop #(.trigger("high")) d_ff_1 (
    .clk(not_1_out), .D(D0), .Q(d_ff_1_q), .en(W400E), .reset(RES));  // open: Qn, preset
  D_Flip_Flop #(.trigger("high")) d_ff_2 (
    .clk(not_1_out), .D(D1), .Q(d_ff_2_q), .en(W400E), .reset(RES));  // open: Qn, preset
  D_Flip_Flop #(.trigger("high")) d_ff_3 (
    .clk(not_1_out), .D(D2), .Q(d_ff_3_q), .en(W400E), .reset(RES));  // open: Qn, preset
  D_Flip_Flop #(.trigger("high")) d_ff_4 (
    .clk(not_1_out), .D(D3), .Q(d_ff_4_q), .en(W400E), .reset(RES));  // open: Qn, preset
  not not_2 (not_2_out, not_3_out);
  not not_3 (not_3_out, nACLK2);
  NOISE_TABLE noise_table_1 (
    .NNF0(noise_table_1_nnf0), .NNF1(noise_table_1_nnf1), .NNF2(noise_table_1_nnf2),
    .NNF3(noise_table_1_nnf3), .NNF4(noise_table_1_nnf4), .NNF5(noise_table_1_nnf5),
    .NNF6(noise_table_1_nnf6), .NNF7(noise_table_1_nnf7), .NNF8(noise_table_1_nnf8),
    .NNF9(noise_table_1_nnf9), .NNF10(noise_table_1_nnf10), .NF3(d_ff_4_q), .NF2(d_ff_3_q), .NF1(d_ff_2_q),
    .NF0(d_ff_1_q));
  not not_4 (not_4_out, _9_out);
  nor _11 (_11_out, not_2_out, _9_out);
  nor _12 (RSTEP, not_4_out, not_2_out);
  Demultiplexer #(.enable("false")) demultiplexer_1 (
    .out0(demultiplexer_1_out0), .out1(demultiplexer_1_out1), .in(RSTEP), .sel(noise_table_1_nnf0));
  Demultiplexer #(.enable("false")) demultiplexer_2 (
    .out0(demultiplexer_2_out0), .out1(demultiplexer_2_out1), .in(RSTEP), .sel(noise_table_1_nnf1));
  Demultiplexer #(.enable("false")) demultiplexer_3 (
    .out0(demultiplexer_3_out0), .out1(demultiplexer_3_out1), .in(RSTEP), .sel(noise_table_1_nnf2));
  Demultiplexer #(.enable("false")) demultiplexer_4 (
    .out0(demultiplexer_4_out0), .out1(demultiplexer_4_out1), .in(RSTEP), .sel(noise_table_1_nnf3));
  Demultiplexer #(.enable("false")) demultiplexer_5 (
    .out0(demultiplexer_5_out0), .out1(demultiplexer_5_out1), .in(RSTEP), .sel(noise_table_1_nnf4));
  Demultiplexer #(.enable("false")) demultiplexer_6 (
    .out0(demultiplexer_6_out0), .out1(demultiplexer_6_out1), .in(RSTEP), .sel(noise_table_1_nnf5));
  Demultiplexer #(.enable("false")) demultiplexer_7 (
    .out0(demultiplexer_7_out0), .out1(demultiplexer_7_out1), .in(RSTEP), .sel(noise_table_1_nnf6));
  Demultiplexer #(.enable("false")) demultiplexer_8 (
    .out0(demultiplexer_8_out0), .out1(demultiplexer_8_out1), .in(RSTEP), .sel(noise_table_1_nnf7));
  Demultiplexer #(.enable("false")) demultiplexer_9 (
    .out0(demultiplexer_9_out0), .out1(demultiplexer_9_out1), .in(RSTEP), .sel(noise_table_1_nnf8));
  Demultiplexer #(.enable("false")) demultiplexer_10 (
    .out0(demultiplexer_10_out0), .out1(demultiplexer_10_out1), .in(RSTEP), .sel(noise_table_1_nnf9));
  Demultiplexer #(.enable("false")) demultiplexer_11 (
    .out0(demultiplexer_11_out0), .out1(demultiplexer_11_out1), .in(RSTEP), .sel(noise_table_1_nnf10));
  nor _9 (_9_out, not_5_out, RES);
  D_Flip_Flop #(.trigger("high")) d_ff_5 (
    .clk(_11_out), .D(_15_2_out), .Qn(d_ff_5_qn), .preset(demultiplexer_1_out1), .reset(demultiplexer_1_out0));  // open: Q, en
  D_Flip_Flop #(.trigger("high")) d_ff_6 (
    .clk(_11_out), .D(d_ff_16_qn), .Qn(d_ff_6_qn), .preset(demultiplexer_2_out1), .reset(demultiplexer_2_out0));  // open: Q, en
  D_Flip_Flop #(.trigger("high")) d_ff_7 (
    .clk(_11_out), .D(d_ff_17_qn), .Qn(d_ff_7_qn), .preset(demultiplexer_3_out1), .reset(demultiplexer_3_out0));  // open: Q, en
  D_Flip_Flop #(.trigger("high")) d_ff_8 (
    .clk(_11_out), .D(d_ff_18_qn), .Qn(d_ff_8_qn), .preset(demultiplexer_4_out1), .reset(demultiplexer_4_out0));  // open: Q, en
  D_Flip_Flop #(.trigger("high")) d_ff_9 (
    .clk(_11_out), .D(d_ff_19_qn), .Qn(d_ff_9_qn), .preset(demultiplexer_5_out1), .reset(demultiplexer_5_out0));  // open: Q, en
  D_Flip_Flop #(.trigger("high")) d_ff_10 (
    .clk(_11_out), .D(d_ff_20_qn), .Qn(d_ff_10_qn), .preset(demultiplexer_6_out1),
    .reset(demultiplexer_6_out0));  // open: Q, en
  D_Flip_Flop #(.trigger("high")) d_ff_11 (
    .clk(_11_out), .D(d_ff_21_qn), .Qn(d_ff_11_qn), .preset(demultiplexer_7_out1),
    .reset(demultiplexer_7_out0));  // open: Q, en
  D_Flip_Flop #(.trigger("high")) d_ff_12 (
    .clk(_11_out), .D(d_ff_22_qn), .Qn(d_ff_12_qn), .preset(demultiplexer_8_out1),
    .reset(demultiplexer_8_out0));  // open: Q, en
  D_Flip_Flop #(.trigger("high")) d_ff_13 (
    .clk(_11_out), .D(d_ff_23_qn), .Qn(d_ff_13_qn), .preset(demultiplexer_9_out1),
    .reset(demultiplexer_9_out0));  // open: Q, en
  D_Flip_Flop #(.trigger("high")) d_ff_14 (
    .clk(_11_out), .D(d_ff_24_qn), .Qn(d_ff_14_qn), .preset(demultiplexer_10_out1),
    .reset(demultiplexer_10_out0));  // open: Q, en
  D_Flip_Flop #(.trigger("high")) d_ff_15 (
    .clk(_11_out), .D(d_ff_25_qn), .Qn(d_ff_15_qn), .preset(demultiplexer_11_out1),
    .reset(demultiplexer_11_out0));  // open: Q, en
  not not_5 (not_5_out, demultiplexer_12_out1);
  D_Flip_Flop #(.trigger("high")) d_ff_16 (.clk(ACLK1), .D(d_ff_5_qn), .Qn(d_ff_16_qn));  // open: Q, preset, en, reset
  D_Flip_Flop #(.trigger("high")) d_ff_17 (.clk(ACLK1), .D(d_ff_6_qn), .Qn(d_ff_17_qn));  // open: Q, preset, en, reset
  D_Flip_Flop #(.trigger("high")) d_ff_18 (.clk(ACLK1), .D(d_ff_7_qn), .Qn(d_ff_18_qn));  // open: Q, preset, en, reset
  D_Flip_Flop #(.trigger("high")) d_ff_19 (.clk(ACLK1), .D(d_ff_8_qn), .Qn(d_ff_19_qn));  // open: Q, preset, en, reset
  D_Flip_Flop #(.trigger("high")) d_ff_20 (.clk(ACLK1), .D(d_ff_9_qn), .Qn(d_ff_20_qn));  // open: Q, preset, en, reset
  D_Flip_Flop #(.trigger("high")) d_ff_21 (.clk(ACLK1), .D(d_ff_10_qn), .Qn(d_ff_21_qn));  // open: Q, preset, en, reset
  D_Flip_Flop #(.trigger("high")) d_ff_22 (.clk(ACLK1), .D(d_ff_11_qn), .Qn(d_ff_22_qn));  // open: Q, preset, en, reset
  D_Flip_Flop #(.trigger("high")) d_ff_23 (.clk(ACLK1), .D(d_ff_12_qn), .Qn(d_ff_23_qn));  // open: Q, preset, en, reset
  D_Flip_Flop #(.trigger("high")) d_ff_24 (.clk(ACLK1), .D(d_ff_13_qn), .Qn(d_ff_24_qn));  // open: Q, preset, en, reset
  D_Flip_Flop #(.trigger("high")) d_ff_25 (.clk(ACLK1), .D(d_ff_14_qn), .Qn(d_ff_25_qn));  // open: Q, preset, en, reset
  D_Flip_Flop #(.trigger("high")) d_ff_26 (.clk(ACLK1), .D(d_ff_15_qn), .Qn(d_ff_26_qn));  // open: Q, preset, en, reset
  and _15 (_15_out, d_ff_24_qn, d_ff_26_qn);
  nor _16 (_16_out, d_ff_16_qn, d_ff_17_qn, d_ff_18_qn, d_ff_19_qn, d_ff_20_qn, d_ff_21_qn, d_ff_22_qn, d_ff_23_qn, d_ff_24_qn, d_ff_25_qn);
  nor _14 (_14_out, d_ff_24_qn, demultiplexer_12_out0, d_ff_26_qn);
  Demultiplexer #(.disabled(0), .enable("false")) demultiplexer_12 (
    .out0(demultiplexer_12_out0), .out1(demultiplexer_12_out1), .in(_16_out), .sel(d_ff_26_qn));
  nor _15_2 (_15_2_out, _14_out, RES, _15_out);

  // Notes on the sheet:
  //   10
  //   8
  //   13
  //   NFSTEP
  //   NFLOAD
  //   17
endmodule

// NOISE TABLE
module NOISE_TABLE (
  input  NF0,
  input  NF1,
  input  NF2,
  input  NF3,
  output NNF0,
  output NNF1,
  output NNF2,
  output NNF3,
  output NNF4,
  output NNF5,
  output NNF6,
  output NNF7,
  output NNF8,
  output NNF9,
  output NNF10
);

  wire button_1_out;
  wire [3:0] counter_1_q;

  Counter #(.width(4), .max('hf)) counter_1 (.Q(counter_1_q), .clk(button_1_out));  // open: load, D, count, carry, clr
  Button button_1 (.out(button_1_out));
  Multiplexer #(.select(4), .width(11), .disabled(0), .enable("false")) multiplexer_1 (
    .in0(11'h200), .in1(11'h280), .in2(11'h2a8), .in3(11'h6ea), .in4(11'h4e4), .in5(11'h674), .in6(11'h630),
    .in7(11'h730), .in8(11'h4ac), .in9(11'h304), .in10(11'h722), .in11(11'h230), .in12(11'h213),
    .in13(11'h782), .in14(11'h6), .in15(11'h14),
    .out({NNF10, NNF9, NNF8, NNF7, NNF6, NNF5, NNF4, NNF3, NNF2, NNF1, NNF0}), .sel(counter_1_q));
  // Probe on {NNF10, NNF9, NNF8, NNF7, NNF6, NNF5, NNF4, NNF3, NNF2, NNF1, NNF0}
  // Probe on {NNF0, NNF1, NNF2, NNF3, NNF4, NNF5, NNF6, NNF7, NNF8, NNF9, NNF10}

  // Notes on the sheet:
  //   PAL
  //   NTSC
endmodule

// RANDOM LFSR
module RANDOM_LFSR (
  input  ACLK1,
  input  RSTEP,
  input  D7,
  input  W400E,
  input  NORND,
  input  LOCK,
  output RNDOUT
);

  wire _2_2_out, _2_out, _3_out, _5_out, _6_out, d_ff_1_qn, d_ff_2_qn, d_ff_3_qn, d_ff_4_qn, d_ff_5_qn,
       d_ff_6_qn, d_ff_7_qn, d_ff_8_qn, d_ff_9_qn, d_ff_10_qn, d_ff_11_qn, d_ff_12_qn, d_ff_13_qn,
       d_ff_14_qn, d_ff_15_qn, d_ff_16_qn, d_ff_17_qn, d_ff_18_qn, d_ff_19_qn, d_ff_20_qn, d_ff_21_qn,
       d_ff_22_qn, d_ff_23_qn, d_ff_24_qn, d_ff_25_qn, d_ff_26_qn, d_ff_27_qn, d_ff_28_qn, d_ff_29_qn,
       d_ff_30_qn, d_ff_31_q, multiplexer_1_out, not_1_out;

  D_Flip_Flop #(.trigger("high")) d_ff_1 (.clk(RSTEP), .D(_2_2_out), .Qn(d_ff_1_qn));  // open: Q, preset, en, reset
  D_Flip_Flop #(.trigger("high")) d_ff_2 (.clk(RSTEP), .D(d_ff_16_qn), .Qn(d_ff_2_qn));  // open: Q, preset, en, reset
  D_Flip_Flop #(.trigger("high")) d_ff_3 (.clk(RSTEP), .D(d_ff_17_qn), .Qn(d_ff_3_qn));  // open: Q, preset, en, reset
  D_Flip_Flop #(.trigger("high")) d_ff_4 (.clk(RSTEP), .D(d_ff_18_qn), .Qn(d_ff_4_qn));  // open: Q, preset, en, reset
  D_Flip_Flop #(.trigger("high")) d_ff_5 (.clk(RSTEP), .D(d_ff_19_qn), .Qn(d_ff_5_qn));  // open: Q, preset, en, reset
  D_Flip_Flop #(.trigger("high")) d_ff_6 (.clk(RSTEP), .D(d_ff_20_qn), .Qn(d_ff_6_qn));  // open: Q, preset, en, reset
  D_Flip_Flop #(.trigger("high")) d_ff_7 (.clk(RSTEP), .D(d_ff_21_qn), .Qn(d_ff_7_qn));  // open: Q, preset, en, reset
  D_Flip_Flop #(.trigger("high")) d_ff_8 (.clk(RSTEP), .D(d_ff_22_qn), .Qn(d_ff_8_qn));  // open: Q, preset, en, reset
  D_Flip_Flop #(.trigger("high")) d_ff_9 (.clk(RSTEP), .D(d_ff_23_qn), .Qn(d_ff_9_qn));  // open: Q, preset, en, reset
  D_Flip_Flop #(.trigger("high")) d_ff_10 (.clk(RSTEP), .D(d_ff_24_qn), .Qn(d_ff_10_qn));  // open: Q, preset, en, reset
  D_Flip_Flop #(.trigger("high")) d_ff_11 (.clk(RSTEP), .D(d_ff_25_qn), .Qn(d_ff_11_qn));  // open: Q, preset, en, reset
  D_Flip_Flop #(.trigger("high")) d_ff_12 (.clk(RSTEP), .D(d_ff_26_qn), .Qn(d_ff_12_qn));  // open: Q, preset, en, reset
  D_Flip_Flop #(.trigger("high")) d_ff_13 (.clk(RSTEP), .D(d_ff_27_qn), .Qn(d_ff_13_qn));  // open: Q, preset, en, reset
  D_Flip_Flop #(.trigger("high")) d_ff_14 (.clk(RSTEP), .D(d_ff_28_qn), .Qn(d_ff_14_qn));  // open: Q, preset, en, reset
  D_Flip_Flop #(.trigger("high")) d_ff_15 (.clk(RSTEP), .D(d_ff_29_qn), .Qn(d_ff_15_qn));  // open: Q, preset, en, reset
  not not_1 (not_1_out, ACLK1);
  D_Flip_Flop #(.trigger("high")) d_ff_16 (.clk(ACLK1), .D(d_ff_1_qn), .Qn(d_ff_16_qn));  // open: Q, preset, en, reset
  D_Flip_Flop #(.trigger("high")) d_ff_17 (.clk(ACLK1), .D(d_ff_2_qn), .Qn(d_ff_17_qn));  // open: Q, preset, en, reset
  D_Flip_Flop #(.trigger("high")) d_ff_18 (.clk(ACLK1), .D(d_ff_3_qn), .Qn(d_ff_18_qn));  // open: Q, preset, en, reset
  D_Flip_Flop #(.trigger("high")) d_ff_19 (.clk(ACLK1), .D(d_ff_4_qn), .Qn(d_ff_19_qn));  // open: Q, preset, en, reset
  D_Flip_Flop #(.trigger("high")) d_ff_20 (.clk(ACLK1), .D(d_ff_5_qn), .Qn(d_ff_20_qn));  // open: Q, preset, en, reset
  D_Flip_Flop #(.trigger("high")) d_ff_21 (.clk(ACLK1), .D(d_ff_6_qn), .Qn(d_ff_21_qn));  // open: Q, preset, en, reset
  D_Flip_Flop #(.trigger("high")) d_ff_22 (.clk(ACLK1), .D(d_ff_7_qn), .Qn(d_ff_22_qn));  // open: Q, preset, en, reset
  D_Flip_Flop #(.trigger("high")) d_ff_23 (.clk(ACLK1), .D(d_ff_8_qn), .Qn(d_ff_23_qn));  // open: Q, preset, en, reset
  D_Flip_Flop #(.trigger("high")) d_ff_24 (.clk(ACLK1), .D(d_ff_9_qn), .Qn(d_ff_24_qn));  // open: Q, preset, en, reset
  D_Flip_Flop #(.trigger("high")) d_ff_25 (.clk(ACLK1), .D(d_ff_10_qn), .Qn(d_ff_25_qn));  // open: Q, preset, en, reset
  D_Flip_Flop #(.trigger("high")) d_ff_26 (.clk(ACLK1), .D(d_ff_11_qn), .Qn(d_ff_26_qn));  // open: Q, preset, en, reset
  D_Flip_Flop #(.trigger("high")) d_ff_27 (.clk(ACLK1), .D(d_ff_12_qn), .Qn(d_ff_27_qn));  // open: Q, preset, en, reset
  D_Flip_Flop #(.trigger("high")) d_ff_28 (.clk(ACLK1), .D(d_ff_13_qn), .Qn(d_ff_28_qn));  // open: Q, preset, en, reset
  D_Flip_Flop #(.trigger("high")) d_ff_29 (.clk(ACLK1), .D(d_ff_14_qn), .Qn(d_ff_29_qn));  // open: Q, preset, en, reset
  D_Flip_Flop #(.trigger("high")) d_ff_30 (.clk(ACLK1), .D(d_ff_15_qn), .Qn(d_ff_30_qn));  // open: Q, preset, en, reset
  D_Flip_Flop #(.trigger("high")) d_ff_31 (
    .clk(not_1_out), .D(D7), .Q(d_ff_31_q), .en(W400E));  // open: Qn, preset, reset
  Multiplexer #(.enable("false")) multiplexer_1 (
    .in0(d_ff_29_qn), .in1(d_ff_24_qn), .out(multiplexer_1_out), .sel(d_ff_31_q));
  nor _5 (_5_out, d_ff_16_qn, d_ff_17_qn, d_ff_18_qn, d_ff_19_qn, d_ff_20_qn, d_ff_21_qn, d_ff_22_qn, d_ff_23_qn, d_ff_24_qn, d_ff_25_qn, d_ff_26_qn, d_ff_27_qn, d_ff_28_qn, d_ff_29_qn, d_ff_30_qn);
  nor _3 (_3_out, d_ff_30_qn, _5_out, multiplexer_1_out);
  and _2 (_2_out, multiplexer_1_out, d_ff_30_qn);
  nor _6 (_6_out, d_ff_30_qn, NORND);
  nor _2_2 (_2_2_out, _3_out, LOCK, _2_out);
  nor _7 (RNDOUT, _6_out, LOCK);

  // Notes on the sheet:
  //   Feedback comes from outputs R13, R14
  //   In the earliest versions of 2A03, the mode flag is missing.
  //   R8
  //   R13
  //   R14
  //   4
endmodule

// DPCM CHANNEL
module DPCM_CHANNEL (
  input  PHI1,
  input  nACLK2,
  input  ACLK1,
  input  W4010,
  input  D0,
  input  D1,
  input  D2,
  input  D3,
  input  D4,
  input  D5,
  input  D6,
  input  D7,
  input  W4015,
  input  nR4015,
  input  LOCK,
  input  R_W,
  input  W4013,
  input  Res,
  input  W4011,
  input  W4012,
  output D4_2,
  output D7_2,
  output DMCINT,
  output RUNDMC,
  output DMCRDY,
  output nDMC_AB,
  output DMC0,
  output DMC1,
  output DMC2,
  output DMC3,
  output DMC4,
  output DMC5,
  output DMC6,
  output DMCA0,
  output DMCA1,
  output DMCA2,
  output DMCA3,
  output DMCA4,
  output DMCA5,
  output DMCA6,
  output DMCA7,
  output DMCA8,
  output DMCA9,
  output DMCA10,
  output DMCA11,
  output DMCA12,
  output DMCA13,
  output DMCA14
);

  wire ACLK2, dpcm_control_1_bload, dpcm_control_1_bstep, dpcm_control_1_dmstep, dpcm_control_1_dsload,
       dpcm_control_1_dsstep, dpcm_control_1_nstep, dpcm_control_1_pcm, dpcm_frequency_lfsr_1_dfload,
       dpcm_output_counter_1_dout, DPCM_SAMPLE_BIT_COUNTER_nnout, dpcm_sample_length_down_counter_1_sout,
       dpcm_sample_shift_register_1_nbout;

  not not_1 (ACLK2, nACLK2);
  DPCM_FREQUENCY_LFSR dpcm_frequency_lfsr_1 (
    .ACLK1(ACLK1), .Res(Res), .D0(D0), .D1(D1), .D2(D2), .D3(D3), .DFLOAD(dpcm_frequency_lfsr_1_dfload),
    .ACLK2(ACLK2), .W4010(W4010));
  DPCM_SAMPLE_BIT_COUNTER DPCM_SAMPLE_BIT_COUNTER (
    .ACLK1(ACLK1), .RES(Res), .NSTEP(dpcm_control_1_nstep), .nNOUT(DPCM_SAMPLE_BIT_COUNTER_nnout));
  DPCM_CONTROL dpcm_control_1 (
    .nACLK2(nACLK2), .ACLK1(ACLK1), .PHI1(PHI1), .D4(D4), .W4015(W4015), .nR4015(nR4015), .D7(D7), .RES(Res),
    .D6(D6), .SOUT(dpcm_sample_length_down_counter_1_sout), .R_W(R_W), .DFLOAD(dpcm_frequency_lfsr_1_dfload),
    .DOUT(dpcm_output_counter_1_dout), .nNOUT(DPCM_SAMPLE_BIT_COUNTER_nnout), .D4_2(D4_2), .DMCINT(DMCINT),
    .D7_2(D7_2), .DSSTEP(dpcm_control_1_dsstep), .DSLOAD(dpcm_control_1_dsload), .RUNDMC(RUNDMC),
    .DMCRDY(DMCRDY), .nDMC_AB(nDMC_AB), .NSTEP(dpcm_control_1_nstep), .DMSTEP(dpcm_control_1_dmstep),
    .PCM(dpcm_control_1_pcm), .BLOAD(dpcm_control_1_bload), .BSTEP(dpcm_control_1_bstep), .LOCK(LOCK),
    .ACLK2(ACLK2), .W4010(W4010));
  DPCM_SAMPLE_LENGTH_DOWN_COUNTER dpcm_sample_length_down_counter_1 (
    .ACLK1(ACLK1), .DSLOAD(dpcm_control_1_dsload), .DSSTEP(dpcm_control_1_dsstep), .RES(Res), .LSC0(D0),
    .LSC1(D1), .LSC2(D2), .LSC3(D3), .LSC4(D4), .LSC5(D5), .LSC6(D6), .LSC7(D7),
    .SOUT(dpcm_sample_length_down_counter_1_sout), .W4013(W4013));
  DPCM_ADDRESS_COUNTER dpcm_address_counter_1 (
    .DSLOAD(dpcm_control_1_dsload), .DSSTEP(dpcm_control_1_dsstep), .RES(Res), .LDMC6(D0), .LDMC7(D1),
    .LDMC8(D2), .LDMC9(D3), .LDMC10(D4), .LDMC11(D5), .LDMC12(D6), .LDMC13(D7), .DMC_A0(DMCA0),
    .DMC_A1(DMCA1), .DMC_A2(DMCA2), .DMC_A3(DMCA3), .DMC_A4(DMCA4), .DMC_A5(DMCA5), .DMC_A6(DMCA6),
    .DMC_A7(DMCA7), .DMC_A8(DMCA8), .DMC_A9(DMCA9), .DMC_A10(DMCA10), .DMC_A11(DMCA11), .DMC_A12(DMCA12),
    .DMC_A13(DMCA13), .DMC_A14(DMCA14), .W4012(W4012), .ACLK1(ACLK1));
  DPCM_OUTPUT_COUNTER dpcm_output_counter_1 (
    .ACLK1(ACLK1), .W4011(W4011), .DSTEP(dpcm_control_1_dmstep), .RES(Res),
    .nBOUT(dpcm_sample_shift_register_1_nbout), .D0(D0), .D1(D1), .D2(D2), .D3(D3), .D4(D4), .D5(D5),
    .D6(D6), .DMC0(DMC0), .DMC1(DMC1), .DMC2(DMC2), .DMC3(DMC3), .DMC4(DMC4), .DMC5(DMC5), .DMC6(DMC6),
    .DOUT(dpcm_output_counter_1_dout));
  DPCM_SAMPLE_SHIFT_REGISTER dpcm_sample_shift_register_1 (
    .ACLK1(ACLK1), .D0(D0), .D1(D1), .D2(D2), .D3(D3), .D4(D4), .D5(D5), .D6(D6), .D7(D7),
    .BSTEP(dpcm_control_1_bstep), .BLOAD(dpcm_control_1_bload), .RES(Res), .PCM(dpcm_control_1_pcm),
    .nBOUT(dpcm_sample_shift_register_1_nbout));

  // Notes on the sheet:
  //   /ACLK2 = NOT ACLK
endmodule

// FREQUENCY LFSR
module DPCM_FREQUENCY_LFSR (
  input  Res,
  input  ACLK1,
  input  D0,
  input  D1,
  input  D2,
  input  D3,
  input  W4010,
  input  ACLK2,
  output DFLOAD
);

  wire _2_out, _5_out, and_1_out, d_ff_1_q, d_ff_2_q, d_ff_3_q, d_ff_4_q, d_ff_5_qn, d_ff_6_qn, d_ff_7_qn,
       d_ff_8_qn, d_ff_9_qn, d_ff_10_qn, d_ff_11_qn, d_ff_12_qn, d_ff_13_qn, d_ff_14_qn, d_ff_15_qn,
       d_ff_16_qn, d_ff_17_qn, d_ff_18_qn, d_ff_19_qn, d_ff_20_qn, d_ff_21_qn, d_ff_22_qn,
       demultiplexer_1_out0, demultiplexer_1_out1, demultiplexer_2_out0, demultiplexer_2_out1,
       demultiplexer_3_out0, demultiplexer_3_out1, demultiplexer_4_out0, demultiplexer_4_out1,
       demultiplexer_5_out0, demultiplexer_5_out1, demultiplexer_6_out0, demultiplexer_6_out1,
       demultiplexer_7_out0, demultiplexer_7_out1, demultiplexer_8_out0, demultiplexer_8_out1,
       demultiplexer_9_out0, demultiplexer_9_out1, dpcm_table_1_lp0, dpcm_table_1_lp1, dpcm_table_1_lp2,
       dpcm_table_1_lp3, dpcm_table_1_lp4, dpcm_table_1_lp5, dpcm_table_1_lp6, dpcm_table_1_lp7,
       dpcm_table_1_lp8, nor_1_out, nor_2_out, nor_3_out, not_1_out, not_2_out, not_3_out, not_4_out,
       or_1_out;

  not not_1 (not_1_out, ACLK1);
  DPCM_TABLE dpcm_table_1 (
    .LP0(dpcm_table_1_lp0), .LP1(dpcm_table_1_lp1), .LP2(dpcm_table_1_lp2), .LP3(dpcm_table_1_lp3),
    .LP4(dpcm_table_1_lp4), .LP5(dpcm_table_1_lp5), .LP6(dpcm_table_1_lp6), .LP7(dpcm_table_1_lp7),
    .LP8(dpcm_table_1_lp8), .F3(d_ff_4_q), .F2(d_ff_3_q), .F1(d_ff_2_q), .F0(d_ff_1_q));
  D_Flip_Flop #(.trigger("high")) d_ff_1 (
    .clk(not_1_out), .D(D0), .Q(d_ff_1_q), .en(W4010));  // open: Qn, preset, reset
  D_Flip_Flop #(.trigger("high")) d_ff_2 (
    .clk(not_1_out), .D(D1), .Q(d_ff_2_q), .en(W4010));  // open: Qn, preset, reset
  D_Flip_Flop #(.trigger("high")) d_ff_3 (
    .clk(not_1_out), .D(D2), .Q(d_ff_3_q), .en(W4010));  // open: Qn, preset, reset
  D_Flip_Flop #(.trigger("high")) d_ff_4 (
    .clk(not_1_out), .D(D3), .Q(d_ff_4_q), .en(W4010));  // open: Qn, preset, reset
  not not_2 (not_2_out, ACLK2);
  nor _2 (_2_out, not_2_out, _5_out);
  not not_3 (not_3_out, _5_out);
  nor _4 (DFLOAD, not_3_out, not_2_out);
  Demultiplexer #(.enable("false")) demultiplexer_1 (
    .out0(demultiplexer_1_out0), .out1(demultiplexer_1_out1), .in(DFLOAD), .sel(dpcm_table_1_lp0));
  Demultiplexer #(.enable("false")) demultiplexer_2 (
    .out0(demultiplexer_2_out0), .out1(demultiplexer_2_out1), .in(DFLOAD), .sel(dpcm_table_1_lp1));
  Demultiplexer #(.enable("false")) demultiplexer_3 (
    .out0(demultiplexer_3_out0), .out1(demultiplexer_3_out1), .in(DFLOAD), .sel(dpcm_table_1_lp2));
  Demultiplexer #(.enable("false")) demultiplexer_4 (
    .out0(demultiplexer_4_out0), .out1(demultiplexer_4_out1), .in(DFLOAD), .sel(dpcm_table_1_lp3));
  Demultiplexer #(.enable("false")) demultiplexer_5 (
    .out0(demultiplexer_5_out0), .out1(demultiplexer_5_out1), .in(DFLOAD), .sel(dpcm_table_1_lp4));
  Demultiplexer #(.enable("false")) demultiplexer_6 (
    .out0(demultiplexer_6_out0), .out1(demultiplexer_6_out1), .in(DFLOAD), .sel(dpcm_table_1_lp5));
  Demultiplexer #(.enable("false")) demultiplexer_7 (
    .out0(demultiplexer_7_out0), .out1(demultiplexer_7_out1), .in(DFLOAD), .sel(dpcm_table_1_lp6));
  Demultiplexer #(.enable("false")) demultiplexer_8 (
    .out0(demultiplexer_8_out0), .out1(demultiplexer_8_out1), .in(DFLOAD), .sel(dpcm_table_1_lp7));
  Demultiplexer #(.enable("false")) demultiplexer_9 (
    .out0(demultiplexer_9_out0), .out1(demultiplexer_9_out1), .in(DFLOAD), .sel(dpcm_table_1_lp8));
  D_Flip_Flop #(.trigger("high")) d_ff_5 (
    .clk(_2_out), .D(nor_1_out), .Qn(d_ff_5_qn), .preset(demultiplexer_1_out1), .reset(demultiplexer_1_out0));  // open: Q, en
  D_Flip_Flop #(.trigger("high")) d_ff_6 (
    .clk(_2_out), .D(d_ff_14_qn), .Qn(d_ff_6_qn), .preset(demultiplexer_2_out1), .reset(demultiplexer_2_out0));  // open: Q, en
  D_Flip_Flop #(.trigger("high")) d_ff_7 (
    .clk(_2_out), .D(d_ff_15_qn), .Qn(d_ff_7_qn), .preset(demultiplexer_3_out1), .reset(demultiplexer_3_out0));  // open: Q, en
  D_Flip_Flop #(.trigger("high")) d_ff_8 (
    .clk(_2_out), .D(d_ff_16_qn), .Qn(d_ff_8_qn), .preset(demultiplexer_4_out1), .reset(demultiplexer_4_out0));  // open: Q, en
  D_Flip_Flop #(.trigger("high")) d_ff_9 (
    .clk(_2_out), .D(d_ff_17_qn), .Qn(d_ff_9_qn), .preset(demultiplexer_5_out1), .reset(demultiplexer_5_out0));  // open: Q, en
  D_Flip_Flop #(.trigger("high")) d_ff_10 (
    .clk(_2_out), .D(d_ff_18_qn), .Qn(d_ff_10_qn), .preset(demultiplexer_6_out1), .reset(demultiplexer_6_out0));  // open: Q, en
  D_Flip_Flop #(.trigger("high")) d_ff_11 (
    .clk(_2_out), .D(d_ff_19_qn), .Qn(d_ff_11_qn), .preset(demultiplexer_7_out1), .reset(demultiplexer_7_out0));  // open: Q, en
  D_Flip_Flop #(.trigger("high")) d_ff_12 (
    .clk(_2_out), .D(d_ff_20_qn), .Qn(d_ff_12_qn), .preset(demultiplexer_8_out1), .reset(demultiplexer_8_out0));  // open: Q, en
  D_Flip_Flop #(.trigger("high")) d_ff_13 (
    .clk(_2_out), .D(d_ff_21_qn), .Qn(d_ff_13_qn), .preset(demultiplexer_9_out1), .reset(demultiplexer_9_out0));  // open: Q, en
  nor nor_1 (nor_1_out, nor_2_out, Res, and_1_out);
  D_Flip_Flop #(.trigger("high")) d_ff_14 (.clk(ACLK1), .D(d_ff_5_qn), .Qn(d_ff_14_qn));  // open: Q, preset, en, reset
  D_Flip_Flop #(.trigger("high")) d_ff_15 (.clk(ACLK1), .D(d_ff_6_qn), .Qn(d_ff_15_qn));  // open: Q, preset, en, reset
  D_Flip_Flop #(.trigger("high")) d_ff_16 (.clk(ACLK1), .D(d_ff_7_qn), .Qn(d_ff_16_qn));  // open: Q, preset, en, reset
  D_Flip_Flop #(.trigger("high")) d_ff_17 (.clk(ACLK1), .D(d_ff_8_qn), .Qn(d_ff_17_qn));  // open: Q, preset, en, reset
  D_Flip_Flop #(.trigger("high")) d_ff_18 (.clk(ACLK1), .D(d_ff_9_qn), .Qn(d_ff_18_qn));  // open: Q, preset, en, reset
  D_Flip_Flop #(.trigger("high")) d_ff_19 (.clk(ACLK1), .D(d_ff_10_qn), .Qn(d_ff_19_qn));  // open: Q, preset, en, reset
  D_Flip_Flop #(.trigger("high")) d_ff_20 (.clk(ACLK1), .D(d_ff_11_qn), .Qn(d_ff_20_qn));  // open: Q, preset, en, reset
  D_Flip_Flop #(.trigger("high")) d_ff_21 (.clk(ACLK1), .D(d_ff_12_qn), .Qn(d_ff_21_qn));  // open: Q, preset, en, reset
  D_Flip_Flop #(.trigger("high")) d_ff_22 (.clk(ACLK1), .D(d_ff_13_qn), .Qn(d_ff_22_qn));  // open: Q, preset, en, reset
  nor nor_2 (nor_2_out, nor_3_out, d_ff_22_qn, d_ff_18_qn);
  and and_1 (and_1_out, d_ff_22_qn, d_ff_18_qn);
  not not_4 (not_4_out, d_ff_22_qn);
  nor nor_3 (nor_3_out, d_ff_14_qn, d_ff_15_qn, d_ff_16_qn, d_ff_17_qn, d_ff_18_qn, d_ff_19_qn, d_ff_20_qn, d_ff_21_qn, d_ff_22_qn);
  or or_1 (or_1_out, d_ff_14_qn, d_ff_15_qn, d_ff_16_qn, d_ff_17_qn, d_ff_18_qn, d_ff_19_qn, d_ff_20_qn, d_ff_21_qn, not_4_out);
  nor _5 (_5_out, or_1_out, Res);

  // Notes on the sheet:
  //   1
  //   3
  //   DFSTEP
  //   S4
  //   S0
endmodule

// DPCM TABLE
module DPCM_TABLE (
  input  F0,
  input  F1,
  input  F2,
  input  F3,
  output LP0,
  output LP1,
  output LP2,
  output LP3,
  output LP4,
  output LP5,
  output LP6,
  output LP7,
  output LP8
);

  Multiplexer #(.select(4), .width(9), .disabled(0), .enable("false")) multiplexer_1 (
    .in0(9'h19d), .in1(9'ha2), .in2(9'h185), .in3(9'h1b6), .in4(9'hef), .in5(9'h1f8), .in6(9'h17c),
    .in7(9'h117), .in8(9'h120), .in9(9'h76), .in10(9'h11e), .in11(9'h13e), .in12(9'h162), .in13(9'h123),
    .in14(9'he3), .in15(9'hd5), .out({LP8, LP7, LP6, LP5, LP4, LP3, LP2, LP1, LP0}), .sel({F3, F2, F1, F0}));

  // Notes on the sheet:
  //   NTSC
  //   NTSC
  //   PAL
endmodule

module DPCM_SAMPLE_BIT_COUNTER (
  input  ACLK1,
  input  NSTEP,
  input  RES,
  output nNOUT
);

  wire d_ff_1_qn, d_ff_2_qn, d_ff_3_qn, d_ff_4_qn, d_ff_5_qn, d_ff_6_qn, nor_1_out, nor_2_out, nor_3_out,
       not_1_out, not_2_out, not_3_out, xor_1_out, xor_2_out, xor_3_out;

  D_Flip_Flop #(.trigger("high")) d_ff_1 (
    .clk(NSTEP), .D(d_ff_4_qn), .Qn(d_ff_1_qn), .reset(RES));  // open: Q, preset, en
  D_Flip_Flop #(.trigger("high")) d_ff_2 (
    .clk(NSTEP), .D(d_ff_5_qn), .Qn(d_ff_2_qn), .reset(RES));  // open: Q, preset, en
  D_Flip_Flop #(.trigger("high")) d_ff_3 (
    .clk(NSTEP), .D(d_ff_6_qn), .Qn(d_ff_3_qn), .reset(RES));  // open: Q, preset, en
  xor xor_1 (xor_1_out, 1'b1, d_ff_1_qn);
  not not_1 (not_1_out, 1'b1);
  nor nor_1 (nor_1_out, not_1_out, d_ff_1_qn);
  xor xor_2 (xor_2_out, nor_1_out, d_ff_2_qn);
  not not_2 (not_2_out, nor_1_out);
  nor nor_2 (nor_2_out, not_2_out, d_ff_2_qn);
  xor xor_3 (xor_3_out, nor_2_out, d_ff_3_qn);
  not not_3 (not_3_out, nor_2_out);
  nor nor_3 (nor_3_out, not_3_out, d_ff_3_qn);
  D_Flip_Flop #(.trigger("high")) d_ff_4 (.clk(ACLK1), .D(xor_1_out), .Qn(d_ff_4_qn));  // open: Q, preset, en, reset
  D_Flip_Flop #(.trigger("high")) d_ff_5 (.clk(ACLK1), .D(xor_2_out), .Qn(d_ff_5_qn));  // open: Q, preset, en, reset
  D_Flip_Flop #(.trigger("high")) d_ff_6 (.clk(ACLK1), .D(xor_3_out), .Qn(d_ff_6_qn));  // open: Q, preset, en, reset
  D_latch d_latch_1 (.EN(ACLK1), .D(nor_3_out), .NOT_Q(nNOUT));  // open: Q
endmodule

// DPCM CONTROL
module DPCM_CONTROL (
  input  PHI1,
  input  nR4015,
  input  ACLK1,
  input  nACLK2,
  input  ACLK2,
  input  RES,
  input  W4015,
  input  D7,
  input  D6,
  input  W4010,
  input  D4,
  input  SOUT,
  input  DFLOAD,
  input  R_W,
  input  nNOUT,
  input  DOUT,
  input  LOCK,
  output D7_2,
  output DMCINT,
  output D4_2,
  output DSSTEP,
  output DSLOAD,
  output NSTEP,
  output RUNDMC,
  output DMCRDY,
  output nDMC_AB,
  output PCM,
  output BLOAD,
  output BSTEP,
  output DMSTEP
);

  wire _3_out, _4_out, _5_out, and_1_out, and_2_out, d_ff_1_qn, d_ff_2_q, d_ff_3_q, d_ff_3_qn,
       d_latch_1_not_q, d_latch_2_not_q, d_latch_3_not_q, d_latch_3_q, d_latch_4_not_q, d_latch_4_q,
       d_latch_5_not_q, d_latch_5_q, d_latch_6_q, d_latch_7_not_q, d_latch_7_q, d_latch_8_q, d_latch_9_q,
       ED1, nACLK1, nand_1_out, nDFLOAD, nDMASTOP, nor_1_out, nor_2_out, nor_3_out, nor_4_out, nor_5_out,
       nor_7_out, nor_8_out, nor_10_out, nor_11_out, nor_12_out, not_3_out, not_4_out, not_5_out, not_6_out,
       not_7_out, or_1_out, PCM_DONE;

  not not_1 (nACLK1, ACLK1);
  D_Flip_Flop #(.trigger("high")) d_ff_1 (.clk(nACLK1), .D(D7), .Qn(d_ff_1_qn), .en(W4010));  // open: Q, preset, reset
  D_Flip_Flop #(.trigger("high")) d_ff_2 (.clk(nACLK1), .D(D6), .Q(d_ff_2_q), .en(W4010));  // open: Qn, preset, reset
  D_Flip_Flop #(.trigger("high")) d_ff_3 (
    .clk(nACLK1), .D(D4), .Q(d_ff_3_q), .Qn(d_ff_3_qn), .en(W4015), .reset(or_1_out));  // open: preset
  not not_2 (nDFLOAD, DFLOAD);
  nand nand_1 (nand_1_out, R_W, not_3_out);
  not not_3 (not_3_out, PHI1);
  or or_1 (or_1_out, ED1, RES);
  D_latch d_latch_1 (.EN(ACLK1), .D(d_ff_3_q), .NOT_Q(d_latch_1_not_q));  // open: Q
  D_latch d_latch_2 (.EN(nACLK2), .D(d_latch_1_not_q), .NOT_Q(d_latch_2_not_q));  // open: Q
  not not_4 (not_4_out, nDMASTOP);
  D_latch d_latch_3 (.EN(ACLK1), .D(SOUT), .Q(d_latch_3_q), .NOT_Q(d_latch_3_not_q));
  D_latch d_latch_4 (.EN(ACLK1), .D(d_latch_2_not_q), .Q(d_latch_4_q), .NOT_Q(d_latch_4_not_q));
  nor _4 (_4_out, nand_1_out, not_4_out, d_latch_4_not_q);
  and and_1 (and_1_out, d_latch_5_q, ACLK1);
  nor _10 (PCM, nDMC_AB, PHI1);
  nor nor_1 (nor_1_out, ED1, nor_2_out);
  nor nor_2 (nor_2_out, nor_1_out, RES, W4015, d_ff_1_qn);
  nor _3 (_3_out, ACLK2, d_latch_4_q, d_latch_1_not_q);
  nor nor_3 (nor_3_out, _4_out, nor_4_out);
  nor nor_4 (nor_4_out, nor_3_out, d_latch_4_not_q, RES, not_4_out);
  nor nor_5 (nor_5_out, nACLK2, nDMC_AB);
  nor nor_6 (nDMC_AB, nor_5_out, and_1_out);
  nor nor_7 (nor_7_out, PCM, nor_8_out);
  nor nor_8 (nor_8_out, nor_7_out, RES, PCM_DONE);
  nor nor_9 (nDMASTOP, PCM, nor_10_out);
  nor nor_10 (nor_10_out, nDMASTOP, RES, BLOAD);
  nor nor_11 (nor_11_out, BLOAD, nor_12_out);
  nor nor_12 (nor_12_out, nor_11_out, RES, _5_out);
  not not_5 (not_5_out, PCM_DONE);
  nor nor_13 (DMCRDY, nor_4_out, nor_5_out);
  D_latch d_latch_5 (.EN(nACLK2), .D(nor_4_out), .Q(d_latch_5_q), .NOT_Q(d_latch_5_not_q));
  D_latch d_latch_6 (.EN(ACLK1), .D(nor_7_out), .Q(d_latch_6_q));  // open: NOT_Q
  D_latch d_latch_7 (.EN(ACLK1), .D(nor_10_out), .Q(d_latch_7_q), .NOT_Q(d_latch_7_not_q));
  D_latch d_latch_8 (.EN(ACLK1), .D(nor_11_out), .Q(d_latch_8_q));  // open: NOT_Q
  D_latch d_latch_9 (.EN(ACLK1), .D(DOUT), .Q(d_latch_9_q));  // open: NOT_Q
  not not_6 (not_6_out, nR4015);
  nor _1 (DMCINT, nor_1_out, d_ff_1_qn);
  and and_2 (and_2_out, d_latch_3_q, PCM_DONE);
  or or_2 (DSLOAD, and_2_out, _3_out);
  not not_7 (not_7_out, nNOUT);
  assign D7_2 = not_6_out ? ~nor_1_out : 1'bz;  // Controlled_Inverter controlled_inverter_1
  assign D4_2 = not_6_out ? ~d_ff_3_qn : 1'bz;  // Controlled_Inverter controlled_inverter_2
  nor nor_14 (ED1, d_ff_2_q, d_latch_3_not_q, not_5_out);
  nor _11 (DSSTEP, d_latch_3_q, not_5_out, _3_out);
  not not_8 (NSTEP, nDFLOAD);
  D_latch d_latch_10 (.EN(ACLK1), .D(d_latch_5_not_q), .NOT_Q(RUNDMC));  // open: Q
  nor _8 (PCM_DONE, ACLK2, d_latch_6_q);
  nor _5 (_5_out, nDFLOAD, d_latch_7_q, nNOUT);
  nor _9 (BLOAD, nDFLOAD, d_latch_7_not_q, nNOUT);
  nor _7 (BSTEP, nDFLOAD, not_7_out);
  nor _8_2 (DMSTEP, nDFLOAD, d_latch_8_q, d_latch_9_q, LOCK);

  // Other names for the same wires on the sheet: ACLK2_t = nACLK2; nACLK2_t = ACLK2

  // Notes on the sheet:
  //   LENGTH = 0
  //   SAMPLE BIT CNT OVF
  //   OUTPUT CNT OVF
  //   /ENIRQ
  //   LOOP
  //   ED2
  //   ED2
  //   RESET ENABLE FLAG
  //   DL3
  //   DL6
  //   DL1
  //   DL14
  //   DL5
  //   ASSERT INT
  //   CTRL2
  //   S
  //   RS1
  //   R
  //   DMA START
  //   S
  //   RS5
  //   R
  //   S
  //   RS6
  //   R
  //   S
  //   RS3
  //   R
  //   S
  //   RS4
  //   R
  //   S
  //   RS2
  //   R
  //   /Q
  //   Q
  //   /Q
  //   Q
  //   /Q
  //   Q
  //   /Q
  //   Q
  //   /Q
  //   Q
  //   LOAD SHIFT REG
  //   /Q
  //   Q
  //   PCM FINISH
  //   RUN LATCH
  //   Nor6
  //   DL10
  //   DL13
  //   DL11
  //   DL12
  //   DMC2
  //   DMC1
  //   DMC3
  //   Delay per 1 cycle ACLK1
  //   RUN LATCH2
  //   DMC1
  //   LOAD SAMPLE BUFFER
endmodule

// SAMPLE LENGTH DOWN COUNTER
module DPCM_SAMPLE_LENGTH_DOWN_COUNTER (
  input  ACLK1,
  input  DSSTEP,
  input  RES,
  input  DSLOAD,
  input  W4013,
  input  LSC0,
  input  LSC1,
  input  LSC2,
  input  LSC3,
  input  LSC4,
  input  LSC5,
  input  LSC6,
  input  LSC7,
  output SOUT
);

  wire d_ff_1_q, d_ff_2_q, d_ff_3_q, d_ff_4_q, d_ff_5_q, d_ff_6_q, d_ff_7_q, d_ff_8_q, d_ff_9_q, d_ff_9_qn,
       d_ff_10_q, d_ff_10_qn, d_ff_11_q, d_ff_11_qn, d_ff_12_q, d_ff_12_qn, d_ff_13_q, d_ff_13_qn, d_ff_14_q,
       d_ff_14_qn, d_ff_15_q, d_ff_15_qn, d_ff_16_q, d_ff_16_qn, d_ff_17_q, d_ff_17_qn, d_ff_18_q,
       d_ff_18_qn, d_ff_19_q, d_ff_19_qn, d_ff_20_q, d_ff_20_qn, d_ff_21_qn, d_ff_22_qn, d_ff_23_qn,
       d_ff_24_qn, d_ff_25_qn, d_ff_26_qn, d_ff_27_qn, d_ff_28_qn, d_ff_29_qn, d_ff_30_qn, d_ff_31_qn,
       d_ff_32_qn, demultiplexer_1_out0, demultiplexer_1_out1, demultiplexer_2_out0, demultiplexer_2_out1,
       demultiplexer_3_out0, demultiplexer_3_out1, demultiplexer_4_out0, demultiplexer_4_out1,
       demultiplexer_5_out0, demultiplexer_5_out1, demultiplexer_6_out0, demultiplexer_6_out1,
       demultiplexer_7_out0, demultiplexer_7_out1, demultiplexer_8_out0, demultiplexer_8_out1, nor_1_out,
       nor_2_out, nor_3_out, nor_4_out, nor_5_out, nor_6_out, nor_7_out, nor_8_out, nor_9_out, nor_10_out,
       nor_11_out, not_1_out, not_2_out, not_3_out, not_4_out, not_5_out, not_6_out, not_7_out, not_8_out,
       not_9_out, not_10_out, not_11_out, not_12_out, not_13_out, or_1_out, or_2_out, or_3_out, or_4_out,
       or_5_out, or_6_out, or_7_out, or_8_out, or_9_out, xor_1_out, xor_2_out, xor_3_out, xor_4_out,
       xor_5_out, xor_6_out, xor_7_out, xor_8_out, xor_9_out, xor_10_out, xor_11_out, xor_12_out;

  not not_1 (not_1_out, ACLK1);
  D_Flip_Flop #(.trigger("high")) d_ff_1 (
    .clk(not_1_out), .D(LSC0), .Q(d_ff_1_q), .en(W4013));  // open: Qn, preset, reset
  D_Flip_Flop #(.trigger("high")) d_ff_2 (
    .clk(not_1_out), .D(LSC1), .Q(d_ff_2_q), .en(W4013));  // open: Qn, preset, reset
  D_Flip_Flop #(.trigger("high")) d_ff_3 (
    .clk(not_1_out), .D(LSC2), .Q(d_ff_3_q), .en(W4013));  // open: Qn, preset, reset
  D_Flip_Flop #(.trigger("high")) d_ff_4 (
    .clk(not_1_out), .D(LSC3), .Q(d_ff_4_q), .en(W4013));  // open: Qn, preset, reset
  D_Flip_Flop #(.trigger("high")) d_ff_5 (
    .clk(not_1_out), .D(LSC4), .Q(d_ff_5_q), .en(W4013));  // open: Qn, preset, reset
  D_Flip_Flop #(.trigger("high")) d_ff_6 (
    .clk(not_1_out), .D(LSC5), .Q(d_ff_6_q), .en(W4013));  // open: Qn, preset, reset
  D_Flip_Flop #(.trigger("high")) d_ff_7 (
    .clk(not_1_out), .D(LSC6), .Q(d_ff_7_q), .en(W4013));  // open: Qn, preset, reset
  D_Flip_Flop #(.trigger("high")) d_ff_8 (
    .clk(not_1_out), .D(LSC7), .Q(d_ff_8_q), .en(W4013));  // open: Qn, preset, reset
  Demultiplexer #(.enable("false")) demultiplexer_1 (
    .out0(demultiplexer_1_out0), .out1(demultiplexer_1_out1), .in(DSLOAD), .sel(d_ff_1_q));
  Demultiplexer #(.enable("false")) demultiplexer_2 (
    .out0(demultiplexer_2_out0), .out1(demultiplexer_2_out1), .in(DSLOAD), .sel(d_ff_2_q));
  Demultiplexer #(.enable("false")) demultiplexer_3 (
    .out0(demultiplexer_3_out0), .out1(demultiplexer_3_out1), .in(DSLOAD), .sel(d_ff_3_q));
  Demultiplexer #(.enable("false")) demultiplexer_4 (
    .out0(demultiplexer_4_out0), .out1(demultiplexer_4_out1), .in(DSLOAD), .sel(d_ff_4_q));
  Demultiplexer #(.enable("false")) demultiplexer_5 (
    .out0(demultiplexer_5_out0), .out1(demultiplexer_5_out1), .in(DSLOAD), .sel(d_ff_5_q));
  Demultiplexer #(.enable("false")) demultiplexer_6 (
    .out0(demultiplexer_6_out0), .out1(demultiplexer_6_out1), .in(DSLOAD), .sel(d_ff_6_q));
  Demultiplexer #(.enable("false")) demultiplexer_7 (
    .out0(demultiplexer_7_out0), .out1(demultiplexer_7_out1), .in(DSLOAD), .sel(d_ff_7_q));
  Demultiplexer #(.enable("false")) demultiplexer_8 (
    .out0(demultiplexer_8_out0), .out1(demultiplexer_8_out1), .in(DSLOAD), .sel(d_ff_8_q));
  or or_1 (or_1_out, DSLOAD, RES);
  or or_2 (or_2_out, RES, demultiplexer_1_out0);
  or or_3 (or_3_out, RES, demultiplexer_2_out0);
  or or_4 (or_4_out, RES, demultiplexer_3_out0);
  or or_5 (or_5_out, RES, demultiplexer_4_out0);
  or or_6 (or_6_out, RES, demultiplexer_5_out0);
  or or_7 (or_7_out, RES, demultiplexer_6_out0);
  or or_8 (or_8_out, RES, demultiplexer_7_out0);
  or or_9 (or_9_out, RES, demultiplexer_8_out0);
  D_Flip_Flop #(.trigger("high")) d_ff_9 (
    .clk(DSSTEP), .D(d_ff_21_qn), .Q(d_ff_9_q), .Qn(d_ff_9_qn), .reset(or_1_out));  // open: preset, en
  D_Flip_Flop #(.trigger("high")) d_ff_10 (
    .clk(DSSTEP), .D(d_ff_22_qn), .Q(d_ff_10_q), .Qn(d_ff_10_qn), .reset(or_1_out));  // open: preset, en
  D_Flip_Flop #(.trigger("high")) d_ff_11 (
    .clk(DSSTEP), .D(d_ff_23_qn), .Q(d_ff_11_q), .Qn(d_ff_11_qn), .reset(or_1_out));  // open: preset, en
  D_Flip_Flop #(.trigger("high")) d_ff_12 (
    .clk(DSSTEP), .D(d_ff_24_qn), .Q(d_ff_12_q), .Qn(d_ff_12_qn), .reset(or_1_out));  // open: preset, en
  D_Flip_Flop #(.trigger("high")) d_ff_13 (
    .clk(DSSTEP), .D(d_ff_25_qn), .Q(d_ff_13_q), .Qn(d_ff_13_qn), .preset(demultiplexer_1_out1),
    .reset(or_2_out));  // open: en
  D_Flip_Flop #(.trigger("high")) d_ff_14 (
    .clk(DSSTEP), .D(d_ff_26_qn), .Q(d_ff_14_q), .Qn(d_ff_14_qn), .preset(demultiplexer_2_out1),
    .reset(or_3_out));  // open: en
  D_Flip_Flop #(.trigger("high")) d_ff_15 (
    .clk(DSSTEP), .D(d_ff_27_qn), .Q(d_ff_15_q), .Qn(d_ff_15_qn), .preset(demultiplexer_3_out1),
    .reset(or_4_out));  // open: en
  D_Flip_Flop #(.trigger("high")) d_ff_16 (
    .clk(DSSTEP), .D(d_ff_28_qn), .Q(d_ff_16_q), .Qn(d_ff_16_qn), .preset(demultiplexer_4_out1),
    .reset(or_5_out));  // open: en
  D_Flip_Flop #(.trigger("high")) d_ff_17 (
    .clk(DSSTEP), .D(d_ff_29_qn), .Q(d_ff_17_q), .Qn(d_ff_17_qn), .preset(demultiplexer_5_out1),
    .reset(or_6_out));  // open: en
  D_Flip_Flop #(.trigger("high")) d_ff_18 (
    .clk(DSSTEP), .D(d_ff_30_qn), .Q(d_ff_18_q), .Qn(d_ff_18_qn), .preset(demultiplexer_6_out1),
    .reset(or_7_out));  // open: en
  D_Flip_Flop #(.trigger("high")) d_ff_19 (
    .clk(DSSTEP), .D(d_ff_31_qn), .Q(d_ff_19_q), .Qn(d_ff_19_qn), .preset(demultiplexer_7_out1),
    .reset(or_8_out));  // open: en
  D_Flip_Flop #(.trigger("high")) d_ff_20 (
    .clk(DSSTEP), .D(d_ff_32_qn), .Q(d_ff_20_q), .Qn(d_ff_20_qn), .preset(demultiplexer_8_out1),
    .reset(or_9_out));  // open: en
  not not_2 (not_2_out, 1'b1);
  not not_3 (not_3_out, nor_1_out);
  not not_4 (not_4_out, nor_2_out);
  not not_5 (not_5_out, nor_3_out);
  not not_6 (not_6_out, nor_4_out);
  not not_7 (not_7_out, nor_5_out);
  not not_8 (not_8_out, nor_6_out);
  not not_9 (not_9_out, nor_7_out);
  not not_10 (not_10_out, nor_8_out);
  not not_11 (not_11_out, nor_9_out);
  not not_12 (not_12_out, nor_10_out);
  not not_13 (not_13_out, nor_11_out);
  xor xor_1 (xor_1_out, 1'b1, d_ff_9_qn);
  nor nor_1 (nor_1_out, not_2_out, d_ff_9_q);
  xor xor_2 (xor_2_out, nor_1_out, d_ff_10_qn);
  nor nor_2 (nor_2_out, not_3_out, d_ff_10_q);
  xor xor_3 (xor_3_out, nor_2_out, d_ff_11_qn);
  nor nor_3 (nor_3_out, not_4_out, d_ff_11_q);
  xor xor_4 (xor_4_out, nor_3_out, d_ff_12_qn);
  nor nor_4 (nor_4_out, not_5_out, d_ff_12_q);
  xor xor_5 (xor_5_out, nor_4_out, d_ff_13_qn);
  nor nor_5 (nor_5_out, not_6_out, d_ff_13_q);
  xor xor_6 (xor_6_out, nor_5_out, d_ff_14_qn);
  nor nor_6 (nor_6_out, not_7_out, d_ff_14_q);
  xor xor_7 (xor_7_out, nor_6_out, d_ff_15_qn);
  nor nor_7 (nor_7_out, not_8_out, d_ff_15_q);
  xor xor_8 (xor_8_out, nor_7_out, d_ff_16_qn);
  nor nor_8 (nor_8_out, not_9_out, d_ff_16_q);
  xor xor_9 (xor_9_out, nor_8_out, d_ff_17_qn);
  nor nor_9 (nor_9_out, not_10_out, d_ff_17_q);
  xor xor_10 (xor_10_out, nor_9_out, d_ff_18_qn);
  nor nor_10 (nor_10_out, not_11_out, d_ff_18_q);
  xor xor_11 (xor_11_out, nor_10_out, d_ff_19_qn);
  nor nor_11 (nor_11_out, not_12_out, d_ff_19_q);
  xor xor_12 (xor_12_out, nor_11_out, d_ff_20_qn);
  nor nor_12 (SOUT, not_13_out, d_ff_20_q);
  D_Flip_Flop #(.trigger("high")) d_ff_21 (.clk(ACLK1), .D(xor_1_out), .Qn(d_ff_21_qn));  // open: Q, preset, en, reset
  D_Flip_Flop #(.trigger("high")) d_ff_22 (.clk(ACLK1), .D(xor_2_out), .Qn(d_ff_22_qn));  // open: Q, preset, en, reset
  D_Flip_Flop #(.trigger("high")) d_ff_23 (.clk(ACLK1), .D(xor_3_out), .Qn(d_ff_23_qn));  // open: Q, preset, en, reset
  D_Flip_Flop #(.trigger("high")) d_ff_24 (.clk(ACLK1), .D(xor_4_out), .Qn(d_ff_24_qn));  // open: Q, preset, en, reset
  D_Flip_Flop #(.trigger("high")) d_ff_25 (.clk(ACLK1), .D(xor_5_out), .Qn(d_ff_25_qn));  // open: Q, preset, en, reset
  D_Flip_Flop #(.trigger("high")) d_ff_26 (.clk(ACLK1), .D(xor_6_out), .Qn(d_ff_26_qn));  // open: Q, preset, en, reset
  D_Flip_Flop #(.trigger("high")) d_ff_27 (.clk(ACLK1), .D(xor_7_out), .Qn(d_ff_27_qn));  // open: Q, preset, en, reset
  D_Flip_Flop #(.trigger("high")) d_ff_28 (.clk(ACLK1), .D(xor_8_out), .Qn(d_ff_28_qn));  // open: Q, preset, en, reset
  D_Flip_Flop #(.trigger("high")) d_ff_29 (.clk(ACLK1), .D(xor_9_out), .Qn(d_ff_29_qn));  // open: Q, preset, en, reset
  D_Flip_Flop #(.trigger("high")) d_ff_30 (.clk(ACLK1), .D(xor_10_out), .Qn(d_ff_30_qn));  // open: Q, preset, en, reset
  D_Flip_Flop #(.trigger("high")) d_ff_31 (.clk(ACLK1), .D(xor_11_out), .Qn(d_ff_31_qn));  // open: Q, preset, en, reset
  D_Flip_Flop #(.trigger("high")) d_ff_32 (.clk(ACLK1), .D(xor_12_out), .Qn(d_ff_32_qn));  // open: Q, preset, en, reset
endmodule

// ADDRESS COUNTER
module DPCM_ADDRESS_COUNTER (
  input  ACLK1,
  input  DSSTEP,
  input  DSLOAD,
  input  RES,
  input  W4012,
  input  LDMC6,
  input  LDMC7,
  input  LDMC8,
  input  LDMC9,
  input  LDMC10,
  input  LDMC11,
  input  LDMC12,
  input  LDMC13,
  output DMC_A0,
  output DMC_A1,
  output DMC_A2,
  output DMC_A3,
  output DMC_A4,
  output DMC_A5,
  output DMC_A6,
  output DMC_A7,
  output DMC_A8,
  output DMC_A9,
  output DMC_A10,
  output DMC_A11,
  output DMC_A12,
  output DMC_A13,
  output DMC_A14
);

  wire d_ff_1_q, d_ff_2_q, d_ff_3_q, d_ff_4_q, d_ff_5_q, d_ff_6_q, d_ff_7_q, d_ff_8_q, d_ff_9_qn, d_ff_10_qn,
       d_ff_11_qn, d_ff_12_qn, d_ff_13_qn, d_ff_14_qn, d_ff_15_qn, d_ff_16_qn, d_ff_17_qn, d_ff_18_qn,
       d_ff_19_qn, d_ff_20_qn, d_ff_21_qn, d_ff_22_qn, d_ff_23_qn, d_ff_24_qn, d_ff_25_qn, d_ff_26_qn,
       d_ff_27_qn, d_ff_28_qn, d_ff_29_qn, d_ff_30_qn, d_ff_31_qn, d_ff_32_qn, d_ff_33_qn, d_ff_34_qn,
       d_ff_35_qn, d_ff_36_qn, d_ff_37_qn, d_ff_38_qn, demultiplexer_1_out0, demultiplexer_1_out1,
       demultiplexer_2_out0, demultiplexer_2_out1, demultiplexer_3_out0, demultiplexer_3_out1,
       demultiplexer_4_out0, demultiplexer_4_out1, demultiplexer_5_out0, demultiplexer_5_out1,
       demultiplexer_6_out0, demultiplexer_6_out1, demultiplexer_7_out0, demultiplexer_7_out1,
       demultiplexer_8_out0, demultiplexer_8_out1, nor_1_out, nor_2_out, nor_3_out, nor_4_out, nor_5_out,
       nor_6_out, nor_7_out, nor_8_out, nor_9_out, nor_10_out, nor_11_out, nor_12_out, nor_13_out,
       nor_14_out, nor_15_out, not_1_out, not_2_out, not_3_out, not_4_out, not_5_out, not_6_out, not_7_out,
       not_8_out, not_9_out, not_10_out, not_11_out, not_12_out, not_13_out, not_14_out, not_15_out,
       not_16_out, or_1_out, or_2_out, or_3_out, or_4_out, or_5_out, or_6_out, or_7_out, or_8_out, or_9_out,
       xor_1_out, xor_2_out, xor_3_out, xor_4_out, xor_5_out, xor_6_out, xor_7_out, xor_8_out, xor_9_out,
       xor_10_out, xor_11_out, xor_12_out, xor_13_out, xor_14_out, xor_15_out;

  not not_1 (not_1_out, ACLK1);
  D_Flip_Flop #(.trigger("high")) d_ff_1 (
    .clk(not_1_out), .D(LDMC6), .Q(d_ff_1_q), .en(W4012));  // open: Qn, preset, reset
  D_Flip_Flop #(.trigger("high")) d_ff_2 (
    .clk(not_1_out), .D(LDMC7), .Q(d_ff_2_q), .en(W4012));  // open: Qn, preset, reset
  D_Flip_Flop #(.trigger("high")) d_ff_3 (
    .clk(not_1_out), .D(LDMC8), .Q(d_ff_3_q), .en(W4012));  // open: Qn, preset, reset
  D_Flip_Flop #(.trigger("high")) d_ff_4 (
    .clk(not_1_out), .D(LDMC9), .Q(d_ff_4_q), .en(W4012));  // open: Qn, preset, reset
  D_Flip_Flop #(.trigger("high")) d_ff_5 (
    .clk(not_1_out), .D(LDMC10), .Q(d_ff_5_q), .en(W4012));  // open: Qn, preset, reset
  D_Flip_Flop #(.trigger("high")) d_ff_6 (
    .clk(not_1_out), .D(LDMC11), .Q(d_ff_6_q), .en(W4012));  // open: Qn, preset, reset
  D_Flip_Flop #(.trigger("high")) d_ff_7 (
    .clk(not_1_out), .D(LDMC12), .Q(d_ff_7_q), .en(W4012));  // open: Qn, preset, reset
  D_Flip_Flop #(.trigger("high")) d_ff_8 (
    .clk(not_1_out), .D(LDMC13), .Q(d_ff_8_q), .en(W4012));  // open: Qn, preset, reset
  Demultiplexer #(.enable("false")) demultiplexer_1 (
    .out0(demultiplexer_1_out0), .out1(demultiplexer_1_out1), .in(DSLOAD), .sel(d_ff_1_q));
  Demultiplexer #(.enable("false")) demultiplexer_2 (
    .out0(demultiplexer_2_out0), .out1(demultiplexer_2_out1), .in(DSLOAD), .sel(d_ff_2_q));
  Demultiplexer #(.enable("false")) demultiplexer_3 (
    .out0(demultiplexer_3_out0), .out1(demultiplexer_3_out1), .in(DSLOAD), .sel(d_ff_3_q));
  Demultiplexer #(.enable("false")) demultiplexer_4 (
    .out0(demultiplexer_4_out0), .out1(demultiplexer_4_out1), .in(DSLOAD), .sel(d_ff_4_q));
  Demultiplexer #(.enable("false")) demultiplexer_5 (
    .out0(demultiplexer_5_out0), .out1(demultiplexer_5_out1), .in(DSLOAD), .sel(d_ff_5_q));
  Demultiplexer #(.enable("false")) demultiplexer_6 (
    .out0(demultiplexer_6_out0), .out1(demultiplexer_6_out1), .in(DSLOAD), .sel(d_ff_6_q));
  Demultiplexer #(.enable("false")) demultiplexer_7 (
    .out0(demultiplexer_7_out0), .out1(demultiplexer_7_out1), .in(DSLOAD), .sel(d_ff_7_q));
  Demultiplexer #(.enable("false")) demultiplexer_8 (
    .out0(demultiplexer_8_out0), .out1(demultiplexer_8_out1), .in(DSLOAD), .sel(d_ff_8_q));
  or or_1 (or_1_out, DSLOAD, RES);
  or or_2 (or_2_out, RES, demultiplexer_1_out0);
  or or_3 (or_3_out, RES, demultiplexer_2_out0);
  or or_4 (or_4_out, RES, demultiplexer_3_out0);
  or or_5 (or_5_out, RES, demultiplexer_4_out0);
  or or_6 (or_6_out, RES, demultiplexer_5_out0);
  or or_7 (or_7_out, RES, demultiplexer_6_out0);
  or or_8 (or_8_out, RES, demultiplexer_7_out0);
  or or_9 (or_9_out, RES, demultiplexer_8_out0);
  D_Flip_Flop #(.trigger("high")) d_ff_9 (
    .clk(DSSTEP), .D(d_ff_24_qn), .Q(DMC_A0), .Qn(d_ff_9_qn), .reset(or_1_out));  // open: preset, en
  D_Flip_Flop #(.trigger("high")) d_ff_10 (
    .clk(DSSTEP), .D(d_ff_25_qn), .Q(DMC_A1), .Qn(d_ff_10_qn), .reset(or_1_out));  // open: preset, en
  D_Flip_Flop #(.trigger("high")) d_ff_11 (
    .clk(DSSTEP), .D(d_ff_26_qn), .Q(DMC_A2), .Qn(d_ff_11_qn), .reset(or_1_out));  // open: preset, en
  D_Flip_Flop #(.trigger("high")) d_ff_12 (
    .clk(DSSTEP), .D(d_ff_27_qn), .Q(DMC_A3), .Qn(d_ff_12_qn), .reset(or_1_out));  // open: preset, en
  D_Flip_Flop #(.trigger("high")) d_ff_13 (
    .clk(DSSTEP), .D(d_ff_28_qn), .Q(DMC_A4), .Qn(d_ff_13_qn), .reset(or_1_out));  // open: preset, en
  D_Flip_Flop #(.trigger("high")) d_ff_14 (
    .clk(DSSTEP), .D(d_ff_29_qn), .Q(DMC_A5), .Qn(d_ff_14_qn), .reset(or_1_out));  // open: preset, en
  D_Flip_Flop #(.trigger("high")) d_ff_15 (
    .clk(DSSTEP), .D(d_ff_30_qn), .Q(DMC_A6), .Qn(d_ff_15_qn), .preset(demultiplexer_1_out1), .reset(or_2_out));  // open: en
  D_Flip_Flop #(.trigger("high")) d_ff_16 (
    .clk(DSSTEP), .D(d_ff_31_qn), .Q(DMC_A7), .Qn(d_ff_16_qn), .preset(demultiplexer_2_out1), .reset(or_3_out));  // open: en
  D_Flip_Flop #(.trigger("high")) d_ff_17 (
    .clk(DSSTEP), .D(d_ff_32_qn), .Q(DMC_A8), .Qn(d_ff_17_qn), .preset(demultiplexer_3_out1), .reset(or_4_out));  // open: en
  D_Flip_Flop #(.trigger("high")) d_ff_18 (
    .clk(DSSTEP), .D(d_ff_33_qn), .Q(DMC_A9), .Qn(d_ff_18_qn), .preset(demultiplexer_4_out1), .reset(or_5_out));  // open: en
  D_Flip_Flop #(.trigger("high")) d_ff_19 (
    .clk(DSSTEP), .D(d_ff_34_qn), .Q(DMC_A10), .Qn(d_ff_19_qn), .preset(demultiplexer_5_out1),
    .reset(or_6_out));  // open: en
  D_Flip_Flop #(.trigger("high")) d_ff_20 (
    .clk(DSSTEP), .D(d_ff_35_qn), .Q(DMC_A11), .Qn(d_ff_20_qn), .preset(demultiplexer_6_out1),
    .reset(or_7_out));  // open: en
  D_Flip_Flop #(.trigger("high")) d_ff_21 (
    .clk(DSSTEP), .D(d_ff_36_qn), .Q(DMC_A12), .Qn(d_ff_21_qn), .preset(demultiplexer_7_out1),
    .reset(or_8_out));  // open: en
  D_Flip_Flop #(.trigger("high")) d_ff_22 (
    .clk(DSSTEP), .D(d_ff_37_qn), .Q(DMC_A13), .Qn(d_ff_22_qn), .preset(demultiplexer_8_out1),
    .reset(or_9_out));  // open: en
  D_Flip_Flop #(.trigger("high")) d_ff_23 (
    .clk(DSSTEP), .D(d_ff_38_qn), .Q(DMC_A14), .Qn(d_ff_23_qn), .preset(DSLOAD), .reset(RES));  // open: en
  not not_2 (not_2_out, 1'b1);
  not not_3 (not_3_out, nor_1_out);
  not not_4 (not_4_out, nor_2_out);
  not not_5 (not_5_out, nor_3_out);
  not not_6 (not_6_out, nor_4_out);
  not not_7 (not_7_out, nor_5_out);
  not not_8 (not_8_out, nor_6_out);
  not not_9 (not_9_out, nor_7_out);
  not not_10 (not_10_out, nor_8_out);
  not not_11 (not_11_out, nor_9_out);
  not not_12 (not_12_out, nor_10_out);
  not not_13 (not_13_out, nor_11_out);
  not not_14 (not_14_out, nor_12_out);
  not not_15 (not_15_out, nor_13_out);
  not not_16 (not_16_out, nor_14_out);
  xor xor_1 (xor_1_out, 1'b1, d_ff_9_qn);
  nor nor_1 (nor_1_out, not_2_out, d_ff_9_qn);
  xor xor_2 (xor_2_out, nor_1_out, d_ff_10_qn);
  nor nor_2 (nor_2_out, not_3_out, d_ff_10_qn);
  xor xor_3 (xor_3_out, nor_2_out, d_ff_11_qn);
  nor nor_3 (nor_3_out, not_4_out, d_ff_11_qn);
  xor xor_4 (xor_4_out, nor_3_out, d_ff_12_qn);
  nor nor_4 (nor_4_out, not_5_out, d_ff_12_qn);
  xor xor_5 (xor_5_out, nor_4_out, d_ff_13_qn);
  nor nor_5 (nor_5_out, not_6_out, d_ff_13_qn);
  xor xor_6 (xor_6_out, nor_5_out, d_ff_14_qn);
  nor nor_6 (nor_6_out, not_7_out, d_ff_14_qn);
  xor xor_7 (xor_7_out, nor_6_out, d_ff_15_qn);
  nor nor_7 (nor_7_out, not_8_out, d_ff_15_qn);
  xor xor_8 (xor_8_out, nor_7_out, d_ff_16_qn);
  nor nor_8 (nor_8_out, not_9_out, d_ff_16_qn);
  xor xor_9 (xor_9_out, nor_8_out, d_ff_17_qn);
  nor nor_9 (nor_9_out, not_10_out, d_ff_17_qn);
  xor xor_10 (xor_10_out, nor_9_out, d_ff_18_qn);
  nor nor_10 (nor_10_out, not_11_out, d_ff_18_qn);
  xor xor_11 (xor_11_out, nor_10_out, d_ff_19_qn);
  nor nor_11 (nor_11_out, not_12_out, d_ff_19_qn);
  xor xor_12 (xor_12_out, nor_11_out, d_ff_20_qn);
  nor nor_12 (nor_12_out, not_13_out, d_ff_20_qn);
  xor xor_13 (xor_13_out, nor_12_out, d_ff_21_qn);
  nor nor_13 (nor_13_out, not_14_out, d_ff_21_qn);
  xor xor_14 (xor_14_out, nor_13_out, d_ff_22_qn);
  nor nor_14 (nor_14_out, not_15_out, d_ff_22_qn);
  xor xor_15 (xor_15_out, nor_14_out, d_ff_23_qn);
  nor nor_15 (nor_15_out, not_16_out, d_ff_23_qn);
  D_Flip_Flop #(.trigger("high")) d_ff_24 (.clk(ACLK1), .D(xor_1_out), .Qn(d_ff_24_qn));  // open: Q, preset, en, reset
  D_Flip_Flop #(.trigger("high")) d_ff_25 (.clk(ACLK1), .D(xor_2_out), .Qn(d_ff_25_qn));  // open: Q, preset, en, reset
  D_Flip_Flop #(.trigger("high")) d_ff_26 (.clk(ACLK1), .D(xor_3_out), .Qn(d_ff_26_qn));  // open: Q, preset, en, reset
  D_Flip_Flop #(.trigger("high")) d_ff_27 (.clk(ACLK1), .D(xor_4_out), .Qn(d_ff_27_qn));  // open: Q, preset, en, reset
  D_Flip_Flop #(.trigger("high")) d_ff_28 (.clk(ACLK1), .D(xor_5_out), .Qn(d_ff_28_qn));  // open: Q, preset, en, reset
  D_Flip_Flop #(.trigger("high")) d_ff_29 (.clk(ACLK1), .D(xor_6_out), .Qn(d_ff_29_qn));  // open: Q, preset, en, reset
  D_Flip_Flop #(.trigger("high")) d_ff_30 (.clk(ACLK1), .D(xor_7_out), .Qn(d_ff_30_qn));  // open: Q, preset, en, reset
  D_Flip_Flop #(.trigger("high")) d_ff_31 (.clk(ACLK1), .D(xor_8_out), .Qn(d_ff_31_qn));  // open: Q, preset, en, reset
  D_Flip_Flop #(.trigger("high")) d_ff_32 (.clk(ACLK1), .D(xor_9_out), .Qn(d_ff_32_qn));  // open: Q, preset, en, reset
  D_Flip_Flop #(.trigger("high")) d_ff_33 (.clk(ACLK1), .D(xor_10_out), .Qn(d_ff_33_qn));  // open: Q, preset, en, reset
  D_Flip_Flop #(.trigger("high")) d_ff_34 (.clk(ACLK1), .D(xor_11_out), .Qn(d_ff_34_qn));  // open: Q, preset, en, reset
  D_Flip_Flop #(.trigger("high")) d_ff_35 (.clk(ACLK1), .D(xor_12_out), .Qn(d_ff_35_qn));  // open: Q, preset, en, reset
  D_Flip_Flop #(.trigger("high")) d_ff_36 (.clk(ACLK1), .D(xor_13_out), .Qn(d_ff_36_qn));  // open: Q, preset, en, reset
  D_Flip_Flop #(.trigger("high")) d_ff_37 (.clk(ACLK1), .D(xor_14_out), .Qn(d_ff_37_qn));  // open: Q, preset, en, reset
  D_Flip_Flop #(.trigger("high")) d_ff_38 (.clk(ACLK1), .D(xor_15_out), .Qn(d_ff_38_qn));  // open: Q, preset, en, reset

  // Notes on the sheet:
  //   not used
endmodule

// OUTPUT COUNTER
module DPCM_OUTPUT_COUNTER (
  input  ACLK1,
  input  D0,
  input  W4011,
  input  DSTEP,
  input  nBOUT,
  input  RES,
  input  D1,
  input  D2,
  input  D3,
  input  D4,
  input  D5,
  input  D6,
  output DMC0,
  output DMC1,
  output DMC2,
  output DMC3,
  output DMC4,
  output DMC5,
  output DMC6,
  output DOUT
);

  wire d_ff_2_qn, d_ff_3_qn, d_ff_4_qn, d_ff_5_qn, d_ff_6_qn, d_ff_7_qn, d_ff_8_q, d_ff_9_q, d_ff_10_q,
       d_ff_11_q, d_ff_12_q, d_ff_13_q, demultiplexer_1_out0, demultiplexer_1_out1, demultiplexer_2_out0,
       demultiplexer_2_out1, demultiplexer_3_out0, demultiplexer_3_out1, demultiplexer_4_out0,
       demultiplexer_4_out1, demultiplexer_5_out0, demultiplexer_5_out1, demultiplexer_6_out0,
       demultiplexer_6_out1, nor_1_out, nor_2_out, nor_3_out, nor_4_out, nor_5_out, not_1_out, not_2_out,
       not_3_out, not_4_out, not_5_out, not_6_out, not_7_out, or_1_out, or_2_out, or_3_out, or_4_out,
       or_5_out, or_6_out, xor_1_out, xor_2_out, xor_3_out, xor_4_out, xor_5_out, xor_6_out, xor_7_out,
       xor_8_out, xor_9_out, xor_10_out, xor_11_out, xor_12_out;

  Demultiplexer #(.enable("false")) demultiplexer_1 (
    .out0(demultiplexer_1_out0), .out1(demultiplexer_1_out1), .in(W4011), .sel(D1));
  Demultiplexer #(.enable("false")) demultiplexer_2 (
    .out0(demultiplexer_2_out0), .out1(demultiplexer_2_out1), .in(W4011), .sel(D2));
  Demultiplexer #(.enable("false")) demultiplexer_3 (
    .out0(demultiplexer_3_out0), .out1(demultiplexer_3_out1), .in(W4011), .sel(D3));
  Demultiplexer #(.enable("false")) demultiplexer_4 (
    .out0(demultiplexer_4_out0), .out1(demultiplexer_4_out1), .in(W4011), .sel(D4));
  Demultiplexer #(.enable("false")) demultiplexer_5 (
    .out0(demultiplexer_5_out0), .out1(demultiplexer_5_out1), .in(W4011), .sel(D5));
  Demultiplexer #(.enable("false")) demultiplexer_6 (
    .out0(demultiplexer_6_out0), .out1(demultiplexer_6_out1), .in(W4011), .sel(D6));
  or or_1 (or_1_out, RES, demultiplexer_1_out0);
  or or_2 (or_2_out, RES, demultiplexer_2_out0);
  or or_3 (or_3_out, RES, demultiplexer_3_out0);
  or or_4 (or_4_out, RES, demultiplexer_4_out0);
  or or_5 (or_5_out, RES, demultiplexer_5_out0);
  or or_6 (or_6_out, RES, demultiplexer_6_out0);
  not not_1 (not_1_out, ACLK1);
  D_Flip_Flop #(.trigger("high")) d_ff_1 (.clk(not_1_out), .D(D0), .Q(DMC0), .en(W4011));  // open: Qn, preset, reset
  D_Flip_Flop #(.trigger("high")) d_ff_2 (
    .clk(DSTEP), .D(d_ff_8_q), .Q(DMC1), .Qn(d_ff_2_qn), .preset(demultiplexer_1_out1), .reset(or_1_out));  // open: en
  D_Flip_Flop #(.trigger("high")) d_ff_3 (
    .clk(DSTEP), .D(d_ff_9_q), .Q(DMC2), .Qn(d_ff_3_qn), .preset(demultiplexer_2_out1), .reset(or_2_out));  // open: en
  D_Flip_Flop #(.trigger("high")) d_ff_4 (
    .clk(DSTEP), .D(d_ff_10_q), .Q(DMC3), .Qn(d_ff_4_qn), .preset(demultiplexer_3_out1), .reset(or_3_out));  // open: en
  D_Flip_Flop #(.trigger("high")) d_ff_5 (
    .clk(DSTEP), .D(d_ff_11_q), .Q(DMC4), .Qn(d_ff_5_qn), .preset(demultiplexer_4_out1), .reset(or_4_out));  // open: en
  D_Flip_Flop #(.trigger("high")) d_ff_6 (
    .clk(DSTEP), .D(d_ff_12_q), .Q(DMC5), .Qn(d_ff_6_qn), .preset(demultiplexer_5_out1), .reset(or_5_out));  // open: en
  D_Flip_Flop #(.trigger("high")) d_ff_7 (
    .clk(DSTEP), .D(d_ff_13_q), .Q(DMC6), .Qn(d_ff_7_qn), .preset(demultiplexer_6_out1), .reset(or_6_out));  // open: en
  xor xor_1 (xor_1_out, DMC1, 1'b1);
  not not_2 (not_2_out, 1'b1);
  xor xor_2 (xor_2_out, d_ff_2_qn, nBOUT);
  xor xor_3 (xor_3_out, DMC2, nor_1_out);
  not not_3 (not_3_out, nor_1_out);
  xor xor_4 (xor_4_out, d_ff_3_qn, nBOUT);
  xor xor_5 (xor_5_out, DMC3, nor_2_out);
  not not_4 (not_4_out, nor_2_out);
  xor xor_6 (xor_6_out, d_ff_4_qn, nBOUT);
  xor xor_7 (xor_7_out, DMC4, nor_3_out);
  not not_5 (not_5_out, nor_3_out);
  xor xor_8 (xor_8_out, d_ff_5_qn, nBOUT);
  xor xor_9 (xor_9_out, DMC5, nor_4_out);
  not not_6 (not_6_out, nor_4_out);
  xor xor_10 (xor_10_out, d_ff_6_qn, nBOUT);
  xor xor_11 (xor_11_out, DMC6, nor_5_out);
  not not_7 (not_7_out, nor_5_out);
  xor xor_12 (xor_12_out, d_ff_7_qn, nBOUT);
  D_Flip_Flop #(.trigger("high")) d_ff_8 (.clk(ACLK1), .D(xor_1_out), .Q(d_ff_8_q));  // open: Qn, preset, en, reset
  nor nor_1 (nor_1_out, not_2_out, xor_2_out);
  D_Flip_Flop #(.trigger("high")) d_ff_9 (.clk(ACLK1), .D(xor_3_out), .Q(d_ff_9_q));  // open: Qn, preset, en, reset
  nor nor_2 (nor_2_out, not_3_out, xor_4_out);
  D_Flip_Flop #(.trigger("high")) d_ff_10 (.clk(ACLK1), .D(xor_5_out), .Q(d_ff_10_q));  // open: Qn, preset, en, reset
  nor nor_3 (nor_3_out, not_4_out, xor_6_out);
  D_Flip_Flop #(.trigger("high")) d_ff_11 (.clk(ACLK1), .D(xor_7_out), .Q(d_ff_11_q));  // open: Qn, preset, en, reset
  nor nor_4 (nor_4_out, not_5_out, xor_8_out);
  D_Flip_Flop #(.trigger("high")) d_ff_12 (.clk(ACLK1), .D(xor_9_out), .Q(d_ff_12_q));  // open: Qn, preset, en, reset
  nor nor_5 (nor_5_out, not_6_out, xor_10_out);
  D_Flip_Flop #(.trigger("high")) d_ff_13 (.clk(ACLK1), .D(xor_11_out), .Q(d_ff_13_q));  // open: Qn, preset, en, reset
  nor nor_6 (DOUT, not_7_out, xor_12_out);
endmodule

// SAMPLE SHIFT REGISTER
module DPCM_SAMPLE_SHIFT_REGISTER (
  input  ACLK1,
  input  BSTEP,
  input  RES,
  input  BLOAD,
  input  PCM,
  input  D0,
  input  D1,
  input  D2,
  input  D3,
  input  D4,
  input  D5,
  input  D6,
  input  D7,
  output nBOUT
);

  wire d_ff_1_qn, d_ff_2_qn, d_ff_3_qn, d_ff_4_qn, d_ff_5_qn, d_ff_6_qn, d_ff_7_qn, d_ff_8_qn, d_ff_10_qn,
       d_ff_11_qn, d_ff_12_qn, d_ff_13_qn, d_ff_14_qn, d_ff_15_qn, d_ff_16_qn, d_latch_1_not_q,
       d_latch_2_not_q, d_latch_3_not_q, d_latch_4_not_q, d_latch_5_not_q, d_latch_6_not_q, d_latch_7_not_q,
       d_latch_8_not_q, demultiplexer_1_out0, demultiplexer_1_out1, demultiplexer_2_out0,
       demultiplexer_2_out1, demultiplexer_3_out0, demultiplexer_3_out1, demultiplexer_4_out0,
       demultiplexer_4_out1, demultiplexer_5_out0, demultiplexer_5_out1, demultiplexer_6_out0,
       demultiplexer_6_out1, demultiplexer_7_out0, demultiplexer_7_out1, demultiplexer_8_out0,
       demultiplexer_8_out1, not_1_out, or_1_out, or_2_out, or_3_out, or_4_out, or_5_out, or_6_out, or_7_out,
       or_8_out;

  not not_1 (not_1_out, ACLK1);
  D_Flip_Flop #(.trigger("high")) d_ff_1 (.clk(not_1_out), .D(D0), .Qn(d_ff_1_qn), .en(PCM));  // open: Q, preset, reset
  D_Flip_Flop #(.trigger("high")) d_ff_2 (.clk(not_1_out), .D(D1), .Qn(d_ff_2_qn), .en(PCM));  // open: Q, preset, reset
  D_Flip_Flop #(.trigger("high")) d_ff_3 (.clk(not_1_out), .D(D2), .Qn(d_ff_3_qn), .en(PCM));  // open: Q, preset, reset
  D_Flip_Flop #(.trigger("high")) d_ff_4 (.clk(not_1_out), .D(D3), .Qn(d_ff_4_qn), .en(PCM));  // open: Q, preset, reset
  D_Flip_Flop #(.trigger("high")) d_ff_5 (.clk(not_1_out), .D(D4), .Qn(d_ff_5_qn), .en(PCM));  // open: Q, preset, reset
  D_Flip_Flop #(.trigger("high")) d_ff_6 (.clk(not_1_out), .D(D5), .Qn(d_ff_6_qn), .en(PCM));  // open: Q, preset, reset
  D_Flip_Flop #(.trigger("high")) d_ff_7 (.clk(not_1_out), .D(D6), .Qn(d_ff_7_qn), .en(PCM));  // open: Q, preset, reset
  D_Flip_Flop #(.trigger("high")) d_ff_8 (.clk(not_1_out), .D(D7), .Qn(d_ff_8_qn), .en(PCM));  // open: Q, preset, reset
  Demultiplexer #(.enable("false")) demultiplexer_1 (
    .out0(demultiplexer_1_out0), .out1(demultiplexer_1_out1), .in(BLOAD), .sel(d_ff_1_qn));
  Demultiplexer #(.enable("false")) demultiplexer_2 (
    .out0(demultiplexer_2_out0), .out1(demultiplexer_2_out1), .in(BLOAD), .sel(d_ff_2_qn));
  Demultiplexer #(.enable("false")) demultiplexer_3 (
    .out0(demultiplexer_3_out0), .out1(demultiplexer_3_out1), .in(BLOAD), .sel(d_ff_3_qn));
  Demultiplexer #(.enable("false")) demultiplexer_4 (
    .out0(demultiplexer_4_out0), .out1(demultiplexer_4_out1), .in(BLOAD), .sel(d_ff_4_qn));
  Demultiplexer #(.enable("false")) demultiplexer_5 (
    .out0(demultiplexer_5_out0), .out1(demultiplexer_5_out1), .in(BLOAD), .sel(d_ff_5_qn));
  Demultiplexer #(.enable("false")) demultiplexer_6 (
    .out0(demultiplexer_6_out0), .out1(demultiplexer_6_out1), .in(BLOAD), .sel(d_ff_6_qn));
  Demultiplexer #(.enable("false")) demultiplexer_7 (
    .out0(demultiplexer_7_out0), .out1(demultiplexer_7_out1), .in(BLOAD), .sel(d_ff_7_qn));
  Demultiplexer #(.enable("false")) demultiplexer_8 (
    .out0(demultiplexer_8_out0), .out1(demultiplexer_8_out1), .in(BLOAD), .sel(d_ff_8_qn));
  or or_1 (or_1_out, demultiplexer_1_out1, RES);
  or or_2 (or_2_out, demultiplexer_2_out1, RES);
  or or_3 (or_3_out, demultiplexer_3_out1, RES);
  or or_4 (or_4_out, demultiplexer_4_out1, RES);
  or or_5 (or_5_out, demultiplexer_5_out1, RES);
  or or_6 (or_6_out, demultiplexer_6_out1, RES);
  or or_7 (or_7_out, demultiplexer_7_out1, RES);
  or or_8 (or_8_out, demultiplexer_8_out1, RES);
  D_latch d_latch_1 (.EN(ACLK1), .D(d_ff_10_qn), .NOT_Q(d_latch_1_not_q));  // open: Q
  D_latch d_latch_2 (.EN(ACLK1), .D(d_ff_11_qn), .NOT_Q(d_latch_2_not_q));  // open: Q
  D_latch d_latch_3 (.EN(ACLK1), .D(d_ff_12_qn), .NOT_Q(d_latch_3_not_q));  // open: Q
  D_latch d_latch_4 (.EN(ACLK1), .D(d_ff_13_qn), .NOT_Q(d_latch_4_not_q));  // open: Q
  D_latch d_latch_5 (.EN(ACLK1), .D(d_ff_14_qn), .NOT_Q(d_latch_5_not_q));  // open: Q
  D_latch d_latch_6 (.EN(ACLK1), .D(d_ff_15_qn), .NOT_Q(d_latch_6_not_q));  // open: Q
  D_latch d_latch_7 (.EN(ACLK1), .D(d_ff_16_qn), .NOT_Q(d_latch_7_not_q));  // open: Q
  D_latch d_latch_8 (.EN(ACLK1), .D(1'b0), .NOT_Q(d_latch_8_not_q));  // open: Q
  D_Flip_Flop #(.trigger("high")) d_ff_9 (
    .clk(BSTEP), .D(d_latch_1_not_q), .Q(nBOUT), .preset(or_1_out), .reset(demultiplexer_1_out0));  // open: Qn, en
  D_Flip_Flop #(.trigger("high")) d_ff_10 (
    .clk(BSTEP), .D(d_latch_2_not_q), .Qn(d_ff_10_qn), .preset(or_2_out), .reset(demultiplexer_2_out0));  // open: Q, en
  D_Flip_Flop #(.trigger("high")) d_ff_11 (
    .clk(BSTEP), .D(d_latch_3_not_q), .Qn(d_ff_11_qn), .preset(or_3_out), .reset(demultiplexer_3_out0));  // open: Q, en
  D_Flip_Flop #(.trigger("high")) d_ff_12 (
    .clk(BSTEP), .D(d_latch_4_not_q), .Qn(d_ff_12_qn), .preset(or_4_out), .reset(demultiplexer_4_out0));  // open: Q, en
  D_Flip_Flop #(.trigger("high")) d_ff_13 (
    .clk(BSTEP), .D(d_latch_5_not_q), .Qn(d_ff_13_qn), .preset(or_5_out), .reset(demultiplexer_5_out0));  // open: Q, en
  D_Flip_Flop #(.trigger("high")) d_ff_14 (
    .clk(BSTEP), .D(d_latch_6_not_q), .Qn(d_ff_14_qn), .preset(or_6_out), .reset(demultiplexer_6_out0));  // open: Q, en
  D_Flip_Flop #(.trigger("high")) d_ff_15 (
    .clk(BSTEP), .D(d_latch_7_not_q), .Qn(d_ff_15_qn), .preset(or_7_out), .reset(demultiplexer_7_out0));  // open: Q, en
  D_Flip_Flop #(.trigger("high")) d_ff_16 (
    .clk(BSTEP), .D(d_latch_8_not_q), .Qn(d_ff_16_qn), .preset(or_8_out), .reset(demultiplexer_8_out0));  // open: Q, en

  // Notes on the sheet:
  //   SAMPLE REGISTER
endmodule

// SPRITE DMA
module SPRITE_DMA (
  input  nACLK2,
  input  ACLK1,
  input  PHI1,
  input  PHI2,
  input  nR4015,
  input  nDBGRD,
  input  R_W__CPU,
  input  D0,
  input  D1,
  input  D2,
  input  D3,
  input  D4,
  input  D5,
  input  D6,
  input  D7,
  input  W4014,
  input  RES,
  input  D0_2,
  input  D1_2,
  input  D2_2,
  input  RUNDMC,
  input  D3_2,
  input  DMC_RDY,
  input  D4_2,
  input  D5_2,
  input  D6_2,
  input  nDMC_AB,
  input  D7_2,
  input  CPUA0,
  input  CPUA1,
  input  CPUA2,
  input  CPUA3,
  input  CPUA4,
  input  CPUA5,
  input  CPUA6,
  input  CPUA7,
  input  CPUA8,
  input  CPUA9,
  input  CPUA10,
  input  CPUA11,
  input  CPUA12,
  input  CPUA13,
  input  CPUA14,
  input  CPUA15,
  input  DMC0,
  input  DMC1,
  input  DMC2,
  input  DMC3,
  input  DMC4,
  input  DMC5,
  input  DMC6,
  input  DMC7,
  input  DMC8,
  input  DMC9,
  input  DMC10,
  input  DMC11,
  input  DMC12,
  input  DMC13,
  input  DMC14,
  output D0_3,
  output D1_3,
  output D2_3,
  output D3_3,
  output D4_3,
  output D5_3,
  output D6_3,
  output D7_3,
  output WR,
  output R_W__to_R_W_ic_pin,
  output RDY,
  output A0,
  output A1,
  output A2,
  output A3,
  output A4,
  output A5,
  output A6,
  output A7,
  output A8,
  output A9,
  output A10,
  output A11,
  output A12,
  output A13,
  output A14,
  output A15
);

  wire d_ff_1_qn, d_ff_2_qn, d_ff_3_qn, d_ff_4_qn, d_ff_5_qn, d_ff_6_qn, d_ff_7_qn, d_ff_8_qn,
       dma_address_counter_1_spre, dma_control_1_sprs, nor_2_out, not_1_out, not_2_out, not_3_out, SPR_CPU,
       SPR_PPU;
  wire [15:0] dma_address_counter_1_spra0;

  not not_1 (not_1_out, R_W__CPU);
  not not_2 (not_2_out, nACLK2);
  nor nor_1 (R_W__to_R_W_ic_pin, SPR_PPU, not_1_out);
  DMA_ADDRESS_COUNTER dma_address_counter_1 (
    .ACLK1(ACLK1), .SPRS(dma_control_1_sprs), .W4014(W4014), .RES(RES), .D0(D0), .D1(D1), .D2(D2), .D3(D3),
    .D4(D4), .D5(D5), .D6(D6), .D7(D7), .SPRA0(dma_address_counter_1_spra0[0]),
    .SPRA1(dma_address_counter_1_spra0[1]), .SPRA2(dma_address_counter_1_spra0[2]),
    .SPRA3(dma_address_counter_1_spra0[3]), .SPRA4(dma_address_counter_1_spra0[4]),
    .SPRA5(dma_address_counter_1_spra0[5]), .SPRA6(dma_address_counter_1_spra0[6]),
    .SPRA7(dma_address_counter_1_spra0[7]), .SPRA8(dma_address_counter_1_spra0[8]),
    .SPRA9(dma_address_counter_1_spra0[9]), .SPRA10(dma_address_counter_1_spra0[10]),
    .SPRA11(dma_address_counter_1_spra0[11]), .SPRA12(dma_address_counter_1_spra0[12]),
    .SPRA13(dma_address_counter_1_spra0[13]), .SPRA14(dma_address_counter_1_spra0[14]),
    .SPRA15(dma_address_counter_1_spra0[15]), .SPRE(dma_address_counter_1_spre));
  DMA_CONTROL dma_control_1 (
    .ACLK2(not_2_out), .PHI1(PHI1), .ACLK1(ACLK1), .W4014(W4014), .SPRE(dma_address_counter_1_spre),
    .RUNDMC(RUNDMC), .DMCRDY(DMC_RDY), .R_W(R_W__CPU), .RES(RES), .SPRS(dma_control_1_sprs), .RDY(RDY),
    .SPR_PPU(SPR_PPU), .SPR_CPU(SPR_CPU));
  nand nand_1 (WR, nR4015, nDBGRD, R_W__to_R_W_ic_pin);
  not not_3 (not_3_out, nDMC_AB);
  nor nor_2 (nor_2_out, SPR_CPU, SPR_PPU, not_3_out);
  assign {A15, A14, A13, A12, A11, A10, A9, A8, A7, A6, A5, A4, A3, A2, A1, A0} = SPR_CPU ? dma_address_counter_1_spra0 : 16'bz;  // Controlled_Buffer controlled_buffer_1
  assign {A15, A14, A13, A12, A11, A10, A9, A8, A7, A6, A5, A4, A3, A2, A1, A0} = nor_2_out ? {CPUA15, CPUA14, CPUA13, CPUA12, CPUA11, CPUA10, CPUA9, CPUA8, CPUA7, CPUA6, CPUA5, CPUA4, CPUA3, CPUA2, CPUA1, CPUA0} : 16'bz;  // Controlled_Buffer controlled_buffer_2
  assign {A15, A14, A13, A12, A11, A10, A9, A8, A7, A6, A5, A4, A3, A2, A1, A0} = SPR_PPU ? 16'h2004 : 16'bz;  // Controlled_Buffer controlled_buffer_3
  assign {A15, A14, A13, A12, A11, A10, A9, A8, A7, A6, A5, A4, A3, A2, A1, A0} = not_3_out ? {1'b1, DMC14, DMC13, DMC12, DMC11, DMC10, DMC9, DMC8, DMC7, DMC6, DMC5, DMC4, DMC3, DMC2, DMC1, DMC0} : 16'bz;  // Controlled_Buffer controlled_buffer_4
  D_Flip_Flop #(.trigger("high")) d_ff_1 (
    .clk(PHI2), .D(D0_2), .Qn(d_ff_1_qn), .en(SPR_CPU));  // open: Q, preset, reset
  D_Flip_Flop #(.trigger("high")) d_ff_2 (
    .clk(PHI2), .D(D1_2), .Qn(d_ff_2_qn), .en(SPR_CPU));  // open: Q, preset, reset
  D_Flip_Flop #(.trigger("high")) d_ff_3 (
    .clk(PHI2), .D(D2_2), .Qn(d_ff_3_qn), .en(SPR_CPU));  // open: Q, preset, reset
  D_Flip_Flop #(.trigger("high")) d_ff_4 (
    .clk(PHI2), .D(D3_2), .Qn(d_ff_4_qn), .en(SPR_CPU));  // open: Q, preset, reset
  D_Flip_Flop #(.trigger("high")) d_ff_5 (
    .clk(PHI2), .D(D4_2), .Qn(d_ff_5_qn), .en(SPR_CPU));  // open: Q, preset, reset
  D_Flip_Flop #(.trigger("high")) d_ff_6 (
    .clk(PHI2), .D(D5_2), .Qn(d_ff_6_qn), .en(SPR_CPU));  // open: Q, preset, reset
  D_Flip_Flop #(.trigger("high")) d_ff_7 (
    .clk(PHI2), .D(D6_2), .Qn(d_ff_7_qn), .en(SPR_CPU));  // open: Q, preset, reset
  D_Flip_Flop #(.trigger("high")) d_ff_8 (
    .clk(PHI2), .D(D7_2), .Qn(d_ff_8_qn), .en(SPR_CPU));  // open: Q, preset, reset
  assign D0_3 = SPR_PPU ? ~d_ff_1_qn : 1'bz;  // Controlled_Inverter controlled_inverter_1
  assign D1_3 = SPR_PPU ? ~d_ff_2_qn : 1'bz;  // Controlled_Inverter controlled_inverter_2
  assign D2_3 = SPR_PPU ? ~d_ff_3_qn : 1'bz;  // Controlled_Inverter controlled_inverter_3
  assign D3_3 = SPR_PPU ? ~d_ff_4_qn : 1'bz;  // Controlled_Inverter controlled_inverter_4
  assign D4_3 = SPR_PPU ? ~d_ff_5_qn : 1'bz;  // Controlled_Inverter controlled_inverter_5
  assign D5_3 = SPR_PPU ? ~d_ff_6_qn : 1'bz;  // Controlled_Inverter controlled_inverter_6
  assign D6_3 = SPR_PPU ? ~d_ff_7_qn : 1'bz;  // Controlled_Inverter controlled_inverter_7
  assign D7_3 = SPR_PPU ? ~d_ff_8_qn : 1'bz;  // Controlled_Inverter controlled_inverter_8

  // Notes on the sheet:
  //   INV1
  //   NOR1
  //   ADDRESS  MUX
  //   0010000000000100
  //   $2004
  //   If /R4015 (read 4015) then disable data buffer (2a03 databus become Z)
  //   SPRITE DMA BUFFER
endmodule

// DMA ADDRESS COUNTER
module DMA_ADDRESS_COUNTER (
  input  ACLK1,
  input  SPRS,
  input  RES,
  input  W4014,
  input  D0,
  input  D1,
  input  D2,
  input  D3,
  input  D4,
  input  D5,
  input  D6,
  input  D7,
  output SPRA0,
  output SPRA1,
  output SPRA2,
  output SPRA3,
  output SPRA4,
  output SPRA5,
  output SPRA6,
  output SPRA7,
  output SPRA8,
  output SPRA9,
  output SPRA10,
  output SPRA11,
  output SPRA12,
  output SPRA13,
  output SPRA14,
  output SPRA15,
  output SPRE
);

  wire d_ff_9_qn, d_ff_10_qn, d_ff_11_qn, d_ff_12_qn, d_ff_13_qn, d_ff_14_qn, d_ff_15_qn, d_ff_16_qn,
       d_ff_17_qn, d_ff_18_qn, d_ff_19_qn, d_ff_20_qn, d_ff_21_qn, d_ff_22_qn, d_ff_23_qn, d_ff_24_qn,
       nor_1_out, nor_2_out, nor_3_out, nor_4_out, nor_5_out, nor_6_out, nor_7_out, not_1_out, not_2_out,
       not_3_out, not_4_out, not_5_out, not_6_out, not_7_out, not_8_out, not_9_out, or_1_out, xor_1_out,
       xor_2_out, xor_3_out, xor_4_out, xor_5_out, xor_6_out, xor_7_out, xor_8_out;

  not not_1 (not_1_out, ACLK1);
  or or_1 (or_1_out, RES, W4014);
  D_Flip_Flop #(.trigger("high")) d_ff_1 (.clk(not_1_out), .D(D0), .Q(SPRA8), .en(W4014));  // open: Qn, preset, reset
  D_Flip_Flop #(.trigger("high")) d_ff_2 (.clk(not_1_out), .D(D1), .Q(SPRA9), .en(W4014));  // open: Qn, preset, reset
  D_Flip_Flop #(.trigger("high")) d_ff_3 (.clk(not_1_out), .D(D2), .Q(SPRA10), .en(W4014));  // open: Qn, preset, reset
  D_Flip_Flop #(.trigger("high")) d_ff_4 (.clk(not_1_out), .D(D3), .Q(SPRA11), .en(W4014));  // open: Qn, preset, reset
  D_Flip_Flop #(.trigger("high")) d_ff_5 (.clk(not_1_out), .D(D4), .Q(SPRA12), .en(W4014));  // open: Qn, preset, reset
  D_Flip_Flop #(.trigger("high")) d_ff_6 (.clk(not_1_out), .D(D5), .Q(SPRA13), .en(W4014));  // open: Qn, preset, reset
  D_Flip_Flop #(.trigger("high")) d_ff_7 (.clk(not_1_out), .D(D6), .Q(SPRA14), .en(W4014));  // open: Qn, preset, reset
  D_Flip_Flop #(.trigger("high")) d_ff_8 (.clk(not_1_out), .D(D7), .Q(SPRA15), .en(W4014));  // open: Qn, preset, reset
  D_Flip_Flop #(.trigger("high")) d_ff_9 (
    .clk(SPRS), .D(d_ff_17_qn), .Q(SPRA0), .Qn(d_ff_9_qn), .reset(or_1_out));  // open: preset, en
  D_Flip_Flop #(.trigger("high")) d_ff_10 (
    .clk(SPRS), .D(d_ff_18_qn), .Q(SPRA1), .Qn(d_ff_10_qn), .reset(or_1_out));  // open: preset, en
  D_Flip_Flop #(.trigger("high")) d_ff_11 (
    .clk(SPRS), .D(d_ff_19_qn), .Q(SPRA2), .Qn(d_ff_11_qn), .reset(or_1_out));  // open: preset, en
  D_Flip_Flop #(.trigger("high")) d_ff_12 (
    .clk(SPRS), .D(d_ff_20_qn), .Q(SPRA3), .Qn(d_ff_12_qn), .reset(or_1_out));  // open: preset, en
  D_Flip_Flop #(.trigger("high")) d_ff_13 (
    .clk(SPRS), .D(d_ff_21_qn), .Q(SPRA4), .Qn(d_ff_13_qn), .reset(or_1_out));  // open: preset, en
  D_Flip_Flop #(.trigger("high")) d_ff_14 (
    .clk(SPRS), .D(d_ff_22_qn), .Q(SPRA5), .Qn(d_ff_14_qn), .reset(or_1_out));  // open: preset, en
  D_Flip_Flop #(.trigger("high")) d_ff_15 (
    .clk(SPRS), .D(d_ff_23_qn), .Q(SPRA6), .Qn(d_ff_15_qn), .reset(or_1_out));  // open: preset, en
  D_Flip_Flop #(.trigger("high")) d_ff_16 (
    .clk(SPRS), .D(d_ff_24_qn), .Q(SPRA7), .Qn(d_ff_16_qn), .reset(or_1_out));  // open: preset, en
  not not_2 (not_2_out, 1'b1);
  not not_3 (not_3_out, nor_1_out);
  not not_4 (not_4_out, nor_2_out);
  not not_5 (not_5_out, nor_3_out);
  not not_6 (not_6_out, nor_4_out);
  not not_7 (not_7_out, nor_5_out);
  not not_8 (not_8_out, nor_6_out);
  not not_9 (not_9_out, nor_7_out);
  xor xor_1 (xor_1_out, 1'b1, d_ff_9_qn);
  nor nor_1 (nor_1_out, d_ff_9_qn, not_2_out);
  xor xor_2 (xor_2_out, nor_1_out, d_ff_10_qn);
  nor nor_2 (nor_2_out, d_ff_10_qn, not_3_out);
  xor xor_3 (xor_3_out, nor_2_out, d_ff_11_qn);
  nor nor_3 (nor_3_out, d_ff_11_qn, not_4_out);
  xor xor_4 (xor_4_out, nor_3_out, d_ff_12_qn);
  nor nor_4 (nor_4_out, d_ff_12_qn, not_5_out);
  xor xor_5 (xor_5_out, nor_4_out, d_ff_13_qn);
  nor nor_5 (nor_5_out, d_ff_13_qn, not_6_out);
  xor xor_6 (xor_6_out, nor_5_out, d_ff_14_qn);
  nor nor_6 (nor_6_out, d_ff_14_qn, not_7_out);
  xor xor_7 (xor_7_out, nor_6_out, d_ff_15_qn);
  nor nor_7 (nor_7_out, d_ff_15_qn, not_8_out);
  xor xor_8 (xor_8_out, nor_7_out, d_ff_16_qn);
  nor nor_8 (SPRE, d_ff_16_qn, not_9_out);
  D_Flip_Flop #(.trigger("high")) d_ff_17 (.clk(ACLK1), .D(xor_1_out), .Qn(d_ff_17_qn));  // open: Q, preset, en, reset
  D_Flip_Flop #(.trigger("high")) d_ff_18 (.clk(ACLK1), .D(xor_2_out), .Qn(d_ff_18_qn));  // open: Q, preset, en, reset
  D_Flip_Flop #(.trigger("high")) d_ff_19 (.clk(ACLK1), .D(xor_3_out), .Qn(d_ff_19_qn));  // open: Q, preset, en, reset
  D_Flip_Flop #(.trigger("high")) d_ff_20 (.clk(ACLK1), .D(xor_4_out), .Qn(d_ff_20_qn));  // open: Q, preset, en, reset
  D_Flip_Flop #(.trigger("high")) d_ff_21 (.clk(ACLK1), .D(xor_5_out), .Qn(d_ff_21_qn));  // open: Q, preset, en, reset
  D_Flip_Flop #(.trigger("high")) d_ff_22 (.clk(ACLK1), .D(xor_6_out), .Qn(d_ff_22_qn));  // open: Q, preset, en, reset
  D_Flip_Flop #(.trigger("high")) d_ff_23 (.clk(ACLK1), .D(xor_7_out), .Qn(d_ff_23_qn));  // open: Q, preset, en, reset
  D_Flip_Flop #(.trigger("high")) d_ff_24 (.clk(ACLK1), .D(xor_8_out), .Qn(d_ff_24_qn));  // open: Q, preset, en, reset
endmodule

// DMA CONTROL
module DMA_CONTROL (
  input  ACLK2,
  input  ACLK1,
  input  RUNDMC,
  input  SPRE,
  input  W4014,
  input  PHI1,
  input  R_W,
  input  DMCRDY,
  input  RES,
  output SPR_PPU,
  output SPR_CPU,
  output SPRS,
  output RDY
);

  wire _1_2_out, _1_out, _2_out, _7_out, _8_out, _9_out, _10_out, _13_out, _14_out, _15_out, _16_out,
       d_latch_1_q, d_latch_2_not_q, d_latch_2_q, d_latch_3_q, not_1_out, not_2_out;

  nor _15 (_15_out, ACLK2, _16_out);
  nor _16 (_16_out, _15_out, ACLK1);
  not not_1 (not_1_out, PHI1);
  not not_2 (not_2_out, ACLK2);
  D_latch d_latch_1 (.EN(ACLK1), .D(SPRE), .Q(d_latch_1_q));  // open: NOT_Q
  D_latch d_latch_2 (.EN(ACLK1), .D(_1_2_out), .Q(d_latch_2_q), .NOT_Q(d_latch_2_not_q));
  nor _8 (_8_out, d_latch_2_q, RES, _7_out);
  nor _7 (_7_out, _8_out, W4014);
  D_latch d_latch_3 (.EN(ACLK2), .D(_7_out), .Q(d_latch_3_q));  // open: NOT_Q
  nand _13 (_13_out, not_1_out, R_W);
  nor _17 (SPR_PPU, _15_out, RUNDMC, d_latch_2_not_q);
  nor _18 (SPR_CPU, RUNDMC, d_latch_2_not_q, _16_out);
  nor _3 (SPRS, RUNDMC, d_latch_2_not_q, not_2_out);
  nor _9 (_9_out, d_latch_2_q, _8_out);
  nor _14 (_14_out, d_latch_3_q, _13_out);
  and _1 (_1_out, SPRS, d_latch_1_q);
  nand _10 (_10_out, _9_out, DMCRDY);
  nor _1_2 (_1_2_out, _1_out, RES, _2_out);
  nor _2 (_2_out, _1_2_out, _14_out);
  not not_3 (RDY, _10_out);

  // Notes on the sheet:
  //   RS3
  //   DMA DIR TOGGLE
  //   1
  //   5
  //   R
  //   RS1
  //   START  DMA
  //   S
  //   14
  //   12
  //   NO Spr
  //   Q
  //   /Q
  //   INCREMENT  DMA ADR
  //   S
  //   STOP  DMA
  //   RS2
  //   R
  //   DO Spr
  //   /Q
  //   Q
  //   11
endmodule

// LENGTH TABLE
module LENGTH_TABLE (
  input  D3,
  input  D4,
  input  D5,
  input  D6,
  input  D7,
  output LC0,
  output LC1,
  output LC2,
  output LC3,
  output LC4,
  output LC5,
  output LC6,
  output LC7
);

  wire [4:0] d_latch_1_q;

  D_latch d_latch_1 (.EN(1'b1), .D(D3), .Q(d_latch_1_q[0]));  // open: NOT_Q
  D_latch d_latch_2 (.EN(1'b1), .D(D4), .Q(d_latch_1_q[1]));  // open: NOT_Q
  D_latch d_latch_3 (.EN(1'b1), .D(D5), .Q(d_latch_1_q[2]));  // open: NOT_Q
  D_latch d_latch_4 (.EN(1'b1), .D(D6), .Q(d_latch_1_q[3]));  // open: NOT_Q
  D_latch d_latch_5 (.EN(1'b1), .D(D7), .Q(d_latch_1_q[4]));  // open: NOT_Q
  Multiplexer #(.select(5), .width(8), .enable("false")) multiplexer_1 (
    .in0(8'h9), .in1(8'hfd), .in2(8'h13), .in3(8'h1), .in4(8'h27), .in5(8'h3), .in6(8'h4f), .in7(8'h5),
    .in8(8'h9f), .in9(8'h7), .in10(8'h3b), .in11(8'h9), .in12(8'hd), .in13(8'hb), .in14(8'h19), .in15(8'hd),
    .in16(8'hb), .in17(8'hf), .in18(8'h17), .in19(8'h11), .in20(8'h2f), .in21(8'h13), .in22(8'h5f),
    .in23(8'h15), .in24(8'hbf), .in25(8'h17), .in26(8'h47), .in27(8'h19), .in28(8'hf), .in29(8'h1b),
    .in30(8'h1f), .in31(8'h1d), .out({LC7, LC6, LC5, LC4, LC3, LC2, LC1, LC0}), .sel(d_latch_1_q));

  // Notes on the sheet:
  //   NTSC = PAL
endmodule

// LENGTH DOWN COUNTER
module LENGTH_DOWN_COUNTER (
  input  ACLK1,
  input  ACLK4,
  input  W4015,
  input  Dx,
  input  nLFO2,
  input  nR4015,
  input  W400x,
  input  RES,
  input  HALT,
  input  LC0,
  input  LC1,
  input  LC2,
  input  LC3,
  input  LC4,
  input  LC5,
  input  LC6,
  input  LC7,
  output NOxxx,
  output Dx_2
);

  wire d_ff_1_q, d_ff_1_qn, d_ff_2_q, d_ff_2_qn, d_ff_3_q, d_ff_3_qn, d_ff_4_q, d_ff_4_qn, d_ff_5_q,
       d_ff_5_qn, d_ff_6_q, d_ff_6_qn, d_ff_7_q, d_ff_7_qn, d_ff_8_q, d_ff_8_qn, d_ff_9_qn, d_ff_10_qn,
       d_ff_11_qn, d_ff_12_qn, d_ff_13_qn, d_ff_14_qn, d_ff_15_qn, d_ff_16_qn, demultiplexer_1_out0,
       demultiplexer_1_out1, demultiplexer_2_out0, demultiplexer_2_out1, demultiplexer_3_out0,
       demultiplexer_3_out1, demultiplexer_4_out0, demultiplexer_4_out1, demultiplexer_5_out0,
       demultiplexer_5_out1, demultiplexer_6_out0, demultiplexer_6_out1, demultiplexer_7_out0,
       demultiplexer_7_out1, demultiplexer_8_out0, demultiplexer_8_out1, length_control_1_step, nor_1_out,
       nor_2_out, nor_3_out, nor_4_out, nor_5_out, nor_6_out, nor_7_out, nor_8_out, not_1_out, not_2_out,
       not_3_out, not_4_out, not_5_out, not_6_out, not_7_out, not_8_out, or_1_out, or_2_out, or_3_out,
       or_4_out, or_5_out, or_6_out, or_7_out, or_8_out, xor_1_out, xor_2_out, xor_3_out, xor_4_out,
       xor_5_out, xor_6_out, xor_7_out, xor_8_out;

  Demultiplexer #(.enable("false")) demultiplexer_1 (
    .out0(demultiplexer_1_out0), .out1(demultiplexer_1_out1), .in(W400x), .sel(LC0));
  Demultiplexer #(.enable("false")) demultiplexer_2 (
    .out0(demultiplexer_2_out0), .out1(demultiplexer_2_out1), .in(W400x), .sel(LC1));
  Demultiplexer #(.enable("false")) demultiplexer_3 (
    .out0(demultiplexer_3_out0), .out1(demultiplexer_3_out1), .in(W400x), .sel(LC2));
  Demultiplexer #(.enable("false")) demultiplexer_4 (
    .out0(demultiplexer_4_out0), .out1(demultiplexer_4_out1), .in(W400x), .sel(LC3));
  Demultiplexer #(.enable("false")) demultiplexer_5 (
    .out0(demultiplexer_5_out0), .out1(demultiplexer_5_out1), .in(W400x), .sel(LC4));
  Demultiplexer #(.enable("false")) demultiplexer_6 (
    .out0(demultiplexer_6_out0), .out1(demultiplexer_6_out1), .in(W400x), .sel(LC5));
  Demultiplexer #(.enable("false")) demultiplexer_7 (
    .out0(demultiplexer_7_out0), .out1(demultiplexer_7_out1), .in(W400x), .sel(LC6));
  Demultiplexer #(.enable("false")) demultiplexer_8 (
    .out0(demultiplexer_8_out0), .out1(demultiplexer_8_out1), .in(W400x), .sel(LC7));
  or or_1 (or_1_out, RES, demultiplexer_1_out0);
  or or_2 (or_2_out, RES, demultiplexer_2_out0);
  or or_3 (or_3_out, RES, demultiplexer_3_out0);
  or or_4 (or_4_out, RES, demultiplexer_4_out0);
  or or_5 (or_5_out, RES, demultiplexer_5_out0);
  or or_6 (or_6_out, RES, demultiplexer_6_out0);
  or or_7 (or_7_out, RES, demultiplexer_7_out0);
  or or_8 (or_8_out, RES, demultiplexer_8_out0);
  LENGTH_CONTROL length_control_1 (
    .ACLK1(ACLK1), .Carry_In(nor_8_out), .W4015(W4015), .Dx(Dx), .Res(RES), .nLFO2(nLFO2), .nR4015(nR4015),
    .W400x(W400x), .NOSQA(NOxxx), .Dx_2(Dx_2), .STEP(length_control_1_step), .ACLK4(ACLK4));
  D_Flip_Flop #(.trigger("high")) d_ff_1 (
    .clk(length_control_1_step), .D(d_ff_9_qn), .Q(d_ff_1_q), .Qn(d_ff_1_qn), .preset(demultiplexer_1_out1),
    .reset(or_1_out));  // open: en
  not not_1 (not_1_out, HALT);
  D_Flip_Flop #(.trigger("high")) d_ff_2 (
    .clk(length_control_1_step), .D(d_ff_10_qn), .Q(d_ff_2_q), .Qn(d_ff_2_qn), .preset(demultiplexer_2_out1),
    .reset(or_2_out));  // open: en
  not not_2 (not_2_out, nor_1_out);
  D_Flip_Flop #(.trigger("high")) d_ff_3 (
    .clk(length_control_1_step), .D(d_ff_11_qn), .Q(d_ff_3_q), .Qn(d_ff_3_qn), .preset(demultiplexer_3_out1),
    .reset(or_3_out));  // open: en
  not not_3 (not_3_out, nor_2_out);
  D_Flip_Flop #(.trigger("high")) d_ff_4 (
    .clk(length_control_1_step), .D(d_ff_12_qn), .Q(d_ff_4_q), .Qn(d_ff_4_qn), .preset(demultiplexer_4_out1),
    .reset(or_4_out));  // open: en
  not not_4 (not_4_out, nor_3_out);
  D_Flip_Flop #(.trigger("high")) d_ff_5 (
    .clk(length_control_1_step), .D(d_ff_13_qn), .Q(d_ff_5_q), .Qn(d_ff_5_qn), .preset(demultiplexer_5_out1),
    .reset(or_5_out));  // open: en
  not not_5 (not_5_out, nor_4_out);
  D_Flip_Flop #(.trigger("high")) d_ff_6 (
    .clk(length_control_1_step), .D(d_ff_14_qn), .Q(d_ff_6_q), .Qn(d_ff_6_qn), .preset(demultiplexer_6_out1),
    .reset(or_6_out));  // open: en
  not not_6 (not_6_out, nor_5_out);
  D_Flip_Flop #(.trigger("high")) d_ff_7 (
    .clk(length_control_1_step), .D(d_ff_15_qn), .Q(d_ff_7_q), .Qn(d_ff_7_qn), .preset(demultiplexer_7_out1),
    .reset(or_7_out));  // open: en
  not not_7 (not_7_out, nor_6_out);
  D_Flip_Flop #(.trigger("high")) d_ff_8 (
    .clk(length_control_1_step), .D(d_ff_16_qn), .Q(d_ff_8_q), .Qn(d_ff_8_qn), .preset(demultiplexer_8_out1),
    .reset(or_8_out));  // open: en
  not not_8 (not_8_out, nor_7_out);
  xor xor_1 (xor_1_out, HALT, d_ff_1_qn);
  nor nor_1 (nor_1_out, not_1_out, d_ff_1_q);
  xor xor_2 (xor_2_out, nor_1_out, d_ff_2_qn);
  nor nor_2 (nor_2_out, not_2_out, d_ff_2_q);
  xor xor_3 (xor_3_out, nor_2_out, d_ff_3_qn);
  nor nor_3 (nor_3_out, not_3_out, d_ff_3_q);
  xor xor_4 (xor_4_out, nor_3_out, d_ff_4_qn);
  nor nor_4 (nor_4_out, not_4_out, d_ff_4_q);
  xor xor_5 (xor_5_out, nor_4_out, d_ff_5_qn);
  nor nor_5 (nor_5_out, not_5_out, d_ff_5_q);
  xor xor_6 (xor_6_out, nor_5_out, d_ff_6_qn);
  nor nor_6 (nor_6_out, not_6_out, d_ff_6_q);
  xor xor_7 (xor_7_out, nor_6_out, d_ff_7_qn);
  nor nor_7 (nor_7_out, not_7_out, d_ff_7_q);
  xor xor_8 (xor_8_out, nor_7_out, d_ff_8_qn);
  nor nor_8 (nor_8_out, not_8_out, d_ff_8_q);
  D_Flip_Flop #(.trigger("high")) d_ff_9 (.clk(ACLK1), .D(xor_1_out), .Qn(d_ff_9_qn));  // open: Q, preset, en, reset
  D_Flip_Flop #(.trigger("high")) d_ff_10 (.clk(ACLK1), .D(xor_2_out), .Qn(d_ff_10_qn));  // open: Q, preset, en, reset
  D_Flip_Flop #(.trigger("high")) d_ff_11 (.clk(ACLK1), .D(xor_3_out), .Qn(d_ff_11_qn));  // open: Q, preset, en, reset
  D_Flip_Flop #(.trigger("high")) d_ff_12 (.clk(ACLK1), .D(xor_4_out), .Qn(d_ff_12_qn));  // open: Q, preset, en, reset
  D_Flip_Flop #(.trigger("high")) d_ff_13 (.clk(ACLK1), .D(xor_5_out), .Qn(d_ff_13_qn));  // open: Q, preset, en, reset
  D_Flip_Flop #(.trigger("high")) d_ff_14 (.clk(ACLK1), .D(xor_6_out), .Qn(d_ff_14_qn));  // open: Q, preset, en, reset
  D_Flip_Flop #(.trigger("high")) d_ff_15 (.clk(ACLK1), .D(xor_7_out), .Qn(d_ff_15_qn));  // open: Q, preset, en, reset
  D_Flip_Flop #(.trigger("high")) d_ff_16 (.clk(ACLK1), .D(xor_8_out), .Qn(d_ff_16_qn));  // open: Q, preset, en, reset
endmodule

// LENGTH CONTROL
module LENGTH_CONTROL (
  input  ACLK4,
  input  ACLK1,
  input  Carry_In,
  input  Dx,
  input  Res,
  input  W4015,
  input  nLFO2,
  input  W400x,
  input  nR4015,
  output STEP,
  output NOSQA,
  output Dx_2
);

  wire _5_out, _6_out, _7_out, _8_out, d_ff_1_qn, d_latch_1_q, d_latch_2_q, d_latch_3_q, not_1_out, not_2_out;

  not not_1 (not_1_out, ACLK1);
  D_Flip_Flop #(.trigger("high")) d_ff_1 (
    .clk(not_1_out), .D(Dx), .Qn(d_ff_1_qn), .en(W4015), .reset(Res));  // open: Q, preset
  D_latch d_latch_1 (.EN(ACLK1), .D(Carry_In), .Q(d_latch_1_q));  // open: NOT_Q
  D_latch d_latch_2 (.EN(ACLK1), .D(d_ff_1_qn), .Q(d_latch_2_q));  // open: NOT_Q
  D_latch d_latch_3 (.EN(ACLK1), .D(_5_out), .Q(d_latch_3_q));  // open: NOT_Q
  and _7 (_7_out, d_latch_1_q, STEP);
  and _8 (_8_out, ACLK4, d_latch_2_q);
  nor _4 (STEP, d_latch_3_q, nLFO2);
  nor _6 (_6_out, _7_out, _8_out, Res, _5_out);
  nor _5 (_5_out, _6_out, W400x);
  not not_2 (not_2_out, nR4015);
  not not_3 (NOSQA, _6_out);
  assign Dx_2 = not_2_out ? ~_5_out : 1'bz;  // Controlled_Inverter controlled_inverter_1

  // Notes on the sheet:
  //   DFF1
  //   3
  //   7
  //   8
  //   4
  //   R
  //   S
  //   Q
  //   1
  //   /Q
  //   9
  //   2
endmodule
// IO CONTROL
module IO_CONTROL (
  input  nACLK2,
  input  ACLK1,
  input  D0,
  input  D1,
  input  D2,
  input  W4016,
  input  nRES_PIN,
  input  [15:0] APU_Ax,
  input  R_W_int,
  input  nR4016,
  input  nR4017,
  input  DBG,
  input  nM2,
  input  nNMI_PIN,
  input  nIRQ_PIN,
  input  INT_from_apu,
  input  CLK_PIN,
  input  WR,
  input  [7:0] DB_IN_EXT,
  input  [7:0] DB_OUT,
  output OUT0_PIN,
  output OUT1_PIN,
  output OUT2_PIN,
  output MASTER_RESET,
  output [15:0] Ax,
  output R_W_PIN,
  output IN0_PIN,
  output IN1_PIN,
  output M2,
  output nNMI_INT,
  output nIRQ_INT,
  output nCLK_INT,
  output [7:0] DB_IN,
  output [7:0] DB_OUT_EXT
);

  wire d_ff_1_q, d_ff_2_q, d_ff_3_q, d_latch_1_q, d_latch_2_q, d_latch_3_q, nor_1_out, not_1_out, not_2_out,
       not_4_out, not_8_out, not_9_out, not_10_out, not_11_out, not_12_out, not_13_out;
  wire [7:0] nor_3_out;
  wire [7:7] not_3_out;

  not not_1 (not_1_out, ACLK1);
  not not_2 (not_2_out, R_W_int);
  not not_3 (not_3_out[7], not_2_out);
  not not_4 (not_4_out, nACLK2);
  D_Flip_Flop #(.trigger("high")) d_ff_1 (
    .clk(not_1_out), .D(D0), .Q(d_ff_1_q), .en(W4016));  // open: Qn, preset, reset
  D_Flip_Flop #(.trigger("high")) d_ff_2 (
    .clk(not_1_out), .D(D1), .Q(d_ff_2_q), .en(W4016));  // open: Qn, preset, reset
  D_Flip_Flop #(.trigger("high")) d_ff_3 (
    .clk(not_1_out), .D(D2), .Q(d_ff_3_q), .en(W4016));  // open: Qn, preset, reset
  not not_5 (MASTER_RESET, nRES_PIN);
  not not_6 (nNMI_INT, not_11_out);
  not not_7 (nCLK_INT, CLK_PIN);
  nor nor_1 (nor_1_out, nRES_PIN, DBG);
  not not_8 (not_8_out, nM2);
  nor nor_2 (nIRQ_INT, not_12_out, INT_from_apu);
  not not_9 (not_9_out, WR);
  assign OUT0_PIN = nRES_PIN ? d_latch_1_q : 1'bz;  // Controlled_Buffer controlled_buffer_1
  D_latch d_latch_1 (.EN(not_4_out), .D(d_ff_1_q), .Q(d_latch_1_q));  // open: NOT_Q
  assign OUT1_PIN = nRES_PIN ? d_latch_2_q : 1'bz;  // Controlled_Buffer controlled_buffer_2
  D_latch d_latch_2 (.EN(not_4_out), .D(d_ff_2_q), .Q(d_latch_2_q));  // open: NOT_Q
  assign OUT2_PIN = nRES_PIN ? d_latch_3_q : 1'bz;  // Controlled_Buffer controlled_buffer_3
  D_latch d_latch_3 (.EN(not_4_out), .D(d_ff_3_q), .Q(d_latch_3_q));  // open: NOT_Q
  assign Ax = nRES_PIN ? APU_Ax : 16'bz;  // Controlled_Buffer controlled_buffer_4
  assign R_W_PIN = nRES_PIN ? R_W_int : 1'bz;  // Controlled_Buffer controlled_buffer_5
  assign IN0_PIN = nRES_PIN ? nR4016 : 1'bz;  // Controlled_Buffer controlled_buffer_6
  assign IN1_PIN = nRES_PIN ? nR4017 : 1'bz;  // Controlled_Buffer controlled_buffer_7
  not not_10 (not_10_out, nor_1_out);
  assign M2 = not_10_out ? not_8_out : 1'bz;  // Controlled_Buffer controlled_buffer_8
  not not_11 (not_11_out, nNMI_PIN);
  not not_12 (not_12_out, nIRQ_PIN);
  assign DB_IN = not_9_out ? DB_IN_EXT : 8'bz;  // Controlled_Buffer controlled_buffer_9
  not not_13 (not_13_out, not_3_out[7]);
  assign nor_3_out = ~({8{not_3_out[7]}} | DB_OUT);  // NOR_Gate nor_3, 8 bits wide
  assign DB_OUT_EXT = not_13_out ? ~nor_3_out : 8'bz;  // Controlled_Inverter controlled_inverter_1

  // Notes on the sheet:
  //   ACLK5
endmodule

module INTERVAL_TIMER (
  input  PHI1,
  input  PHI2,
  input  W401C,
  input  W401D,
  input  W401E,
  input  W401F,
  input  [7:0] DATA_BUS,
  input  nEN,
  input  TOPAD,
  input  IN,
  output [7:0] DATA_BUS_2,
  output t1,
  output IRQ,
  output OUT,
  output OUT_2,
  output OUT_3,
  output OUT_4
);

  wire _1_2_out, _1_out, _2_out, _3_out, _4_2_out, _4_out, _5_out, _6_2_out, _9_out, _10_out, _14_out,
       _15_out, _16_out, _17_out, _18_out, _19_out, _20_out, _21_out, _22_out, _23_out, _24_out, _26_out,
       _27_out, _28_out, _29_out, _31_out, _32_out, _33_out, _37_out, _38_out, _39_out, _40_out, _46_out,
       _47_out, _51_out, _52_out, _53_out, _56_out, _57_out, _58_2_out, _58_3_out, _58_4_out, _58_out,
       _61_out, _65_out, _66_out, _67_out, _68_out, _69_out, B1, B2, B3, B4, B6, d_ff_1_q, d_ff_1_qn,
       d_latch_1_not_q, d_latch_2_not_q, d_latch_3_q, d_latch_4_not_q, d_latch_5_q, d_latch_7_not_q,
       d_latch_8_q, d_latch_9_not_q, d_latch_10_not_q, d_latch_11_q, DEC, DIN0, DIN1, DIN2, DIN3, DIN4, DIN5,
       DIN6, DIN7, INC, IRQ_DIS, nEN_t, nLD0, nLD1, nLD2, not_2_out, not_4_out, nPRESCALER_EN, PHI1_t,
       PHI2_t, PR_16, PR_256, RELOAD, SLATCH_3_qn, SLATCH_4_qn, SLATCH_5_q, SLATCH_6_q, SLATCH_7_q,
       SLATCH_8_q, SLATCH_9_q, SLATCH_q, STEP, timer_cnt_8bit_1_cout, timer_cnt_8bit_1_norout,
       timer_cnt_8bit_2_cout, timer_cnt_8bit_2_norout, timer_cnt_8bit_3_cout, timer_cnt_8bit_3_norout;
  wire [7:0] controlled_buffer_2_out, not_3_out, timer_cnt_8bit_1_q0, timer_cnt_8bit_2_q0,
       timer_cnt_8bit_3_q0;

  Clock clock_1 (.out(PHI1_t));
  not not_1 (PHI2_t, PHI1_t);
  assign DATA_BUS_2 = not_2_out ? not_3_out : 8'bz;  // Controlled_Buffer controlled_buffer_1
  not not_2 (not_2_out, nEN_t);
  assign not_3_out = ~controlled_buffer_2_out;  // NOT_Gate not_3, 8 bits wide
  assign {DIN7, DIN6, DIN5, DIN4, DIN3, DIN2, DIN1, DIN0} = DATA_BUS;  // Buffer buffer_1, 8 bits wide
  TIMER_CNT_8BIT timer_cnt_8bit_1 (
    .PHI2(PHI2_t), .CIN(1'b1), .DEC(DEC), .STEP(STEP), .LD(nLD0), .D0(DIN0), .RELOAD(RELOAD), .D1(DIN1),
    .D2(DIN2), .D3(DIN3), .D4(DIN4), .D5(DIN5), .D6(DIN6), .D7(DIN7), .Q0(timer_cnt_8bit_1_q0[0]),
    .Q1(timer_cnt_8bit_1_q0[1]), .Q2(timer_cnt_8bit_1_q0[2]), .Q3(timer_cnt_8bit_1_q0[3]),
    .Q4(timer_cnt_8bit_1_q0[4]), .Q5(timer_cnt_8bit_1_q0[5]), .Q6(timer_cnt_8bit_1_q0[6]),
    .Q7(timer_cnt_8bit_1_q0[7]), .COUT(timer_cnt_8bit_1_cout), .NOROUT(timer_cnt_8bit_1_norout));
  TIMER_CNT_8BIT timer_cnt_8bit_2 (
    .PHI2(PHI2_t), .CIN(timer_cnt_8bit_1_cout), .DEC(DEC), .STEP(STEP), .LD(nLD1), .D0(DIN0),
    .RELOAD(RELOAD), .D1(DIN1), .D2(DIN2), .D3(DIN3), .D4(DIN4), .D5(DIN5), .D6(DIN6), .D7(DIN7),
    .Q0(timer_cnt_8bit_2_q0[0]), .Q1(timer_cnt_8bit_2_q0[1]), .Q2(timer_cnt_8bit_2_q0[2]),
    .Q3(timer_cnt_8bit_2_q0[3]), .Q4(timer_cnt_8bit_2_q0[4]), .Q5(timer_cnt_8bit_2_q0[5]),
    .Q6(timer_cnt_8bit_2_q0[6]), .Q7(timer_cnt_8bit_2_q0[7]), .COUT(timer_cnt_8bit_2_cout),
    .NOROUT(timer_cnt_8bit_2_norout));
  TIMER_CNT_8BIT timer_cnt_8bit_3 (
    .PHI2(PHI2_t), .CIN(timer_cnt_8bit_2_cout), .DEC(DEC), .STEP(STEP), .LD(nLD2), .D0(DIN0),
    .RELOAD(RELOAD), .D1(DIN1), .D2(DIN2), .D3(DIN3), .D4(DIN4), .D5(DIN5), .D6(DIN6), .D7(DIN7),
    .Q0(timer_cnt_8bit_3_q0[0]), .Q1(timer_cnt_8bit_3_q0[1]), .Q2(timer_cnt_8bit_3_q0[2]),
    .Q3(timer_cnt_8bit_3_q0[3]), .Q4(timer_cnt_8bit_3_q0[4]), .Q5(timer_cnt_8bit_3_q0[5]),
    .Q6(timer_cnt_8bit_3_q0[6]), .Q7(timer_cnt_8bit_3_q0[7]), .COUT(timer_cnt_8bit_3_cout),
    .NOROUT(timer_cnt_8bit_3_norout));
  PRESCALER prescaler_1 (
    .PHI1(PHI1_t), .PHI2(PHI2_t), .nEN(nPRESCALER_EN), .Q3(PR_16), .Q7(PR_256));  // open: Q0, Q1, Q2, Q4, Q5, Q6
  Controlled_Buffer #(.width(8)) controlled_buffer_2 (
    .in(timer_cnt_8bit_1_q0), .out(controlled_buffer_2_out));  // open: en
  Controlled_Buffer #(.width(8)) controlled_buffer_3 (
    .in(timer_cnt_8bit_2_q0), .out(controlled_buffer_2_out));  // open: en
  Controlled_Buffer #(.width(8)) controlled_buffer_4 (
    .in(timer_cnt_8bit_3_q0), .out(controlled_buffer_2_out));  // open: en
  and _1 (_1_out, timer_cnt_8bit_1_norout, timer_cnt_8bit_2_norout, timer_cnt_8bit_3_norout);
  D_latch d_latch_1 (.EN(PHI2_t), .D(_1_out), .NOT_Q(d_latch_1_not_q));  // open: Q
  not _26 (_26_out, B2);
  not _28 (_28_out, B3);
  not _19 (_19_out, B4);
  D_latch d_latch_2 (.EN(PHI1_t), .D(d_latch_1_not_q), .NOT_Q(d_latch_2_not_q));  // open: Q
  not _27 (_27_out, _26_out);
  not _29 (_29_out, _28_out);
  not _18 (_18_out, _19_out);
  nor _21 (_21_out, PHI1_t, B6);
  not _20 (_20_out, _21_out);
  D_latch d_latch_3 (.EN(PHI2_t), .D(d_latch_2_not_q), .Q(d_latch_3_q));  // open: NOT_Q
  nor _4 (_4_out, d_latch_3_q, d_latch_1_not_q, PHI2_t);
  nor _14 (_14_out, _26_out, _28_out, _18_out, _20_out);
  nor _15 (_15_out, _28_out, _27_out, _18_out, _20_out);
  nor _16 (_16_out, _26_out, _29_out, _18_out, _20_out);
  nor _17 (_17_out, _27_out, _29_out, _18_out, _20_out);
  nor _22 (_22_out, _20_out, _19_out);
  nor _23 (_23_out, _20_out, _28_out, _26_out, _19_out);
  not _10 (_10_out, _14_out);
  not _9 (_9_out, _10_out);
  not _11 (nLD2, _15_out);
  not _12 (nLD1, _16_out);
  not _13 (nLD0, _17_out);
  buf _25 (nEN_t, _24_out);
  not _24 (_24_out, _22_out);
  D_Flip_Flop #(.trigger("high")) SLATCH (.clk(PHI2_t), .D(_23_out), .Q(SLATCH_q));  // open: Qn, preset, en, reset
  nor _61 (_61_out, d_latch_1_not_q, _9_out);
  D_Flip_Flop #(.trigger("high")) SLATCH_2 (.clk(_10_out), .D(DIN7), .Q(IRQ_DIS));  // open: Qn, preset, en, reset
  D_latch d_latch_4 (.EN(_9_out), .D(DIN6), .NOT_Q(d_latch_4_not_q));  // open: Q
  D_Flip_Flop #(.trigger("high")) SLATCH_3 (.clk(_9_out), .D(DIN5), .Qn(SLATCH_3_qn));  // open: Q, preset, en, reset
  D_Flip_Flop #(.trigger("high")) SLATCH_4 (.clk(_9_out), .D(DIN4), .Qn(SLATCH_4_qn));  // open: Q, preset, en, reset
  D_Flip_Flop #(.trigger("high")) d_ff_1 (
    .clk(_9_out), .D(DIN3), .Q(d_ff_1_q), .Qn(d_ff_1_qn));  // open: preset, en, reset
  D_Flip_Flop #(.trigger("high")) SLATCH_5 (.clk(_9_out), .D(DIN2), .Q(SLATCH_5_q));  // open: Qn, preset, en, reset
  D_Flip_Flop #(.trigger("high")) SLATCH_6 (.clk(_9_out), .D(DIN1), .Q(SLATCH_6_q));  // open: Qn, preset, en, reset
  D_Flip_Flop #(.trigger("high")) SLATCH_7 (.clk(_9_out), .D(DIN0), .Q(SLATCH_7_q));  // open: Qn, preset, en, reset
  D_latch d_latch_5 (.EN(PHI1_t), .D(SLATCH_q), .Q(d_latch_5_q));  // open: NOT_Q
  D_latch d_latch_6 (.EN(_10_out), .D(d_latch_4_not_q), .NOT_Q(nPRESCALER_EN));  // open: Q
  buf _7 (INC, d_ff_1_q);
  buf _6 (DEC, d_ff_1_qn);
  nor _31 (_31_out, d_latch_5_q, _32_out);
  nor _32 (_32_out, _31_out, _4_out);
  D_Flip_Flop #(.trigger("high")) SLATCH_8 (
    .clk(_61_out), .D(SLATCH_6_q), .Q(SLATCH_8_q));  // open: Qn, preset, en, reset
  D_latch d_latch_7 (.EN(PHI2_t), .D(nPRESCALER_EN), .NOT_Q(d_latch_7_not_q));  // open: Q
  nor _33 (_33_out, IRQ_DIS, _32_out);
  buf _35 (IRQ, _33_out);
  nor _38 (_38_out, d_latch_1_not_q, SLATCH_3_qn, PHI2_t);
  nor _40 (_40_out, PHI2_t, d_latch_7_not_q);
  not _37 (_37_out, _39_out);
  nor _39 (_39_out, _38_out, _40_out);
  buf _37_2 (RELOAD, _37_out);
  not _53 (_53_out, SLATCH_4_qn);
  not _69 (_69_out, SLATCH_7_q);
  nor _2 (_2_out, nEN, TOPAD);
  nor _4_2 (_4_2_out, nEN, _2_out);
  not _46 (_46_out, B1);
  not _51 (_51_out, d_latch_10_not_q);
  nor _6_2 (_6_2_out, nEN, _4_2_out);
  not _3 (_3_out, IN);
  not _47 (_47_out, _46_out);
  nor _52 (_52_out, _51_out, SLATCH_7_q, _53_out);
  nor _68 (_68_out, SLATCH_7_q, d_latch_10_not_q, SLATCH_4_qn);
  nor _67 (_67_out, SLATCH_4_qn, _69_out, PR_16);
  nor _66 (_66_out, _53_out, _69_out, PR_256);
  not not_4 (not_4_out, nEN);
  nor _1_2 (_1_2_out, nEN, _2_out);
  not _5 (_5_out, _3_out);
  buf buffer_2 (OUT_4, IN);
  D_Flip_Flop #(.trigger("high")) SLATCH_9 (.clk(PHI1_t), .D(_47_out), .Q(SLATCH_9_q));  // open: Qn, preset, en, reset
  assign OUT = not_4_out ? TOPAD : 1'bz;  // Controlled_Buffer controlled_buffer_5
  Transistor #(.\type ("n")) transistor_1 (.in(1'b1), .out(OUT_2), .gate(_1_2_out));
  Transistor #(.\type ("n")) transistor_2 (.in(1'b0), .out(OUT_2), .gate(_6_2_out));
  Transistor #(.\type ("n")) transistor_3 (.in(1'b1), .out(OUT_3), .gate(_5_out));
  Transistor #(.\type ("n")) transistor_4 (.in(1'b0), .out(OUT_3), .gate(_3_out));
  nor _65 (_65_out, _52_out, _68_out, _67_out, _66_out);
  and _58 (_58_out, SLATCH_8_q, SLATCH_5_q);
  not _58_2 (_58_2_out, SLATCH_5_q);
  and _58_3 (_58_3_out, _58_2_out, _4_out);
  D_latch d_latch_8 (.EN(PHI2_t), .D(SLATCH_9_q), .Q(d_latch_8_q));  // open: NOT_Q
  D_latch d_latch_9 (.EN(PHI2_t), .D(_65_out), .NOT_Q(d_latch_9_not_q));  // open: Q
  nor _58_4 (_58_4_out, _58_out, _58_3_out);
  D_latch d_latch_10 (.EN(PHI1_t), .D(d_latch_8_q), .NOT_Q(d_latch_10_not_q));  // open: Q
  D_latch d_latch_11 (.EN(PHI1_t), .D(d_latch_9_not_q), .Q(d_latch_11_q));  // open: NOT_Q
  not _57 (_57_out, _58_4_out);
  not _56 (_56_out, _57_out);
  not _55 (t1, _56_out);
  nor _62 (STEP, d_latch_1_not_q, d_latch_11_q, PHI2_t, _65_out);

  // Notes on the sheet:
  //   NOT USED
  //   2
  //   3
  //   4
  //   30
  //   36
  //   43
  //   44
  //   45
  //   SLATCH
  //   8
  //   54
  //   60
  //   5
  //   31
  //   42
  //   59
  //   41
  //   34
  //   TO DATA BUS
  //   48
  //   49
  //   64
  //   TO DATA BUS
  //   TO DATA BUS
  //   FROMPAD
  //   50
  //   63
endmodule

// REVERSE COUNTER
module TIMER_CNT_8BIT (
  input  PHI2,
  input  CIN,
  input  DEC,
  input  STEP,
  input  LD,
  input  D0,
  input  RELOAD,
  input  D1,
  input  D2,
  input  D3,
  input  D4,
  input  D5,
  input  D6,
  input  D7,
  output Q0,
  output Q1,
  output Q2,
  output Q3,
  output Q4,
  output Q5,
  output Q6,
  output Q7,
  output COUT,
  output NOROUT
);

  wire _1_2_out, _1_3_out, _1_4_out, _1_5_out, _1_6_out, _1_7_out, _1_8_out, _1_out, _2_2_out, _2_3_out,
       _2_4_out, _2_5_out, _2_6_out, _2_7_out, _2_out, _4_2_out, _4_3_out, _4_4_out, _4_5_out, _4_6_out,
       _4_7_out, _4_8_out, _4_out, _6_2_out, _6_3_out, _6_4_out, _6_5_out, _6_6_out, _6_7_out, _6_8_out,
       _6_out, _9_2_out, _9_3_out, _9_4_out, _9_5_out, _9_6_out, _9_7_out, _9_8_out, _9_out, d_ff_1_q,
       d_ff_2_q, d_ff_3_q, d_ff_4_q, d_ff_5_q, d_ff_6_q, d_ff_7_q, d_ff_8_q, d_ff_9_qn, d_ff_10_qn,
       d_ff_11_qn, d_ff_12_qn, d_ff_13_qn, d_ff_14_qn, d_ff_15_qn, d_ff_16_qn, d_latch_1_not_q,
       d_latch_2_not_q, d_latch_3_not_q, d_latch_4_not_q, d_latch_5_not_q, d_latch_6_not_q, d_latch_7_not_q,
       d_latch_8_not_q, demultiplexer_1_out0, demultiplexer_1_out1, demultiplexer_2_out0,
       demultiplexer_2_out1, demultiplexer_3_out0, demultiplexer_3_out1, demultiplexer_4_out0,
       demultiplexer_4_out1, demultiplexer_5_out0, demultiplexer_5_out1, demultiplexer_6_out0,
       demultiplexer_6_out1, demultiplexer_7_out0, demultiplexer_7_out1, demultiplexer_8_out0,
       demultiplexer_8_out1;

  D_Flip_Flop #(.trigger("high")) d_ff_1 (.clk(LD), .D(D0), .Q(d_ff_1_q));  // open: Qn, preset, en, reset
  Demultiplexer #(.disabled(0), .enable("false")) demultiplexer_1 (
    .out0(demultiplexer_1_out0), .out1(demultiplexer_1_out1), .in(RELOAD), .sel(d_ff_1_q));
  D_Flip_Flop #(.trigger("high")) d_ff_2 (.clk(LD), .D(D1), .Q(d_ff_2_q));  // open: Qn, preset, en, reset
  Demultiplexer #(.disabled(0), .enable("false")) demultiplexer_2 (
    .out0(demultiplexer_2_out0), .out1(demultiplexer_2_out1), .in(RELOAD), .sel(d_ff_2_q));
  D_Flip_Flop #(.trigger("high")) d_ff_3 (.clk(LD), .D(D2), .Q(d_ff_3_q));  // open: Qn, preset, en, reset
  Demultiplexer #(.disabled(0), .enable("false")) demultiplexer_3 (
    .out0(demultiplexer_3_out0), .out1(demultiplexer_3_out1), .in(RELOAD), .sel(d_ff_3_q));
  D_Flip_Flop #(.trigger("high")) d_ff_4 (.clk(LD), .D(D3), .Q(d_ff_4_q));  // open: Qn, preset, en, reset
  Demultiplexer #(.disabled(0), .enable("false")) demultiplexer_4 (
    .out0(demultiplexer_4_out0), .out1(demultiplexer_4_out1), .in(RELOAD), .sel(d_ff_4_q));
  D_Flip_Flop #(.trigger("high")) d_ff_5 (.clk(LD), .D(D4), .Q(d_ff_5_q));  // open: Qn, preset, en, reset
  Demultiplexer #(.disabled(0), .enable("false")) demultiplexer_5 (
    .out0(demultiplexer_5_out0), .out1(demultiplexer_5_out1), .in(RELOAD), .sel(d_ff_5_q));
  D_Flip_Flop #(.trigger("high")) d_ff_6 (.clk(LD), .D(D5), .Q(d_ff_6_q));  // open: Qn, preset, en, reset
  Demultiplexer #(.disabled(0), .enable("false")) demultiplexer_6 (
    .out0(demultiplexer_6_out0), .out1(demultiplexer_6_out1), .in(RELOAD), .sel(d_ff_6_q));
  D_Flip_Flop #(.trigger("high")) d_ff_7 (.clk(LD), .D(D6), .Q(d_ff_7_q));  // open: Qn, preset, en, reset
  Demultiplexer #(.disabled(0), .enable("false")) demultiplexer_7 (
    .out0(demultiplexer_7_out0), .out1(demultiplexer_7_out1), .in(RELOAD), .sel(d_ff_7_q));
  D_Flip_Flop #(.trigger("high")) d_ff_8 (.clk(LD), .D(D7), .Q(d_ff_8_q));  // open: Qn, preset, en, reset
  Demultiplexer #(.disabled(0), .enable("false")) demultiplexer_8 (
    .out0(demultiplexer_8_out0), .out1(demultiplexer_8_out1), .in(RELOAD), .sel(d_ff_8_q));
  D_Flip_Flop #(.trigger("high")) d_ff_9 (
    .clk(STEP), .D(_4_out), .Q(Q0), .Qn(d_ff_9_qn), .preset(demultiplexer_1_out1),
    .reset(demultiplexer_1_out0));  // open: en
  not _4 (_4_out, d_latch_1_not_q);
  D_Flip_Flop #(.trigger("high")) d_ff_10 (
    .clk(STEP), .D(_4_2_out), .Q(Q1), .Qn(d_ff_10_qn), .preset(demultiplexer_2_out1),
    .reset(demultiplexer_2_out0));  // open: en
  not _4_2 (_4_2_out, d_latch_2_not_q);
  D_Flip_Flop #(.trigger("high")) d_ff_11 (
    .clk(STEP), .D(_4_3_out), .Q(Q2), .Qn(d_ff_11_qn), .preset(demultiplexer_3_out1),
    .reset(demultiplexer_3_out0));  // open: en
  not _4_3 (_4_3_out, d_latch_3_not_q);
  D_Flip_Flop #(.trigger("high")) d_ff_12 (
    .clk(STEP), .D(_4_4_out), .Q(Q3), .Qn(d_ff_12_qn), .preset(demultiplexer_4_out1),
    .reset(demultiplexer_4_out0));  // open: en
  not _4_4 (_4_4_out, d_latch_4_not_q);
  D_Flip_Flop #(.trigger("high")) d_ff_13 (
    .clk(STEP), .D(_4_5_out), .Q(Q4), .Qn(d_ff_13_qn), .preset(demultiplexer_5_out1),
    .reset(demultiplexer_5_out0));  // open: en
  not _4_5 (_4_5_out, d_latch_5_not_q);
  D_Flip_Flop #(.trigger("high")) d_ff_14 (
    .clk(STEP), .D(_4_6_out), .Q(Q5), .Qn(d_ff_14_qn), .preset(demultiplexer_6_out1),
    .reset(demultiplexer_6_out0));  // open: en
  not _4_6 (_4_6_out, d_latch_6_not_q);
  D_Flip_Flop #(.trigger("high")) d_ff_15 (
    .clk(STEP), .D(_4_7_out), .Q(Q6), .Qn(d_ff_15_qn), .preset(demultiplexer_7_out1),
    .reset(demultiplexer_7_out0));  // open: en
  not _4_7 (_4_7_out, d_latch_7_not_q);
  D_Flip_Flop #(.trigger("high")) d_ff_16 (
    .clk(STEP), .D(_4_8_out), .Q(Q7), .Qn(d_ff_16_qn), .preset(demultiplexer_8_out1),
    .reset(demultiplexer_8_out0));  // open: en
  not _4_8 (_4_8_out, d_latch_8_not_q);
  xor _9 (_9_out, Q0, CIN);
  xor _6 (_6_out, DEC, d_ff_9_qn);
  not _1 (_1_out, CIN);
  xor _9_2 (_9_2_out, Q1, _2_out);
  xor _6_2 (_6_2_out, DEC, d_ff_10_qn);
  not _1_2 (_1_2_out, _2_out);
  xor _9_3 (_9_3_out, Q2, _2_2_out);
  xor _6_3 (_6_3_out, DEC, d_ff_11_qn);
  not _1_3 (_1_3_out, _2_2_out);
  xor _9_4 (_9_4_out, Q3, _2_3_out);
  xor _6_4 (_6_4_out, DEC, d_ff_12_qn);
  not _1_4 (_1_4_out, _2_3_out);
  xor _9_5 (_9_5_out, Q4, _2_4_out);
  xor _6_5 (_6_5_out, DEC, d_ff_13_qn);
  not _1_5 (_1_5_out, _2_4_out);
  xor _9_6 (_9_6_out, Q5, _2_5_out);
  xor _6_6 (_6_6_out, DEC, d_ff_14_qn);
  not _1_6 (_1_6_out, _2_5_out);
  xor _9_7 (_9_7_out, Q6, _2_6_out);
  xor _6_7 (_6_7_out, DEC, d_ff_15_qn);
  not _1_7 (_1_7_out, _2_6_out);
  xor _9_8 (_9_8_out, Q7, _2_7_out);
  xor _6_8 (_6_8_out, DEC, d_ff_16_qn);
  not _1_8 (_1_8_out, _2_7_out);
  D_latch d_latch_1 (.EN(PHI2), .D(_9_out), .NOT_Q(d_latch_1_not_q));  // open: Q
  nor _2 (_2_out, _6_out, _1_out);
  D_latch d_latch_2 (.EN(PHI2), .D(_9_2_out), .NOT_Q(d_latch_2_not_q));  // open: Q
  nor _2_2 (_2_2_out, _6_2_out, _1_2_out);
  D_latch d_latch_3 (.EN(PHI2), .D(_9_3_out), .NOT_Q(d_latch_3_not_q));  // open: Q
  nor _2_3 (_2_3_out, _6_3_out, _1_3_out);
  D_latch d_latch_4 (.EN(PHI2), .D(_9_4_out), .NOT_Q(d_latch_4_not_q));  // open: Q
  nor _2_4 (_2_4_out, _6_4_out, _1_4_out);
  D_latch d_latch_5 (.EN(PHI2), .D(_9_5_out), .NOT_Q(d_latch_5_not_q));  // open: Q
  nor _2_5 (_2_5_out, _6_5_out, _1_5_out);
  D_latch d_latch_6 (.EN(PHI2), .D(_9_6_out), .NOT_Q(d_latch_6_not_q));  // open: Q
  nor _2_6 (_2_6_out, _6_6_out, _1_6_out);
  D_latch d_latch_7 (.EN(PHI2), .D(_9_7_out), .NOT_Q(d_latch_7_not_q));  // open: Q
  nor _2_7 (_2_7_out, _6_7_out, _1_7_out);
  D_latch d_latch_8 (.EN(PHI2), .D(_9_8_out), .NOT_Q(d_latch_8_not_q));  // open: Q
  nor _2_8 (COUT, _6_8_out, _1_8_out);
  nor nor_1 (NOROUT, Q7, Q6, Q5, Q4, Q3, Q2, Q1, Q0);

  // Notes on the sheet:
  //   8
  //   7
  //   7
  //   8
  //   8
  //   7
  //   7
  //   8
  //   8
  //   7
  //   8
  //   7
  //   8
  //   7
  //   7
  //   8
  //   5
  //   12
  //   5
  //   12
  //   5
  //   12
  //   12
  //   5
  //   5
  //   12
  //   12
  //   5
  //   5
  //   12
  //   5
  //   12
  //   3
  //   3
  //   3
  //   3
  //   3
  //   3
  //   3
  //   3
endmodule

module PRESCALER (
  input  PHI1,
  input  PHI2,
  input  nEN,
  output Q0,
  output Q1,
  output Q2,
  output Q3,
  output Q4,
  output Q5,
  output Q6,
  output Q7
);

  wire _1_2_out, _1_3_out, _1_4_out, _1_5_out, _1_6_out, _1_7_out, _1_8_out, _1_out, _4_2_out, _4_3_out,
       _4_4_out, _4_5_out, _4_6_out, _4_7_out, _4_8_out, _4_out, _6_2_out, _6_3_out, _6_4_out, _6_5_out,
       _6_6_out, _6_7_out, _6_8_out, _6_out, d_latch_1_not_q, d_latch_2_not_q, d_latch_3_not_q,
       d_latch_4_not_q, d_latch_5_not_q, d_latch_6_not_q, d_latch_7_not_q, d_latch_8_not_q, d_latch_9_not_q,
       d_latch_10_not_q, d_latch_11_not_q, d_latch_12_not_q, d_latch_13_not_q, d_latch_14_not_q,
       d_latch_15_not_q, d_latch_16_not_q, multiplexer_1_out, multiplexer_2_out, multiplexer_3_out,
       multiplexer_4_out, multiplexer_5_out, multiplexer_6_out, multiplexer_7_out, multiplexer_8_out;

  nor _2 (Q0, d_latch_9_not_q, nEN);
  nor _2_2 (Q1, d_latch_10_not_q, nEN);
  nor _2_3 (Q2, d_latch_11_not_q, nEN);
  nor _2_4 (Q3, d_latch_12_not_q, nEN);
  nor _2_5 (Q4, d_latch_13_not_q, nEN);
  nor _2_6 (Q5, d_latch_14_not_q, nEN);
  nor _2_7 (Q6, d_latch_15_not_q, nEN);
  nor _2_8 (Q7, d_latch_16_not_q, nEN);
  Multiplexer #(.disabled(0), .enable("false")) multiplexer_1 (
    .in0(d_latch_9_not_q), .in1(Q0), .out(multiplexer_1_out), .sel(_6_out));
  Multiplexer #(.disabled(0), .enable("false")) multiplexer_2 (
    .in0(d_latch_10_not_q), .in1(Q1), .out(multiplexer_2_out), .sel(_6_2_out));
  Multiplexer #(.disabled(0), .enable("false")) multiplexer_3 (
    .in0(d_latch_11_not_q), .in1(Q2), .out(multiplexer_3_out), .sel(_6_3_out));
  Multiplexer #(.disabled(0), .enable("false")) multiplexer_4 (
    .in0(d_latch_12_not_q), .in1(Q3), .out(multiplexer_4_out), .sel(_6_4_out));
  Multiplexer #(.disabled(0), .enable("false")) multiplexer_5 (
    .in0(d_latch_13_not_q), .in1(Q4), .out(multiplexer_5_out), .sel(_6_5_out));
  Multiplexer #(.disabled(0), .enable("false")) multiplexer_6 (
    .in0(d_latch_14_not_q), .in1(Q5), .out(multiplexer_6_out), .sel(_6_6_out));
  Multiplexer #(.disabled(0), .enable("false")) multiplexer_7 (
    .in0(d_latch_15_not_q), .in1(Q6), .out(multiplexer_7_out), .sel(_6_7_out));
  Multiplexer #(.disabled(0), .enable("false")) multiplexer_8 (
    .in0(d_latch_16_not_q), .in1(Q7), .out(multiplexer_8_out), .sel(_6_8_out));
  D_latch d_latch_1 (.EN(PHI2), .D(multiplexer_1_out), .NOT_Q(d_latch_1_not_q));  // open: Q
  D_latch d_latch_2 (.EN(PHI2), .D(multiplexer_2_out), .NOT_Q(d_latch_2_not_q));  // open: Q
  D_latch d_latch_3 (.EN(PHI2), .D(multiplexer_3_out), .NOT_Q(d_latch_3_not_q));  // open: Q
  D_latch d_latch_4 (.EN(PHI2), .D(multiplexer_4_out), .NOT_Q(d_latch_4_not_q));  // open: Q
  D_latch d_latch_5 (.EN(PHI2), .D(multiplexer_5_out), .NOT_Q(d_latch_5_not_q));  // open: Q
  D_latch d_latch_6 (.EN(PHI2), .D(multiplexer_6_out), .NOT_Q(d_latch_6_not_q));  // open: Q
  D_latch d_latch_7 (.EN(PHI2), .D(multiplexer_7_out), .NOT_Q(d_latch_7_not_q));  // open: Q
  D_latch d_latch_8 (.EN(PHI2), .D(multiplexer_8_out), .NOT_Q(d_latch_8_not_q));  // open: Q
  nor _4 (_4_out, nEN, d_latch_1_not_q);
  nor _4_2 (_4_2_out, nEN, d_latch_2_not_q);
  nor _4_3 (_4_3_out, nEN, d_latch_3_not_q);
  nor _4_4 (_4_4_out, nEN, d_latch_4_not_q);
  nor _4_5 (_4_5_out, nEN, d_latch_5_not_q);
  nor _4_6 (_4_6_out, nEN, d_latch_6_not_q);
  nor _4_7 (_4_7_out, nEN, d_latch_7_not_q);
  nor _4_8 (_4_8_out, nEN, d_latch_8_not_q);
  D_latch d_latch_9 (.EN(PHI1), .D(_4_out), .NOT_Q(d_latch_9_not_q));  // open: Q
  D_latch d_latch_10 (.EN(PHI1), .D(_4_2_out), .NOT_Q(d_latch_10_not_q));  // open: Q
  D_latch d_latch_11 (.EN(PHI1), .D(_4_3_out), .NOT_Q(d_latch_11_not_q));  // open: Q
  D_latch d_latch_12 (.EN(PHI1), .D(_4_4_out), .NOT_Q(d_latch_12_not_q));  // open: Q
  D_latch d_latch_13 (.EN(PHI1), .D(_4_5_out), .NOT_Q(d_latch_13_not_q));  // open: Q
  D_latch d_latch_14 (.EN(PHI1), .D(_4_6_out), .NOT_Q(d_latch_14_not_q));  // open: Q
  D_latch d_latch_15 (.EN(PHI1), .D(_4_7_out), .NOT_Q(d_latch_15_not_q));  // open: Q
  D_latch d_latch_16 (.EN(PHI1), .D(_4_8_out), .NOT_Q(d_latch_16_not_q));  // open: Q
  not _6 (_6_out, 1'b1);
  nor _1 (_1_out, d_latch_9_not_q, _6_out);
  not _6_2 (_6_2_out, _1_out);
  nor _1_2 (_1_2_out, d_latch_10_not_q, _6_2_out);
  not _6_3 (_6_3_out, _1_2_out);
  nor _1_3 (_1_3_out, d_latch_11_not_q, _6_3_out);
  not _6_4 (_6_4_out, _1_3_out);
  nor _1_4 (_1_4_out, d_latch_12_not_q, _6_4_out);
  not _6_5 (_6_5_out, _1_4_out);
  nor _1_5 (_1_5_out, d_latch_13_not_q, _6_5_out);
  not _6_6 (_6_6_out, _1_5_out);
  nor _1_6 (_1_6_out, d_latch_14_not_q, _6_6_out);
  not _6_7 (_6_7_out, _1_6_out);
  nor _1_7 (_1_7_out, d_latch_15_not_q, _6_7_out);
  not _6_8 (_6_8_out, _1_7_out);
  nor _1_8 (_1_8_out, d_latch_16_not_q, _6_8_out);

  // Notes on the sheet:
  //   5
  //   5
  //   5
  //   5
  //   5
  //   5
  //   5
  //   5
  //   3
  //   3
  //   3
  //   3
  //   3
  //   3
  //   3
  //   3
  //   cout
  //   cout
  //   cout
  //   cout
  //   cout
  //   cout
  //   cout
  //   cout
  //   NOT USED
endmodule
