// Logisim project PPU_Evo.circ as structural Verilog: 122 circuits, main circuit PPU_2C02G
module PPU_Test (
  input  n_RES,
  output [10:0] out_2
);

  wire clock_1_out, ppu_2c02g_1_ale, ppu_2c02g_1_n_int, ppu_2c02g_1_n_rd, ppu_2c02g_1_n_wr;
  wire [5:0] ppu_2c02g_1_a8_13;
  wire [7:0] ppu_2c02g_1_ad_out;

  Clock clock_1 (.out(clock_1_out));
  LED led_1 (.in(ppu_2c02g_1_n_int));
  PPU_2C02G ppu_2c02g_1 (
    .CLK(clock_1_out), .n_RES(n_RES), .RnW(1'b1), .D_in({8{1'b0}}), .RS(3'b000), .n_DBE(1'b1),
    .AD_in({8{1'b0}}), .n_INT(ppu_2c02g_1_n_int), .n_RD(ppu_2c02g_1_n_rd), .n_WR(ppu_2c02g_1_n_wr),
    .ALE(ppu_2c02g_1_ale), .AD_out(ppu_2c02g_1_ad_out), .A8_13(ppu_2c02g_1_a8_13), .VOUT(out_2));  // open: EXT_in, D_out, EXT_out
endmodule

module PPU_2C02G (
  input  CLK,
  input  n_RES,
  input  RnW,
  input  [7:0] D_in,
  input  [2:0] RS,
  input  n_DBE,
  input  [3:0] EXT_in,
  input  [7:0] AD_in,
  output n_INT,
  output [7:0] D_out,
  output [3:0] EXT_out,
  output n_RD,
  output n_WR,
  output ALE,
  output [7:0] AD_out,
  output [5:0] A8_13,
  output [10:0] VOUT
);

  wire clipper_clpo, clipper_n_clpb, ctrl0_bgsel, ctrl0_i_1_32, ctrl0_n_slave, ctrl0_o_8_16, ctrl0_obsel,
       ctrl0_vbl, ctrl1_bge, ctrl1_black, ctrl1_bnw, ctrl1_n_bgclip, ctrl1_n_obclip, ctrl1_obe,
       eval_n_spr0_ev, eval_oam8, eval_oamctr2, eval_pd_fifo, eval_spr_ov, fifo_n_obj_rd_attr,
       fifo_n_spr0hit, fifo_n_zcol0, fifo_n_zcol1, fifo_n_zprio, fifo_zcol2, fifo_zcol3, fsm_blnk, fsm_burst,
       fsm_clip_b, fsm_clip_o, fsm_e_ev, fsm_fat, fsm_fta, fsm_ftb, fsm_h0_d, fsm_h0_dd, fsm_h1_dd,
       fsm_h2_dd, fsm_h3_dd, fsm_h4_dd, fsm_h5_dd, fsm_i_oam2, fsm_int, fsm_n_eval, fsm_n_fnt, fsm_n_fo,
       fsm_n_h1_d, fsm_n_h2_d, fsm_n_picture, fsm_n_vis, fsm_obj_read, fsm_rescl, fsm_s_ev, fsm_sc_cnt,
       fsm_sync, fsm_vb, fsm_z_hpos, n_PCLK, not_1_out, not_3_out, not_5_out, not_6_out, not_7_out,
       oam_ofetch, PCLK, regops_n_r2, regops_n_r4, regops_n_r7, regops_n_w0, regops_n_w1, regops_n_w3,
       regops_n_w4, regops_n_w5_1, regops_n_w5_2, regops_n_w6_1, regops_n_w6_2, regops_n_w7, regops_n_w56,
       respad_rc, respad_res, rw_decode_n_rd, rw_decode_n_wr, scc_first_scnd_firstwrite,
       scc_first_scnd_secondwrite, vram_ctrl_db_par, vram_ctrl_n_ale, vram_ctrl_pd_rb, vram_ctrl_rd,
       vram_ctrl_th_mux, vram_ctrl_tstep, vram_ctrl_wr, vram_ctrl_xrb;
  wire [1:0] cram_n_ll;
  wire [2:0] ctrl1_n_tr, fsm_hc;
  wire [3:0] cram_n_cc, data_reader_bgc, eval_ov, extpads_1_ext_in, mx_n_ext_out;
  wire [4:0] data_reader_tho, mx_cga;
  wire [5:0] data_reader_n_pax_2;
  wire [7:0] bit_extender_1_out, bit_extender_2_out, controlled_buffer_1_out, data_reader_n_pax,
       dlatch_x8_1_n_val_out, dlatch_x8_2_n_val_out, dlatch_x8_3_val_out, dlatch_x8_4_val_out, eval_n_oamx,
       fsm_db_out, hv_v, nor_1_out, nor_2_out, not_2_out, not_4_out, oam_ob_out;
  wire [7:4] eval_ov_2;
  wire [8:0] hv_dec_vpla_out, hv_h;
  wire [8:8] hv_v_2;
  wire [23:0] hv_dec_hpla_out;

  ResetPad respad (.n_RES(n_RES), .RESCL(fsm_rescl), .RES(respad_res), .RC(respad_rc));
  not not_1 (not_1_out, CLK);
  SCC_FirstSecond scc_first_scnd (
    .RC(respad_rc), .n_DBE(n_DBE), .n_R2(regops_n_r2), .n_W56(regops_n_w56),
    .FirstWrite(scc_first_scnd_firstwrite), .SecondWrite(scc_first_scnd_secondwrite));
  Reg_RW_Decoder rw_decode (.RnW(RnW), .n_DBE(n_DBE), .n_RD(rw_decode_n_rd), .n_WR(rw_decode_n_wr));
  EXTPads extpads_1 (
    .EXT_Pad_In(EXT_in), .n_SLAVE(ctrl0_n_slave), .n_PCLK(n_PCLK), .n_EXT_OUT(mx_n_ext_out),
    .EXT_IN(extpads_1_ext_in), .EXT_Pad_Out(EXT_out));
  DLatch_x8 dlatch_x8_1 (.enable(1'b1), .val(AD_in), .n_val_out(dlatch_x8_1_n_val_out));  // open: val_out
  assign not_2_out = ~dlatch_x8_1_n_val_out;  // NOT_Gate not_2, 8 bits wide
  not not_3 (not_3_out, rw_decode_n_wr);
  DLatch_x8 dlatch_x8_2 (.enable(1'b1), .val(D_in), .n_val_out(dlatch_x8_2_n_val_out));  // open: val_out
  assign not_4_out = ~dlatch_x8_2_n_val_out;  // NOT_Gate not_4, 8 bits wide
  PCLK_Ntsc u_pclk (.CLK(CLK), .n_CLK(not_1_out), .RES(respad_res), .n_PCLK(n_PCLK), .PCLK(PCLK));
  HV_Counters hv (
    .PCLK(PCLK), .n_PCLK(n_PCLK), .RES(respad_res), .HC(fsm_hc[0]), .VC(fsm_hc[1]), .V_IN(fsm_hc[2]),
    .H(hv_h), .V({hv_v_2[8], hv_v}));
  assign controlled_buffer_1_out = not_3_out ? not_4_out : 8'bz;  // Controlled_Buffer controlled_buffer_1
  RegSelect regops (
    .RS0(RS[0]), .RS1(RS[1]), .RS2(RS[2]), .RnW(RnW), .First(scc_first_scnd_firstwrite),
    .Scnd(scc_first_scnd_secondwrite), .n_W6_1(regops_n_w6_1), .n_R7(regops_n_r7), .n_W6_2(regops_n_w6_2),
    .n_W7(regops_n_w7), .n_W5_1(regops_n_w5_1), .n_W4(regops_n_w4), .n_W5_2(regops_n_w5_2),
    .n_W3(regops_n_w3), .n_R2(regops_n_r2), .n_W56(regops_n_w56), .n_W1(regops_n_w1), .n_W0(regops_n_w0),
    .n_R4(regops_n_r4));
  HV_Decoders hv_dec (
    .H(hv_h), .V({hv_v_2[8], hv_v}), .VB(fsm_vb), .BLNK(fsm_blnk), .HPLA_out(hv_dec_hpla_out),
    .VPLA_out(hv_dec_vpla_out));
  PPU_CTRL0 ctrl0 (
    .RC(respad_rc), .n_W0(regops_n_w0), .n_DBE(n_DBE), .DB_in(controlled_buffer_1_out),
    .I_1_32(ctrl0_i_1_32), .OBSEL(ctrl0_obsel), .BGSEL(ctrl0_bgsel), .O_8_16(ctrl0_o_8_16),
    .n_SLAVE(ctrl0_n_slave), .VBL(ctrl0_vbl));
  PPU_CTRL1 ctrl1 (
    .RC(respad_rc), .n_W1(regops_n_w1), .n_DBE(n_DBE), .DB_in(controlled_buffer_1_out), .BnW(ctrl1_bnw),
    .n_BGCLIP(ctrl1_n_bgclip), .n_OBCLIP(ctrl1_n_obclip), .BGE(ctrl1_bge), .BLACK(ctrl1_black),
    .OBE(ctrl1_obe), .n_TR(ctrl1_n_tr[0]), .n_TG(ctrl1_n_tr[1]), .n_TB(ctrl1_n_tr[2]));
  HV_FSM fsm (
    .PCLK(PCLK), .n_PCLK(n_PCLK), .n_OBCLIP(ctrl1_n_obclip), .n_BGCLIP(ctrl1_n_bgclip), .BLACK(ctrl1_black),
    .H(hv_h), .V({hv_v_2[8], hv_v}), .VPLA_out(hv_dec_vpla_out), .HPLA_out(hv_dec_hpla_out),
    .RES(respad_res), .VBL_EN(ctrl0_vbl), .n_R2(regops_n_r2), .n_DBE(n_DBE), .H5_DD(fsm_h5_dd),
    .H4_DD(fsm_h4_dd), .H3_DD(fsm_h3_dd), .H2_DD(fsm_h2_dd), .n_H2_D(fsm_n_h2_d), .H1_DD(fsm_h1_dd),
    .n_H1_D(fsm_n_h1_d), .H0_DD(fsm_h0_dd), .H0_D(fsm_h0_d), .S_EV(fsm_s_ev), .CLIP_O(fsm_clip_o),
    .SC_CNT(fsm_sc_cnt), .CLIP_B(fsm_clip_b), .Z_HPOS(fsm_z_hpos), .n_EVAL(fsm_n_eval), .E_EV(fsm_e_ev),
    .BURST(fsm_burst), .I_OAM2(fsm_i_oam2), .SYNC(fsm_sync), .OBJ_READ(fsm_obj_read), .n_VIS(fsm_n_vis),
    .n_FNT(fsm_n_fnt), .FTB(fsm_ftb), .FTA(fsm_fta), .n_FO(fsm_n_fo), .FAT(fsm_fat), .VB(fsm_vb),
    .RESCL(fsm_rescl), .n_PICTURE(fsm_n_picture), .BLNK(fsm_blnk), .INT(fsm_int), .DB_out(fsm_db_out),
    .V_IN(fsm_hc[2]), .HC(fsm_hc[0]), .VC(fsm_hc[1]));
  Clip clipper (
    .n_PCLK(n_PCLK), .n_VIS(fsm_n_vis), .CLIP_B(fsm_clip_b), .CLIP_O(fsm_clip_o), .BGE(ctrl1_bge),
    .OBE(ctrl1_obe), .n_CLPB(clipper_n_clpb), .CLPO(clipper_clpo));
  VRAM_Control vram_ctrl (
    .PCLK(PCLK), .n_PCLK(n_PCLK), .n_R7(regops_n_r7), .n_W7(regops_n_w7), .n_DBE(n_DBE), .H0_Dash(fsm_h0_d),
    .BLNK(fsm_blnk), .n_PA8_13(data_reader_n_pax_2), .DB_PAR(vram_ctrl_db_par), .TSTEP(vram_ctrl_tstep),
    .WR(vram_ctrl_wr), .PD_RB(vram_ctrl_pd_rb), .n_ALE(vram_ctrl_n_ale), .RD(vram_ctrl_rd),
    .TH_MUX(vram_ctrl_th_mux), .XRB(vram_ctrl_xrb));
  ReadBuffer rb (.XRB(vram_ctrl_xrb), .RC(respad_rc), .PD_RB(vram_ctrl_pd_rb), .PD_in(not_2_out), .DB_out(fsm_db_out));
  FIFO_All fifo (
    .PCLK(PCLK), .n_PCLK(n_PCLK), .OBJ_READ(fsm_obj_read), .H0_DD(fsm_h0_dd), .H1_DD(fsm_h1_dd),
    .H2_DD(fsm_h2_dd), .H3_DD(fsm_h3_dd), .H4_DD(fsm_h4_dd), .H5_DD(fsm_h5_dd), .Z_HPOS(fsm_z_hpos),
    .n_VIS(fsm_n_vis), .OB(oam_ob_out), .PD_FIFO(eval_pd_fifo), .PD(not_2_out), .CLPO(clipper_clpo),
    .n_SPR0HIT(fifo_n_spr0hit), .n_ZCOL0(fifo_n_zcol0), .n_ZCOL1(fifo_n_zcol1), .ZCOL2(fifo_zcol2),
    .ZCOL3(fifo_zcol3), .n_ZPRIO(fifo_n_zprio), .n_OBJ_RD_ATTR(fifo_n_obj_rd_attr));
  DataReader_All data_reader (
    .PCLK(PCLK), .n_PCLK(n_PCLK), .n_W0(regops_n_w0), .n_W5_1(regops_n_w5_1), .n_W5_2(regops_n_w5_2),
    .n_W6_1(regops_n_w6_1), .n_W6_2(regops_n_w6_2), .n_DBE(n_DBE), .H0_DD(fsm_h0_dd), .n_H1_D(fsm_n_h1_d),
    .n_H2_D(fsm_n_h2_d), .n_OBJ_RD_ATTR(fifo_n_obj_rd_attr), .nF_NT(fsm_n_fnt), .F_AT(fsm_fat),
    .F_TA(fsm_fta), .F_TB(fsm_ftb), .n_FO(fsm_n_fo), .OBJ_READ(fsm_obj_read), .SC_CNT(fsm_sc_cnt),
    .E_EV(fsm_e_ev), .DB_PAR(vram_ctrl_db_par), .RESCL(fsm_rescl), .BLNK(fsm_blnk), .OV(eval_ov),
    .OB(oam_ob_out), .PD(not_2_out), .DB(controlled_buffer_1_out), .TSTEP(vram_ctrl_tstep), .RC(respad_rc),
    .n_CLPB(clipper_n_clpb), .BGSEL(ctrl0_bgsel), .OBSEL(ctrl0_obsel), .I1_32(ctrl0_i_1_32),
    .O8_16(ctrl0_o_8_16), .THO(data_reader_tho), .BGC(data_reader_bgc),
    .n_PAx({data_reader_n_pax_2, data_reader_n_pax}));
  MUX_All mx (
    .PCLK(PCLK), .n_PCLK(n_PCLK), .n_ZPRIO(fifo_n_zprio), .BGC(data_reader_bgc), .n_ZCOL0(fifo_n_zcol0),
    .n_ZCOL1(fifo_n_zcol1), .ZCOL2(fifo_zcol2), .ZCOL3(fifo_zcol3), .EXT_In(extpads_1_ext_in),
    .THO(data_reader_tho), .TH_MUX(vram_ctrl_th_mux), .CGA(mx_cga), .n_EXT_Out(mx_n_ext_out));
  CRAM_All cram (
    .PCLK(PCLK), .n_PCLK(n_PCLK), .n_R7(regops_n_r7), .n_DBE(n_DBE), .TH_MUX(vram_ctrl_th_mux),
    .DB_PAR(vram_ctrl_db_par), .n_PICTURE(fsm_n_picture), .BnW(ctrl1_bnw), .CGA(mx_cga),
    .DB_in(controlled_buffer_1_out), .n_CC(cram_n_cc), .n_LL(cram_n_ll), .DB_out(fsm_db_out));
  assign bit_extender_1_out = {{7{vram_ctrl_rd}}, vram_ctrl_rd};  // Bit_Extender bit_extender_1
  DLatch_x8 dlatch_x8_3 (.enable(1'b1), .val(data_reader_n_pax), .val_out(dlatch_x8_3_val_out));  // open: n_val_out
  not not_5 (not_5_out, vram_ctrl_rd);
  assign nor_1_out = ~(bit_extender_1_out | dlatch_x8_3_val_out);  // NOR_Gate nor_1, 8 bits wide
  assign AD_out = not_5_out ? nor_1_out : 8'bz;  // Controlled_Buffer controlled_buffer_2
  Obj_Eval eval (
    .PCLK(PCLK), .n_PCLK(n_PCLK), .n_R2(regops_n_r2), .BLNK(fsm_blnk), .I_OAM2(fsm_i_oam2),
    .n_VIS(fsm_n_vis), .OBJ_READ(fsm_obj_read), .n_EVAL(fsm_n_eval), .RESCL(fsm_rescl), .H0_DD(fsm_h0_dd),
    .H0_D(fsm_h0_d), .n_H2_D(fsm_n_h2_d), .OFETCH(oam_ofetch), .n_W3(regops_n_w3), .n_DBE(n_DBE),
    .DB_In(controlled_buffer_1_out), .OB(oam_ob_out), .V(hv_v), .O8_16(ctrl0_o_8_16), .n_F_NT(fsm_n_fnt),
    .S_EV(fsm_s_ev), .DB5(fsm_db_out[5]), .n_OAMx(eval_n_oamx), .OAM8(eval_oam8), .OAMCTR2(eval_oamctr2),
    .SPR_OV(eval_spr_ov), .OV({eval_ov_2, eval_ov}), .PD_FIFO(eval_pd_fifo), .n_SPR0_EV(eval_n_spr0_ev));
  SPR0_Hit alien_feature (
    .PCLK(PCLK), .BGC(data_reader_bgc), .n_SPR0HIT(fifo_n_spr0hit), .n_SPR0_EV(eval_n_spr0_ev),
    .n_VIS(fsm_n_vis), .n_R2(regops_n_r2), .n_DBE(n_DBE), .RESCL(fsm_rescl), .DB6(fsm_db_out[6]));
  not not_6 (not_6_out, CLK);
  VideoGen video_gen (
    .CLK(CLK), .n_CLK(not_6_out), .PCLK(PCLK), .n_PCLK(n_PCLK), .RES(respad_res), .n_CC(cram_n_cc),
    .n_TR(ctrl1_n_tr[0]), .n_LL(cram_n_ll), .n_TG(ctrl1_n_tr[1]), .n_TB(ctrl1_n_tr[2]), .BURST(fsm_burst),
    .SYNC(fsm_sync), .n_PICTURE(fsm_n_picture), .VOUT(VOUT));
  assign bit_extender_2_out = {{7{rw_decode_n_rd}}, rw_decode_n_rd};  // Bit_Extender bit_extender_2
  DLatch_x8 dlatch_x8_4 (.enable(1'b1), .val(fsm_db_out), .val_out(dlatch_x8_4_val_out));  // open: n_val_out
  OAM_All oam (
    .PCLK(PCLK), .n_PCLK(n_PCLK), .n_OAMx(eval_n_oamx), .OAM8(eval_oam8), .BLNK(fsm_blnk),
    .SPR_OV(eval_spr_ov), .OAMCTR2(eval_oamctr2), .H0_DD(fsm_h0_dd), .n_VIS(fsm_n_vis), .I_OAM2(fsm_i_oam2),
    .n_W4(regops_n_w4), .n_R4(regops_n_r4), .n_DBE(n_DBE), .DB_In(controlled_buffer_1_out),
    .OB_Out(oam_ob_out), .DB_Out(fsm_db_out), .OFETCH(oam_ofetch));
  not not_7 (not_7_out, rw_decode_n_rd);
  assign nor_2_out = ~(bit_extender_2_out | dlatch_x8_4_val_out);  // NOR_Gate nor_2, 8 bits wide
  assign D_out = not_7_out ? ~nor_2_out : 8'bz;  // Controlled_Inverter controlled_inverter_1
  assign n_INT = fsm_int ? ~fsm_int : 1'bz;  // Controlled_Inverter controlled_inverter_2
  not not_8 (n_RD, vram_ctrl_rd);
  not not_9 (n_WR, vram_ctrl_wr);
  not not_10 (ALE, vram_ctrl_n_ale);
  assign A8_13 = ~data_reader_n_pax_2;  // NOT_Gate not_11, 6 bits wide

  // Notes on the sheet:
  //   /RD
endmodule

module HV_FSM (
  input  PCLK,
  input  n_PCLK,
  input  n_OBCLIP,
  input  n_BGCLIP,
  input  BLACK,
  input  [8:0] H,
  input  [8:0] V,
  input  [8:0] VPLA_out,
  input  [23:0] HPLA_out,
  input  RES,
  input  VBL_EN,
  input  n_R2,
  input  n_DBE,
  output H5_DD,
  output H4_DD,
  output H3_DD,
  output H2_DD,
  output n_H2_D,
  output H1_DD,
  output n_H1_D,
  output H0_DD,
  output H0_D,
  output S_EV,
  output CLIP_O,
  output SC_CNT,
  output CLIP_B,
  output Z_HPOS,
  output n_EVAL,
  output E_EV,
  output BURST,
  output I_OAM2,
  output SYNC,
  output OBJ_READ,
  output n_VIS,
  output n_FNT,
  output FTB,
  output FTA,
  output n_FO,
  output FAT,
  output VB,
  output RESCL,
  output n_PICTURE,
  output BLNK,
  output INT,
  output [7:0] DB_out,
  output V_IN,
  output HC,
  output VC
);

  wire EvenOdd_inst_evenoddout, HPos_inst_bporch, HPos_inst_n_hb, not_1_out, VPos_inst_n_vset,
       VPos_inst_vsync;

  not not_1 (not_1_out, HPLA_out[5]);
  DelayedH DelayedH_inst (
    .PCLK(PCLK), .n_PCLK(n_PCLK), .H_Input(H), .H5_DashDash(H5_DD), .H4_DashDash(H4_DD), .H3_DashDash(H3_DD),
    .H2_DashDash(H2_DD), .n_H2_Dash(n_H2_D), .H1_DashDash(H1_DD), .n_H1_Dash(n_H1_D), .H0_DashDash(H0_DD),
    .H0_Dash(H0_D));
  EvenOdd EvenOdd_inst (
    .V8(V[8]), .RES(RES), .n_HPLA_5(not_1_out), .RESCL(RESCL), .EvenOddOut(EvenOdd_inst_evenoddout));
  VBlankInterrupt VB_Intr_inst (
    .PCLK(PCLK), .n_PCLK(n_PCLK), .n_VSET(VPos_inst_n_vset), .VBL(VBL_EN), .RESCL(RESCL), .n_R2(n_R2),
    .n_DBE(n_DBE), .INT(INT), .DB7_Out(DB_out[7]));
  HVCountersControl HV_Counter_Ctrl_inst (
    .n_PCLK(n_PCLK), .HPLA_23(HPLA_out[23]), .EvenOddOut(EvenOdd_inst_evenoddout), .VPLA_2(VPLA_out[2]),
    .V_IN(V_IN), .HC(HC), .VC(VC));
  HPosLogic HPos_inst (
    .PCLK(PCLK), .n_PCLK(n_PCLK), .HPLA_In(HPLA_out), .n_OBCLIP(n_OBCLIP), .n_BGCLIP(n_BGCLIP),
    .VSYNC(VPos_inst_vsync), .BLACK(BLACK), .S_EV(S_EV), .BPORCH(HPos_inst_bporch), .CLIP_O(CLIP_O),
    .SC_CNT(SC_CNT), .CLIP_B(CLIP_B), .n_HB(HPos_inst_n_hb), .Z_HPOS(Z_HPOS), .n_EVAL(n_EVAL), .E_EV(E_EV),
    .BURST(BURST), .I_OAM2(I_OAM2), .SYNC(SYNC), .OBJ_READ(OBJ_READ), .n_VIS(n_VIS), .n_F_NT(n_FNT),
    .F_TB(FTB), .F_TA(FTA), .n_FO(n_FO), .F_AT(FAT));
  VPosLogic VPos_inst (
    .PCLK(PCLK), .n_PCLK(n_PCLK), .n_HB(HPos_inst_n_hb), .BPORCH(HPos_inst_bporch), .VPLA_In(VPLA_out),
    .BLACK(BLACK), .VSYNC(VPos_inst_vsync), .VB(VB), .n_PICTURE(n_PICTURE), .BLNK(BLNK),
    .n_VSET(VPos_inst_n_vset), .RESCL(RESCL));
endmodule

module DLatch (
  input  Enable,
  input  Value,
  output ValOut,
  output n_ValOut
);

  D_Flip_Flop #(.trigger("high")) d_ff_1 (.D(Value), .clk(Enable), .Q(ValOut), .Qn(n_ValOut));  // open: preset, reset
endmodule

module DelayedH (
  input  PCLK,
  input  n_PCLK,
  input  [8:0] H_Input,
  output H5_DashDash,
  output H4_DashDash,
  output H3_DashDash,
  output H2_DashDash,
  output n_H2_Dash,
  output H1_DashDash,
  output n_H1_Dash,
  output H0_DashDash,
  output H0_Dash
);

  wire h0_latch1_n_valout, h0_latch2_n_valout, h2_latch1_n_valout, h3_latch1_n_valout, h4_latch1_n_valout,
       h5_latch1_n_valout;

  DLatch h5_latch1 (.Enable(n_PCLK), .Value(H_Input[5]), .n_ValOut(h5_latch1_n_valout));  // open: ValOut
  DLatch h4_latch1 (.Enable(n_PCLK), .Value(H_Input[4]), .n_ValOut(h4_latch1_n_valout));  // open: ValOut
  DLatch h3_latch1 (.Enable(n_PCLK), .Value(H_Input[3]), .n_ValOut(h3_latch1_n_valout));  // open: ValOut
  DLatch h2_latch1 (.Enable(n_PCLK), .Value(H_Input[2]), .n_ValOut(h2_latch1_n_valout));  // open: ValOut
  DLatch h1_latch1 (.Enable(n_PCLK), .Value(H_Input[1]), .n_ValOut(n_H1_Dash));  // open: ValOut
  DLatch h0_latch1 (.Enable(n_PCLK), .Value(H_Input[0]), .n_ValOut(h0_latch1_n_valout));  // open: ValOut
  DLatch h5_latch2 (.Enable(PCLK), .Value(h5_latch1_n_valout), .n_ValOut(H5_DashDash));  // open: ValOut
  DLatch h4_latch2 (.Enable(PCLK), .Value(h4_latch1_n_valout), .n_ValOut(H4_DashDash));  // open: ValOut
  DLatch h3_latch2 (.Enable(PCLK), .Value(h3_latch1_n_valout), .n_ValOut(H3_DashDash));  // open: ValOut
  DLatch h2_latch2 (.Enable(PCLK), .Value(h2_latch1_n_valout), .n_ValOut(H2_DashDash));  // open: ValOut
  DLatch h1_latch2 (.Enable(PCLK), .Value(n_H1_Dash), .n_ValOut(H1_DashDash));  // open: ValOut
  DLatch h0_latch2 (.Enable(PCLK), .Value(h0_latch1_n_valout), .n_ValOut(h0_latch2_n_valout));  // open: ValOut
  buf buffer_1 (n_H2_Dash, h2_latch1_n_valout);
  buf buffer_2 (H0_DashDash, h0_latch2_n_valout);
  not not_1 (H0_Dash, h0_latch1_n_valout);
endmodule

module EvenOdd (
  input  V8,
  input  RES,
  input  n_HPLA_5,
  input  RESCL,
  output EvenOddOut
);

  wire multiplexer_1_out, multiplexer_2_out, nor_1_out, not_1_out, not_2_out, not_3_out, not_4_out;

  not not_1 (not_1_out, multiplexer_1_out);
  Multiplexer multiplexer_1 (.in0(not_3_out), .in1(not_2_out), .out(multiplexer_1_out), .sel(V8));
  not not_2 (not_2_out, not_1_out);
  Multiplexer multiplexer_2 (.in0(nor_1_out), .in1(not_2_out), .out(multiplexer_2_out), .sel(V8));
  not not_3 (not_3_out, multiplexer_2_out);
  nor nor_1 (nor_1_out, RES, not_3_out);
  not not_4 (not_4_out, RESCL);
  nor nor_2 (EvenOddOut, nor_1_out, n_HPLA_5, not_4_out);

  // Notes on the sheet:
  //   FF_1
  //   FF_2
endmodule

module EvenOdd_PAL (
  input  n_PCLK,
  input  PCLK,
  input  BLNK,
  input  H0_D,
  input  VPLA_8,
  input  VPLA_9,
  output EvenOddOut
);

  wire latch1_valout, latch2_valout, latch3_n_valout, nand_1_out, nor_1_out, nor_2_out, not_1_out;

  DLatch latch2 (.Enable(n_PCLK), .Value(VPLA_8), .ValOut(latch2_valout));  // open: n_ValOut
  DLatch latch1 (.Enable(n_PCLK), .Value(VPLA_9), .ValOut(latch1_valout));  // open: n_ValOut
  nor nor_1 (nor_1_out, latch2_valout, nor_2_out);
  nor nor_2 (nor_2_out, nor_1_out, latch1_valout);
  DLatch latch3 (.Enable(PCLK), .Value(nor_2_out), .n_ValOut(latch3_n_valout));  // open: ValOut
  not not_1 (not_1_out, H0_D);
  nand nand_1 (nand_1_out, BLNK, latch3_n_valout);
  nor nor_3 (EvenOddOut, not_1_out, nand_1_out, n_PCLK);

  // Notes on the sheet:
  //   311
  //   265
  //   S
  //   R
  //   FF_1
endmodule

module HPosLogic (
  input  PCLK,
  input  n_PCLK,
  input  [23:0] HPLA_In,
  input  n_OBCLIP,
  input  n_BGCLIP,
  input  VSYNC,
  input  BLACK,
  output S_EV,
  output BPORCH,
  output CLIP_O,
  output SC_CNT,
  output CLIP_B,
  output n_HB,
  output Z_HPOS,
  output n_EVAL,
  output E_EV,
  output BURST,
  output I_OAM2,
  output SYNC,
  output OBJ_READ,
  output n_VIS,
  output n_F_NT,
  output F_TB,
  output F_TA,
  output n_FO,
  output F_AT
);

  wire bp_latch1_valout, bp_latch2_valout, cb_latch1_valout, cb_latch2_valout, clpb_latch1_n_valout,
       clpb_latch2_valout, clpo_latch1_valout, clpo_latch2_valout, eev_latch1_n_valout, eev_latch1_valout,
       eval_latch1_valout, eval_latch2_n_valout, fat_latch1_n_valout, fnt_latch1_n_valout,
       fnt_latch2_n_valout, fo_latch1_valout, fo_latch2_valout, fo_latch3_n_valout, fo_latch3_valout,
       fp_latch1_valout, fp_latch2_valout, fta_latch1_n_valout, fta_latch2_valout, ftb_latch1_n_valout,
       ftb_latch2_valout, hb_latch1_valout, hb_latch2_valout, hpos_latch1_n_valout, hpos_latch1_valout,
       ioam_latch1_n_valout, nor_1_out, nor_2_out, nor_3_out, nor_4_out, nor_5_out, nor_6_out, nor_11_out,
       nor_13_out, nor_15_out, nor_16_out, not_2_out, not_4_out, nvis_latch1_n_valout, nvis_latch2_n_valout,
       objrd_latch1_n_valout, sev_latch1_n_valout, sync_latch1_valout, sync_latch2_valout;

  DLatch fp_latch1 (.Enable(n_PCLK), .Value(HPLA_In[0]), .ValOut(fp_latch1_valout));  // open: n_ValOut
  DLatch fp_latch2 (.Enable(n_PCLK), .Value(HPLA_In[1]), .ValOut(fp_latch2_valout));  // open: n_ValOut
  nor nor_1 (nor_1_out, fp_latch1_valout, nor_2_out);
  nor nor_2 (nor_2_out, fp_latch2_valout, nor_1_out);
  DLatch sev_latch1 (.Enable(n_PCLK), .Value(HPLA_In[2]), .n_ValOut(sev_latch1_n_valout));  // open: ValOut
  DLatch clpo_latch1 (.Enable(n_PCLK), .Value(HPLA_In[3]), .ValOut(clpo_latch1_valout));  // open: n_ValOut
  DLatch clpb_latch1 (.Enable(n_PCLK), .Value(HPLA_In[4]), .n_ValOut(clpb_latch1_n_valout));  // open: ValOut
  DLatch hpos_latch1 (
    .Enable(n_PCLK), .Value(HPLA_In[5]), .ValOut(hpos_latch1_valout), .n_ValOut(hpos_latch1_n_valout));
  DLatch eval_latch1 (.Enable(n_PCLK), .Value(HPLA_In[6]), .ValOut(eval_latch1_valout));  // open: n_ValOut
  DLatch eev_latch1 (.Enable(n_PCLK), .Value(HPLA_In[7]), .ValOut(eev_latch1_valout), .n_ValOut(eev_latch1_n_valout));
  DLatch ioam_latch1 (.Enable(n_PCLK), .Value(HPLA_In[8]), .n_ValOut(ioam_latch1_n_valout));  // open: ValOut
  DLatch objrd_latch1 (.Enable(n_PCLK), .Value(HPLA_In[9]), .n_ValOut(objrd_latch1_n_valout));  // open: ValOut
  DLatch nvis_latch1 (.Enable(n_PCLK), .Value(HPLA_In[10]), .n_ValOut(nvis_latch1_n_valout));  // open: ValOut
  DLatch fnt_latch1 (.Enable(n_PCLK), .Value(HPLA_In[11]), .n_ValOut(fnt_latch1_n_valout));  // open: ValOut
  DLatch ftb_latch1 (.Enable(n_PCLK), .Value(HPLA_In[12]), .n_ValOut(ftb_latch1_n_valout));  // open: ValOut
  DLatch fta_latch1 (.Enable(n_PCLK), .Value(HPLA_In[13]), .n_ValOut(fta_latch1_n_valout));  // open: ValOut
  DLatch fo_latch1 (.Enable(n_PCLK), .Value(HPLA_In[14]), .ValOut(fo_latch1_valout));  // open: n_ValOut
  DLatch fo_latch2 (.Enable(n_PCLK), .Value(HPLA_In[15]), .ValOut(fo_latch2_valout));  // open: n_ValOut
  DLatch fat_latch1 (.Enable(n_PCLK), .Value(HPLA_In[16]), .n_ValOut(fat_latch1_n_valout));  // open: ValOut
  nor nor_3 (nor_3_out, fo_latch1_valout, fo_latch2_valout);
  DLatch sev_latch2 (.Enable(PCLK), .Value(sev_latch1_n_valout), .n_ValOut(S_EV));  // open: ValOut
  DLatch clpo_latch2 (.Enable(PCLK), .Value(nor_4_out), .ValOut(clpo_latch2_valout));  // open: n_ValOut
  nor nor_4 (nor_4_out, clpo_latch1_valout, clpb_latch1_n_valout);
  DLatch clpb_latch2 (.Enable(PCLK), .Value(nor_4_out), .ValOut(clpb_latch2_valout));  // open: n_ValOut
  DLatch hpos_latch2 (.Enable(PCLK), .Value(hpos_latch1_n_valout), .n_ValOut(Z_HPOS));  // open: ValOut
  DLatch eval_latch2 (.Enable(PCLK), .Value(nor_5_out), .n_ValOut(eval_latch2_n_valout));  // open: ValOut
  nor nor_5 (nor_5_out, hpos_latch1_valout, eval_latch1_valout, eev_latch1_valout);
  DLatch eev_latch2 (.Enable(PCLK), .Value(eev_latch1_n_valout), .n_ValOut(E_EV));  // open: ValOut
  DLatch ioam_latch2 (.Enable(PCLK), .Value(ioam_latch1_n_valout), .n_ValOut(I_OAM2));  // open: ValOut
  DLatch objrd_latch2 (.Enable(PCLK), .Value(objrd_latch1_n_valout), .n_ValOut(OBJ_READ));  // open: ValOut
  DLatch nvis_latch2 (.Enable(PCLK), .Value(nvis_latch1_n_valout), .n_ValOut(nvis_latch2_n_valout));  // open: ValOut
  DLatch fnt_latch2 (.Enable(PCLK), .Value(fnt_latch1_n_valout), .n_ValOut(fnt_latch2_n_valout));  // open: ValOut
  DLatch ftb_latch2 (.Enable(PCLK), .Value(ftb_latch1_n_valout), .ValOut(ftb_latch2_valout));  // open: n_ValOut
  DLatch fta_latch2 (.Enable(PCLK), .Value(fta_latch1_n_valout), .ValOut(fta_latch2_valout));  // open: n_ValOut
  DLatch fo_latch3 (.Enable(PCLK), .Value(nor_3_out), .ValOut(fo_latch3_valout), .n_ValOut(fo_latch3_n_valout));
  nor nor_6 (nor_6_out, nor_3_out, fat_latch1_n_valout);
  not not_1 (n_EVAL, eval_latch2_n_valout);
  not not_2 (not_2_out, nvis_latch2_n_valout);
  buf buffer_1 (n_VIS, not_2_out);
  not not_3 (n_F_NT, fnt_latch2_n_valout);
  buf buffer_2 (n_FO, fo_latch3_n_valout);
  buf buffer_3 (F_AT, nor_6_out);
  nor nor_7 (CLIP_O, n_OBCLIP, clpo_latch2_valout);
  nor nor_8 (CLIP_B, clpb_latch2_valout, n_BGCLIP);
  nor nor_9 (F_TB, ftb_latch2_valout, fo_latch3_valout);
  nor nor_10 (F_TA, fta_latch2_valout, fo_latch3_valout);
  DLatch bp_latch1 (.Enable(n_PCLK), .Value(HPLA_In[17]), .ValOut(bp_latch1_valout));  // open: n_ValOut
  DLatch bp_latch2 (.Enable(n_PCLK), .Value(HPLA_In[18]), .ValOut(bp_latch2_valout));  // open: n_ValOut
  DLatch hb_latch1 (.Enable(n_PCLK), .Value(HPLA_In[19]), .ValOut(hb_latch1_valout));  // open: n_ValOut
  DLatch hb_latch2 (.Enable(n_PCLK), .Value(HPLA_In[20]), .ValOut(hb_latch2_valout));  // open: n_ValOut
  DLatch cb_latch1 (.Enable(n_PCLK), .Value(HPLA_In[21]), .ValOut(cb_latch1_valout));  // open: n_ValOut
  DLatch cb_latch2 (.Enable(n_PCLK), .Value(HPLA_In[22]), .ValOut(cb_latch2_valout));  // open: n_ValOut
  DLatch sync_latch1 (.Enable(PCLK), .Value(nor_16_out), .ValOut(sync_latch1_valout));  // open: n_ValOut
  DLatch sync_latch2 (.Enable(PCLK), .Value(not_4_out), .ValOut(sync_latch2_valout));  // open: n_ValOut
  not not_4 (not_4_out, nor_2_out);
  nor nor_11 (nor_11_out, bp_latch1_valout, BPORCH);
  nor nor_12 (BPORCH, bp_latch2_valout, nor_11_out);
  nor nor_13 (nor_13_out, hb_latch1_valout, n_HB);
  nor nor_14 (n_HB, hb_latch2_valout, nor_13_out);
  nor nor_15 (nor_15_out, cb_latch1_valout, nor_16_out);
  nor nor_16 (nor_16_out, cb_latch2_valout, nor_15_out);
  nor nor_17 (BURST, sync_latch1_valout, SYNC);
  nor nor_18 (SYNC, sync_latch2_valout, VSYNC);
  nor nor_19 (SC_CNT, BLACK, nor_13_out);

  // Notes on the sheet:
  //   0
  //   1
  //   FPORCH_FF
  //   R
  //   S
  //   /FPORCH
  //   2
  //   3
  //   4
  //   5
  //   6
  //   7
  //   8
  //   9
  //   10
  //   11
  //   12
  //   13
  //   14
  //   15
  //   16
  //   17
  //   18
  //   19
  //   20
  //   21
  //   22
  //   BPORCH_FF
  //   S
  //   R
  //   S
  //   R
  //   HBLANK_FF
  //   BURST_FF
  //   R
  //   S
endmodule

module VPosLogic (
  input  PCLK,
  input  n_PCLK,
  input  n_HB,
  input  BPORCH,
  input  [8:0] VPLA_In,
  input  BLACK,
  output VSYNC,
  output VB,
  output n_PICTURE,
  output BLNK,
  output n_VSET,
  output RESCL
);

  wire and_1_out, and_2_out, and_3_out, and_4_out, blnk_latch1_valout, nor_1_out, nor_2_out, nor_3_out,
       nor_4_out, nor_5_out, nor_6_out, nor_7_out, nor_8_out, nor_9_out, nor_10_out, not_3_out, not_4_out,
       pic_latch1_valout, pic_latch2_valout, vb_latch1_valout, vb_latch2_valout, vclr_latch1_n_valout;

  and and_1 (and_1_out, n_HB, VPLA_In[0]);
  and and_2 (and_2_out, n_HB, VPLA_In[1]);
  and and_3 (and_3_out, BPORCH, VPLA_In[2]);
  and and_4 (and_4_out, BPORCH, VPLA_In[3]);
  DLatch vset_latch1 (.Enable(n_PCLK), .Value(VPLA_In[4]), .n_ValOut(n_VSET));  // open: ValOut
  nor nor_1 (nor_1_out, and_1_out, nor_2_out);
  nor nor_2 (nor_2_out, and_2_out, nor_1_out);
  nor nor_3 (nor_3_out, and_3_out, nor_4_out);
  nor nor_4 (nor_4_out, and_4_out, nor_3_out);
  nor nor_5 (nor_5_out, n_HB, nor_1_out);
  DLatch pic_latch1 (.Enable(PCLK), .Value(nor_3_out), .ValOut(pic_latch1_valout));  // open: n_ValOut
  DLatch pic_latch2 (.Enable(PCLK), .Value(BPORCH), .ValOut(pic_latch2_valout));  // open: n_ValOut
  DLatch vsync_latch1 (.Enable(PCLK), .Value(nor_5_out), .ValOut(VSYNC));  // open: n_ValOut
  nor nor_6 (nor_6_out, pic_latch1_valout, pic_latch2_valout);
  not not_1 (n_PICTURE, nor_6_out);
  DLatch vb_latch1 (.Enable(n_PCLK), .Value(VPLA_In[5]), .ValOut(vb_latch1_valout));  // open: n_ValOut
  DLatch vb_latch2 (.Enable(n_PCLK), .Value(VPLA_In[6]), .ValOut(vb_latch2_valout));  // open: n_ValOut
  DLatch blnk_latch1 (.Enable(n_PCLK), .Value(VPLA_In[7]), .ValOut(blnk_latch1_valout));  // open: n_ValOut
  DLatch vclr_latch1 (.Enable(n_PCLK), .Value(VPLA_In[8]), .n_ValOut(vclr_latch1_n_valout));  // open: ValOut
  nor nor_7 (nor_7_out, vb_latch1_valout, nor_8_out);
  nor nor_8 (nor_8_out, vb_latch2_valout, nor_7_out);
  nor nor_9 (nor_9_out, vb_latch2_valout, nor_10_out);
  nor nor_10 (nor_10_out, blnk_latch1_valout, nor_9_out);
  DLatch vclr_latch2 (.Enable(PCLK), .Value(vclr_latch1_n_valout), .n_ValOut(RESCL));  // open: ValOut
  not not_2 (VB, nor_8_out);
  not not_3 (not_3_out, nor_10_out);
  not not_4 (not_4_out, BLACK);
  nand nand_1 (BLNK, not_3_out, not_4_out);

  // Notes on the sheet:
  //   0
  //   1
  //   2
  //   3
  //   4
  //   R
  //   S
  //   VSYNC_FF
  //   R
  //   S
  //   PICTURE_FF
  //   5
  //   6
  //   7
  //   8
  //   VB_FF
  //   R
  //   S
  //   BLNK_FF
  //   S
  //   R
endmodule

module HVCountersControl (
  input  n_PCLK,
  input  HPLA_23,
  input  EvenOddOut,
  input  VPLA_2,
  output V_IN,
  output HC,
  output VC
);

  wire ctrl_latch2_n_valout, nor_1_out, not_1_out;

  DLatch ctrl_latch1 (.Enable(n_PCLK), .Value(nor_1_out), .n_ValOut(HC));  // open: ValOut
  nor nor_1 (nor_1_out, HPLA_23, EvenOddOut);
  DLatch ctrl_latch2 (.Enable(n_PCLK), .Value(VPLA_2), .n_ValOut(ctrl_latch2_n_valout));  // open: ValOut
  not not_1 (not_1_out, HC);
  nor nor_2 (VC, not_1_out, ctrl_latch2_n_valout);

  assign V_IN = HPLA_23;
endmodule

module VBlankInterrupt (
  input  PCLK,
  input  n_PCLK,
  input  n_VSET,
  input  VBL,
  input  RESCL,
  input  n_R2,
  input  n_DBE,
  output INT,
  output DB7_Out
);

  wire db_latch_n_valout, nor_1_out, nor_2_out, nor_3_out, nor_4_out, not_1_out, not_2_out, not_3_out,
       vset_latch1_n_valout, vset_latch2_valout;

  DLatch vset_latch1 (.Enable(PCLK), .Value(n_VSET), .n_ValOut(vset_latch1_n_valout));  // open: ValOut
  nor nor_1 (nor_1_out, n_R2, n_DBE);
  DLatch vset_latch2 (.Enable(n_PCLK), .Value(vset_latch1_n_valout), .ValOut(vset_latch2_valout));  // open: n_ValOut
  nor nor_2 (nor_2_out, n_PCLK, n_VSET, vset_latch2_valout);
  nor nor_3 (nor_3_out, nor_2_out, nor_4_out);
  nor nor_4 (nor_4_out, nor_3_out, RESCL, nor_1_out);
  not not_1 (not_1_out, nor_4_out);
  not not_2 (not_2_out, VBL);
  nor nor_5 (INT, not_2_out, not_1_out);
  not not_3 (not_3_out, nor_1_out);
  DLatch db_latch (.Enable(not_3_out), .Value(not_1_out), .n_ValOut(db_latch_n_valout));  // open: ValOut
  assign DB7_Out = nor_1_out ? db_latch_n_valout : 1'bz;  // Controlled_Buffer controlled_buffer_1

  // Notes on the sheet:
  //   Read Enabler
  //   NegEdge Detect
  //   R2_EN
  //   S
  //   INT_FF
  //   R
endmodule

module Pads (
  input  RnW_Pad,
  input  EXT_Pad_In,
  input  n_WR,
  input  n_SLAVE,
  input  DPad_In,
  input  n_PCLK,
  input  n_EXT_OUT,
  input  n_RD,
  input  n_RES,
  input  DBx_In,
  input  RSx_Pad,
  input  n_DBE_Pad,
  input  RESCL,
  input  n_ALE,
  input  INT,
  input  ADPad_In,
  input  RD,
  input  RD_int,
  input  n_PAx,
  input  WR_int,
  input  n_PA8,
  output RnW,
  output EXT_IN,
  output DBx_Out,
  output EXT_Pad_Out,
  output DPad_Out,
  output RES,
  output RSx,
  output RC,
  output n_DBE,
  output ALE_Pad,
  output n_INT_Pad,
  output PDx,
  output ADPad_Out,
  output n_RD_Pad,
  output n_WR_Pad,
  output Ax_Pad
);

  wire dlatch_1_n_valout, dlatch_2_valout, dlatch_3_n_valout, dlatch_4_valout, dlatch_5_n_valout,
       dlatch_6_valout, nor_1_out, nor_2_out, nor_3_out, nor_4_out, nor_5_out, nor_6_out, not_1_out,
       not_2_out, not_3_out, not_4_out, not_5_out, not_6_out, not_7_out, not_8_out, not_9_out, not_10_out,
       not_11_out, not_12_out, not_13_out, not_14_out, not_15_out, not_16_out, not_17_out, not_18_out,
       not_21_out, not_22_out;

  not not_1 (not_1_out, RnW_Pad);
  DLatch dlatch_1 (.Enable(1'b1), .Value(DPad_In), .n_ValOut(dlatch_1_n_valout));  // open: ValOut
  DLatch dlatch_2 (.Enable(1'b1), .Value(DBx_In), .ValOut(dlatch_2_valout));  // open: n_ValOut
  not not_2 (not_2_out, RSx_Pad);
  not not_3 (not_3_out, n_DBE_Pad);
  not not_4 (not_4_out, not_3_out);
  DLatch dlatch_3 (.Enable(1'b1), .Value(ADPad_In), .n_ValOut(dlatch_3_n_valout));  // open: ValOut
  DLatch dlatch_4 (.Enable(1'b1), .Value(n_PAx), .ValOut(dlatch_4_valout));  // open: n_ValOut
  not not_5 (not_5_out, not_1_out);
  buf buffer_1 (RnW, not_5_out);
  not not_6 (not_6_out, n_WR);
  not not_7 (not_7_out, dlatch_1_n_valout);
  assign DBx_Out = not_6_out ? not_7_out : 1'bz;  // Controlled_Buffer controlled_buffer_1
  not not_8 (not_8_out, n_RD);
  nor nor_1 (nor_1_out, n_RD, dlatch_2_valout);
  assign DPad_Out = not_8_out ? ~nor_1_out : 1'bz;  // Controlled_Inverter controlled_inverter_1
  not not_9 (not_9_out, not_2_out);
  buf buffer_2 (RSx, not_9_out);
  not not_10 (not_10_out, not_4_out);
  not \strong  (n_DBE, not_10_out);
  not not_11 (not_11_out, n_ALE);
  buf buffer_3 (ALE_Pad, not_11_out);
  not not_12 (not_12_out, dlatch_3_n_valout);
  buf buffer_4 (PDx, not_12_out);
  not not_13 (not_13_out, RD);
  nor nor_2 (nor_2_out, RD, dlatch_4_valout);
  assign ADPad_Out = not_13_out ? nor_2_out : 1'bz;  // Controlled_Buffer controlled_buffer_2
  not not_14 (not_14_out, n_PA8);
  buf buffer_5 (Ax_Pad, not_14_out);
  DLatch dlatch_5 (.Enable(1'b1), .Value(EXT_Pad_In), .n_ValOut(dlatch_5_n_valout));  // open: ValOut
  DLatch dlatch_6 (.Enable(n_PCLK), .Value(n_EXT_OUT), .ValOut(dlatch_6_valout));  // open: n_ValOut
  not not_15 (not_15_out, dlatch_5_n_valout);
  not not_16 (not_16_out, not_15_out);
  not not_17 (not_17_out, n_SLAVE);
  not not_18 (not_18_out, n_RES);
  buf buffer_6 (RES, not_18_out);
  nor nor_3 (nor_3_out, RES, nor_4_out);
  nor nor_4 (nor_4_out, nor_3_out, RESCL);
  assign n_INT_Pad = INT ? ~INT : 1'bz;  // Controlled_Inverter controlled_inverter_2
  not not_19 (n_RD_Pad, RD_int);
  not not_20 (n_WR_Pad, WR_int);
  nor nor_5 (nor_5_out, not_16_out, n_SLAVE);
  buf buffer_7 (EXT_IN, nor_5_out);
  not not_21 (not_21_out, not_17_out);
  nor nor_6 (nor_6_out, not_17_out, dlatch_6_valout);
  assign EXT_Pad_Out = not_21_out ? nor_6_out : 1'bz;  // Controlled_Buffer controlled_buffer_3
  not not_22 (not_22_out, nor_3_out);
  buf buffer_8 (RC, not_22_out);

  // Notes on the sheet:
  //   S
  //   R
  //   RD
  //   WR
  //   "self-notif1"
  //   Reset_FF
endmodule

module PCLK_Ntsc (
  input  CLK,
  input  n_CLK,
  input  RES,
  output n_PCLK,
  output PCLK
);

  wire buffer_1_out, buffer_2_out, nor_1_out, nor_2_out, nor_3_out, not_1_out, pclk_1_n_valout,
       pclk_2_n_valout, pclk_3_n_valout, pclk_4_n_valout;

  DLatch pclk_1 (.Enable(n_CLK), .Value(nor_1_out), .n_ValOut(pclk_1_n_valout));  // open: ValOut
  nor nor_1 (nor_1_out, RES, pclk_4_n_valout);
  DLatch pclk_2 (.Enable(CLK), .Value(pclk_1_n_valout), .n_ValOut(pclk_2_n_valout));  // open: ValOut
  DLatch pclk_3 (.Enable(n_CLK), .Value(pclk_2_n_valout), .n_ValOut(pclk_3_n_valout));  // open: ValOut
  DLatch pclk_4 (.Enable(CLK), .Value(pclk_3_n_valout), .n_ValOut(pclk_4_n_valout));  // open: ValOut
  not not_1 (not_1_out, pclk_4_n_valout);
  nor nor_2 (nor_2_out, not_1_out, nor_3_out);
  nor nor_3 (nor_3_out, nor_2_out, pclk_4_n_valout);
  buf buffer_1 (buffer_1_out, nor_2_out);
  not not_2 (n_PCLK, buffer_1_out);
  buf buffer_2 (buffer_2_out, nor_3_out);
  not not_3 (PCLK, buffer_2_out);

  // Notes on the sheet:
  //   PCLK
  //   PCLK_FF
endmodule

module PCLK_Pal (
  input  CLK,
  input  n_CLK,
  input  RES,
  output n_PCLK,
  output PCLK
);

  wire buffer_1_out, buffer_2_out, nor_1_out, nor_2_out, nor_3_out, nor_4_out, nor_5_out, not_1_out,
       not_2_out, pclk_1_valout, pclk_2_n_valout, pclk_3_n_valout, pclk_4_n_valout, pclk_5_n_valout,
       pclk_6_n_valout;

  DLatch pclk_1 (.Enable(n_CLK), .Value(nor_3_out), .ValOut(pclk_1_valout));  // open: n_ValOut
  DLatch pclk_2 (.Enable(CLK), .Value(nor_1_out), .n_ValOut(pclk_2_n_valout));  // open: ValOut
  nor nor_1 (nor_1_out, pclk_1_valout, RES);
  DLatch pclk_3 (.Enable(n_CLK), .Value(pclk_2_n_valout), .n_ValOut(pclk_3_n_valout));  // open: ValOut
  DLatch pclk_4 (.Enable(CLK), .Value(pclk_3_n_valout), .n_ValOut(pclk_4_n_valout));  // open: ValOut
  DLatch pclk_5 (.Enable(n_CLK), .Value(pclk_4_n_valout), .n_ValOut(pclk_5_n_valout));  // open: ValOut
  DLatch pclk_6 (.Enable(CLK), .Value(pclk_5_n_valout), .n_ValOut(pclk_6_n_valout));  // open: ValOut
  not not_1 (not_1_out, pclk_5_n_valout);
  nor nor_2 (nor_2_out, pclk_6_n_valout, not_1_out);
  nor nor_3 (nor_3_out, pclk_6_n_valout, pclk_4_n_valout);
  not not_2 (not_2_out, nor_2_out);
  nor nor_4 (nor_4_out, not_2_out, nor_5_out);
  nor nor_5 (nor_5_out, nor_4_out, nor_2_out);
  buf buffer_1 (buffer_1_out, nor_4_out);
  not not_3 (n_PCLK, buffer_1_out);
  buf buffer_2 (buffer_2_out, nor_5_out);
  not not_4 (PCLK, buffer_2_out);

  // Notes on the sheet:
  //   PCLK
  //   PCLK_FF
endmodule

module PCLK_Test (
  input  RES
);

  wire CLK_out, not_1_out, pclk_ntsc_1_n_pclk, pclk_ntsc_1_pclk, pclk_pal_1_n_pclk, pclk_pal_1_pclk;

  Clock CLK (.out(CLK_out));
  not not_1 (not_1_out, CLK_out);
  LED led_1 (.in(pclk_ntsc_1_n_pclk));
  PCLK_Ntsc pclk_ntsc_1 (
    .CLK(CLK_out), .n_CLK(not_1_out), .RES(RES), .n_PCLK(pclk_ntsc_1_n_pclk), .PCLK(pclk_ntsc_1_pclk));
  LED led_2 (.in(pclk_ntsc_1_pclk));
  LED led_3 (.in(pclk_pal_1_n_pclk));
  PCLK_Pal pclk_pal_1 (.CLK(CLK_out), .n_CLK(not_1_out), .RES(RES), .n_PCLK(pclk_pal_1_n_pclk), .PCLK(pclk_pal_1_pclk));
  LED led_4 (.in(pclk_pal_1_pclk));
endmodule

module VRAM_Control (
  input  PCLK,
  input  n_PCLK,
  input  n_R7,
  input  n_W7,
  input  n_DBE,
  input  H0_Dash,
  input  BLNK,
  input  [5:0] n_PA8_13,
  output DB_PAR,
  output TSTEP,
  output WR,
  output PD_RB,
  output n_ALE,
  output RD,
  output TH_MUX,
  output XRB
);

  wire and_1_out, blnk_latch_n_valout, h0_latch_valout, multiplexer_1_out, multiplexer_2_out, nor_1_out,
       nor_3_out, nor_4_out, nor_5_out, nor_6_out, nor_7_out, nor_8_out, nor_9_out, nor_10_out, nor_11_out,
       nor_16_out, nor_18_out, nor_19_out, not_1_out, not_2_out, not_3_out, not_4_out, not_5_out, not_6_out,
       not_7_out, R7_EN, rd_latch1_n_valout, rd_latch2_n_valout, rd_latch2_valout, rd_latch3_n_valout,
       rd_latch4_n_valout, rd_latch4_valout, tmp_1, tmp_2, tstep_latch_valout, wr_latch1_n_valout,
       wr_latch2_n_valout, wr_latch3_n_valout, wr_latch3_valout, wr_latch4_valout;

  nor nor_1 (nor_1_out, n_W7, n_DBE);
  nor nor_2 (R7_EN, n_R7, n_DBE);
  nor nor_3 (nor_3_out, H0_Dash, BLNK, n_PCLK);
  DLatch blnk_latch (.Enable(PCLK), .Value(BLNK), .n_ValOut(blnk_latch_n_valout));  // open: ValOut
  DLatch wr_latch2 (.Enable(PCLK), .Value(wr_latch1_n_valout), .n_ValOut(wr_latch2_n_valout));  // open: ValOut
  DLatch rd_latch2 (
    .Enable(PCLK), .Value(rd_latch1_n_valout), .ValOut(rd_latch2_valout), .n_ValOut(rd_latch2_n_valout));
  nor nor_4 (nor_4_out, nor_3_out, tmp_1, tmp_2);
  nor nor_5 (nor_5_out, nor_1_out, nor_6_out);
  nor nor_6 (nor_6_out, nor_5_out, wr_latch3_n_valout);
  DLatch wr_latch3 (
    .Enable(n_PCLK), .Value(wr_latch2_n_valout), .ValOut(wr_latch3_valout), .n_ValOut(wr_latch3_n_valout));
  nor nor_7 (nor_7_out, R7_EN, nor_8_out);
  nor nor_8 (nor_8_out, nor_7_out, rd_latch3_n_valout);
  DLatch rd_latch3 (.Enable(n_PCLK), .Value(rd_latch2_n_valout), .n_ValOut(rd_latch3_n_valout));  // open: ValOut
  buf buffer_1 (n_ALE, nor_4_out);
  nor nor_9 (nor_9_out, blnk_latch_n_valout, n_PA8_13[0], n_PA8_13[1], n_PA8_13[2], n_PA8_13[3], n_PA8_13[4], n_PA8_13[5]);
  nor nor_10 (nor_10_out, nor_1_out, nor_5_out);
  nor nor_11 (nor_11_out, R7_EN, nor_7_out);
  buf buffer_2 (TH_MUX, nor_9_out);
  not not_1 (not_1_out, multiplexer_1_out);
  Multiplexer multiplexer_1 (.in0(not_2_out), .in1(nor_10_out), .out(multiplexer_1_out), .sel(PCLK));
  not not_2 (not_2_out, not_1_out);
  DLatch wr_latch4 (.Enable(PCLK), .Value(wr_latch3_n_valout), .ValOut(wr_latch4_valout));  // open: n_ValOut
  nor nor_12 (DB_PAR, wr_latch3_valout, wr_latch1_n_valout);
  not not_3 (not_3_out, multiplexer_2_out);
  Multiplexer multiplexer_2 (.in0(not_4_out), .in1(nor_11_out), .out(multiplexer_2_out), .sel(PCLK));
  not not_4 (not_4_out, not_3_out);
  DLatch rd_latch4 (
    .Enable(PCLK), .Value(rd_latch3_n_valout), .ValOut(rd_latch4_valout), .n_ValOut(rd_latch4_n_valout));
  nor nor_13 (tmp_2, rd_latch4_valout, rd_latch2_n_valout);
  DLatch wr_latch1 (.Enable(n_PCLK), .Value(not_1_out), .n_ValOut(wr_latch1_n_valout));  // open: ValOut
  nor nor_14 (tmp_1, wr_latch4_valout, wr_latch2_n_valout);
  DLatch tstep_latch (.Enable(PCLK), .Value(DB_PAR), .ValOut(tstep_latch_valout));  // open: n_ValOut
  not not_5 (not_5_out, DB_PAR);
  DLatch rd_latch1 (.Enable(n_PCLK), .Value(not_3_out), .n_ValOut(rd_latch1_n_valout));  // open: ValOut
  nor nor_15 (PD_RB, rd_latch4_n_valout, rd_latch2_valout);
  DLatch h0_latch (.Enable(PCLK), .Value(H0_Dash), .ValOut(h0_latch_valout));  // open: n_ValOut
  nor nor_16 (nor_16_out, tstep_latch_valout, PD_RB);
  nor nor_17 (WR, not_5_out, TH_MUX);
  not not_6 (not_6_out, BLNK);
  not not_7 (not_7_out, R7_EN);
  nor nor_18 (nor_18_out, not_7_out, TH_MUX);
  not not_8 (TSTEP, nor_16_out);
  and and_1 (and_1_out, h0_latch_valout, not_6_out);
  not not_9 (XRB, nor_18_out);
  nor nor_19 (nor_19_out, and_1_out, PD_RB);
  not not_10 (RD, nor_19_out);

  // Notes on the sheet:
  //   W7_EN
  //   W7_FF
  //   R7_FF
  //   WR_FF
  //   Write timing pipeline
  //   RD_FF
  //   Read timing pipeline
endmodule

module VRAM_Control_Test (
  input  n_R7,
  input  n_W7,
  input  n_DBE,
  input  H0_Dash,
  input  BLNK,
  input  [5:0] n_PA_Top
);

  wire not_1_out, PCLK_out, vram_control_1_db_par, vram_control_1_n_ale, vram_control_1_pd_rb,
       vram_control_1_rd, vram_control_1_th_mux, vram_control_1_tstep, vram_control_1_wr, vram_control_1_xrb;

  Clock PCLK (.out(PCLK_out));
  not not_1 (not_1_out, PCLK_out);
  LED led_1 (.in(vram_control_1_db_par));
  VRAM_Control vram_control_1 (
    .PCLK(PCLK_out), .n_PCLK(not_1_out), .n_R7(n_R7), .n_W7(n_W7), .n_DBE(n_DBE), .H0_Dash(H0_Dash),
    .BLNK(BLNK), .n_PA8_13(n_PA_Top), .DB_PAR(vram_control_1_db_par), .TSTEP(vram_control_1_tstep),
    .WR(vram_control_1_wr), .PD_RB(vram_control_1_pd_rb), .n_ALE(vram_control_1_n_ale),
    .RD(vram_control_1_rd), .TH_MUX(vram_control_1_th_mux), .XRB(vram_control_1_xrb));
  LED led_2 (.in(vram_control_1_tstep));
  LED led_3 (.in(vram_control_1_wr));
  LED led_4 (.in(vram_control_1_pd_rb));
  LED led_5 (.in(vram_control_1_n_ale));
  LED led_6 (.in(vram_control_1_rd));
  LED led_7 (.in(vram_control_1_th_mux));
  LED led_8 (.in(vram_control_1_xrb));
endmodule

module Reg_RW_Decoder (
  input  RnW,
  input  n_DBE,
  output n_RD,
  output n_WR
);

  wire nor_1_out, nor_2_out, not_1_out;

  not not_1 (not_1_out, RnW);
  nor nor_1 (nor_1_out, not_1_out, n_DBE);
  nor nor_2 (nor_2_out, RnW, n_DBE);
  not not_2 (n_RD, nor_1_out);
  not not_3 (n_WR, nor_2_out);
endmodule

module RW_Enabler (
  input  n_RegOp,
  input  n_DBE,
  output RegOp_Enable
);

  nor nor_1 (RegOp_Enable, n_RegOp, n_DBE);
endmodule

module SCC_FirstSecond (
  input  RC,
  input  n_DBE,
  input  n_R2,
  input  n_W56,
  output FirstWrite,
  output SecondWrite
);

  wire multiplexer_1_out, multiplexer_2_out, nor_2_out, not_2_out, rw_enabler_1_regop_enable,
       rw_enabler_2_regop_enable;

  RW_Enabler rw_enabler_1 (.n_RegOp(n_R2), .n_DBE(n_DBE), .RegOp_Enable(rw_enabler_1_regop_enable));
  RW_Enabler rw_enabler_2 (.n_RegOp(n_W56), .n_DBE(n_DBE), .RegOp_Enable(rw_enabler_2_regop_enable));
  nor nor_1 (SecondWrite, RC, rw_enabler_1_regop_enable, multiplexer_1_out);
  not not_1 (FirstWrite, SecondWrite);
  Multiplexer multiplexer_1 (
    .in0(not_2_out), .in1(FirstWrite), .out(multiplexer_1_out), .sel(rw_enabler_2_regop_enable));
  Multiplexer multiplexer_2 (
    .in0(not_2_out), .in1(SecondWrite), .out(multiplexer_2_out), .sel(rw_enabler_2_regop_enable));
  nor nor_2 (nor_2_out, RC, rw_enabler_1_regop_enable, multiplexer_2_out);
  not not_2 (not_2_out, nor_2_out);

  // Notes on the sheet:
  //   R2
  //   W5/6
  //   FF_1
  //   FF_2
endmodule

module RegSelect (
  input  RS0,
  input  RS1,
  input  RS2,
  input  RnW,
  input  First,
  input  Scnd,
  output n_W6_1,
  output n_R7,
  output n_W6_2,
  output n_W7,
  output n_W5_1,
  output n_W4,
  output n_W5_2,
  output n_W3,
  output n_R2,
  output n_W56,
  output n_W1,
  output n_W0,
  output n_R4
);

  wire nor_1_out, nor_2_out, nor_3_out, nor_4_out, nor_6_out, nor_7_out, nor_8_out, nor_9_out, nor_10_out,
       nor_11_out, nor_12_out, nor_13_out, not_1_out, not_2_out, not_3_out, not_4_out;

  not not_1 (not_1_out, RS0);
  not not_2 (not_2_out, RS1);
  not not_3 (not_3_out, RS2);
  not not_4 (not_4_out, RnW);
  nor nor_1 (nor_1_out, RS0, not_3_out, not_2_out, RnW, Scnd);
  nor nor_2 (nor_2_out, RS0, not_3_out, not_2_out, RnW, First);
  nor nor_3 (nor_3_out, not_3_out, RS1, not_1_out, RnW, Scnd);
  nor nor_4 (nor_4_out, not_3_out, RS1, not_1_out, RnW, First);
  not not_5 (n_W6_1, nor_1_out);
  not not_6 (n_W6_2, nor_2_out);
  not not_7 (n_W5_1, nor_3_out);
  not not_8 (n_W5_2, nor_4_out);
  nor nor_5 (n_W56, nor_4_out, nor_3_out, nor_2_out, nor_1_out);
  nor nor_6 (nor_6_out, not_3_out, not_2_out, not_1_out, not_4_out);
  not not_9 (n_R7, nor_6_out);
  nor nor_7 (nor_7_out, not_3_out, not_2_out, not_1_out, RnW);
  not not_10 (n_W7, nor_7_out);
  nor nor_8 (nor_8_out, not_3_out, RS1, RS0, RnW);
  not not_11 (n_W4, nor_8_out);
  nor nor_9 (nor_9_out, RS2, not_2_out, not_1_out, RnW);
  not not_12 (n_W3, nor_9_out);
  nor nor_10 (nor_10_out, RS2, not_2_out, RS0, not_4_out);
  not not_13 (n_R2, nor_10_out);
  nor nor_11 (nor_11_out, RS2, RS1, not_1_out, RnW);
  not not_14 (n_W1, nor_11_out);
  nor nor_12 (nor_12_out, RS2, RS1, RS0, RnW);
  not not_15 (n_W0, nor_12_out);
  nor nor_13 (nor_13_out, not_3_out, RS1, RS0, not_4_out);
  not not_16 (n_R4, nor_13_out);
endmodule

module RegFF (
  input  Res,
  input  Enable,
  input  Val_in,
  output Val_out
);

  wire multiplexer_1_out, not_1_out;

  Multiplexer multiplexer_1 (.in0(Val_out), .in1(Val_in), .out(multiplexer_1_out), .sel(Enable));
  nor nor_1 (Val_out, Res, not_1_out);
  not not_1 (not_1_out, multiplexer_1_out);
endmodule

module PPU_CTRL0 (
  input  RC,
  input  n_W0,
  input  n_DBE,
  input  [7:0] DB_in,
  output I_1_32,
  output OBSEL,
  output BGSEL,
  output O_8_16,
  output n_SLAVE,
  output VBL
);

  wire i132_latch_n_valout, nor_1_out, not_1_out, o816_latch_n_valout, regff_1_val_out, regff_2_val_out,
       regff_3_val_out, regff_4_val_out;

  nor nor_1 (nor_1_out, n_W0, n_DBE);
  not not_1 (not_1_out, nor_1_out);
  RegFF regff_1 (.Res(RC), .Enable(nor_1_out), .Val_in(DB_in[2]), .Val_out(regff_1_val_out));
  RegFF regff_2 (.Res(RC), .Enable(nor_1_out), .Val_in(DB_in[3]), .Val_out(regff_2_val_out));
  RegFF regff_3 (.Res(RC), .Enable(nor_1_out), .Val_in(DB_in[4]), .Val_out(regff_3_val_out));
  RegFF regff_4 (.Res(RC), .Enable(nor_1_out), .Val_in(DB_in[5]), .Val_out(regff_4_val_out));
  RegFF regff_5 (.Res(RC), .Enable(nor_1_out), .Val_in(DB_in[6]), .Val_out(n_SLAVE));
  RegFF regff_6 (.Res(RC), .Enable(nor_1_out), .Val_in(DB_in[7]), .Val_out(VBL));
  DLatch i132_latch (.Enable(not_1_out), .Value(regff_1_val_out), .n_ValOut(i132_latch_n_valout));  // open: ValOut
  DLatch obsel_latch (.Enable(not_1_out), .Value(regff_2_val_out), .n_ValOut(OBSEL));  // open: ValOut
  DLatch bgsel_latch (.Enable(not_1_out), .Value(regff_3_val_out), .n_ValOut(BGSEL));  // open: ValOut
  DLatch o816_latch (.Enable(not_1_out), .Value(regff_4_val_out), .n_ValOut(o816_latch_n_valout));  // open: ValOut
  not not_2 (I_1_32, i132_latch_n_valout);
  not not_3 (O_8_16, o816_latch_n_valout);

  // Notes on the sheet:
  //   Bits 0 and 1 in the PAR Generator
  //   W0_EN
endmodule

module PPU_CTRL1 (
  input  RC,
  input  n_W1,
  input  n_DBE,
  input  [7:0] DB_in,
  output BnW,
  output n_BGCLIP,
  output n_OBCLIP,
  output BGE,
  output BLACK,
  output OBE,
  output n_TR,
  output n_TG,
  output n_TB
);

  wire bgclip_latch_n_valout, nor_1_out, not_1_out, obclip_latch_n_valout, regff_2_val_out, regff_3_val_out,
       regff_4_val_out, regff_5_val_out, regff_6_val_out, regff_7_val_out, regff_8_val_out;

  nor nor_1 (nor_1_out, n_W1, n_DBE);
  not not_1 (not_1_out, nor_1_out);
  RegFF regff_1 (.Res(RC), .Enable(nor_1_out), .Val_in(DB_in[0]), .Val_out(BnW));
  RegFF regff_2 (.Res(RC), .Enable(nor_1_out), .Val_in(DB_in[1]), .Val_out(regff_2_val_out));
  RegFF regff_3 (.Res(RC), .Enable(nor_1_out), .Val_in(DB_in[2]), .Val_out(regff_3_val_out));
  RegFF regff_4 (.Res(RC), .Enable(nor_1_out), .Val_in(DB_in[3]), .Val_out(regff_4_val_out));
  RegFF regff_5 (.Res(RC), .Enable(nor_1_out), .Val_in(DB_in[4]), .Val_out(regff_5_val_out));
  RegFF regff_6 (.Res(RC), .Enable(nor_1_out), .Val_in(DB_in[5]), .Val_out(regff_6_val_out));
  RegFF regff_7 (.Res(RC), .Enable(nor_1_out), .Val_in(DB_in[6]), .Val_out(regff_7_val_out));
  RegFF regff_8 (.Res(RC), .Enable(nor_1_out), .Val_in(DB_in[7]), .Val_out(regff_8_val_out));
  DLatch bgclip_latch (.Enable(not_1_out), .Value(regff_2_val_out), .n_ValOut(bgclip_latch_n_valout));  // open: ValOut
  DLatch obclip_latch (.Enable(not_1_out), .Value(regff_3_val_out), .n_ValOut(obclip_latch_n_valout));  // open: ValOut
  DLatch bge_latch (.Enable(not_1_out), .Value(regff_4_val_out), .ValOut(BGE));  // open: n_ValOut
  DLatch obe_latch (.Enable(not_1_out), .Value(regff_5_val_out), .ValOut(OBE));  // open: n_ValOut
  DLatch tr_latch (.Enable(not_1_out), .Value(regff_6_val_out), .n_ValOut(n_TR));  // open: ValOut
  DLatch tg_latch (.Enable(not_1_out), .Value(regff_7_val_out), .n_ValOut(n_TG));  // open: ValOut
  not not_2 (n_TB, regff_8_val_out);
  not not_3 (n_BGCLIP, bgclip_latch_n_valout);
  not not_4 (n_OBCLIP, obclip_latch_n_valout);
  nor nor_2 (BLACK, BGE, OBE);

  // Notes on the sheet:
  //   W1_EN
endmodule

module PPU_CTRL1_BLACK_PAL (
  input  PCLK,
  input  n_PCLK,
  input  BLACK_Regs,
  output BLACK
);

  wire black_latch1_n_valout, multiplexer_1_out, multiplexer_2_out, not_1_out, not_2_out, not_3_out,
       not_4_out;

  Multiplexer multiplexer_1 (.in0(not_1_out), .in1(BLACK_Regs), .out(multiplexer_1_out), .sel(PCLK));
  not not_1 (not_1_out, not_2_out);
  not not_2 (not_2_out, multiplexer_1_out);
  Multiplexer multiplexer_2 (.in0(not_3_out), .in1(not_1_out), .out(multiplexer_2_out), .sel(n_PCLK));
  not not_3 (not_3_out, not_4_out);
  not not_4 (not_4_out, multiplexer_2_out);
  DLatch black_latch1 (.Enable(PCLK), .Value(not_3_out), .n_ValOut(black_latch1_n_valout));  // open: ValOut
  DLatch black_latch2 (.Enable(n_PCLK), .Value(black_latch1_n_valout), .n_ValOut(BLACK));  // open: ValOut

  // Notes on the sheet:
  //   BLACK_FF1
  //   BLACK_FF2
  //   /BLACK
endmodule

module Clip (
  input  n_PCLK,
  input  n_VIS,
  input  CLIP_B,
  input  CLIP_O,
  input  BGE,
  input  OBE,
  output n_CLPB,
  output CLPO
);

  wire clipb_latch_valout, nor_2_out, not_1_out, not_2_out, nvis_latch_valout;

  DLatch nvis_latch (.Enable(n_PCLK), .Value(n_VIS), .ValOut(nvis_latch_valout));  // open: n_ValOut
  DLatch clipb_latch (.Enable(n_PCLK), .Value(CLIP_B), .ValOut(clipb_latch_valout));  // open: n_ValOut
  not not_1 (not_1_out, BGE);
  not not_2 (not_2_out, OBE);
  nor nor_1 (n_CLPB, nvis_latch_valout, clipb_latch_valout, not_1_out);
  DLatch clipo_latch (.Enable(n_PCLK), .Value(nor_2_out), .n_ValOut(CLPO));  // open: ValOut
  nor nor_2 (nor_2_out, nvis_latch_valout, CLIP_O, not_2_out);

  // Notes on the sheet:
  //   From FSM
  //   From CtrlRegs
endmodule

module H_Carry (
  input  n_H0,
  input  n_H1,
  input  n_H2,
  input  n_H3,
  input  n_H4,
  output CarryH
);

  nor nor_1 (CarryH, n_H0, n_H1, n_H2, n_H3, n_H4);
endmodule

module V_Carry (
  input  n_V0,
  input  n_V1,
  input  n_V2,
  input  n_V3,
  input  n_V4,
  input  V_IN,
  output CarryV
);

  wire not_1_out;

  not not_1 (not_1_out, V_IN);
  nor nor_1 (CarryV, n_V0, n_V1, n_V2, n_V3, n_V4, not_1_out);
endmodule

module CRAM_Decoder (
  input  [4:0] CGA,
  input  PCLK,
  output COL0,
  output COL1,
  output COL2,
  output COL3,
  output ROW0_4,
  output ROW1,
  output ROW2,
  output ROW3,
  output ROW5,
  output ROW6,
  output ROW7
);

  wire demultiplexer_2_out0, demultiplexer_2_out1, demultiplexer_2_out2, demultiplexer_2_out3,
       demultiplexer_2_out4, demultiplexer_2_out5, demultiplexer_2_out6, demultiplexer_2_out7, or_1_out;

  Demultiplexer #(.select(2)) demultiplexer_1 (
    .out0(COL0), .out1(COL1), .out2(COL2), .out3(COL3), .in(1'b1), .sel(CGA[3:2]));
  Demultiplexer #(.select(3)) demultiplexer_2 (
    .out0(demultiplexer_2_out0), .out1(demultiplexer_2_out1), .out2(demultiplexer_2_out2),
    .out3(demultiplexer_2_out3), .out4(demultiplexer_2_out4), .out5(demultiplexer_2_out5),
    .out6(demultiplexer_2_out6), .out7(demultiplexer_2_out7), .in(1'b1), .sel({CGA[4], CGA[1:0]}));
  or or_1 (or_1_out, demultiplexer_2_out0, demultiplexer_2_out4);
  and and_1 (ROW0_4, or_1_out, ~PCLK);  // AND_Gate
  and and_2 (ROW1, demultiplexer_2_out1, ~PCLK);  // AND_Gate
  and and_3 (ROW2, demultiplexer_2_out2, ~PCLK);  // AND_Gate
  and and_4 (ROW3, demultiplexer_2_out3, ~PCLK);  // AND_Gate
  and and_5 (ROW5, demultiplexer_2_out5, ~PCLK);  // AND_Gate
  and and_6 (ROW6, demultiplexer_2_out6, ~PCLK);  // AND_Gate
  and and_7 (ROW7, demultiplexer_2_out7, ~PCLK);  // AND_Gate

  // Notes on the sheet:
  //   This `or` gate is not really there
  //   It is used for the convenience of combining 0 and 4 outputs from DMX.
endmodule

module CB_Control (
  input  PCLK,
  input  n_R7,
  input  n_DBE,
  input  TH_MUX,
  input  DB_PAR,
  input  n_PICTURE,
  input  BnW,
  output n_CB_DB,
  output n_BW,
  output n_DB_CB
);

  wire and_1_out, dbpar_latch_valout, nand_1_out, nor_1_out, not_1_out;

  nor nor_1 (nor_1_out, n_R7, n_DBE, not_1_out);
  not not_1 (not_1_out, TH_MUX);
  and and_1 (and_1_out, n_CB_DB, n_PICTURE);
  DLatch dbpar_latch (.Enable(PCLK), .Value(DB_PAR), .ValOut(dbpar_latch_valout));  // open: n_ValOut
  not not_2 (n_CB_DB, nor_1_out);
  nor nor_2 (n_BW, and_1_out, BnW);
  nand nand_1 (nand_1_out, dbpar_latch_valout, TH_MUX);
  buf buffer_1 (n_DB_CB, nand_1_out);
endmodule

module CB_Bit (
  input  PCLK,
  input  n_PCLK,
  input  DB_In,
  input  n_DB_CB,
  input  n_CB_DB,
  input  BL_in,
  input  n_BL_in,
  input  n_OE,
  output BL_out,
  output n_BL_out,
  output DB_Out,
  output CB_Out
);

  wire controlled_buffer_1_out, controlled_buffer_2_out, dlatch_1_n_valout, dlatch_2_n_valout, nand_1_out,
       nor_1_out, nor_2_out, not_1_out, not_2_out, not_3_out, not_5_out;

  not not_1 (not_1_out, DB_In);
  not not_2 (not_2_out, n_DB_CB);
  not not_3 (not_3_out, n_DB_CB);
  assign controlled_buffer_1_out = not_2_out ? DB_In : 1'bz;  // Controlled_Buffer controlled_buffer_1
  buf buffer_1 (BL_in, controlled_buffer_1_out);
  assign controlled_buffer_2_out = not_3_out ? not_1_out : 1'bz;  // Controlled_Buffer controlled_buffer_2
  buf buffer_2 (n_BL_in, controlled_buffer_2_out);
  assign n_BL_in = PCLK ? 1'b1 : 1'bz;  // Controlled_Buffer controlled_buffer_3
  nor nor_1 (nor_1_out, BL_in, nor_2_out);
  Transistor #(.\type ("n")) transistor_1 ();  // open: in, out, gate
  nor nor_2 (nor_2_out, nor_1_out, n_BL_in);
  assign BL_in = PCLK ? 1'b1 : 1'bz;  // Controlled_Buffer controlled_buffer_4
  nand nand_1 (nand_1_out, nor_2_out, n_OE);
  not not_4 (CB_Out, nand_1_out);
  DLatch dlatch_1 (.Enable(n_PCLK), .Value(CB_Out), .n_ValOut(dlatch_1_n_valout));  // open: ValOut
  DLatch dlatch_2 (.Enable(PCLK), .Value(dlatch_1_n_valout), .n_ValOut(dlatch_2_n_valout));  // open: ValOut
  not not_5 (not_5_out, n_CB_DB);
  assign DB_Out = not_5_out ? dlatch_2_n_valout : 1'bz;  // Controlled_Buffer controlled_buffer_5

  assign BL_out = BL_in;
  assign n_BL_out = n_BL_in;

  // Notes on the sheet:
  //   Sense Amp
  //   In the original circuit here is the PCLK pass FET, which connects the NOR outputs
  //   PCLK
endmodule

module Vid_SR_Bit (
  input  CLK,
  input  n_CLK,
  input  n_shift_in,
  input  RES,
  output shift_out,
  output n_shift_out,
  output val_out
);

  wire in_latch_valout;

  DLatch in_latch (.Enable(CLK), .Value(n_shift_in), .ValOut(in_latch_valout));  // open: n_ValOut
  DLatch out_latch (.Enable(n_CLK), .Value(val_out), .ValOut(shift_out), .n_ValOut(n_shift_out));
  nor nor_1 (val_out, in_latch_valout, RES);
endmodule

module PhaseShifter (
  input  CLK,
  input  n_CLK,
  input  RES,
  input  [12:0] P,
  output n_PR,
  output n_PG,
  output n_PB,
  output n_PZ
);

  wire and_1_out, and_2_out, and_3_out, and_4_out, and_5_out, and_6_out, and_7_out, and_8_out, and_9_out,
       and_10_out, and_11_out, and_12_out, bit_0_n_shift_out, bit_0_val_out, bit_1_n_shift_out,
       bit_2_n_shift_out, bit_2_val_out, bit_3_n_shift_out, bit_4_n_shift_out, bit_4_val_out,
       bit_5_shift_out, nor_1_out, nor_2_out, not_1_out;

  not not_1 (not_1_out, bit_3_n_shift_out);
  nor nor_1 (nor_1_out, not_1_out, bit_4_n_shift_out);
  nor nor_2 (nor_2_out, bit_5_shift_out, nor_1_out);
  Vid_SR_Bit bit_5 (
    .CLK(CLK), .n_CLK(n_CLK), .n_shift_in(not_1_out), .RES(RES), .shift_out(bit_5_shift_out), .val_out(n_PR));  // open: n_shift_out
  Vid_SR_Bit bit_4 (
    .CLK(CLK), .n_CLK(n_CLK), .n_shift_in(nor_2_out), .RES(RES), .n_shift_out(bit_4_n_shift_out),
    .val_out(bit_4_val_out));  // open: shift_out
  Vid_SR_Bit bit_3 (
    .CLK(CLK), .n_CLK(n_CLK), .n_shift_in(bit_4_n_shift_out), .RES(RES), .n_shift_out(bit_3_n_shift_out),
    .val_out(n_PB));  // open: shift_out
  Vid_SR_Bit bit_2 (
    .CLK(CLK), .n_CLK(n_CLK), .n_shift_in(bit_3_n_shift_out), .RES(RES), .n_shift_out(bit_2_n_shift_out),
    .val_out(bit_2_val_out));  // open: shift_out
  Vid_SR_Bit bit_1 (
    .CLK(CLK), .n_CLK(n_CLK), .n_shift_in(bit_2_n_shift_out), .RES(RES), .n_shift_out(bit_1_n_shift_out),
    .val_out(n_PG));  // open: shift_out
  Vid_SR_Bit bit_0 (
    .CLK(CLK), .n_CLK(n_CLK), .n_shift_in(bit_1_n_shift_out), .RES(RES), .n_shift_out(bit_0_n_shift_out),
    .val_out(bit_0_val_out));  // open: shift_out
  and and_1 (and_1_out, P[0], ~n_PR);  // AND_Gate
  and and_2 (and_2_out, P[1], ~nor_2_out);  // AND_Gate
  and and_3 (and_3_out, P[2], ~bit_4_val_out);  // AND_Gate
  and and_4 (and_4_out, P[3], ~bit_4_n_shift_out);  // AND_Gate
  and and_5 (and_5_out, P[5], ~n_PB);  // AND_Gate
  and and_6 (and_6_out, P[6], ~bit_3_n_shift_out);  // AND_Gate
  and and_7 (and_7_out, P[7], ~bit_2_val_out);  // AND_Gate
  and and_8 (and_8_out, P[8], ~bit_2_n_shift_out);  // AND_Gate
  and and_9 (and_9_out, P[9], ~n_PG);  // AND_Gate
  and and_10 (and_10_out, P[10], ~bit_1_n_shift_out);  // AND_Gate
  and and_11 (and_11_out, P[11], ~bit_0_val_out);  // AND_Gate
  and and_12 (and_12_out, P[12], ~bit_0_n_shift_out);  // AND_Gate
  nor nor_3 (n_PZ, and_1_out, and_2_out, and_3_out, and_4_out, and_5_out, and_6_out, and_7_out, and_8_out, and_9_out, and_10_out, and_11_out, and_12_out, P[4]);

  // Notes on the sheet:
  //   PZ0
  //   PZ2
  //   PZ3
  //   PZ1
  //   PZ6
  //   PZ7
  //   PZ8
  //   PZ10
  //   PZ11
  //   PZ12
  //   PZ5
  //   PZ9
  //   Except P4
endmodule

module ChromaDecoder (
  input  PCLK,
  input  n_PCLK,
  input  BURST,
  input  n_CC0,
  input  n_CC1,
  input  n_CC2,
  input  n_CC3,
  output PBLACK,
  output [12:0] P
);

  wire burst_latch_valout, cc0_latch1_n_valout, cc1_latch1_n_valout, cc2_latch1_n_valout,
       cc3_latch1_n_valout, cc3_latch2_valout, demultiplexer_1_out0, demultiplexer_1_out1,
       demultiplexer_1_out2;
  wire [3:0] cc0_latch2_n_valout;

  DLatch cc0_latch1 (.Enable(PCLK), .Value(n_CC0), .n_ValOut(cc0_latch1_n_valout));  // open: ValOut
  DLatch cc1_latch1 (.Enable(PCLK), .Value(n_CC1), .n_ValOut(cc1_latch1_n_valout));  // open: ValOut
  DLatch cc2_latch1 (.Enable(PCLK), .Value(n_CC2), .n_ValOut(cc2_latch1_n_valout));  // open: ValOut
  DLatch cc3_latch1 (.Enable(PCLK), .Value(n_CC3), .n_ValOut(cc3_latch1_n_valout));  // open: ValOut
  DLatch cc0_latch2 (.Enable(n_PCLK), .Value(cc0_latch1_n_valout), .n_ValOut(cc0_latch2_n_valout[0]));  // open: ValOut
  DLatch cc1_latch2 (.Enable(n_PCLK), .Value(cc1_latch1_n_valout), .n_ValOut(cc0_latch2_n_valout[1]));  // open: ValOut
  DLatch cc2_latch2 (.Enable(n_PCLK), .Value(cc2_latch1_n_valout), .n_ValOut(cc0_latch2_n_valout[2]));  // open: ValOut
  DLatch cc3_latch2 (.Enable(n_PCLK), .Value(cc3_latch1_n_valout), .ValOut(cc3_latch2_valout));  // open: n_ValOut
  DLatch burst_latch (.Enable(n_PCLK), .Value(BURST), .ValOut(burst_latch_valout));  // open: n_ValOut
  nor nor_1 (cc0_latch2_n_valout[3], cc3_latch2_valout, burst_latch_valout);
  nor nor_2 (PBLACK, cc0_latch2_n_valout[1], cc0_latch2_n_valout[2], cc0_latch2_n_valout[3]);
  // NoConnect on demultiplexer_1_out0
  // NoConnect on demultiplexer_1_out1
  // NoConnect on demultiplexer_1_out2
  Demultiplexer #(.select(4)) demultiplexer_1 (
    .out0(demultiplexer_1_out0), .out1(demultiplexer_1_out1), .out2(demultiplexer_1_out2), .out3(P[0]),
    .out4(P[8]), .out5(P[2]), .out6(P[10]), .out7(P[5]), .out8(P[12]), .out9(P[7]), .out10(P[1]),
    .out11(P[9]), .out12(P[3]), .out13(P[11]), .out14(P[6]), .out15(P[4]), .in(1'b1),
    .sel(cc0_latch2_n_valout));
endmodule

module LumaDecoder (
  input  n_LL0,
  input  n_LL1,
  input  n_POUT,
  output [3:0] n_LU
);

  wire nor_1_out, nor_2_out, nor_3_out, nor_4_out, not_1_out, not_2_out;

  not not_1 (not_1_out, n_LL0);
  not not_2 (not_2_out, n_LL1);
  nor nor_1 (nor_1_out, n_LL0, n_LL1, n_POUT);
  nor nor_2 (nor_2_out, not_1_out, n_LL1, n_POUT);
  nor nor_3 (nor_3_out, n_LL0, not_2_out, n_POUT);
  nor nor_4 (nor_4_out, not_1_out, not_2_out, n_POUT);
  not not_3 (n_LU[3], nor_1_out);
  not not_4 (n_LU[2], nor_2_out);
  not not_5 (n_LU[1], nor_3_out);
  not not_6 (n_LU[0], nor_4_out);
endmodule

module Emphasis (
  input  n_POUT,
  input  n_PR,
  input  n_PG,
  input  n_PB,
  input  n_TR,
  input  n_TG,
  input  n_TB,
  output TINT
);

  wire nor_1_out, nor_2_out, nor_3_out, nor_4_out;

  nor nor_1 (nor_1_out, n_POUT, n_PR, n_TR);
  nor nor_2 (nor_2_out, n_POUT, n_PG, n_TG);
  nor nor_3 (nor_3_out, n_POUT, n_PB, n_TB);
  nor nor_4 (nor_4_out, nor_1_out, nor_2_out, nor_3_out);
  not not_1 (TINT, nor_4_out);
endmodule

module Video_DAC (
  input  n_PCLK,
  input  SYNC,
  input  PBLACK,
  input  n_PICTURE,
  input  BURST,
  input  TINT,
  input  [3:0] n_LU,
  input  n_PZ,
  output [10:0] VidOut,
  output n_POUT
);

  wire black_latch_n_valout, cb_latch_n_valout, nor_1_out, nor_2_out, nor_8_out, nor_9_out, nor_12_out,
       not_1_out, not_2_out;

  nor nor_1 (nor_1_out, nor_2_out, SYNC, BURST);
  DLatch sync_latch (.Enable(n_PCLK), .Value(not_1_out), .n_ValOut(VidOut[0]));  // open: ValOut
  not not_1 (not_1_out, SYNC);
  DLatch pic_out_latch (.Enable(n_PCLK), .Value(nor_2_out), .n_ValOut(n_POUT));  // open: ValOut
  nor nor_2 (nor_2_out, PBLACK, n_PICTURE);
  DLatch black_latch (.Enable(n_PCLK), .Value(not_2_out), .n_ValOut(black_latch_n_valout));  // open: ValOut
  not not_2 (not_2_out, nor_1_out);
  DLatch cb_latch (.Enable(n_PCLK), .Value(BURST), .n_ValOut(cb_latch_n_valout));  // open: ValOut
  nor nor_3 (VidOut[4], cb_latch_n_valout, n_PZ);
  nor nor_4 (VidOut[1], VidOut[4], cb_latch_n_valout);
  nor nor_5 (VidOut[2], n_LU[0], VidOut[6]);
  nor nor_6 (VidOut[6], n_LU[0], n_PZ);
  nor nor_7 (VidOut[8], n_LU[3], nor_8_out);
  nor nor_8 (nor_8_out, n_LU[3], n_PZ);
  nor nor_9 (nor_9_out, n_LU[1], VidOut[7]);
  nor nor_10 (VidOut[7], n_LU[1], n_PZ);
  nor nor_11 (VidOut[5], n_LU[2], nor_12_out);
  nor nor_12 (nor_12_out, n_LU[2], n_PZ);
  or or_1 (VidOut[3], black_latch_n_valout, nor_9_out);
  or or_2 (VidOut[9], nor_8_out, nor_12_out);

  assign VidOut[10] = TINT;

  // Notes on the sheet:
  //   Instead of OR actually a direct connection of wires
  //   L0 is the closest to GND. L10 is closest to Vdd.
endmodule

module VideoGen (
  input  CLK,
  input  n_CLK,
  input  PCLK,
  input  n_PCLK,
  input  RES,
  input  [3:0] n_CC,
  input  n_TR,
  input  [1:0] n_LL,
  input  n_TG,
  input  n_TB,
  input  BURST,
  input  SYNC,
  input  n_PICTURE,
  output [10:0] VOUT
);

  wire chromadecoder_1_pblack, emphasis_1_tint, phaseshifter_1_n_pb, phaseshifter_1_n_pg,
       phaseshifter_1_n_pr, phaseshifter_1_n_pz, video_dac_1_n_pout;
  wire [3:0] lumadecoder_1_n_lu;
  wire [12:0] chromadecoder_1_p;

  ChromaDecoder chromadecoder_1 (
    .PCLK(PCLK), .n_PCLK(n_PCLK), .BURST(BURST), .n_CC0(n_CC[0]), .n_CC1(n_CC[1]), .n_CC2(n_CC[2]),
    .n_CC3(n_CC[3]), .PBLACK(chromadecoder_1_pblack), .P(chromadecoder_1_p));
  LumaDecoder lumadecoder_1 (.n_LL0(n_LL[0]), .n_LL1(n_LL[1]), .n_POUT(video_dac_1_n_pout), .n_LU(lumadecoder_1_n_lu));
  PhaseShifter phaseshifter_1 (
    .CLK(CLK), .n_CLK(n_CLK), .RES(RES), .P(chromadecoder_1_p), .n_PR(phaseshifter_1_n_pr),
    .n_PG(phaseshifter_1_n_pg), .n_PB(phaseshifter_1_n_pb), .n_PZ(phaseshifter_1_n_pz));
  Emphasis emphasis_1 (
    .n_POUT(video_dac_1_n_pout), .n_PR(phaseshifter_1_n_pr), .n_PG(phaseshifter_1_n_pg),
    .n_PB(phaseshifter_1_n_pb), .n_TR(n_TR), .n_TG(n_TG), .n_TB(n_TB), .TINT(emphasis_1_tint));
  Video_DAC video_dac_1 (
    .n_PCLK(n_PCLK), .SYNC(SYNC), .PBLACK(chromadecoder_1_pblack), .n_PICTURE(n_PICTURE), .BURST(BURST),
    .TINT(emphasis_1_tint), .n_LU(lumadecoder_1_n_lu), .n_PZ(phaseshifter_1_n_pz), .VidOut(VOUT),
    .n_POUT(video_dac_1_n_pout));

  // Notes on the sheet:
  //   "Pixel" Chroma/Luma
  //   Signal Features
  //   Emphasis Ctrl
endmodule

module PICTURE_PAL (
  input  PCLK,
  input  n_PCLK,
  input  n_PICTURE_In,
  output n_PICTURE
);

  wire not_1_out, npicture_latch1_n_valout;

  DLatch npicture_latch1 (.Enable(n_PCLK), .Value(not_1_out), .n_ValOut(npicture_latch1_n_valout));  // open: ValOut
  not not_1 (not_1_out, n_PICTURE_In);
  DLatch npicture_latch2 (.Enable(PCLK), .Value(npicture_latch1_n_valout), .ValOut(n_PICTURE));  // open: n_ValOut

  // Notes on the sheet:
  //   From FSM
  //   To VideoGen
endmodule

module DLatch_x4 (
  input  enable,
  input  [3:0] val,
  output [3:0] val_out,
  output [3:0] n_val_out
);

  DLatch dlatch_1 (.Enable(enable), .Value(val[0]), .ValOut(val_out[0]), .n_ValOut(n_val_out[0]));
  DLatch dlatch_2 (.Enable(enable), .Value(val[1]), .ValOut(val_out[1]), .n_ValOut(n_val_out[1]));
  DLatch dlatch_3 (.Enable(enable), .Value(val[2]), .ValOut(val_out[2]), .n_ValOut(n_val_out[2]));
  DLatch dlatch_4 (.Enable(enable), .Value(val[3]), .ValOut(val_out[3]), .n_ValOut(n_val_out[3]));
endmodule

module MUX_All (
  input  PCLK,
  input  n_PCLK,
  input  n_ZPRIO,
  input  [3:0] BGC,
  input  n_ZCOL0,
  input  n_ZCOL1,
  input  ZCOL2,
  input  ZCOL3,
  input  [3:0] EXT_In,
  input  [4:0] THO,
  input  TH_MUX,
  output [4:0] CGA,
  output [3:0] n_EXT_Out
);

  wire multiplexer_4_out, mux_control_1_ext, mux_control_1_n_pal4, mux_control_1_ocol, tho4_latch_n_valout;
  wire [3:0] dir_color_latch_n_val_out, multiplexer_1_out, multiplexer_2_out, multiplexer_3_out,
       step1_latch_n_val_out, step2_latch_n_val_out, step3_latch_n_val_out;
  wire [3:2] not_1_out;

  not not_1 (not_1_out[2], ZCOL2);
  not not_2 (not_1_out[3], ZCOL3);
  DLatch tho4_latch (.Enable(PCLK), .Value(THO[4]), .n_ValOut(tho4_latch_n_valout));  // open: ValOut
  DLatch_x4 step1_latch (
    .enable(PCLK), .val({not_1_out, n_ZCOL1, n_ZCOL0}), .n_val_out(step1_latch_n_val_out));  // open: val_out
  DLatch_x4 dir_color_latch (.enable(PCLK), .val(THO[3:0]), .n_val_out(dir_color_latch_n_val_out));  // open: val_out
  MUX_Control mux_control_1 (
    .PCLK(PCLK), .n_PCLK(n_PCLK), .n_ZPRIO(n_ZPRIO), .BGC(BGC), .OBJC(step1_latch_n_val_out),
    .n_PAL4(mux_control_1_n_pal4), .OCOL(mux_control_1_ocol), .EXT(mux_control_1_ext));
  Multiplexer #(.width(4)) multiplexer_1 (
    .in0(BGC), .in1(step1_latch_n_val_out), .out(multiplexer_1_out), .sel(mux_control_1_ocol));
  assign n_EXT_Out = ~multiplexer_1_out;  // NOT_Gate not_3, 4 bits wide
  DLatch_x4 step2_latch (.enable(n_PCLK), .val(n_EXT_Out), .n_val_out(step2_latch_n_val_out));  // open: val_out
  Multiplexer #(.width(4)) multiplexer_2 (
    .in0(step2_latch_n_val_out), .in1(EXT_In), .out(multiplexer_2_out), .sel(mux_control_1_ext));
  DLatch_x4 step3_latch (.enable(PCLK), .val(multiplexer_2_out), .n_val_out(step3_latch_n_val_out));  // open: val_out
  Multiplexer #(.width(4)) multiplexer_3 (
    .in0(step3_latch_n_val_out), .in1(dir_color_latch_n_val_out), .out(multiplexer_3_out), .sel(TH_MUX));
  DLatch pal4_latch (.Enable(PCLK), .Value(multiplexer_4_out), .n_ValOut(CGA[4]));  // open: ValOut
  Multiplexer multiplexer_4 (
    .in0(mux_control_1_n_pal4), .in1(tho4_latch_n_valout), .out(multiplexer_4_out), .sel(TH_MUX));
  assign CGA[3:0] = ~multiplexer_3_out;  // NOT_Gate not_4, 4 bits wide
endmodule

module MUX_Control (
  input  PCLK,
  input  n_PCLK,
  input  n_ZPRIO,
  input  [3:0] BGC,
  input  [3:0] OBJC,
  output n_PAL4,
  output OCOL,
  output EXT
);

  wire bgc_latch_valout, nand_1_out, nor_1_out, nor_2_out, not_1_out, not_2_out, not_3_out, not_4_out,
       zcol_latch2_valout, zprio_latch_n_valout;

  nor nor_1 (nor_1_out, BGC[0], BGC[1]);
  nor nor_2 (nor_2_out, OBJC[0], OBJC[1]);
  not not_1 (not_1_out, nor_1_out);
  DLatch zprio_latch (.Enable(PCLK), .Value(not_2_out), .n_ValOut(zprio_latch_n_valout));  // open: ValOut
  not not_2 (not_2_out, n_ZPRIO);
  nand nand_1 (nand_1_out, not_1_out, zprio_latch_n_valout);
  not not_3 (not_3_out, nor_2_out);
  and and_1 (OCOL, nand_1_out, not_3_out);
  DLatch bgc_latch (.Enable(n_PCLK), .Value(not_1_out), .ValOut(bgc_latch_valout));  // open: n_ValOut
  DLatch zcol_latch2 (.Enable(n_PCLK), .Value(not_4_out), .ValOut(zcol_latch2_valout));  // open: n_ValOut
  not not_4 (not_4_out, nor_2_out);
  nor nor_3 (EXT, bgc_latch_valout, zcol_latch2_valout);
  DLatch ocol_latch (.Enable(n_PCLK), .Value(OCOL), .n_ValOut(n_PAL4));  // open: ValOut

  // Notes on the sheet:
  //   OCOL
  //   EXT
endmodule

module SPR0_Hit (
  input  PCLK,
  input  [3:0] BGC,
  input  n_SPR0HIT,
  input  n_SPR0_EV,
  input  n_VIS,
  input  n_R2,
  input  n_DBE,
  input  RESCL,
  output DB6
);

  wire nor_1_out, nor_2_out, nor_3_out, nor_4_out, nor_5_out, not_1_out, not_2_out;

  nor nor_1 (nor_1_out, n_R2, n_DBE);
  nor nor_2 (nor_2_out, BGC[0], BGC[1]);
  not not_1 (not_1_out, nor_1_out);
  nor nor_3 (nor_3_out, PCLK, nor_2_out, n_SPR0HIT, n_SPR0_EV, n_VIS);
  nor nor_4 (nor_4_out, RESCL, nor_5_out);
  nor nor_5 (nor_5_out, nor_4_out, nor_3_out);
  not not_2 (not_2_out, not_1_out);
  assign DB6 = not_2_out ? nor_4_out : 1'bz;  // Controlled_Buffer controlled_buffer_1

  // Notes on the sheet:
  //   STRIKE
  //   R
  //   S
  //   STRIKE_FF
endmodule

module Eval_CounterBit (
  input  Clock,
  input  Load,
  input  Step,
  input  BlockCount,
  input  Reset,
  input  val_in,
  input  carry_in,
  output val_out,
  output n_val_out,
  output carry_out
);

  wire cnt_latch_valout, controlled_buffer_1_out, multiplexer_1_out, nor_1_out, nor_3_out, not_1_out;

  Multiplexer multiplexer_1 (.in0(n_val_out), .in1(nor_1_out), .out(multiplexer_1_out), .sel(carry_in));
  nor nor_1 (nor_1_out, Reset, n_val_out);
  nor nor_2 (carry_out, n_val_out, not_1_out);
  not not_1 (not_1_out, carry_in);
  DLatch cnt_latch (.Enable(Clock), .Value(multiplexer_1_out), .ValOut(cnt_latch_valout));  // open: n_ValOut
  nor nor_3 (nor_3_out, cnt_latch_valout, BlockCount);
  assign controlled_buffer_1_out = Step ? nor_3_out : 1'bz;  // Controlled_Buffer controlled_buffer_1
  assign controlled_buffer_1_out = Load ? val_in : 1'bz;  // Controlled_Buffer controlled_buffer_2
  assign controlled_buffer_1_out = Clock ? nor_1_out : 1'bz;  // Controlled_Buffer controlled_buffer_3
  D_Flip_Flop #(.trigger("high")) keep_ff (
    .D(controlled_buffer_1_out), .clk(1'b1), .Qn(n_val_out));  // open: Q, preset, reset
  not not_2 (val_out, n_val_out);

  // Notes on the sheet:
  //   BlockCount can be used for the +4 counting mode.
  //   But in this case the carry circuity must be outside for the most significant bits.
  //   The value is actually stored on the FET gate (which acts as an inverter).
endmodule

module Eval_CounterTest (
  input  Load,
  input  Step,
  input  Reset,
  input  BlockCount,
  input  [1:0] val_in,
  output [1:0] val_out
);

  wire bit0_carry_out, CLK_out;

  Clock CLK (.out(CLK_out));
  Eval_CounterBit bit0 (
    .Clock(CLK_out), .Load(Load), .Step(Step), .BlockCount(1'b0), .Reset(Reset), .val_in(val_in[0]),
    .carry_in(1'b1), .val_out(val_out[0]), .carry_out(bit0_carry_out));  // open: n_val_out
  Eval_CounterBit bit1 (
    .Clock(CLK_out), .Load(Load), .Step(Step), .BlockCount(BlockCount), .Reset(Reset), .val_in(val_in[1]),
    .carry_in(bit0_carry_out), .val_out(val_out[1]));  // open: n_val_out, carry_out
endmodule

module Eval_MainCounter (
  input  BLNK,
  input  OMFG,
  input  OMOUT,
  input  OMSTEP,
  input  OBJ_READ,
  input  W3_Enable,
  input  [7:0] DB_In,
  output [7:0] OAM_x,
  output OMV
);

  wire and_1_out, bit0_carry_out, bit1_carry_out, bit2_carry_out, bit3_carry_out, bit4_carry_out,
       bit5_carry_out, bit6_carry_out, Mode4, n_out0, n_out1, n_out2, n_out3, n_out4, n_out5, n_out6, n_out7,
       nand_1_out, nor_1_out, nor_3_out, nor_4_out, nor_5_out, nor_6_out, nor_7_out, not_1_out, not_2_out,
       not_3_out;

  not not_1 (not_1_out, Mode4);
  nor nor_1 (nor_1_out, n_out0, n_out1);
  not not_2 (not_2_out, nor_1_out);
  nor nor_2 (Mode4, BLNK, not_3_out);
  not not_3 (not_3_out, OMFG);
  nand nand_1 (nand_1_out, not_1_out, not_2_out);
  and and_1 (and_1_out, not_2_out, not_1_out);
  nor nor_3 (nor_3_out, and_1_out, n_out2);
  Eval_CounterBit bit0 (
    .Clock(OMOUT), .Load(W3_Enable), .Step(OMSTEP), .BlockCount(Mode4), .Reset(OBJ_READ), .val_in(DB_In[0]),
    .carry_in(1'b1), .val_out(OAM_x[0]), .n_val_out(n_out0), .carry_out(bit0_carry_out));
  Eval_CounterBit bit1 (
    .Clock(OMOUT), .Load(W3_Enable), .Step(OMSTEP), .BlockCount(Mode4), .Reset(OBJ_READ), .val_in(DB_In[1]),
    .carry_in(bit0_carry_out), .val_out(OAM_x[1]), .n_val_out(n_out1), .carry_out(bit1_carry_out));
  Eval_CounterBit bit2 (
    .Clock(OMOUT), .Load(W3_Enable), .Step(OMSTEP), .BlockCount(1'b0), .Reset(OBJ_READ), .val_in(DB_In[2]),
    .carry_in(nand_1_out), .val_out(OAM_x[2]), .n_val_out(n_out2), .carry_out(bit2_carry_out));
  Eval_CounterBit bit3 (
    .Clock(OMOUT), .Load(W3_Enable), .Step(OMSTEP), .BlockCount(1'b0), .Reset(OBJ_READ), .val_in(DB_In[3]),
    .carry_in(nor_3_out), .val_out(OAM_x[3]), .n_val_out(n_out3), .carry_out(bit3_carry_out));
  // NoConnect on bit1_carry_out
  // NoConnect on bit2_carry_out
  // NoConnect on bit3_carry_out
  nor nor_4 (nor_4_out, and_1_out, n_out2, n_out3);
  nor nor_5 (nor_5_out, and_1_out, n_out2, n_out3, n_out4);
  nor nor_6 (nor_6_out, and_1_out, n_out2, n_out3, n_out4, n_out5);
  nor nor_7 (nor_7_out, and_1_out, n_out2, n_out3, n_out4, n_out5, n_out6);
  Eval_CounterBit bit4 (
    .Clock(OMOUT), .Load(W3_Enable), .Step(OMSTEP), .BlockCount(1'b0), .Reset(OBJ_READ), .val_in(DB_In[4]),
    .carry_in(nor_4_out), .val_out(OAM_x[4]), .n_val_out(n_out4), .carry_out(bit4_carry_out));
  // NoConnect on bit4_carry_out
  Eval_CounterBit bit5 (
    .Clock(OMOUT), .Load(W3_Enable), .Step(OMSTEP), .BlockCount(1'b0), .Reset(OBJ_READ), .val_in(DB_In[5]),
    .carry_in(nor_5_out), .val_out(OAM_x[5]), .n_val_out(n_out5), .carry_out(bit5_carry_out));
  // NoConnect on bit5_carry_out
  Eval_CounterBit bit6 (
    .Clock(OMOUT), .Load(W3_Enable), .Step(OMSTEP), .BlockCount(1'b0), .Reset(OBJ_READ), .val_in(DB_In[6]),
    .carry_in(nor_6_out), .val_out(OAM_x[6]), .n_val_out(n_out6), .carry_out(bit6_carry_out));
  // NoConnect on bit6_carry_out
  Eval_CounterBit bit7 (
    .Clock(OMOUT), .Load(W3_Enable), .Step(OMSTEP), .BlockCount(1'b0), .Reset(OBJ_READ), .val_in(DB_In[7]),
    .carry_in(nor_7_out), .val_out(OAM_x[7]), .n_val_out(n_out7), .carry_out(OMV));

  // Other names for the same wires on the sheet: Clock = OMOUT; in_0 = DB_In[0]; in_1 = DB_In[1]; in_2 = DB_In[2];
  //   in_3 = DB_In[3]; in_4 = DB_In[4]; in_5 = DB_In[5]; in_6 = DB_In[6]; in_7 = DB_In[7]; Load = W3_Enable;
  //   OAM_0 = OAM_x[0]; OAM_1 = OAM_x[1]; OAM_2 = OAM_x[2]; OAM_3 = OAM_x[3]; OAM_4 = OAM_x[4]; OAM_5 = OAM_x[5];
  //   OAM_6 = OAM_x[6]; OAM_7 = OAM_x[7]; Reset = OBJ_READ; Step = OMSTEP

  // Notes on the sheet:
  //   Mode4 = 0: Count +1
  //   Mode4 = 1: Count +4
  //   External carry chain
endmodule

module Eval_TempCounter (
  input  n_PCLK,
  input  OSTEP,
  input  ORES,
  output [4:0] OAMTemp,
  output TMV
);

  wire bit0_carry_out, bit1_carry_out, bit2_carry_out, bit3_carry_out;

  Eval_CounterBit bit0 (
    .Clock(n_PCLK), .Load(ORES), .Step(OSTEP), .BlockCount(1'b0), .Reset(1'b0), .val_in(1'b0),
    .carry_in(1'b1), .val_out(OAMTemp[0]), .carry_out(bit0_carry_out));  // open: n_val_out
  Eval_CounterBit bit1 (
    .Clock(n_PCLK), .Load(ORES), .Step(OSTEP), .BlockCount(1'b0), .Reset(1'b0), .val_in(1'b0),
    .carry_in(bit0_carry_out), .val_out(OAMTemp[1]), .carry_out(bit1_carry_out));  // open: n_val_out
  Eval_CounterBit bit2 (
    .Clock(n_PCLK), .Load(ORES), .Step(OSTEP), .BlockCount(1'b0), .Reset(1'b0), .val_in(1'b0),
    .carry_in(bit1_carry_out), .val_out(OAMTemp[2]), .carry_out(bit2_carry_out));  // open: n_val_out
  Eval_CounterBit bit3 (
    .Clock(n_PCLK), .Load(ORES), .Step(OSTEP), .BlockCount(1'b0), .Reset(1'b0), .val_in(1'b0),
    .carry_in(bit2_carry_out), .val_out(OAMTemp[3]), .carry_out(bit3_carry_out));  // open: n_val_out
  Eval_CounterBit bit4 (
    .Clock(n_PCLK), .Load(ORES), .Step(OSTEP), .BlockCount(1'b0), .Reset(1'b0), .val_in(1'b0),
    .carry_in(bit3_carry_out), .val_out(OAMTemp[4]), .carry_out(TMV));  // open: n_val_out

  // Other names for the same wires on the sheet: Clock = n_PCLK; Load = ORES; Step = OSTEP
endmodule

module Eval_CountersControl (
  input  n_PCLK,
  input  OMFG,
  input  I_OAM2,
  input  n_VIS,
  input  OBJ_READ,
  input  n_EVAL,
  input  RESCL,
  input  H0_DD,
  input  H0_D,
  input  n_H2_D,
  input  OFETCH,
  input  OMV,
  input  TMV,
  input  n_W3,
  input  n_DBE,
  output OMSTEP,
  output OMOUT,
  output OSTEP,
  output ORES,
  output OAMCTR2,
  output SPR_OV,
  output SPR_OV_Reg,
  output W3_Enable
);

  wire and_1_out, and_2_out, and_3_out, eval_latch_valout, init_latch_valout, ioam2_latch_valout,
       latch1_valout, nand_1_out, nand_3_out, nomfg_latch_valout, nor_2_out, nor_3_out, nor_5_out, nor_7_out,
       nor_8_out, nor_9_out, nor_10_out, nor_11_out, nor_15_out, not_1_out, not_2_out, ofetch_latch_n_valout,
       omfg_latch_valout, omv_latch_valout, or_1_out, setov_latch_valout, tmv_latch_valout;

  nor nor_1 (W3_Enable, n_W3, n_DBE);
  nor nor_2 (nor_2_out, I_OAM2, n_VIS);
  DLatch ofetch_latch (.Enable(n_PCLK), .Value(OFETCH), .n_ValOut(ofetch_latch_n_valout));  // open: ValOut
  DLatch eval_latch (.Enable(n_PCLK), .Value(n_EVAL), .ValOut(eval_latch_valout));  // open: n_ValOut
  DLatch tmv_latch (.Enable(n_PCLK), .Value(TMV), .ValOut(tmv_latch_valout));  // open: n_ValOut
  not not_1 (not_1_out, OMFG);
  nand nand_1 (nand_1_out, nor_2_out, H0_DD);
  nor nor_3 (nor_3_out, ofetch_latch_n_valout, n_PCLK);
  and and_1 (and_1_out, tmv_latch_valout, OSTEP);
  DLatch nomfg_latch (.Enable(n_PCLK), .Value(not_1_out), .ValOut(nomfg_latch_valout));  // open: n_ValOut
  DLatch ioam2_latch (.Enable(n_PCLK), .Value(I_OAM2), .ValOut(ioam2_latch_valout));  // open: n_ValOut
  DLatch omfg_latch (.Enable(n_PCLK), .Value(OMFG), .ValOut(omfg_latch_valout));  // open: n_ValOut
  DLatch setov_latch (.Enable(n_PCLK), .Value(nor_7_out), .ValOut(setov_latch_valout));  // open: n_ValOut
  DLatch init_latch (.Enable(n_PCLK), .Value(nand_1_out), .ValOut(init_latch_valout));  // open: n_ValOut
  not not_2 (not_2_out, nor_3_out);
  DLatch omv_latch (.Enable(n_PCLK), .Value(OMV), .ValOut(omv_latch_valout));  // open: n_ValOut
  nor nor_4 (ORES, n_PCLK, eval_latch_valout);
  nor nor_5 (nor_5_out, nomfg_latch_valout, ioam2_latch_valout);
  or or_1 (or_1_out, init_latch_valout, n_PCLK);
  nor nor_6 (OAMCTR2, ORES, nor_7_out);
  nor nor_7 (nor_7_out, OAMCTR2, and_1_out);
  nor nor_8 (nor_8_out, omfg_latch_valout, setov_latch_valout, H0_D, n_PCLK);
  nand nand_2 (OMSTEP, or_1_out, not_2_out);
  and and_2 (and_2_out, OMSTEP, omv_latch_valout);
  DLatch latch1 (.Enable(n_PCLK), .Value(nand_3_out), .ValOut(latch1_valout));  // open: n_ValOut
  nand nand_3 (nand_3_out, nor_7_out, n_EVAL);
  nor nor_9 (nor_9_out, nor_5_out, H0_D);
  nor nor_10 (nor_10_out, nor_9_out, and_3_out);
  and and_3 (and_3_out, n_H2_D, OBJ_READ);
  nor nor_11 (nor_11_out, nor_8_out, SPR_OV_Reg);
  nor nor_12 (SPR_OV_Reg, nor_11_out, RESCL);
  nor nor_13 (OMOUT, OMSTEP, W3_Enable);
  nor nor_14 (OSTEP, latch1_valout, n_PCLK, nor_10_out);
  nor nor_15 (nor_15_out, and_2_out, nor_8_out, SPR_OV);
  nor nor_16 (SPR_OV, nor_15_out, I_OAM2);

  // Notes on the sheet:
  //   OAM2_CNT_FF
  //   Sprite Overflow
  //   SPR_OV_REG_FF
  //   Main Counter Control
  //   Temp Counter Control
  //   SPR_OV_FF
endmodule

module Eval_CmpBitPair (
  input  PCLK,
  input  OB_Even,
  input  V_Even,
  input  OB_Odd,
  input  V_Odd,
  input  carry_in,
  output OV_Even,
  output OV_Odd,
  output carry_out
);

  wire and_1_out, and_2_out, even_latch_n_valout, nand_1_out, nand_2_out, nor_1_out, nor_2_out, nor_3_out,
       nor_4_out, nor_6_out, nor_7_out, nor_8_out, nor_9_out, nor_10_out, nor_11_out, nor_12_out, nor_13_out,
       not_1_out, not_2_out, odd_latch_n_valout;

  DLatch even_latch (.Enable(PCLK), .Value(OB_Even), .n_ValOut(even_latch_n_valout));  // open: ValOut
  DLatch odd_latch (.Enable(PCLK), .Value(OB_Odd), .n_ValOut(odd_latch_n_valout));  // open: ValOut
  nand nand_1 (nand_1_out, even_latch_n_valout, V_Even);
  nor nor_1 (nor_1_out, even_latch_n_valout, V_Even);
  nand nand_2 (nand_2_out, odd_latch_n_valout, V_Odd);
  nor nor_2 (nor_2_out, V_Odd, odd_latch_n_valout);
  not not_1 (not_1_out, nand_2_out);
  not not_2 (not_2_out, nand_1_out);
  nor nor_3 (nor_3_out, carry_in, nor_1_out);
  nor nor_4 (nor_4_out, nand_1_out, nor_2_out);
  nor nor_5 (carry_out, nor_4_out, not_1_out, nor_6_out);
  nor nor_6 (nor_6_out, nor_1_out, nor_2_out, carry_in);
  nor nor_7 (nor_7_out, not_2_out, nor_1_out);
  nor nor_8 (nor_8_out, not_2_out, nor_3_out);
  nor nor_9 (nor_9_out, nor_2_out, not_1_out);
  nor nor_10 (nor_10_out, carry_in, nor_7_out);
  nor nor_11 (nor_11_out, nor_10_out, and_1_out);
  and and_1 (and_1_out, carry_in, nor_7_out);
  nor nor_12 (nor_12_out, nor_9_out, nor_8_out);
  nor nor_13 (nor_13_out, nor_12_out, and_2_out);
  and and_2 (and_2_out, nor_8_out, nor_9_out);
  not not_3 (OV_Even, nor_11_out);
  not not_4 (OV_Odd, nor_13_out);

  // Other names for the same wires on the sheet: cin = carry_in

  // Notes on the sheet:
  //   Between pairs of bits the carry chain is preserved in direct logic.
  //   Even and odd bits are combined into one circuit to compact the inverted carry chain.
endmodule

module Eval_Cmp (
  input  PCLK,
  input  [7:0] OB,
  input  [7:0] V,
  input  O8_16,
  input  COPY_OVF,
  output [7:0] OV,
  output OVZ
);

  wire and_1_out, bits01_carry_out, bits23_carry_out, bits45_carry_out, bits67_carry_out, dlatch_1_n_valout,
       nor_1_out, not_1_out;

  not not_1 (not_1_out, O8_16);
  DLatch dlatch_1 (.Enable(PCLK), .Value(OB[7]), .n_ValOut(dlatch_1_n_valout));  // open: ValOut
  Eval_CmpBitPair bits01 (
    .PCLK(PCLK), .OB_Even(OB[0]), .V_Even(V[0]), .OB_Odd(OB[1]), .V_Odd(V[1]), .carry_in(1'b0),
    .OV_Even(OV[0]), .OV_Odd(OV[1]), .carry_out(bits01_carry_out));
  Eval_CmpBitPair bits23 (
    .PCLK(PCLK), .OB_Even(OB[2]), .V_Even(V[2]), .OB_Odd(OB[3]), .V_Odd(V[3]), .carry_in(bits01_carry_out),
    .OV_Even(OV[2]), .OV_Odd(OV[3]), .carry_out(bits23_carry_out));
  Eval_CmpBitPair bits45 (
    .PCLK(PCLK), .OB_Even(OB[4]), .V_Even(V[4]), .OB_Odd(OB[5]), .V_Odd(V[5]), .carry_in(bits23_carry_out),
    .OV_Even(OV[4]), .OV_Odd(OV[5]), .carry_out(bits45_carry_out));
  Eval_CmpBitPair bits67 (
    .PCLK(PCLK), .OB_Even(OB[6]), .V_Even(V[6]), .OB_Odd(OB[7]), .V_Odd(V[7]), .carry_in(bits45_carry_out),
    .OV_Even(OV[6]), .OV_Odd(OV[7]), .carry_out(bits67_carry_out));
  // NoConnect on bits67_carry_out
  and and_1 (and_1_out, not_1_out, OV[3]);
  nor nor_1 (nor_1_out, dlatch_1_n_valout, V[7]);
  nor nor_2 (OVZ, OV[4], OV[5], OV[6], OV[7], and_1_out, nor_1_out, COPY_OVF);

  // Notes on the sheet:
  //   OV = V - OB
endmodule

module Eval_FSM (
  input  PCLK,
  input  n_F_NT,
  input  H0_DD,
  input  I_OAM2,
  input  n_VIS,
  input  SPR_OV,
  input  S_EV,
  input  OBJ_READ,
  input  OVZ,
  output PD_FIFO,
  output n_SPR0_EV,
  output COPY_OVF,
  output OMFG
);

  wire FF2_n_q, fnt_latch_valout, latch1_n_valout, latch2_n_valout, latch3_n_valout, latch4_n_valout,
       latch5_n_valout, latch6_n_valout, n_PCLK2, nor_1_out, nor_2_out, nor_3_out, nor_4_out, not_2_out,
       not_3_out, not_4_out, not_5_out, not_6_out, novz_latch_n_valout;

  not not_1 (n_PCLK2, PCLK);
  not not_2 (not_2_out, H0_DD);
  not not_3 (not_3_out, S_EV);
  not not_4 (not_4_out, OBJ_READ);
  not not_5 (not_5_out, OVZ);
  nor nor_1 (nor_1_out, I_OAM2, n_VIS, SPR_OV, not_5_out);
  nor nor_2 (nor_2_out, n_F_NT, not_2_out);
  not not_6 (not_6_out, nor_2_out);
  nor nor_3 (nor_3_out, PCLK, not_2_out);
  DLatch latch1 (.Enable(nor_3_out), .Value(nor_1_out), .n_ValOut(latch1_n_valout));  // open: ValOut
  PosedgeDFFE FF2 (.CLK(PCLK), .n_EN(not_3_out), .val_in(nor_1_out), .n_Q(FF2_n_q));  // open: Q
  DLatch fnt_latch (.Enable(n_PCLK2), .Value(not_6_out), .ValOut(fnt_latch_valout));  // open: n_ValOut
  DLatch novz_latch (.Enable(n_PCLK2), .Value(not_5_out), .n_ValOut(novz_latch_n_valout));  // open: ValOut
  DLatch latch2 (.Enable(PCLK), .Value(latch1_n_valout), .n_ValOut(latch2_n_valout));  // open: ValOut
  DLatch latch3 (.Enable(nor_3_out), .Value(latch2_n_valout), .n_ValOut(latch3_n_valout));  // open: ValOut
  DLatch latch4 (.Enable(PCLK), .Value(latch3_n_valout), .n_ValOut(latch4_n_valout));  // open: ValOut
  DLatch latch5 (.Enable(nor_3_out), .Value(latch4_n_valout), .n_ValOut(latch5_n_valout));  // open: ValOut
  PosedgeDFFE FF1 (.CLK(PCLK), .n_EN(not_4_out), .val_in(FF2_n_q), .Q(n_SPR0_EV));  // open: n_Q
  PosedgeDFFE FF3 (.CLK(n_PCLK2), .n_EN(fnt_latch_valout), .val_in(novz_latch_n_valout), .Q(PD_FIFO));  // open: n_Q
  DLatch latch6 (.Enable(PCLK), .Value(latch5_n_valout), .n_ValOut(latch6_n_valout));  // open: ValOut
  nor nor_4 (nor_4_out, latch6_n_valout, latch4_n_valout, latch2_n_valout);
  not not_7 (COPY_OVF, nor_4_out);
  nor nor_5 (OMFG, COPY_OVF, nor_1_out);

  // Notes on the sheet:
  //   DO_COPY
  //   COPY_STEP
endmodule

module Eval_OAM_Address (
  input  n_VIS,
  input  H0_DD,
  input  BLNK,
  input  [7:0] OAM_x,
  input  [4:0] OAMTemp,
  output [7:0] n_OAM_x,
  output OAM8
);

  wire nand_1_out, not_1_out, or_1_out;
  wire [4:0] multiplexer_1_out;

  or or_1 (or_1_out, n_VIS, H0_DD);
  not not_1 (not_1_out, BLNK);
  nand nand_1 (nand_1_out, or_1_out, not_1_out);
  not not_2 (OAM8, nand_1_out);
  Multiplexer #(.width(5)) multiplexer_1 (.in0(OAM_x[7:3]), .in1(OAMTemp), .out(multiplexer_1_out), .sel(OAM8));
  assign n_OAM_x = ~{multiplexer_1_out, OAM_x[2:0]};  // NOT_Gate not_3, 8 bits wide

  // Notes on the sheet:
  //   H0''
  //   OAP
  //   OAM8 = 1: Use Temp OAM
  //   OAM8 = 0: Use Main OAM
endmodule

module Eval_SprOV_Flag (
  input  n_R2,
  input  n_DBE,
  input  SPR_OV_Reg,
  output DB5
);

  wire nor_1_out, not_1_out, not_2_out;

  nor nor_1 (nor_1_out, n_R2, n_DBE);
  not not_1 (not_1_out, nor_1_out);
  not not_2 (not_2_out, not_1_out);
  assign DB5 = not_2_out ? SPR_OV_Reg : 1'bz;  // Controlled_Buffer controlled_buffer_1
endmodule

module Obj_Eval (
  input  PCLK,
  input  n_PCLK,
  input  n_R2,
  input  BLNK,
  input  I_OAM2,
  input  n_VIS,
  input  OBJ_READ,
  input  n_EVAL,
  input  RESCL,
  input  H0_DD,
  input  H0_D,
  input  n_H2_D,
  input  OFETCH,
  input  n_W3,
  input  n_DBE,
  input  [7:0] DB_In,
  input  [7:0] OB,
  input  [7:0] V,
  input  O8_16,
  input  n_F_NT,
  input  S_EV,
  output DB5,
  output [7:0] n_OAMx,
  output OAM8,
  output OAMCTR2,
  output SPR_OV,
  output [7:0] OV,
  output PD_FIFO,
  output n_SPR0_EV
);

  wire eval_cmp_1_ovz, eval_counterscontrol_1_omout, eval_counterscontrol_1_omstep,
       eval_counterscontrol_1_ores, eval_counterscontrol_1_ostep, eval_counterscontrol_1_spr_ov_reg,
       eval_counterscontrol_1_w3_enable, eval_fsm_1_copy_ovf, eval_fsm_1_omfg, eval_maincounter_1_omv,
       eval_tempcounter_1_tmv;
  wire [4:0] eval_tempcounter_1_oamtemp;
  wire [7:0] eval_maincounter_1_oam_x;

  Eval_CountersControl eval_counterscontrol_1 (
    .n_PCLK(n_PCLK), .OMFG(eval_fsm_1_omfg), .I_OAM2(I_OAM2), .n_VIS(n_VIS), .OBJ_READ(OBJ_READ),
    .n_EVAL(n_EVAL), .RESCL(RESCL), .H0_DD(H0_DD), .H0_D(H0_D), .n_H2_D(n_H2_D), .OFETCH(OFETCH),
    .OMV(eval_maincounter_1_omv), .TMV(eval_tempcounter_1_tmv), .n_W3(n_W3), .n_DBE(n_DBE),
    .OMSTEP(eval_counterscontrol_1_omstep), .OMOUT(eval_counterscontrol_1_omout),
    .OSTEP(eval_counterscontrol_1_ostep), .ORES(eval_counterscontrol_1_ores), .OAMCTR2(OAMCTR2),
    .SPR_OV(SPR_OV), .SPR_OV_Reg(eval_counterscontrol_1_spr_ov_reg),
    .W3_Enable(eval_counterscontrol_1_w3_enable));
  Eval_SprOV_Flag eval_sprov_flag_1 (
    .n_R2(n_R2), .n_DBE(n_DBE), .SPR_OV_Reg(eval_counterscontrol_1_spr_ov_reg), .DB5(DB5));
  Eval_MainCounter eval_maincounter_1 (
    .BLNK(BLNK), .OMFG(eval_fsm_1_omfg), .OMOUT(eval_counterscontrol_1_omout),
    .OMSTEP(eval_counterscontrol_1_omstep), .OBJ_READ(OBJ_READ),
    .W3_Enable(eval_counterscontrol_1_w3_enable), .DB_In(DB_In), .OAM_x(eval_maincounter_1_oam_x),
    .OMV(eval_maincounter_1_omv));
  Eval_TempCounter eval_tempcounter_1 (
    .n_PCLK(n_PCLK), .OSTEP(eval_counterscontrol_1_ostep), .ORES(eval_counterscontrol_1_ores),
    .OAMTemp(eval_tempcounter_1_oamtemp), .TMV(eval_tempcounter_1_tmv));
  Eval_Cmp eval_cmp_1 (
    .PCLK(PCLK), .OB(OB), .V(V), .O8_16(O8_16), .COPY_OVF(eval_fsm_1_copy_ovf), .OV(OV), .OVZ(eval_cmp_1_ovz));
  Eval_OAM_Address eval_oam_address_1 (
    .n_VIS(n_VIS), .H0_DD(H0_DD), .BLNK(BLNK), .OAM_x(eval_maincounter_1_oam_x),
    .OAMTemp(eval_tempcounter_1_oamtemp), .n_OAM_x(n_OAMx), .OAM8(OAM8));
  Eval_FSM eval_fsm_1 (
    .PCLK(PCLK), .n_F_NT(n_F_NT), .H0_DD(H0_DD), .I_OAM2(I_OAM2), .n_VIS(n_VIS), .SPR_OV(SPR_OV),
    .S_EV(S_EV), .OBJ_READ(OBJ_READ), .OVZ(eval_cmp_1_ovz), .PD_FIFO(PD_FIFO), .n_SPR0_EV(n_SPR0_EV),
    .COPY_OVF(eval_fsm_1_copy_ovf), .OMFG(eval_fsm_1_omfg));
endmodule

module PosedgeDFFE (
  input  CLK,
  input  n_EN,
  input  val_in,
  output Q,
  output n_Q
);

  wire nor_1_out;

  nor nor_1 (nor_1_out, CLK, n_EN);
  D_Flip_Flop d_ff_1 (.D(val_in), .clk(nor_1_out), .Q(Q), .Qn(n_Q));  // open: preset, reset
endmodule

module PosedgeDFFE_Real (
  input  CLK,
  input  n_EN,
  input  val_in,
  output Q,
  output n_Q
);

  wire controlled_buffer_1_out, multiplexer_1_out, nor_1_out;

  nor nor_1 (nor_1_out, CLK, n_EN);
  assign controlled_buffer_1_out = nor_1_out ? val_in : 1'bz;  // Controlled_Buffer controlled_buffer_1
  not not_1 (n_Q, multiplexer_1_out);
  Multiplexer multiplexer_1 (.in0(controlled_buffer_1_out), .in1(Q), .out(multiplexer_1_out), .sel(CLK));
  not not_2 (Q, n_Q);

  // Notes on the sheet:
  //   FF
endmodule

module OAM_All (
  input  PCLK,
  input  n_PCLK,
  input  [7:0] n_OAMx,
  input  OAM8,
  input  BLNK,
  input  SPR_OV,
  input  OAMCTR2,
  input  H0_DD,
  input  n_VIS,
  input  I_OAM2,
  input  n_W4,
  input  n_R4,
  input  n_DBE,
  input  [7:0] DB_In,
  output [7:0] OB_Out,
  output [7:0] DB_Out,
  output OFETCH
);

  wire nor_1_out, not_1_out, oam_addressdecoder_1_col0, oam_addressdecoder_1_col1, oam_addressdecoder_1_col2,
       oam_addressdecoder_1_col3, oam_addressdecoder_1_col4, oam_addressdecoder_1_col5,
       oam_addressdecoder_1_col6, oam_addressdecoder_1_col7, oam_addressdecoder_1_colz, oam_control_1_n_we,
       oam_control_1_ob_oam;
  wire [4:0] oam_addressdecoder_1_row;
  wire [7:0] oam_1_bl_out, oam_buffer_1_bl_out;

  nor nor_1 (nor_1_out, n_R4, n_DBE);
  not not_1 (not_1_out, nor_1_out);
  OAM_AddressDecoder oam_addressdecoder_1 (
    .n_OAMx(n_OAMx), .UseTempOAM(OAM8), .PCLK(PCLK), .COL0(oam_addressdecoder_1_col0),
    .COL1(oam_addressdecoder_1_col1), .COL2(oam_addressdecoder_1_col2), .COL3(oam_addressdecoder_1_col3),
    .COL4(oam_addressdecoder_1_col4), .COL5(oam_addressdecoder_1_col5), .COL6(oam_addressdecoder_1_col6),
    .COL7(oam_addressdecoder_1_col7), .COLZ(oam_addressdecoder_1_colz), .ROW(oam_addressdecoder_1_row));  // open: ROW_0_31
  OAM_Control oam_control_1 (
    .PCLK(PCLK), .n_PCLK(n_PCLK), .BLNK(BLNK), .SPR_OV(SPR_OV), .OAMCTR2(OAMCTR2), .H0_DD(H0_DD),
    .n_VIS(n_VIS), .n_W4(n_W4), .n_DBE(n_DBE), .OFETCH(OFETCH), .OB_OAM(oam_control_1_ob_oam),
    .n_WE(oam_control_1_n_we));
  OAM oam_1 (
    .ROW(oam_addressdecoder_1_row), .BL_in(oam_buffer_1_bl_out), .COL0(oam_addressdecoder_1_col0),
    .COL1(oam_addressdecoder_1_col1), .COL2(oam_addressdecoder_1_col2), .COL3(oam_addressdecoder_1_col3),
    .COL4(oam_addressdecoder_1_col4), .COL5(oam_addressdecoder_1_col5), .COL6(oam_addressdecoder_1_col6),
    .COL7(oam_addressdecoder_1_col7), .COLZ(oam_addressdecoder_1_colz), .BL_out(oam_1_bl_out));
  OAM_Buffer oam_buffer_1 (
    .PCLK(PCLK), .n_R4_Enable(not_1_out), .BLNK(BLNK), .OB_OAM(oam_control_1_ob_oam),
    .n_WE(oam_control_1_n_we), .I_OAM2(I_OAM2), .DB_In(DB_In), .BL_in(oam_1_bl_out), .OB_Out(OB_Out),
    .DB_Out(DB_Out), .BL_out(oam_buffer_1_bl_out));

  // Notes on the sheet:
  //   Located next to RW Decoder
endmodule

module OAM_AddressDecoder (
  input  [7:0] n_OAMx,
  input  UseTempOAM,
  input  PCLK,
  output COL0,
  output COL1,
  output COL2,
  output COL3,
  output COL4,
  output COL5,
  output COL6,
  output COL7,
  output COLZ,
  output [31:0] ROW_0_31,
  output [4:0] ROW
);

  wire not_1_out, not_2_out, not_3_out;
  wire [4:0] bit_extender_2_out;
  wire [31:0] bit_extender_1_out, demultiplexer_1_out31;

  Demultiplexer #(.select(5)) demultiplexer_1 (
    .out0(demultiplexer_1_out31[31]), .out1(demultiplexer_1_out31[30]), .out2(demultiplexer_1_out31[29]),
    .out3(demultiplexer_1_out31[28]), .out4(demultiplexer_1_out31[27]), .out5(demultiplexer_1_out31[26]),
    .out6(demultiplexer_1_out31[25]), .out7(demultiplexer_1_out31[24]), .out8(demultiplexer_1_out31[23]),
    .out9(demultiplexer_1_out31[22]), .out10(demultiplexer_1_out31[21]), .out11(demultiplexer_1_out31[20]),
    .out12(demultiplexer_1_out31[19]), .out13(demultiplexer_1_out31[18]), .out14(demultiplexer_1_out31[17]),
    .out15(demultiplexer_1_out31[16]), .out16(demultiplexer_1_out31[15]), .out17(demultiplexer_1_out31[14]),
    .out18(demultiplexer_1_out31[13]), .out19(demultiplexer_1_out31[12]), .out20(demultiplexer_1_out31[11]),
    .out21(demultiplexer_1_out31[10]), .out22(demultiplexer_1_out31[9]), .out23(demultiplexer_1_out31[8]),
    .out24(demultiplexer_1_out31[7]), .out25(demultiplexer_1_out31[6]), .out26(demultiplexer_1_out31[5]),
    .out27(demultiplexer_1_out31[4]), .out28(demultiplexer_1_out31[3]), .out29(demultiplexer_1_out31[2]),
    .out30(demultiplexer_1_out31[1]), .out31(demultiplexer_1_out31[0]), .in(1'b1), .sel(n_OAMx[7:3]));
  not not_1 (not_1_out, n_OAMx[0]);
  not not_2 (not_2_out, n_OAMx[1]);
  not not_3 (not_3_out, n_OAMx[2]);
  assign bit_extender_1_out = {{31{PCLK}}, PCLK};  // Bit_Extender bit_extender_1
  assign bit_extender_2_out = {{4{PCLK}}, PCLK};  // Bit_Extender bit_extender_2
  assign ROW_0_31 = demultiplexer_1_out31 & ~bit_extender_1_out;  // AND_Gate and_1, 32 bits wide
  assign ROW = n_OAMx[7:3] & ~bit_extender_2_out;  // AND_Gate and_2, 5 bits wide
  nor nor_1 (COL0, not_1_out, not_2_out, not_3_out, UseTempOAM);
  nor nor_2 (COL1, n_OAMx[0], not_2_out, not_3_out, UseTempOAM);
  nor nor_3 (COL2, not_1_out, n_OAMx[1], not_3_out, UseTempOAM);
  nor nor_4 (COL3, n_OAMx[0], n_OAMx[1], not_3_out, UseTempOAM);
  nor nor_5 (COL4, not_1_out, not_2_out, n_OAMx[2], UseTempOAM);
  nor nor_6 (COL5, n_OAMx[0], not_2_out, n_OAMx[2], UseTempOAM);
  nor nor_7 (COL6, not_1_out, n_OAMx[1], n_OAMx[2], UseTempOAM);
  nor nor_8 (COL7, n_OAMx[0], n_OAMx[1], n_OAMx[2], UseTempOAM);

  assign COLZ = UseTempOAM;

  // Notes on the sheet:
  //   During precharge all ROW outputs are 0.
  //   Unused for OB[2-4]
  //   Unused for OB[2-4]
endmodule

module OAM (
  input  [4:0] ROW,
  input  [7:0] BL_in,
  input  COL0,
  input  COL1,
  input  COL2,
  input  COL3,
  input  COL4,
  input  COL5,
  input  COL6,
  input  COL7,
  input  COLZ,
  output [7:0] BL_out
);

  wire [4:2] oam_lane_3_bl_out, oam_lane_7_bl_out;

  OAM_Lane oam_lane_1 (.ROW(ROW), .ColEnable(COL0), .BL_in(BL_in), .BL_out(BL_out));
  OAM_Lane oam_lane_2 (.ROW(ROW), .ColEnable(COL1), .BL_in(BL_in), .BL_out(BL_out));
  OAM_Lane oam_lane_3 (
    .ROW(ROW), .ColEnable(COL2), .BL_in(BL_in), .BL_out({BL_out[7:5], oam_lane_3_bl_out, BL_out[1:0]}));
  OAM_Lane oam_lane_4 (.ROW(ROW), .ColEnable(COL3), .BL_in(BL_in), .BL_out(BL_out));
  OAM_Lane oam_lane_5 (.ROW(ROW), .ColEnable(COL4), .BL_in(BL_in), .BL_out(BL_out));
  OAM_Lane oam_lane_6 (.ROW(ROW), .ColEnable(COL5), .BL_in(BL_in), .BL_out(BL_out));
  OAM_Lane oam_lane_7 (
    .ROW(ROW), .ColEnable(COL6), .BL_in(BL_in), .BL_out({BL_out[7:5], oam_lane_7_bl_out, BL_out[1:0]}));
  OAM_Lane oam_lane_8 (.ROW(ROW), .ColEnable(COL7), .BL_in(BL_in), .BL_out(BL_out));
  OAM_Lane oam_lane_9 (.ROW(ROW), .ColEnable(COLZ), .BL_in(BL_in), .BL_out(BL_out));
endmodule

module OAM_Lane (
  input  [4:0] ROW,
  input  ColEnable,
  input  [7:0] BL_in,
  output [7:0] BL_out
);

  wire [7:0] ram_1_dout, undriven;

  RAM #(.addrWidth(5), .trigger("high")) ram_1 (
    .addr(ROW), .we(ColEnable), .oe(ColEnable), .din(BL_in), .dout(ram_1_dout));
  // NoConnect on undriven
  Multiplexer #(.width(8)) multiplexer_1 (.in0(undriven), .in1(ram_1_dout), .out(BL_out), .sel(ColEnable));

  // Notes on the sheet:
  //   Select row (0-31)
  //   One lane corresponds to one COL.
  //   One lane is 32 cells (rows) x 8 bits for the OAM Buffer.
endmodule

module OAM_Control (
  input  PCLK,
  input  n_PCLK,
  input  BLNK,
  input  SPR_OV,
  input  OAMCTR2,
  input  H0_DD,
  input  n_VIS,
  input  n_W4,
  input  n_DBE,
  output OFETCH,
  output OB_OAM,
  output n_WE
);

  wire latch1_n_valout, latch2_n_valout, latch3_n_valout, latch4_valout, multiplexer_1_out, nor_1_out,
       nor_3_out, nor_4_out, nor_5_out, nor_6_out, not_1_out, not_2_out, not_3_out;

  nor nor_1 (nor_1_out, n_W4, n_DBE);
  nor nor_2 (OB_OAM, n_PCLK, BLNK);
  Multiplexer multiplexer_1 (.in0(not_2_out), .in1(nor_5_out), .out(multiplexer_1_out), .sel(PCLK));
  nor nor_3 (nor_3_out, nor_1_out, nor_4_out);
  nor nor_4 (nor_4_out, nor_3_out, latch3_n_valout);
  DLatch latch1 (.Enable(n_PCLK), .Value(not_1_out), .n_ValOut(latch1_n_valout));  // open: ValOut
  not not_1 (not_1_out, multiplexer_1_out);
  not not_2 (not_2_out, not_1_out);
  nor nor_5 (nor_5_out, nor_1_out, nor_3_out);
  DLatch latch2 (.Enable(PCLK), .Value(latch1_n_valout), .n_ValOut(latch2_n_valout));  // open: ValOut
  DLatch latch3 (.Enable(n_PCLK), .Value(latch2_n_valout), .n_ValOut(latch3_n_valout));  // open: ValOut
  not not_3 (not_3_out, H0_DD);
  DLatch latch4 (.Enable(PCLK), .Value(latch3_n_valout), .ValOut(latch4_valout));  // open: n_ValOut
  nor nor_6 (nor_6_out, BLNK, SPR_OV, PCLK, not_3_out, OAMCTR2, n_VIS);
  nor nor_7 (OFETCH, latch4_valout, latch2_n_valout);
  nor nor_8 (n_WE, OFETCH, nor_6_out);

  // Notes on the sheet:
  //   S
  //   W4_Enable
  //   R
  //   OFETCH_FF
  //   W4_FF
endmodule
module OAM_BufferBit (
  input  PCLK,
  input  n_R4_Enable,
  input  BLNK,
  input  OB_OAM,
  input  n_WE,
  input  I_OAM2,
  input  DB_In,
  input  BL_in,
  output OB_Out,
  output DB_Out,
  output BL_out
);

  wire controlled_buffer_1_out, multiplexer_1_out, multiplexer_2_out, multiplexer_3_out, nor_1_out,
       nor_2_out, nor_3_out, not_1_out, not_2_out, not_4_out, not_5_out, out_latch_q, R4_out_latch_valout;

  not not_1 (not_1_out, BL_in);
  Multiplexer multiplexer_1 (.in0(not_1_out), .in1(1'b1), .out(multiplexer_1_out), .sel(PCLK));
  Multiplexer multiplexer_2 (.in0(BL_in), .in1(1'b1), .out(multiplexer_2_out), .sel(PCLK));
  assign controlled_buffer_1_out = OB_OAM ? OB_Out : 1'bz;  // Controlled_Buffer controlled_buffer_1
  assign controlled_buffer_1_out = BLNK ? DB_In : 1'bz;  // Controlled_Buffer controlled_buffer_2
  nor nor_1 (nor_1_out, multiplexer_1_out, nor_2_out);
  nor nor_2 (nor_2_out, nor_1_out, multiplexer_2_out);
  D_Flip_Flop #(.trigger("high")) out_latch (
    .D(controlled_buffer_1_out), .clk(1'b1), .Q(out_latch_q));  // open: Qn, preset, reset
  Transistor #(.\type ("n")) transistor_1 ();  // open: in, out, gate
  nor nor_3 (nor_3_out, I_OAM2, nor_1_out);
  Multiplexer multiplexer_3 (.in0(nor_3_out), .in1(not_4_out), .out(multiplexer_3_out), .sel(PCLK));
  DLatch R4_out_latch (.Enable(PCLK), .Value(OB_Out), .ValOut(R4_out_latch_valout));  // open: n_ValOut
  not not_2 (not_2_out, n_WE);
  assign BL_out = not_2_out ? out_latch_q : 1'bz;  // Controlled_Buffer controlled_buffer_3
  not not_3 (OB_Out, multiplexer_3_out);
  not not_4 (not_4_out, OB_Out);
  not not_5 (not_5_out, n_R4_Enable);
  assign DB_Out = not_5_out ? R4_out_latch_valout : 1'bz;  // Controlled_Buffer controlled_buffer_4

  // Other names for the same wires on the sheet: n_R4 = n_R4_Enable

  // Notes on the sheet:
  //   Direct writing to OAM Cells from DB
  //   actually complement BL+BLBar
  //   imitatation of BL+BLBar
  //   __
  //   BL
  //   BL
  //   Auto clear on PCLK
  //   Output for OAM Cells
  //   Sense Amp
  //   PCLK
  //   OB_FF
  //   In the original circuit here is the PCLK pass FET, which connects the NOR outputs
  //   Output for $2004
  //   actually complement BL+BLBar
endmodule

module OAM_Buffer (
  input  PCLK,
  input  n_R4_Enable,
  input  BLNK,
  input  OB_OAM,
  input  n_WE,
  input  I_OAM2,
  input  [7:0] DB_In,
  input  [7:0] BL_in,
  output [7:0] OB_Out,
  output [7:0] DB_Out,
  output [7:0] BL_out
);

  OAM_BufferBit oam_bufferbit_1 (
    .PCLK(PCLK), .n_R4_Enable(n_R4_Enable), .BLNK(BLNK), .OB_OAM(OB_OAM), .n_WE(n_WE), .I_OAM2(I_OAM2),
    .DB_In(DB_In[0]), .BL_in(BL_in[0]), .OB_Out(OB_Out[0]), .DB_Out(DB_Out[0]), .BL_out(BL_out[0]));
  OAM_BufferBit oam_bufferbit_2 (
    .PCLK(PCLK), .n_R4_Enable(n_R4_Enable), .BLNK(BLNK), .OB_OAM(OB_OAM), .n_WE(n_WE), .I_OAM2(I_OAM2),
    .DB_In(DB_In[1]), .BL_in(BL_in[1]), .OB_Out(OB_Out[1]), .DB_Out(DB_Out[1]), .BL_out(BL_out[1]));
  OAM_BufferBit oam_bufferbit_3 (
    .PCLK(PCLK), .n_R4_Enable(n_R4_Enable), .BLNK(BLNK), .OB_OAM(OB_OAM), .n_WE(n_WE), .I_OAM2(I_OAM2),
    .DB_In(DB_In[2]), .BL_in(BL_in[2]), .OB_Out(OB_Out[2]), .DB_Out(DB_Out[2]), .BL_out(BL_out[2]));
  OAM_BufferBit oam_bufferbit_4 (
    .PCLK(PCLK), .n_R4_Enable(n_R4_Enable), .BLNK(BLNK), .OB_OAM(OB_OAM), .n_WE(n_WE), .I_OAM2(I_OAM2),
    .DB_In(DB_In[3]), .BL_in(BL_in[3]), .OB_Out(OB_Out[3]), .DB_Out(DB_Out[3]), .BL_out(BL_out[3]));
  OAM_BufferBit oam_bufferbit_5 (
    .PCLK(PCLK), .n_R4_Enable(n_R4_Enable), .BLNK(BLNK), .OB_OAM(OB_OAM), .n_WE(n_WE), .I_OAM2(I_OAM2),
    .DB_In(DB_In[4]), .BL_in(BL_in[4]), .OB_Out(OB_Out[4]), .DB_Out(DB_Out[4]), .BL_out(BL_out[4]));
  OAM_BufferBit oam_bufferbit_6 (
    .PCLK(PCLK), .n_R4_Enable(n_R4_Enable), .BLNK(BLNK), .OB_OAM(OB_OAM), .n_WE(n_WE), .I_OAM2(I_OAM2),
    .DB_In(DB_In[5]), .BL_in(BL_in[5]), .OB_Out(OB_Out[5]), .DB_Out(DB_Out[5]), .BL_out(BL_out[5]));
  OAM_BufferBit oam_bufferbit_7 (
    .PCLK(PCLK), .n_R4_Enable(n_R4_Enable), .BLNK(BLNK), .OB_OAM(OB_OAM), .n_WE(n_WE), .I_OAM2(I_OAM2),
    .DB_In(DB_In[6]), .BL_in(BL_in[6]), .OB_Out(OB_Out[6]), .DB_Out(DB_Out[6]), .BL_out(BL_out[6]));
  OAM_BufferBit oam_bufferbit_8 (
    .PCLK(PCLK), .n_R4_Enable(n_R4_Enable), .BLNK(BLNK), .OB_OAM(OB_OAM), .n_WE(n_WE), .I_OAM2(I_OAM2),
    .DB_In(DB_In[7]), .BL_in(BL_in[7]), .OB_Out(OB_Out[7]), .DB_Out(DB_Out[7]), .BL_out(BL_out[7]));
endmodule

module FIFO_CounterControl (
  input  PCLK,
  input  n_PCLK,
  input  n_ZH,
  input  n_VIS,
  input  LOAD,
  input  Carry,
  output UPD,
  output STEP,
  output n_xEN
);

  wire and_1_out, nor_1_out, nor_2_out, nor_3_out, nor_5_out;

  nor nor_1 (nor_1_out, n_PCLK, n_ZH, Carry);
  and and_1 (and_1_out, PCLK, Carry);
  nor nor_2 (nor_2_out, nor_1_out, nor_3_out);
  nor nor_3 (nor_3_out, nor_2_out, and_1_out);
  nor nor_4 (STEP, PCLK, nor_2_out);
  DLatch en_latch (.Enable(n_PCLK), .Value(nor_5_out), .n_ValOut(n_xEN));  // open: ValOut
  nor nor_5 (nor_5_out, nor_3_out, n_VIS);
  nor nor_6 (UPD, LOAD, STEP);

  // Notes on the sheet:
  //   ZH_FF
endmodule

module FIFO_CounterBit (
  input  Clock,
  input  Load,
  input  Step,
  input  val_in,
  input  carry_in,
  output val_out,
  output n_val_out,
  output carry_out
);

  wire multiplexer_1_out, multiplexer_2_out, multiplexer_3_out, multiplexer_4_out, not_1_out,
       step_latch_n_valout, undriven;

  // NoConnect on undriven
  Multiplexer multiplexer_1 (.in0(undriven), .in1(val_in), .out(multiplexer_1_out), .sel(Load));
  DLatch step_latch (.Enable(Clock), .Value(multiplexer_4_out), .n_ValOut(step_latch_n_valout));  // open: ValOut
  Multiplexer multiplexer_2 (.in0(multiplexer_1_out), .in1(step_latch_n_valout), .out(multiplexer_2_out), .sel(Step));
  Multiplexer multiplexer_3 (.in0(multiplexer_2_out), .in1(val_out), .out(multiplexer_3_out), .sel(Clock));
  D_Flip_Flop #(.trigger("high")) d_ff_1 (
    .D(multiplexer_3_out), .clk(1'b1), .Q(val_out), .Qn(n_val_out));  // open: preset, reset
  Multiplexer multiplexer_4 (.in0(n_val_out), .in1(val_out), .out(multiplexer_4_out), .sel(carry_in));
  not not_1 (not_1_out, carry_in);
  nor nor_1 (carry_out, val_out, not_1_out);
endmodule

module FIFO_DownCounter (
  input  UPD,
  input  LOAD,
  input  STEP,
  input  [7:0] OB,
  output CarryOut
);

  wire fifo_counterbit_1_carry_out, fifo_counterbit_1_val_out, fifo_counterbit_2_carry_out,
       fifo_counterbit_2_val_out, fifo_counterbit_3_carry_out, fifo_counterbit_3_val_out,
       fifo_counterbit_4_carry_out, fifo_counterbit_4_val_out, fifo_counterbit_5_carry_out,
       fifo_counterbit_5_val_out, fifo_counterbit_6_carry_out, fifo_counterbit_7_carry_out, nor_1_out;

  FIFO_CounterBit fifo_counterbit_1 (
    .Clock(UPD), .Load(LOAD), .Step(STEP), .val_in(OB[0]), .carry_in(1'b1),
    .val_out(fifo_counterbit_1_val_out), .carry_out(fifo_counterbit_1_carry_out));  // open: n_val_out
  FIFO_CounterBit fifo_counterbit_2 (
    .Clock(UPD), .Load(LOAD), .Step(STEP), .val_in(OB[1]), .carry_in(fifo_counterbit_1_carry_out),
    .val_out(fifo_counterbit_2_val_out), .carry_out(fifo_counterbit_2_carry_out));  // open: n_val_out
  FIFO_CounterBit fifo_counterbit_3 (
    .Clock(UPD), .Load(LOAD), .Step(STEP), .val_in(OB[2]), .carry_in(fifo_counterbit_2_carry_out),
    .val_out(fifo_counterbit_3_val_out), .carry_out(fifo_counterbit_3_carry_out));  // open: n_val_out
  FIFO_CounterBit fifo_counterbit_4 (
    .Clock(UPD), .Load(LOAD), .Step(STEP), .val_in(OB[3]), .carry_in(fifo_counterbit_3_carry_out),
    .val_out(fifo_counterbit_4_val_out), .carry_out(fifo_counterbit_4_carry_out));  // open: n_val_out
  FIFO_CounterBit fifo_counterbit_5 (
    .Clock(UPD), .Load(LOAD), .Step(STEP), .val_in(OB[4]), .carry_in(fifo_counterbit_4_carry_out),
    .val_out(fifo_counterbit_5_val_out), .carry_out(fifo_counterbit_5_carry_out));  // open: n_val_out
  // NoConnect on fifo_counterbit_5_carry_out
  nor nor_1 (nor_1_out, fifo_counterbit_1_val_out, fifo_counterbit_2_val_out, fifo_counterbit_3_val_out, fifo_counterbit_4_val_out, fifo_counterbit_5_val_out);
  FIFO_CounterBit fifo_counterbit_6 (
    .Clock(UPD), .Load(LOAD), .Step(STEP), .val_in(OB[5]), .carry_in(nor_1_out),
    .carry_out(fifo_counterbit_6_carry_out));  // open: val_out, n_val_out
  FIFO_CounterBit fifo_counterbit_7 (
    .Clock(UPD), .Load(LOAD), .Step(STEP), .val_in(OB[6]), .carry_in(fifo_counterbit_6_carry_out),
    .carry_out(fifo_counterbit_7_carry_out));  // open: val_out, n_val_out
  FIFO_CounterBit fifo_counterbit_8 (
    .Clock(UPD), .Load(LOAD), .Step(STEP), .val_in(OB[7]), .carry_in(fifo_counterbit_7_carry_out),
    .carry_out(CarryOut));  // open: val_out, n_val_out
endmodule

module FIFO_LaneControl (
  input  n_PCLK,
  input  [7:0] OB,
  input  n_xEN,
  input  HSel,
  input  n_RD_ATTR,
  input  n_RD_X,
  input  n_RD_A,
  input  n_RD_B,
  output Z_COL2,
  output Z_COL3,
  output nZ_PRIO,
  output SR_EN,
  output LOAD,
  output T_SR0,
  output T_SR1
);

  wire hsel_latch_n_valout, nor_2_out, ob0_latch1_n_valout, ob1_latch1_n_valout, ob5_latch1_n_valout;

  // NoConnect on OB[2]
  // NoConnect on OB[3]
  // NoConnect on OB[4]
  DLatch ob0_latch1 (.Enable(nor_2_out), .Value(OB[0]), .n_ValOut(ob0_latch1_n_valout));  // open: ValOut
  DLatch ob1_latch1 (.Enable(nor_2_out), .Value(OB[1]), .n_ValOut(ob1_latch1_n_valout));  // open: ValOut
  DLatch ob5_latch1 (.Enable(nor_2_out), .Value(OB[5]), .n_ValOut(ob5_latch1_n_valout));  // open: ValOut
  DLatch hsel_latch (.Enable(n_PCLK), .Value(HSel), .n_ValOut(hsel_latch_n_valout));  // open: ValOut
  DLatch ob0_latch2 (.Enable(n_PCLK), .Value(ob0_latch1_n_valout), .n_ValOut(Z_COL2));  // open: ValOut
  DLatch ob1_latch2 (.Enable(n_PCLK), .Value(ob1_latch1_n_valout), .n_ValOut(Z_COL3));  // open: ValOut
  DLatch ob5_latch2 (.Enable(n_PCLK), .Value(ob5_latch1_n_valout), .n_ValOut(nZ_PRIO));  // open: ValOut
  nor nor_1 (SR_EN, n_PCLK, n_xEN);
  nor nor_2 (nor_2_out, n_PCLK, hsel_latch_n_valout, n_RD_ATTR);
  nor nor_3 (LOAD, n_PCLK, hsel_latch_n_valout, n_RD_X);
  nor nor_4 (T_SR0, n_PCLK, hsel_latch_n_valout, n_RD_A);
  nor nor_5 (T_SR1, n_PCLK, hsel_latch_n_valout, n_RD_B);

  // Notes on the sheet:
  //   0-1: Palette (4 to 7) of sprite
  //   5: Priority (0: in front of background; 1: behind background)
  //   LDAT
endmodule

module FIFO_SRBit (
  input  n_PCLK,
  input  T_SR,
  input  SR_EN,
  input  nTx,
  input  shift_in,
  output shift_out
);

  wire in_latch_qn, multiplexer_1_out, multiplexer_2_out, undriven;

  // NoConnect on undriven
  Multiplexer multiplexer_1 (.in0(undriven), .in1(nTx), .out(multiplexer_1_out), .sel(T_SR));
  Multiplexer multiplexer_2 (.in0(multiplexer_1_out), .in1(shift_in), .out(multiplexer_2_out), .sel(SR_EN));
  D_Flip_Flop #(.trigger("high")) in_latch (
    .D(multiplexer_2_out), .clk(1'b1), .Qn(in_latch_qn));  // open: Q, preset, reset
  DLatch out_latch (.Enable(n_PCLK), .Value(in_latch_qn), .n_ValOut(shift_out));  // open: ValOut

  // Notes on the sheet:
  //   Load
  //   Step
endmodule

module FIFO_PairedSR (
  input  n_PCLK,
  input  T_SR0,
  input  T_SR1,
  input  SR_EN,
  input  [7:0] n_Tx,
  output nZ_COL0,
  output nZ_COL1
);

  wire fifo_srbit_1_shift_out, fifo_srbit_2_shift_out, fifo_srbit_3_shift_out, fifo_srbit_4_shift_out,
       fifo_srbit_5_shift_out, fifo_srbit_6_shift_out, fifo_srbit_7_shift_out, fifo_srbit_8_shift_out,
       fifo_srbit_9_shift_out, fifo_srbit_10_shift_out, fifo_srbit_11_shift_out, fifo_srbit_12_shift_out,
       fifo_srbit_13_shift_out, fifo_srbit_14_shift_out;

  FIFO_SRBit fifo_srbit_1 (
    .n_PCLK(n_PCLK), .T_SR(T_SR0), .SR_EN(SR_EN), .nTx(n_Tx[7]), .shift_in(1'b1),
    .shift_out(fifo_srbit_1_shift_out));
  FIFO_SRBit fifo_srbit_2 (
    .n_PCLK(n_PCLK), .T_SR(T_SR1), .SR_EN(SR_EN), .nTx(n_Tx[7]), .shift_in(1'b1),
    .shift_out(fifo_srbit_2_shift_out));
  FIFO_SRBit fifo_srbit_3 (
    .n_PCLK(n_PCLK), .T_SR(T_SR0), .SR_EN(SR_EN), .nTx(n_Tx[6]), .shift_in(fifo_srbit_1_shift_out),
    .shift_out(fifo_srbit_3_shift_out));
  FIFO_SRBit fifo_srbit_4 (
    .n_PCLK(n_PCLK), .T_SR(T_SR1), .SR_EN(SR_EN), .nTx(n_Tx[6]), .shift_in(fifo_srbit_2_shift_out),
    .shift_out(fifo_srbit_4_shift_out));
  FIFO_SRBit fifo_srbit_5 (
    .n_PCLK(n_PCLK), .T_SR(T_SR0), .SR_EN(SR_EN), .nTx(n_Tx[5]), .shift_in(fifo_srbit_3_shift_out),
    .shift_out(fifo_srbit_5_shift_out));
  FIFO_SRBit fifo_srbit_6 (
    .n_PCLK(n_PCLK), .T_SR(T_SR1), .SR_EN(SR_EN), .nTx(n_Tx[5]), .shift_in(fifo_srbit_4_shift_out),
    .shift_out(fifo_srbit_6_shift_out));
  FIFO_SRBit fifo_srbit_7 (
    .n_PCLK(n_PCLK), .T_SR(T_SR0), .SR_EN(SR_EN), .nTx(n_Tx[4]), .shift_in(fifo_srbit_5_shift_out),
    .shift_out(fifo_srbit_7_shift_out));
  FIFO_SRBit fifo_srbit_8 (
    .n_PCLK(n_PCLK), .T_SR(T_SR1), .SR_EN(SR_EN), .nTx(n_Tx[4]), .shift_in(fifo_srbit_6_shift_out),
    .shift_out(fifo_srbit_8_shift_out));
  FIFO_SRBit fifo_srbit_9 (
    .n_PCLK(n_PCLK), .T_SR(T_SR0), .SR_EN(SR_EN), .nTx(n_Tx[3]), .shift_in(fifo_srbit_7_shift_out),
    .shift_out(fifo_srbit_9_shift_out));
  FIFO_SRBit fifo_srbit_10 (
    .n_PCLK(n_PCLK), .T_SR(T_SR1), .SR_EN(SR_EN), .nTx(n_Tx[3]), .shift_in(fifo_srbit_8_shift_out),
    .shift_out(fifo_srbit_10_shift_out));
  FIFO_SRBit fifo_srbit_11 (
    .n_PCLK(n_PCLK), .T_SR(T_SR0), .SR_EN(SR_EN), .nTx(n_Tx[2]), .shift_in(fifo_srbit_9_shift_out),
    .shift_out(fifo_srbit_11_shift_out));
  FIFO_SRBit fifo_srbit_12 (
    .n_PCLK(n_PCLK), .T_SR(T_SR1), .SR_EN(SR_EN), .nTx(n_Tx[2]), .shift_in(fifo_srbit_10_shift_out),
    .shift_out(fifo_srbit_12_shift_out));
  FIFO_SRBit fifo_srbit_13 (
    .n_PCLK(n_PCLK), .T_SR(T_SR0), .SR_EN(SR_EN), .nTx(n_Tx[1]), .shift_in(fifo_srbit_11_shift_out),
    .shift_out(fifo_srbit_13_shift_out));
  FIFO_SRBit fifo_srbit_14 (
    .n_PCLK(n_PCLK), .T_SR(T_SR1), .SR_EN(SR_EN), .nTx(n_Tx[1]), .shift_in(fifo_srbit_12_shift_out),
    .shift_out(fifo_srbit_14_shift_out));
  FIFO_SRBit fifo_srbit_15 (
    .n_PCLK(n_PCLK), .T_SR(T_SR0), .SR_EN(SR_EN), .nTx(n_Tx[0]), .shift_in(fifo_srbit_13_shift_out),
    .shift_out(nZ_COL0));
  FIFO_SRBit fifo_srbit_16 (
    .n_PCLK(n_PCLK), .T_SR(T_SR1), .SR_EN(SR_EN), .nTx(n_Tx[0]), .shift_in(fifo_srbit_14_shift_out),
    .shift_out(nZ_COL1));
endmodule

module FIFO_Priority (
  input  PCLK,
  input  CLPO,
  input  [5:0] Lane0,
  input  [5:0] Lane1,
  input  [5:0] Lane2,
  input  [5:0] Lane3,
  input  [5:0] Lane4,
  input  [5:0] Lane5,
  input  [5:0] Lane6,
  input  [5:0] Lane7,
  output n_SPR0HIT,
  output [4:0] ZOut
);

  wire and_1_out, and_2_out, and_3_out, and_4_out, and_5_out, and_6_out, and_7_out, and_8_out, nor_9_out,
       not_1_out, Z0, Z1, Z2, Z3, Z4, Z5, Z6, Z7;
  wire [4:0] multiplexer_1_out, multiplexer_2_out, multiplexer_3_out, multiplexer_4_out, multiplexer_5_out,
       multiplexer_6_out, multiplexer_7_out;
  wire [4:2] col2_latch_valout;

  and and_1 (and_1_out, Lane0[0], Lane0[1]);
  and and_2 (and_2_out, Lane1[0], Lane1[1]);
  and and_3 (and_3_out, Lane2[0], Lane2[1]);
  and and_4 (and_4_out, Lane3[0], Lane3[1]);
  and and_5 (and_5_out, Lane4[0], Lane4[1]);
  and and_6 (and_6_out, Lane5[0], Lane5[1]);
  and and_7 (and_7_out, Lane6[0], Lane6[1]);
  and and_8 (and_8_out, Lane7[0], Lane7[1]);
  nor nor_1 (Z0, and_1_out, CLPO, Lane0[5]);
  nor nor_2 (Z1, and_2_out, CLPO, Lane1[5], Z0);
  nor nor_3 (Z2, and_3_out, CLPO, Z0, Z1, Lane2[5]);
  nor nor_4 (Z3, and_4_out, CLPO, Lane3[5], Z0, Z1, Z2);
  nor nor_5 (Z4, and_5_out, CLPO, Lane4[5], Z0, Z1, Z2, Z3);
  nor nor_6 (Z5, and_6_out, CLPO, Lane5[5], Z0, Z1, Z2, Z3, Z4);
  nor nor_7 (Z6, and_7_out, CLPO, Lane6[5], Z0, Z1, Z2, Z3, Z4, Z5);
  nor nor_8 (Z7, and_8_out, CLPO, Lane7[5], Z0, Z1, Z2, Z3, Z4, Z5, Z6);
  DLatch s0_latch (.Enable(PCLK), .Value(Z0), .n_ValOut(n_SPR0HIT));  // open: ValOut
  DLatch col2_latch (.Enable(not_1_out), .Value(ZOut[2]), .ValOut(col2_latch_valout[2]));  // open: n_ValOut
  DLatch col3_latch (.Enable(not_1_out), .Value(ZOut[3]), .ValOut(col2_latch_valout[3]));  // open: n_ValOut
  DLatch prio_latch (.Enable(not_1_out), .Value(ZOut[4]), .ValOut(col2_latch_valout[4]));  // open: n_ValOut
  nor nor_9 (nor_9_out, Z0, Z1, Z2, Z3, Z4, Z5, Z6, Z7);
  not not_1 (not_1_out, nor_9_out);
  Multiplexer #(.width(5)) multiplexer_1 (
    .in0({col2_latch_valout, 2'b11}), .in1(Lane7[4:0]), .out(multiplexer_1_out), .sel(Z7));
  Multiplexer #(.width(5)) multiplexer_2 (.in0(multiplexer_1_out), .in1(Lane6[4:0]), .out(multiplexer_2_out), .sel(Z6));
  Multiplexer #(.width(5)) multiplexer_3 (.in0(multiplexer_2_out), .in1(Lane5[4:0]), .out(multiplexer_3_out), .sel(Z5));
  Multiplexer #(.width(5)) multiplexer_4 (.in0(multiplexer_3_out), .in1(Lane4[4:0]), .out(multiplexer_4_out), .sel(Z4));
  Multiplexer #(.width(5)) multiplexer_5 (.in0(multiplexer_4_out), .in1(Lane3[4:0]), .out(multiplexer_5_out), .sel(Z3));
  Multiplexer #(.width(5)) multiplexer_6 (.in0(multiplexer_5_out), .in1(Lane2[4:0]), .out(multiplexer_6_out), .sel(Z2));
  Multiplexer #(.width(5)) multiplexer_7 (.in0(multiplexer_6_out), .in1(Lane1[4:0]), .out(multiplexer_7_out), .sel(Z1));
  Multiplexer #(.width(5)) multiplexer_8 (.in0(multiplexer_7_out), .in1(Lane0[4:0]), .out(ZOut), .sel(Z0));

  // Notes on the sheet:
  //   /COL0-1 are set to 1 if no Z0-7 output is selected.
  //   COL2-3 and PRIO are not specifically set if Z0-7 is not selected, so they are effectively stored as latches on the MUX inputs.
endmodule

module FIFO_Lane (
  input  PCLK,
  input  n_PCLK,
  input  [7:0] n_Tx,
  input  [7:0] OB,
  input  HSel,
  input  n_RD_ATTR,
  input  n_RD_X,
  input  n_RD_A,
  input  n_RD_B,
  input  n_ZH,
  input  n_VIS,
  output nZ_COL0,
  output nZ_COL1,
  output Z_COL2,
  output Z_COL3,
  output nZ_PRIO,
  output n_xEN
);

  wire fifo_countercontrol_1_step, fifo_countercontrol_1_upd, fifo_downcounter_1_carryout,
       fifo_lanecontrol_1_load, fifo_lanecontrol_1_sr_en, fifo_lanecontrol_1_t_sr0, fifo_lanecontrol_1_t_sr1;

  FIFO_PairedSR fifo_pairedsr_1 (
    .n_PCLK(n_PCLK), .T_SR0(fifo_lanecontrol_1_t_sr0), .T_SR1(fifo_lanecontrol_1_t_sr1),
    .SR_EN(fifo_lanecontrol_1_sr_en),
    .n_Tx({n_Tx[0], n_Tx[1], n_Tx[2], n_Tx[3], n_Tx[4], n_Tx[5], n_Tx[6], n_Tx[7]}), .nZ_COL0(nZ_COL0),
    .nZ_COL1(nZ_COL1));
  FIFO_LaneControl fifo_lanecontrol_1 (
    .n_PCLK(n_PCLK), .OB(OB), .n_xEN(n_xEN), .HSel(HSel), .n_RD_ATTR(n_RD_ATTR), .n_RD_X(n_RD_X),
    .n_RD_A(n_RD_A), .n_RD_B(n_RD_B), .Z_COL2(Z_COL2), .Z_COL3(Z_COL3), .nZ_PRIO(nZ_PRIO),
    .SR_EN(fifo_lanecontrol_1_sr_en), .LOAD(fifo_lanecontrol_1_load), .T_SR0(fifo_lanecontrol_1_t_sr0),
    .T_SR1(fifo_lanecontrol_1_t_sr1));
  FIFO_CounterControl fifo_countercontrol_1 (
    .PCLK(PCLK), .n_PCLK(n_PCLK), .n_ZH(n_ZH), .n_VIS(n_VIS), .LOAD(fifo_lanecontrol_1_load),
    .Carry(fifo_downcounter_1_carryout), .UPD(fifo_countercontrol_1_upd), .STEP(fifo_countercontrol_1_step),
    .n_xEN(n_xEN));
  FIFO_DownCounter fifo_downcounter_1 (
    .UPD(fifo_countercontrol_1_upd), .LOAD(fifo_lanecontrol_1_load), .STEP(fifo_countercontrol_1_step),
    .OB(OB), .CarryOut(fifo_downcounter_1_carryout));

  // Notes on the sheet:
  //   Attr (Byte 2)
  //   X (Byte 3)
  //   The value is fed to SR8 in reversed form, because the pixels are output backwards.
endmodule

module H_Inversion (
  input  n_PCLK,
  input  n_OBJ_RD_ATTR,
  input  OB6,
  input  PD_FIFO,
  input  [7:0] PD,
  output [7:0] n_Tx
);

  wire multiplexer_1_out, nor_1_out, not_1_out, not_2_out;
  wire [7:0] bit_extender_1_out, multiplexer_2_out, tout_latch_val_out;

  nor nor_1 (nor_1_out, n_PCLK, n_OBJ_RD_ATTR);
  Multiplexer multiplexer_1 (.in0(not_2_out), .in1(OB6), .out(multiplexer_1_out), .sel(nor_1_out));
  not not_1 (not_1_out, multiplexer_1_out);
  not not_2 (not_2_out, not_1_out);
  Multiplexer #(.width(8)) multiplexer_2 (
    .in0(PD), .in1({PD[0], PD[1], PD[2], PD[3], PD[4], PD[5], PD[6], PD[7]}), .out(multiplexer_2_out),
    .sel(multiplexer_1_out));
  assign bit_extender_1_out = {{7{PD_FIFO}}, PD_FIFO};  // Bit_Extender bit_extender_1
  DLatch_x8 tout_latch (.enable(n_PCLK), .val(multiplexer_2_out), .val_out(tout_latch_val_out));  // open: n_val_out
  assign n_Tx = ~(bit_extender_1_out & tout_latch_val_out);  // NAND_Gate nand_1, 8 bits wide

  // Notes on the sheet:
  //   6: Flip sprite horizontally
  //   HINV_FF
  //   HINV
endmodule

module SpriteH (
  input  n_PCLK,
  input  OBJ_READ,
  input  H0_DD,
  input  H1_DD,
  input  H2_DD,
  output n_OBJ_RD_ATTR,
  output n_OBJ_RD_X,
  output n_OBJ_RD_A,
  output n_OBJ_RD_B
);

  wire decoder_1_out2, decoder_1_out3, decoder_1_out5, decoder_1_out7, sh2_latch_n_valout,
       sh3_latch_n_valout, sh5_latch_n_valout, sh7_latch_n_valout;

  Decoder #(.select(3)) decoder_1 (
    .out2(decoder_1_out2), .out3(decoder_1_out3), .out5(decoder_1_out5), .out7(decoder_1_out7),
    .sel({H2_DD, H1_DD, H0_DD}), .en(OBJ_READ));  // open: out0, out1, out4, out6
  DLatch sh2_latch (.Enable(n_PCLK), .Value(decoder_1_out2), .n_ValOut(sh2_latch_n_valout));  // open: ValOut
  DLatch sh3_latch (.Enable(n_PCLK), .Value(decoder_1_out3), .n_ValOut(sh3_latch_n_valout));  // open: ValOut
  DLatch sh5_latch (.Enable(n_PCLK), .Value(decoder_1_out5), .n_ValOut(sh5_latch_n_valout));  // open: ValOut
  DLatch sh7_latch (.Enable(n_PCLK), .Value(decoder_1_out7), .n_ValOut(sh7_latch_n_valout));  // open: ValOut
  buf buffer_1 (n_OBJ_RD_ATTR, sh2_latch_n_valout);
  buf buffer_2 (n_OBJ_RD_X, sh3_latch_n_valout);
  buf buffer_3 (n_OBJ_RD_A, sh5_latch_n_valout);
  buf buffer_4 (n_OBJ_RD_B, sh7_latch_n_valout);
endmodule

module FIFO_All (
  input  PCLK,
  input  n_PCLK,
  input  OBJ_READ,
  input  H0_DD,
  input  H1_DD,
  input  H2_DD,
  input  H3_DD,
  input  H4_DD,
  input  H5_DD,
  input  Z_HPOS,
  input  n_VIS,
  input  [7:0] OB,
  input  PD_FIFO,
  input  [7:0] PD,
  input  CLPO,
  output n_SPR0HIT,
  output n_ZCOL0,
  output n_ZCOL1,
  output ZCOL2,
  output ZCOL3,
  output n_ZPRIO,
  output n_OBJ_RD_ATTR
);

  wire decoder_1_out0, decoder_1_out1, decoder_1_out2, decoder_1_out3, decoder_1_out4, decoder_1_out5,
       decoder_1_out6, decoder_1_out7, zh_latch1_n_valout, zh_latch2_n_valout;
  wire [4:1] spriteh_1_n_obj_rd_x;
  wire [5:0] fifo_lane_1_nz_col0, fifo_lane_2_nz_col0, fifo_lane_3_nz_col0, fifo_lane_4_nz_col0,
       fifo_lane_5_nz_col0, fifo_lane_6_nz_col0, fifo_lane_7_nz_col0, fifo_lane_8_nz_col0;
  wire [7:0] h_inversion_1_n_tx;

  DLatch zh_latch1 (.Enable(n_PCLK), .Value(Z_HPOS), .n_ValOut(zh_latch1_n_valout));  // open: ValOut
  DLatch zh_latch2 (.Enable(PCLK), .Value(zh_latch1_n_valout), .n_ValOut(zh_latch2_n_valout));  // open: ValOut
  DLatch zh_latch3 (.Enable(n_PCLK), .Value(zh_latch2_n_valout), .n_ValOut(spriteh_1_n_obj_rd_x[4]));  // open: ValOut
  SpriteH spriteh_1 (
    .n_PCLK(n_PCLK), .OBJ_READ(OBJ_READ), .H0_DD(H0_DD), .H1_DD(H1_DD), .H2_DD(H2_DD),
    .n_OBJ_RD_ATTR(n_OBJ_RD_ATTR), .n_OBJ_RD_X(spriteh_1_n_obj_rd_x[1]),
    .n_OBJ_RD_A(spriteh_1_n_obj_rd_x[2]), .n_OBJ_RD_B(spriteh_1_n_obj_rd_x[3]));
  Decoder #(.enable("false"), .select(3)) decoder_1 (
    .out0(decoder_1_out0), .out1(decoder_1_out1), .out2(decoder_1_out2), .out3(decoder_1_out3),
    .out4(decoder_1_out4), .out5(decoder_1_out5), .out6(decoder_1_out6), .out7(decoder_1_out7),
    .sel({H5_DD, H4_DD, H3_DD}));
  H_Inversion h_inversion_1 (
    .n_PCLK(n_PCLK), .n_OBJ_RD_ATTR(n_OBJ_RD_ATTR), .OB6(OB[6]), .PD_FIFO(PD_FIFO), .PD(PD),
    .n_Tx(h_inversion_1_n_tx));
  FIFO_Lane fifo_lane_1 (
    .PCLK(PCLK), .n_PCLK(n_PCLK), .n_Tx(h_inversion_1_n_tx), .OB(OB), .HSel(decoder_1_out0),
    .n_RD_ATTR(n_OBJ_RD_ATTR), .n_RD_X(spriteh_1_n_obj_rd_x[1]), .n_RD_A(spriteh_1_n_obj_rd_x[2]),
    .n_RD_B(spriteh_1_n_obj_rd_x[3]), .n_ZH(spriteh_1_n_obj_rd_x[4]), .n_VIS(n_VIS),
    .nZ_COL0(fifo_lane_1_nz_col0[0]), .nZ_COL1(fifo_lane_1_nz_col0[1]), .Z_COL2(fifo_lane_1_nz_col0[2]),
    .Z_COL3(fifo_lane_1_nz_col0[3]), .nZ_PRIO(fifo_lane_1_nz_col0[4]), .n_xEN(fifo_lane_1_nz_col0[5]));
  FIFO_Lane fifo_lane_2 (
    .PCLK(PCLK), .n_PCLK(n_PCLK), .n_Tx(h_inversion_1_n_tx), .OB(OB), .HSel(decoder_1_out1),
    .n_RD_ATTR(n_OBJ_RD_ATTR), .n_RD_X(spriteh_1_n_obj_rd_x[1]), .n_RD_A(spriteh_1_n_obj_rd_x[2]),
    .n_RD_B(spriteh_1_n_obj_rd_x[3]), .n_ZH(spriteh_1_n_obj_rd_x[4]), .n_VIS(n_VIS),
    .nZ_COL0(fifo_lane_2_nz_col0[0]), .nZ_COL1(fifo_lane_2_nz_col0[1]), .Z_COL2(fifo_lane_2_nz_col0[2]),
    .Z_COL3(fifo_lane_2_nz_col0[3]), .nZ_PRIO(fifo_lane_2_nz_col0[4]), .n_xEN(fifo_lane_2_nz_col0[5]));
  FIFO_Lane fifo_lane_3 (
    .PCLK(PCLK), .n_PCLK(n_PCLK), .n_Tx(h_inversion_1_n_tx), .OB(OB), .HSel(decoder_1_out2),
    .n_RD_ATTR(n_OBJ_RD_ATTR), .n_RD_X(spriteh_1_n_obj_rd_x[1]), .n_RD_A(spriteh_1_n_obj_rd_x[2]),
    .n_RD_B(spriteh_1_n_obj_rd_x[3]), .n_ZH(spriteh_1_n_obj_rd_x[4]), .n_VIS(n_VIS),
    .nZ_COL0(fifo_lane_3_nz_col0[0]), .nZ_COL1(fifo_lane_3_nz_col0[1]), .Z_COL2(fifo_lane_3_nz_col0[2]),
    .Z_COL3(fifo_lane_3_nz_col0[3]), .nZ_PRIO(fifo_lane_3_nz_col0[4]), .n_xEN(fifo_lane_3_nz_col0[5]));
  FIFO_Lane fifo_lane_4 (
    .PCLK(PCLK), .n_PCLK(n_PCLK), .n_Tx(h_inversion_1_n_tx), .OB(OB), .HSel(decoder_1_out3),
    .n_RD_ATTR(n_OBJ_RD_ATTR), .n_RD_X(spriteh_1_n_obj_rd_x[1]), .n_RD_A(spriteh_1_n_obj_rd_x[2]),
    .n_RD_B(spriteh_1_n_obj_rd_x[3]), .n_ZH(spriteh_1_n_obj_rd_x[4]), .n_VIS(n_VIS),
    .nZ_COL0(fifo_lane_4_nz_col0[0]), .nZ_COL1(fifo_lane_4_nz_col0[1]), .Z_COL2(fifo_lane_4_nz_col0[2]),
    .Z_COL3(fifo_lane_4_nz_col0[3]), .nZ_PRIO(fifo_lane_4_nz_col0[4]), .n_xEN(fifo_lane_4_nz_col0[5]));
  FIFO_Lane fifo_lane_5 (
    .PCLK(PCLK), .n_PCLK(n_PCLK), .n_Tx(h_inversion_1_n_tx), .OB(OB), .HSel(decoder_1_out4),
    .n_RD_ATTR(n_OBJ_RD_ATTR), .n_RD_X(spriteh_1_n_obj_rd_x[1]), .n_RD_A(spriteh_1_n_obj_rd_x[2]),
    .n_RD_B(spriteh_1_n_obj_rd_x[3]), .n_ZH(spriteh_1_n_obj_rd_x[4]), .n_VIS(n_VIS),
    .nZ_COL0(fifo_lane_5_nz_col0[0]), .nZ_COL1(fifo_lane_5_nz_col0[1]), .Z_COL2(fifo_lane_5_nz_col0[2]),
    .Z_COL3(fifo_lane_5_nz_col0[3]), .nZ_PRIO(fifo_lane_5_nz_col0[4]), .n_xEN(fifo_lane_5_nz_col0[5]));
  FIFO_Lane fifo_lane_6 (
    .PCLK(PCLK), .n_PCLK(n_PCLK), .n_Tx(h_inversion_1_n_tx), .OB(OB), .HSel(decoder_1_out5),
    .n_RD_ATTR(n_OBJ_RD_ATTR), .n_RD_X(spriteh_1_n_obj_rd_x[1]), .n_RD_A(spriteh_1_n_obj_rd_x[2]),
    .n_RD_B(spriteh_1_n_obj_rd_x[3]), .n_ZH(spriteh_1_n_obj_rd_x[4]), .n_VIS(n_VIS),
    .nZ_COL0(fifo_lane_6_nz_col0[0]), .nZ_COL1(fifo_lane_6_nz_col0[1]), .Z_COL2(fifo_lane_6_nz_col0[2]),
    .Z_COL3(fifo_lane_6_nz_col0[3]), .nZ_PRIO(fifo_lane_6_nz_col0[4]), .n_xEN(fifo_lane_6_nz_col0[5]));
  FIFO_Lane fifo_lane_7 (
    .PCLK(PCLK), .n_PCLK(n_PCLK), .n_Tx(h_inversion_1_n_tx), .OB(OB), .HSel(decoder_1_out6),
    .n_RD_ATTR(n_OBJ_RD_ATTR), .n_RD_X(spriteh_1_n_obj_rd_x[1]), .n_RD_A(spriteh_1_n_obj_rd_x[2]),
    .n_RD_B(spriteh_1_n_obj_rd_x[3]), .n_ZH(spriteh_1_n_obj_rd_x[4]), .n_VIS(n_VIS),
    .nZ_COL0(fifo_lane_7_nz_col0[0]), .nZ_COL1(fifo_lane_7_nz_col0[1]), .Z_COL2(fifo_lane_7_nz_col0[2]),
    .Z_COL3(fifo_lane_7_nz_col0[3]), .nZ_PRIO(fifo_lane_7_nz_col0[4]), .n_xEN(fifo_lane_7_nz_col0[5]));
  FIFO_Lane fifo_lane_8 (
    .PCLK(PCLK), .n_PCLK(n_PCLK), .n_Tx(h_inversion_1_n_tx), .OB(OB), .HSel(decoder_1_out7),
    .n_RD_ATTR(n_OBJ_RD_ATTR), .n_RD_X(spriteh_1_n_obj_rd_x[1]), .n_RD_A(spriteh_1_n_obj_rd_x[2]),
    .n_RD_B(spriteh_1_n_obj_rd_x[3]), .n_ZH(spriteh_1_n_obj_rd_x[4]), .n_VIS(n_VIS),
    .nZ_COL0(fifo_lane_8_nz_col0[0]), .nZ_COL1(fifo_lane_8_nz_col0[1]), .Z_COL2(fifo_lane_8_nz_col0[2]),
    .Z_COL3(fifo_lane_8_nz_col0[3]), .nZ_PRIO(fifo_lane_8_nz_col0[4]), .n_xEN(fifo_lane_8_nz_col0[5]));
  FIFO_Priority fifo_priority_1 (
    .PCLK(PCLK), .CLPO(CLPO), .Lane0(fifo_lane_1_nz_col0), .Lane1(fifo_lane_2_nz_col0),
    .Lane2(fifo_lane_3_nz_col0), .Lane3(fifo_lane_4_nz_col0), .Lane4(fifo_lane_5_nz_col0),
    .Lane5(fifo_lane_6_nz_col0), .Lane6(fifo_lane_7_nz_col0), .Lane7(fifo_lane_8_nz_col0),
    .n_SPR0HIT(n_SPR0HIT), .ZOut({n_ZPRIO, ZCOL3, ZCOL2, n_ZCOL1, n_ZCOL0}));

  // Notes on the sheet:
  //   PCLK
  //   OB6
  //   #0/H
endmodule

module DLatch_x8 (
  input  enable,
  input  [7:0] val,
  output [7:0] val_out,
  output [7:0] n_val_out
);

  DLatch dlatch_1 (.Enable(enable), .Value(val[0]), .ValOut(val_out[0]), .n_ValOut(n_val_out[0]));
  DLatch dlatch_2 (.Enable(enable), .Value(val[1]), .ValOut(val_out[1]), .n_ValOut(n_val_out[1]));
  DLatch dlatch_3 (.Enable(enable), .Value(val[2]), .ValOut(val_out[2]), .n_ValOut(n_val_out[2]));
  DLatch dlatch_4 (.Enable(enable), .Value(val[3]), .ValOut(val_out[3]), .n_ValOut(n_val_out[3]));
  DLatch dlatch_5 (.Enable(enable), .Value(val[4]), .ValOut(val_out[4]), .n_ValOut(n_val_out[4]));
  DLatch dlatch_6 (.Enable(enable), .Value(val[5]), .ValOut(val_out[5]), .n_ValOut(n_val_out[5]));
  DLatch dlatch_7 (.Enable(enable), .Value(val[6]), .ValOut(val_out[6]), .n_ValOut(n_val_out[6]));
  DLatch dlatch_8 (.Enable(enable), .Value(val[7]), .ValOut(val_out[7]), .n_ValOut(n_val_out[7]));
endmodule

module DataReader_All (
  input  PCLK,
  input  n_PCLK,
  input  n_W0,
  input  n_W5_1,
  input  n_W5_2,
  input  n_W6_1,
  input  n_W6_2,
  input  n_DBE,
  input  H0_DD,
  input  n_H1_D,
  input  n_H2_D,
  input  n_OBJ_RD_ATTR,
  input  nF_NT,
  input  F_AT,
  input  F_TA,
  input  F_TB,
  input  n_FO,
  input  OBJ_READ,
  input  SC_CNT,
  input  E_EV,
  input  DB_PAR,
  input  RESCL,
  input  BLNK,
  input  [3:0] OV,
  input  [7:0] OB,
  input  [7:0] PD,
  input  [7:0] DB,
  input  TSTEP,
  input  RC,
  input  n_CLPB,
  input  BGSEL,
  input  OBSEL,
  input  I1_32,
  input  O8_16,
  output [4:0] THO,
  output [3:0] BGC,
  output [13:0] n_PAx
);

  wire scrollregs_1_nth, scrollregs_1_ntv, scrollregs_1_w6_2_enable;
  wire [2:0] scrollregs_1_fhx, scrollregs_1_fvx, tilecounters_all_1_n_fvo;
  wire [4:0] scrollregs_1_thx, scrollregs_1_tvx, tilecounters_all_1_tvo;
  wire [13:0] par_1_pat_adr, tilecounters_all_1_at_adr, tilecounters_all_1_nt_adr;

  PAR par_1 (
    .n_PCLK(n_PCLK), .H0_DD(H0_DD), .nF_NT(nF_NT), .BGSEL(BGSEL), .OBSEL(OBSEL), .O8_16(O8_16),
    .OBJ_READ(OBJ_READ), .n_OBJ_RD_ATTR(n_OBJ_RD_ATTR), .n_H1_D(n_H1_D), .OB(OB), .PD_In(PD), .OV(OV),
    .n_FVO(tilecounters_all_1_n_fvo), .PAT_ADR(par_1_pat_adr));
  ScrollRegs scrollregs_1 (
    .n_W0(n_W0), .n_W5_1(n_W5_1), .n_W5_2(n_W5_2), .n_W6_1(n_W6_1), .n_W6_2(n_W6_2), .n_DBE(n_DBE), .RC(RC),
    .DB(DB), .FHx(scrollregs_1_fhx), .FVx(scrollregs_1_fvx), .NTH(scrollregs_1_nth), .NTV(scrollregs_1_ntv),
    .TVx(scrollregs_1_tvx), .THx(scrollregs_1_thx), .W6_2_Enable(scrollregs_1_w6_2_enable));
  TileCounters_All tilecounters_all_1 (
    .n_PCLK(n_PCLK), .PCLK(PCLK), .W62_EN(scrollregs_1_w6_2_enable), .SC_CNT(SC_CNT), .RESCL(RESCL),
    .E_EV(E_EV), .TSTEP(TSTEP), .F_TB(F_TB), .H0_DD(H0_DD), .BLNK(BLNK), .I1_32(I1_32),
    .FVx(scrollregs_1_fvx), .NTH(scrollregs_1_nth), .NTV(scrollregs_1_ntv), .TVx(scrollregs_1_tvx),
    .THx(scrollregs_1_thx), .n_FVO(tilecounters_all_1_n_fvo), .THO(THO), .TVO(tilecounters_all_1_tvo),
    .AT_ADR(tilecounters_all_1_at_adr), .NT_ADR(tilecounters_all_1_nt_adr));
  BGC_All bgc_all_1 (
    .PCLK(PCLK), .n_PCLK(n_PCLK), .H0_DD(H0_DD), .F_TA(F_TA), .F_TB(F_TB), .n_FO(n_FO), .F_AT(F_AT),
    .THO(THO), .TVO(tilecounters_all_1_tvo), .FH(scrollregs_1_fhx), .PD(PD), .n_CLPB(n_CLPB), .BGC(BGC));
  PAMUX_All pamux_all_1 (
    .PCLK(PCLK), .n_H2_D(n_H2_D), .BLNK(BLNK), .F_AT(F_AT), .DB_PAR(DB_PAR),
    .AT_ADR(tilecounters_all_1_at_adr), .NT_ADR(tilecounters_all_1_nt_adr), .PAT_ADR(par_1_pat_adr),
    .DB_in(DB), .n_PAx(n_PAx));
endmodule

module ParControl (
  input  n_PCLK,
  input  H0_DD,
  input  nF_NT,
  input  BGSEL,
  input  OBSEL,
  input  O8_16,
  input  OBJ_READ,
  input  [7:0] OB,
  output O,
  output PAD12
);

  wire fnt_latch_valout, multiplexer_1_out, multiplexer_2_out, nor_1_out, not_1_out, not_2_out,
       ob0_latch_n_valout;

  not not_1 (not_1_out, H0_DD);
  DLatch ob0_latch (.Enable(O), .Value(OB[0]), .n_ValOut(ob0_latch_n_valout));  // open: ValOut
  nor nor_1 (nor_1_out, not_1_out, nF_NT);
  DLatch fnt_latch (.Enable(n_PCLK), .Value(not_2_out), .ValOut(fnt_latch_valout));  // open: n_ValOut
  not not_2 (not_2_out, nor_1_out);
  Multiplexer multiplexer_1 (.in0(OBSEL), .in1(ob0_latch_n_valout), .out(multiplexer_1_out), .sel(O8_16));
  Multiplexer multiplexer_2 (.in0(BGSEL), .in1(multiplexer_1_out), .out(multiplexer_2_out), .sel(OBJ_READ));
  nor nor_2 (O, fnt_latch_valout, n_PCLK);
  DLatch pad12_latch (.Enable(n_PCLK), .Value(multiplexer_2_out), .n_ValOut(PAD12));  // open: ValOut

  // Notes on the sheet:
  //   0: Bank ($0000 or $1000) of tiles
  //   /PAD12
endmodule

module V_Inversion (
  input  n_PCLK,
  input  n_OBJ_RD_ATTR,
  input  [7:0] OB,
  output VDIR,
  output VINV
);

  wire controlled_buffer_1_out, multiplexer_1_out, nor_1_out;

  nor nor_1 (nor_1_out, n_PCLK, n_OBJ_RD_ATTR);
  assign controlled_buffer_1_out = nor_1_out ? OB[7] : 1'bz;  // Controlled_Buffer controlled_buffer_1
  not not_1 (VDIR, multiplexer_1_out);
  Multiplexer multiplexer_1 (.in0(controlled_buffer_1_out), .in1(VINV), .out(multiplexer_1_out), .sel(n_PCLK));
  not not_2 (VINV, VDIR);

  // Notes on the sheet:
  //   7: Flip sprite vertically
  //   VINV_FF
endmodule

module ParBitInv (
  input  n_PCLK,
  input  O,
  input  INV,
  input  val_in,
  output val_out
);

  wire in_latch_n_valout, multiplexer_1_out, not_1_out, out_latch_n_valout;

  DLatch in_latch (.Enable(n_PCLK), .Value(val_in), .n_ValOut(in_latch_n_valout));  // open: ValOut
  DLatch out_latch (.Enable(O), .Value(in_latch_n_valout), .n_ValOut(out_latch_n_valout));  // open: ValOut
  Multiplexer multiplexer_1 (.in0(out_latch_n_valout), .in1(not_1_out), .out(multiplexer_1_out), .sel(INV));
  not not_1 (not_1_out, out_latch_n_valout);
  not not_2 (val_out, multiplexer_1_out);
endmodule

module ParBit (
  input  n_PCLK,
  input  O,
  input  val_OB,
  input  val_PD,
  input  OBJ_READ,
  output PADx
);

  wire multiplexer_1_out, not_1_out, ob_latch_n_valout, pdin_latch_n_valout, pdout_latch_n_valout;

  not not_1 (not_1_out, val_PD);
  DLatch pdin_latch (.Enable(n_PCLK), .Value(not_1_out), .n_ValOut(pdin_latch_n_valout));  // open: ValOut
  DLatch ob_latch (.Enable(O), .Value(val_OB), .n_ValOut(ob_latch_n_valout));  // open: ValOut
  DLatch pdout_latch (.Enable(O), .Value(pdin_latch_n_valout), .n_ValOut(pdout_latch_n_valout));  // open: ValOut
  DLatch padx_latch (.Enable(n_PCLK), .Value(multiplexer_1_out), .n_ValOut(PADx));  // open: ValOut
  Multiplexer multiplexer_1 (
    .in0(pdout_latch_n_valout), .in1(ob_latch_n_valout), .out(multiplexer_1_out), .sel(OBJ_READ));
endmodule

module ParBit4 (
  input  n_PCLK,
  input  O,
  input  val_OB,
  input  val_PD,
  input  OBJ_READ,
  input  O8_16,
  input  val_OBPrev,
  output PADx
);

  wire multiplexer_1_out, multiplexer_2_out, not_1_out, ob_latch_n_valout, pdin_latch_n_valout,
       pdout_latch_n_valout;

  not not_1 (not_1_out, val_PD);
  DLatch pdin_latch (.Enable(n_PCLK), .Value(not_1_out), .n_ValOut(pdin_latch_n_valout));  // open: ValOut
  Multiplexer multiplexer_1 (.in0(ob_latch_n_valout), .in1(val_OBPrev), .out(multiplexer_1_out), .sel(O8_16));
  DLatch ob_latch (.Enable(O), .Value(val_OB), .n_ValOut(ob_latch_n_valout));  // open: ValOut
  DLatch pdout_latch (.Enable(O), .Value(pdin_latch_n_valout), .n_ValOut(pdout_latch_n_valout));  // open: ValOut
  DLatch padx_latch (.Enable(n_PCLK), .Value(multiplexer_2_out), .n_ValOut(PADx));  // open: ValOut
  Multiplexer multiplexer_2 (
    .in0(pdout_latch_n_valout), .in1(multiplexer_1_out), .out(multiplexer_2_out), .sel(OBJ_READ));
endmodule

module PAR (
  input  n_PCLK,
  input  H0_DD,
  input  nF_NT,
  input  BGSEL,
  input  OBSEL,
  input  O8_16,
  input  OBJ_READ,
  input  n_OBJ_RD_ATTR,
  input  n_H1_D,
  input  [7:0] OB,
  input  [7:0] PD_In,
  input  [3:0] OV,
  input  [2:0] n_FVO,
  output [13:0] PAT_ADR
);

  wire parbitinv_1_val_out, parcontrol_1_o, v_inversion_1_vinv;
  wire [2:0] multiplexer_1_out, parbitinv_4_val_out;

  ParControl parcontrol_1 (
    .n_PCLK(n_PCLK), .H0_DD(H0_DD), .nF_NT(nF_NT), .BGSEL(BGSEL), .OBSEL(OBSEL), .O8_16(O8_16),
    .OBJ_READ(OBJ_READ), .OB(OB), .O(parcontrol_1_o), .PAD12(PAT_ADR[12]));
  V_Inversion v_inversion_1 (
    .n_PCLK(n_PCLK), .n_OBJ_RD_ATTR(n_OBJ_RD_ATTR), .OB(OB), .VINV(v_inversion_1_vinv));  // open: VDIR
  ParBit4 parbit4_1 (
    .n_PCLK(n_PCLK), .O(parcontrol_1_o), .val_OB(OB[0]), .val_PD(PD_In[0]), .OBJ_READ(OBJ_READ),
    .O8_16(O8_16), .val_OBPrev(parbitinv_1_val_out), .PADx(PAT_ADR[4]));
  ParBitInv parbitinv_1 (
    .n_PCLK(n_PCLK), .O(parcontrol_1_o), .INV(v_inversion_1_vinv), .val_in(OV[3]),
    .val_out(parbitinv_1_val_out));
  ParBitInv parbitinv_2 (
    .n_PCLK(n_PCLK), .O(parcontrol_1_o), .INV(v_inversion_1_vinv), .val_in(OV[2]),
    .val_out(parbitinv_4_val_out[2]));
  ParBitInv parbitinv_3 (
    .n_PCLK(n_PCLK), .O(parcontrol_1_o), .INV(v_inversion_1_vinv), .val_in(OV[1]),
    .val_out(parbitinv_4_val_out[1]));
  ParBitInv parbitinv_4 (
    .n_PCLK(n_PCLK), .O(parcontrol_1_o), .INV(v_inversion_1_vinv), .val_in(OV[0]),
    .val_out(parbitinv_4_val_out[0]));
  Multiplexer #(.width(3)) multiplexer_1 (
    .in0(n_FVO), .in1(parbitinv_4_val_out), .out(multiplexer_1_out), .sel(OBJ_READ));
  ParBit parbit_1 (
    .n_PCLK(n_PCLK), .O(parcontrol_1_o), .val_OB(OB[7]), .val_PD(PD_In[7]), .OBJ_READ(OBJ_READ),
    .PADx(PAT_ADR[11]));
  ParBit parbit_2 (
    .n_PCLK(n_PCLK), .O(parcontrol_1_o), .val_OB(OB[6]), .val_PD(PD_In[6]), .OBJ_READ(OBJ_READ),
    .PADx(PAT_ADR[10]));
  ParBit parbit_3 (
    .n_PCLK(n_PCLK), .O(parcontrol_1_o), .val_OB(OB[5]), .val_PD(PD_In[5]), .OBJ_READ(OBJ_READ),
    .PADx(PAT_ADR[9]));
  ParBit parbit_4 (
    .n_PCLK(n_PCLK), .O(parcontrol_1_o), .val_OB(OB[4]), .val_PD(PD_In[4]), .OBJ_READ(OBJ_READ),
    .PADx(PAT_ADR[8]));
  ParBit parbit_5 (
    .n_PCLK(n_PCLK), .O(parcontrol_1_o), .val_OB(OB[3]), .val_PD(PD_In[3]), .OBJ_READ(OBJ_READ),
    .PADx(PAT_ADR[7]));
  ParBit parbit_6 (
    .n_PCLK(n_PCLK), .O(parcontrol_1_o), .val_OB(OB[2]), .val_PD(PD_In[2]), .OBJ_READ(OBJ_READ),
    .PADx(PAT_ADR[6]));
  ParBit parbit_7 (
    .n_PCLK(n_PCLK), .O(parcontrol_1_o), .val_OB(OB[1]), .val_PD(PD_In[1]), .OBJ_READ(OBJ_READ),
    .PADx(PAT_ADR[5]));
  DLatch pad2_latch (.Enable(n_PCLK), .Value(multiplexer_1_out[2]), .n_ValOut(PAT_ADR[2]));  // open: ValOut
  DLatch pad1_latch (.Enable(n_PCLK), .Value(multiplexer_1_out[1]), .n_ValOut(PAT_ADR[1]));  // open: ValOut
  DLatch pad0_latch (.Enable(n_PCLK), .Value(multiplexer_1_out[0]), .n_ValOut(PAT_ADR[0]));  // open: ValOut
  not not_1 (PAT_ADR[3], n_H1_D);

  assign PAT_ADR[13] = 1'b0;

  // Notes on the sheet:
  //   bit12
  //   bit4
  //   bit3
  //   bit2
  //   bit1
  //   bit0
  //   OB1-7 / PD1-7
  //   bit11
  //   bit10
  //   bit9
  //   bit8
  //   bit7
  //   bit6
  //   bit5
  //   actual bit3
  //   PAT_ADR[13] = 0
  //   The address to load the object/background tile.
endmodule

module SCC_FF (
  input  val_in,
  input  n_DBE,
  input  RC,
  output val_out
);

  wire multiplexer_1_out, not_1_out;

  not not_1 (not_1_out, multiplexer_1_out);
  Multiplexer multiplexer_1 (.in0(val_in), .in1(val_out), .out(multiplexer_1_out), .sel(n_DBE));
  nor nor_1 (val_out, not_1_out, RC);
endmodule

module Fine_H (
  input  W5_1,
  input  n_DBE,
  input  RC,
  input  [7:0] DB,
  output [2:0] FHx
);

  wire controlled_buffer_1_out, controlled_buffer_2_out, controlled_buffer_3_out;

  assign controlled_buffer_1_out = W5_1 ? DB[0] : 1'bz;  // Controlled_Buffer controlled_buffer_1
  assign controlled_buffer_2_out = W5_1 ? DB[1] : 1'bz;  // Controlled_Buffer controlled_buffer_2
  assign controlled_buffer_3_out = W5_1 ? DB[2] : 1'bz;  // Controlled_Buffer controlled_buffer_3
  SCC_FF scc_ff_1 (.val_in(controlled_buffer_1_out), .n_DBE(n_DBE), .RC(RC), .val_out(FHx[0]));
  SCC_FF scc_ff_2 (.val_in(controlled_buffer_2_out), .n_DBE(n_DBE), .RC(RC), .val_out(FHx[1]));
  SCC_FF scc_ff_3 (.val_in(controlled_buffer_3_out), .n_DBE(n_DBE), .RC(RC), .val_out(FHx[2]));
endmodule

module Fine_V (
  input  W5_2,
  input  W6_1,
  input  n_DBE,
  input  RC,
  input  [7:0] DB,
  output [2:0] FVx
);

  wire controlled_buffer_1_out, controlled_buffer_2_out, controlled_buffer_3_out;

  assign controlled_buffer_1_out = W5_2 ? DB[0] : 1'bz;  // Controlled_Buffer controlled_buffer_1
  assign controlled_buffer_2_out = W5_2 ? DB[1] : 1'bz;  // Controlled_Buffer controlled_buffer_2
  assign controlled_buffer_3_out = W5_2 ? DB[2] : 1'bz;  // Controlled_Buffer controlled_buffer_3
  assign controlled_buffer_1_out = W6_1 ? DB[4] : 1'bz;  // Controlled_Buffer controlled_buffer_4
  assign controlled_buffer_2_out = W6_1 ? DB[5] : 1'bz;  // Controlled_Buffer controlled_buffer_5
  assign controlled_buffer_3_out = W6_1 ? 1'b0 : 1'bz;  // Controlled_Buffer controlled_buffer_6
  SCC_FF scc_ff_1 (.val_in(controlled_buffer_1_out), .n_DBE(n_DBE), .RC(RC), .val_out(FVx[0]));
  SCC_FF scc_ff_2 (.val_in(controlled_buffer_2_out), .n_DBE(n_DBE), .RC(RC), .val_out(FVx[1]));
  SCC_FF scc_ff_3 (.val_in(controlled_buffer_3_out), .n_DBE(n_DBE), .RC(RC), .val_out(FVx[2]));
endmodule

module NT_Select (
  input  W0,
  input  W6_1,
  input  n_DBE,
  input  RC,
  input  [7:0] DB,
  output NTH,
  output NTV
);

  wire controlled_buffer_1_out, controlled_buffer_2_out;

  assign controlled_buffer_1_out = W0 ? DB[0] : 1'bz;  // Controlled_Buffer controlled_buffer_1
  assign controlled_buffer_2_out = W0 ? DB[1] : 1'bz;  // Controlled_Buffer controlled_buffer_2
  assign controlled_buffer_1_out = W6_1 ? DB[2] : 1'bz;  // Controlled_Buffer controlled_buffer_3
  assign controlled_buffer_2_out = W6_1 ? DB[3] : 1'bz;  // Controlled_Buffer controlled_buffer_4
  SCC_FF scc_ff_1 (.val_in(controlled_buffer_1_out), .n_DBE(n_DBE), .RC(RC), .val_out(NTH));
  SCC_FF scc_ff_2 (.val_in(controlled_buffer_2_out), .n_DBE(n_DBE), .RC(RC), .val_out(NTV));
endmodule

module Tile_V (
  input  W5_2,
  input  W6_1,
  input  W6_2,
  input  n_DBE,
  input  RC,
  input  [7:0] DB,
  output [4:0] TVx
);

  wire controlled_buffer_1_out, controlled_buffer_2_out, controlled_buffer_3_out, controlled_buffer_4_out,
       controlled_buffer_5_out;

  assign controlled_buffer_1_out = W5_2 ? DB[3] : 1'bz;  // Controlled_Buffer controlled_buffer_1
  assign controlled_buffer_2_out = W5_2 ? DB[4] : 1'bz;  // Controlled_Buffer controlled_buffer_2
  assign controlled_buffer_3_out = W5_2 ? DB[5] : 1'bz;  // Controlled_Buffer controlled_buffer_3
  assign controlled_buffer_4_out = W5_2 ? DB[6] : 1'bz;  // Controlled_Buffer controlled_buffer_4
  assign controlled_buffer_5_out = W5_2 ? DB[7] : 1'bz;  // Controlled_Buffer controlled_buffer_5
  assign controlled_buffer_4_out = W6_1 ? DB[0] : 1'bz;  // Controlled_Buffer controlled_buffer_6
  assign controlled_buffer_5_out = W6_1 ? DB[1] : 1'bz;  // Controlled_Buffer controlled_buffer_7
  assign controlled_buffer_1_out = W6_2 ? DB[5] : 1'bz;  // Controlled_Buffer controlled_buffer_8
  assign controlled_buffer_2_out = W6_2 ? DB[6] : 1'bz;  // Controlled_Buffer controlled_buffer_9
  assign controlled_buffer_3_out = W6_2 ? DB[7] : 1'bz;  // Controlled_Buffer controlled_buffer_10
  SCC_FF scc_ff_1 (.val_in(controlled_buffer_1_out), .n_DBE(n_DBE), .RC(RC), .val_out(TVx[0]));
  SCC_FF scc_ff_2 (.val_in(controlled_buffer_2_out), .n_DBE(n_DBE), .RC(RC), .val_out(TVx[1]));
  SCC_FF scc_ff_3 (.val_in(controlled_buffer_3_out), .n_DBE(n_DBE), .RC(RC), .val_out(TVx[2]));
  SCC_FF scc_ff_4 (.val_in(controlled_buffer_4_out), .n_DBE(n_DBE), .RC(RC), .val_out(TVx[3]));
  SCC_FF scc_ff_5 (.val_in(controlled_buffer_5_out), .n_DBE(n_DBE), .RC(RC), .val_out(TVx[4]));
endmodule

module Tile_H (
  input  W5_1,
  input  W6_2,
  input  n_DBE,
  input  RC,
  input  [7:0] DB,
  output [4:0] THx
);

  wire controlled_buffer_1_out, controlled_buffer_2_out, controlled_buffer_3_out, controlled_buffer_4_out,
       controlled_buffer_5_out;

  assign controlled_buffer_1_out = W5_1 ? DB[3] : 1'bz;  // Controlled_Buffer controlled_buffer_1
  assign controlled_buffer_2_out = W5_1 ? DB[4] : 1'bz;  // Controlled_Buffer controlled_buffer_2
  assign controlled_buffer_3_out = W5_1 ? DB[5] : 1'bz;  // Controlled_Buffer controlled_buffer_3
  assign controlled_buffer_4_out = W5_1 ? DB[6] : 1'bz;  // Controlled_Buffer controlled_buffer_4
  assign controlled_buffer_5_out = W5_1 ? DB[7] : 1'bz;  // Controlled_Buffer controlled_buffer_5
  assign controlled_buffer_1_out = W6_2 ? DB[0] : 1'bz;  // Controlled_Buffer controlled_buffer_6
  assign controlled_buffer_2_out = W6_2 ? DB[1] : 1'bz;  // Controlled_Buffer controlled_buffer_7
  assign controlled_buffer_3_out = W6_2 ? DB[2] : 1'bz;  // Controlled_Buffer controlled_buffer_8
  assign controlled_buffer_4_out = W6_2 ? DB[3] : 1'bz;  // Controlled_Buffer controlled_buffer_9
  assign controlled_buffer_5_out = W6_2 ? DB[4] : 1'bz;  // Controlled_Buffer controlled_buffer_10
  SCC_FF scc_ff_1 (.val_in(controlled_buffer_1_out), .n_DBE(n_DBE), .RC(RC), .val_out(THx[0]));
  SCC_FF scc_ff_2 (.val_in(controlled_buffer_2_out), .n_DBE(n_DBE), .RC(RC), .val_out(THx[1]));
  SCC_FF scc_ff_3 (.val_in(controlled_buffer_3_out), .n_DBE(n_DBE), .RC(RC), .val_out(THx[2]));
  SCC_FF scc_ff_4 (.val_in(controlled_buffer_4_out), .n_DBE(n_DBE), .RC(RC), .val_out(THx[3]));
  SCC_FF scc_ff_5 (.val_in(controlled_buffer_5_out), .n_DBE(n_DBE), .RC(RC), .val_out(THx[4]));
endmodule

module ScrollRegs (
  input  n_W0,
  input  n_W5_1,
  input  n_W5_2,
  input  n_W6_1,
  input  n_W6_2,
  input  n_DBE,
  input  RC,
  input  [7:0] DB,
  output [2:0] FHx,
  output [2:0] FVx,
  output NTH,
  output NTV,
  output [4:0] TVx,
  output [4:0] THx,
  output W6_2_Enable
);

  wire W0, W5_1, W5_2, W6_1;

  nor nor_1 (W0, n_W0, n_DBE);
  nor nor_2 (W5_1, n_W5_1, n_DBE);
  nor nor_3 (W5_2, n_W5_2, n_DBE);
  nor nor_4 (W6_1, n_W6_1, n_DBE);
  nor nor_5 (W6_2_Enable, n_W6_2, n_DBE);
  Fine_H fine_h_1 (.W5_1(W5_1), .n_DBE(n_DBE), .RC(RC), .DB(DB), .FHx(FHx));
  Fine_V fine_v_1 (.W5_2(W5_2), .W6_1(W6_1), .n_DBE(n_DBE), .RC(RC), .DB(DB), .FVx(FVx));
  NT_Select nt_select_1 (.W0(W0), .W6_1(W6_1), .n_DBE(n_DBE), .RC(RC), .DB(DB), .NTH(NTH), .NTV(NTV));
  Tile_V tile_v_1 (.W5_2(W5_2), .W6_1(W6_1), .W6_2(W6_2_Enable), .n_DBE(n_DBE), .RC(RC), .DB(DB), .TVx(TVx));
  Tile_H tile_h_1 (.W5_1(W5_1), .W6_2(W6_2_Enable), .n_DBE(n_DBE), .RC(RC), .DB(DB), .THx(THx));

  // Other names for the same wires on the sheet: W6_2 = W6_2_Enable
endmodule

module TileCountersControl (
  input  n_PCLK,
  input  PCLK,
  input  W6_2_Enable,
  input  SC_CNT,
  input  RESCL,
  input  E_EV,
  input  TSTEP,
  input  F_TB,
  input  H0_DD,
  output TVLOAD,
  output THLOAD,
  output THSTEP,
  output TVSTEP
);

  wire and_1_out, and_2_out, and_3_out, eev_latch1_n_valout, eev_latch2_n_valout, multiplexer_1_out,
       nor_1_out, nor_2_out, nor_3_out, nor_5_out, nor_6_out, nor_7_out, nor_8_out, not_1_out, not_2_out,
       not_3_out, not_4_out, not_5_out, sccnt_latch_n_valout, w62_latch_n_valout;

  DLatch sccnt_latch (.Enable(PCLK), .Value(SC_CNT), .n_ValOut(sccnt_latch_n_valout));  // open: ValOut
  DLatch eev_latch1 (.Enable(n_PCLK), .Value(E_EV), .n_ValOut(eev_latch1_n_valout));  // open: ValOut
  and and_1 (and_1_out, F_TB, H0_DD);
  and and_2 (and_2_out, n_PCLK, not_5_out);
  not not_1 (not_1_out, sccnt_latch_n_valout);
  DLatch eev_latch2 (.Enable(PCLK), .Value(eev_latch1_n_valout), .n_ValOut(eev_latch2_n_valout));  // open: ValOut
  nor nor_1 (nor_1_out, TSTEP, and_1_out);
  nor nor_2 (nor_2_out, and_2_out, nor_3_out);
  nor nor_3 (nor_3_out, nor_2_out, W6_2_Enable);
  and and_3 (and_3_out, not_1_out, RESCL);
  nor nor_4 (THSTEP, nor_1_out, PCLK);
  nor nor_5 (nor_5_out, nor_3_out, W6_2_Enable);
  nor nor_6 (nor_6_out, and_3_out, not_5_out);
  not not_2 (not_2_out, n_PCLK);
  nor nor_7 (nor_7_out, not_5_out, eev_latch2_n_valout);
  nor nor_8 (nor_8_out, E_EV, TSTEP);
  not not_3 (not_3_out, multiplexer_1_out);
  Multiplexer multiplexer_1 (.in0(nor_5_out), .in1(not_4_out), .out(multiplexer_1_out), .sel(PCLK));
  not not_4 (not_4_out, not_3_out);
  nor nor_9 (TVLOAD, nor_6_out, not_2_out);
  nor nor_10 (THLOAD, nor_7_out, PCLK);
  nor nor_11 (TVSTEP, nor_8_out, PCLK);
  DLatch w62_latch (.Enable(PCLK), .Value(not_4_out), .n_ValOut(w62_latch_n_valout));  // open: ValOut
  not not_5 (not_5_out, w62_latch_n_valout);

  // Notes on the sheet:
  //   W6_2_FF1
  //   W6_2_FF2
  //   Temp93
endmodule

module TileCountersControl2 (
  input  n_PCLK,
  input  PCLK,
  input  BLNK,
  input  [4:0] n_THO,
  input  [4:0] n_TVO,
  input  NTHO,
  input  NTVO,
  input  [2:0] n_FVO,
  input  I1_32,
  input  TVSTEP,
  output NTHIN,
  output NTVIN,
  output FVIN,
  output TVIN,
  output THIN,
  output Z_TV
);

  wire and_1_out, and_2_out, and_3_out, nor_3_out, nor_4_out, nor_5_out, nor_6_out, nor_7_out, not_1_out,
       not_2_out, not_3_out, not_7_out, not_8_out, not_9_out, not_10_out, THZ, THZB, tvstep_latch_valout,
       TVZ, tvz_latch1_n_valout, tvz_latch2_valout, TVZB;

  not not_1 (not_1_out, TVSTEP);
  not not_2 (not_2_out, BLNK);
  DLatch tvz_latch1 (.Enable(PCLK), .Value(TVZ), .n_ValOut(tvz_latch1_n_valout));  // open: ValOut
  not not_3 (not_3_out, BLNK);
  and and_1 (and_1_out, NTHO, ~not_2_out);  // AND_Gate
  and and_2 (and_2_out, NTVO, ~not_2_out);  // AND_Gate
  DLatch tvz_latch2 (.Enable(n_PCLK), .Value(tvz_latch1_n_valout), .ValOut(tvz_latch2_valout));  // open: n_ValOut
  DLatch tvstep_latch (.Enable(n_PCLK), .Value(not_1_out), .ValOut(tvstep_latch_valout));  // open: n_ValOut
  nor nor_1 (THZB, not_3_out, n_THO[0], n_THO[1], n_THO[2], n_THO[3], n_THO[4]);
  nor nor_2 (THZ, BLNK, n_THO[0], n_THO[1], n_THO[2], n_THO[3], n_THO[4]);
  nor nor_3 (nor_3_out, nor_6_out, BLNK, n_FVO[0], n_FVO[1], n_FVO[2]);
  and and_3 (and_3_out, BLNK, I1_32);
  nor nor_4 (nor_4_out, TVZB, THZ);
  not not_4 (NTHIN, nor_4_out);
  nor nor_5 (nor_5_out, and_1_out, TVZ);
  not not_5 (NTVIN, nor_5_out);
  nor nor_6 (nor_6_out, not_2_out, and_2_out);
  not not_6 (FVIN, nor_6_out);
  nor nor_7 (nor_7_out, nor_3_out, THZB, and_3_out);
  nor nor_8 (Z_TV, tvz_latch2_valout, tvstep_latch_valout);
  not not_7 (not_7_out, BLNK);
  not not_8 (not_8_out, TVIN);
  not not_9 (not_9_out, TVIN);
  not not_10 (not_10_out, n_TVO[1]);
  not not_11 (TVIN, nor_7_out);
  nand nand_1 (THIN, BLNK, I1_32);
  nor nor_9 (TVZB, not_7_out, not_8_out, n_TVO[0], n_TVO[1], n_TVO[2], n_TVO[3], n_TVO[4]);
  nor nor_10 (TVZ, BLNK, not_9_out, n_TVO[0], not_10_out, n_TVO[2], n_TVO[3], n_TVO[4]);

  // Notes on the sheet:
  //   FVZ
  //   TVIN
  //   [!] Note that TVO1 is here
endmodule

module TileCounterBit (
  input  Clock,
  input  Load,
  input  Step,
  input  val_in,
  input  carry_in,
  output val_out,
  output n_val_out,
  output carry_out
);

  wire controlled_buffer_1_out, multiplexer_1_out, not_1_out, not_2_out, not_3_out, step_latch_n_valout;

  assign controlled_buffer_1_out = Clock ? val_out : 1'bz;  // Controlled_Buffer controlled_buffer_1
  assign controlled_buffer_1_out = Load ? val_in : 1'bz;  // Controlled_Buffer controlled_buffer_2
  assign controlled_buffer_1_out = Step ? step_latch_n_valout : 1'bz;  // Controlled_Buffer controlled_buffer_3
  D_Flip_Flop #(.trigger("high")) d_ff_1 (
    .D(controlled_buffer_1_out), .clk(1'b1), .Q(val_out), .Qn(n_val_out));  // open: preset, reset
  not not_1 (not_1_out, not_2_out);
  not not_2 (not_2_out, not_1_out);
  DLatch step_latch (.Enable(Clock), .Value(multiplexer_1_out), .n_ValOut(step_latch_n_valout));  // open: ValOut
  Multiplexer multiplexer_1 (.in0(n_val_out), .in1(val_out), .out(multiplexer_1_out), .sel(carry_in));
  not not_3 (not_3_out, carry_in);
  nor nor_1 (carry_out, n_val_out, not_3_out);

  // Notes on the sheet:
  //   FF
endmodule

module TileCounterBitReset (
  input  Clock,
  input  Load,
  input  Step,
  input  val_in,
  input  carry_in,
  input  Reset,
  output val_out,
  output n_val_out,
  output carry_out
);

  wire controlled_buffer_1_out, d_ff_1_q, multiplexer_1_out, not_1_out, not_2_out, not_3_out,
       step_latch_n_valout;

  assign controlled_buffer_1_out = Clock ? val_out : 1'bz;  // Controlled_Buffer controlled_buffer_1
  assign controlled_buffer_1_out = Load ? val_in : 1'bz;  // Controlled_Buffer controlled_buffer_2
  assign controlled_buffer_1_out = Step ? step_latch_n_valout : 1'bz;  // Controlled_Buffer controlled_buffer_3
  D_Flip_Flop #(.trigger("high")) d_ff_1 (
    .D(controlled_buffer_1_out), .clk(1'b1), .Q(d_ff_1_q), .Qn(n_val_out));  // open: preset, reset
  not not_1 (not_1_out, not_2_out);
  not not_2 (not_2_out, not_1_out);
  and and_1 (val_out, d_ff_1_q, ~Reset);  // AND_Gate
  DLatch step_latch (.Enable(Clock), .Value(multiplexer_1_out), .n_ValOut(step_latch_n_valout));  // open: ValOut
  Multiplexer multiplexer_1 (.in0(n_val_out), .in1(d_ff_1_q), .out(multiplexer_1_out), .sel(carry_in));
  not not_3 (not_3_out, carry_in);
  nor nor_1 (carry_out, n_val_out, not_3_out);

  // Notes on the sheet:
  //   FF
endmodule

module Tile_FV_Counter (
  input  PCLK,
  input  TVLOAD,
  input  TVSTEP,
  input  FVIN,
  input  [2:0] FVx,
  output [2:0] n_FVO,
  output [2:0] FVO
);

  wire tilecounterbit_1_carry_out, tilecounterbit_2_carry_out, tilecounterbit_3_carry_out;

  TileCounterBit tilecounterbit_1 (
    .Clock(PCLK), .Load(TVLOAD), .Step(TVSTEP), .val_in(FVx[0]), .carry_in(FVIN), .val_out(FVO[0]),
    .n_val_out(n_FVO[0]), .carry_out(tilecounterbit_1_carry_out));
  TileCounterBit tilecounterbit_2 (
    .Clock(PCLK), .Load(TVLOAD), .Step(TVSTEP), .val_in(FVx[1]), .carry_in(tilecounterbit_1_carry_out),
    .val_out(FVO[1]), .n_val_out(n_FVO[1]), .carry_out(tilecounterbit_2_carry_out));
  TileCounterBit tilecounterbit_3 (
    .Clock(PCLK), .Load(TVLOAD), .Step(TVSTEP), .val_in(FVx[2]), .carry_in(tilecounterbit_2_carry_out),
    .val_out(FVO[2]), .n_val_out(n_FVO[2]), .carry_out(tilecounterbit_3_carry_out));
  // NoConnect on tilecounterbit_3_carry_out
endmodule

module Tile_NT_Counters (
  input  PCLK,
  input  THLOAD,
  input  THSTEP,
  input  NTHIN,
  input  NTH,
  input  TVLOAD,
  input  TVSTEP,
  input  NTVIN,
  input  NTV,
  output NTHOut,
  output NTHO,
  output NTVOut,
  output NTVO
);

  TileCounterBit tilecounterbit_1 (
    .Clock(PCLK), .Load(THLOAD), .Step(THSTEP), .val_in(NTH), .carry_in(NTHIN), .val_out(NTHOut),
    .carry_out(NTHO));  // open: n_val_out
  TileCounterBit tilecounterbit_2 (
    .Clock(PCLK), .Load(TVLOAD), .Step(TVSTEP), .val_in(NTV), .carry_in(NTVIN), .val_out(NTVOut),
    .carry_out(NTVO));  // open: n_val_out
endmodule

module Tile_TV_Counter (
  input  PCLK,
  input  TVLOAD,
  input  TVSTEP,
  input  TVIN,
  input  [4:0] TVx,
  input  Z_TV,
  output [4:0] n_TVO,
  output [4:0] TVO
);

  wire tilecounterbitreset_1_carry_out, tilecounterbitreset_2_carry_out, tilecounterbitreset_3_carry_out,
       tilecounterbitreset_4_carry_out, tilecounterbitreset_5_carry_out;

  TileCounterBitReset tilecounterbitreset_1 (
    .Clock(PCLK), .Load(TVLOAD), .Step(TVSTEP), .val_in(TVx[0]), .carry_in(TVIN), .Reset(Z_TV),
    .val_out(TVO[0]), .n_val_out(n_TVO[0]), .carry_out(tilecounterbitreset_1_carry_out));
  TileCounterBitReset tilecounterbitreset_2 (
    .Clock(PCLK), .Load(TVLOAD), .Step(TVSTEP), .val_in(TVx[1]), .carry_in(tilecounterbitreset_1_carry_out),
    .Reset(Z_TV), .val_out(TVO[1]), .n_val_out(n_TVO[1]), .carry_out(tilecounterbitreset_2_carry_out));
  TileCounterBitReset tilecounterbitreset_3 (
    .Clock(PCLK), .Load(TVLOAD), .Step(TVSTEP), .val_in(TVx[2]), .carry_in(tilecounterbitreset_2_carry_out),
    .Reset(Z_TV), .val_out(TVO[2]), .n_val_out(n_TVO[2]), .carry_out(tilecounterbitreset_3_carry_out));
  TileCounterBitReset tilecounterbitreset_4 (
    .Clock(PCLK), .Load(TVLOAD), .Step(TVSTEP), .val_in(TVx[3]), .carry_in(tilecounterbitreset_3_carry_out),
    .Reset(Z_TV), .val_out(TVO[3]), .n_val_out(n_TVO[3]), .carry_out(tilecounterbitreset_4_carry_out));
  TileCounterBitReset tilecounterbitreset_5 (
    .Clock(PCLK), .Load(TVLOAD), .Step(TVSTEP), .val_in(TVx[4]), .carry_in(tilecounterbitreset_4_carry_out),
    .Reset(Z_TV), .val_out(TVO[4]), .n_val_out(n_TVO[4]), .carry_out(tilecounterbitreset_5_carry_out));
  // NoConnect on tilecounterbitreset_5_carry_out
endmodule

module Tile_TH_Counter (
  input  PCLK,
  input  THLOAD,
  input  THSTEP,
  input  THIN,
  input  [4:0] THx,
  output [4:0] n_THO,
  output [4:0] THO
);

  wire tilecounterbit_1_carry_out, tilecounterbit_2_carry_out, tilecounterbit_3_carry_out,
       tilecounterbit_4_carry_out, tilecounterbit_5_carry_out;

  TileCounterBit tilecounterbit_1 (
    .Clock(PCLK), .Load(THLOAD), .Step(THSTEP), .val_in(THx[0]), .carry_in(THIN), .val_out(THO[0]),
    .n_val_out(n_THO[0]), .carry_out(tilecounterbit_1_carry_out));
  TileCounterBit tilecounterbit_2 (
    .Clock(PCLK), .Load(THLOAD), .Step(THSTEP), .val_in(THx[1]), .carry_in(tilecounterbit_1_carry_out),
    .val_out(THO[1]), .n_val_out(n_THO[1]), .carry_out(tilecounterbit_2_carry_out));
  TileCounterBit tilecounterbit_3 (
    .Clock(PCLK), .Load(THLOAD), .Step(THSTEP), .val_in(THx[2]), .carry_in(tilecounterbit_2_carry_out),
    .val_out(THO[2]), .n_val_out(n_THO[2]), .carry_out(tilecounterbit_3_carry_out));
  TileCounterBit tilecounterbit_4 (
    .Clock(PCLK), .Load(THLOAD), .Step(THSTEP), .val_in(THx[3]), .carry_in(tilecounterbit_3_carry_out),
    .val_out(THO[3]), .n_val_out(n_THO[3]), .carry_out(tilecounterbit_4_carry_out));
  TileCounterBit tilecounterbit_5 (
    .Clock(PCLK), .Load(THLOAD), .Step(THSTEP), .val_in(THx[4]), .carry_in(tilecounterbit_4_carry_out),
    .val_out(THO[4]), .n_val_out(n_THO[4]), .carry_out(tilecounterbit_5_carry_out));
  // NoConnect on tilecounterbit_5_carry_out
endmodule

module PamuxControl (
  input  n_H2_D,
  input  BLNK,
  input  F_AT,
  input  DB_PAR,
  output PARR,
  output PAH,
  output PAL
);

  wire not_1_out;

  nor nor_1 (PARR, n_H2_D, BLNK);
  nor nor_2 (PAH, PARR, F_AT);
  not not_1 (not_1_out, PAH);
  nor nor_3 (PAL, not_1_out, DB_PAR);
endmodule

module PamuxHighBit (
  input  PCLK,
  input  PARR,
  input  PAH,
  input  F_AT,
  input  AT_ADR,
  input  NT_ADR,
  input  PAT_ADR,
  output n_PAx
);

  wire in_latch_n_valout, multiplexer_1_out, multiplexer_2_out, multiplexer_3_out, out_latch_valout, undriven;

  // NoConnect on undriven
  Multiplexer multiplexer_1 (.in0(undriven), .in1(AT_ADR), .out(multiplexer_1_out), .sel(F_AT));
  Multiplexer multiplexer_2 (.in0(multiplexer_1_out), .in1(NT_ADR), .out(multiplexer_2_out), .sel(PAH));
  DLatch in_latch (.Enable(1'b1), .Value(multiplexer_3_out), .n_ValOut(in_latch_n_valout));  // open: ValOut
  Multiplexer multiplexer_3 (.in0(multiplexer_2_out), .in1(PAT_ADR), .out(multiplexer_3_out), .sel(PARR));
  DLatch out_latch (.Enable(PCLK), .Value(in_latch_n_valout), .ValOut(out_latch_valout));  // open: n_ValOut
  buf buffer_1 (n_PAx, out_latch_valout);
endmodule

module PamuxLowBit (
  input  PCLK,
  input  PARR,
  input  DB_PAR,
  input  PAL,
  input  F_AT,
  input  AT_ADR,
  input  NT_ADR,
  input  PAT_ADR,
  input  DBx,
  output n_PAx
);

  wire in_latch_n_valout, multiplexer_1_out, multiplexer_2_out, multiplexer_3_out, multiplexer_4_out,
       out_latch_valout, undriven;

  // NoConnect on undriven
  Multiplexer multiplexer_1 (.in0(undriven), .in1(AT_ADR), .out(multiplexer_1_out), .sel(F_AT));
  Multiplexer multiplexer_2 (.in0(multiplexer_1_out), .in1(NT_ADR), .out(multiplexer_2_out), .sel(PAL));
  Multiplexer multiplexer_3 (.in0(multiplexer_2_out), .in1(PAT_ADR), .out(multiplexer_3_out), .sel(PARR));
  DLatch in_latch (.Enable(1'b1), .Value(multiplexer_4_out), .n_ValOut(in_latch_n_valout));  // open: ValOut
  Multiplexer multiplexer_4 (.in0(multiplexer_3_out), .in1(DBx), .out(multiplexer_4_out), .sel(DB_PAR));
  DLatch out_latch (.Enable(PCLK), .Value(in_latch_n_valout), .ValOut(out_latch_valout));  // open: n_ValOut
  buf buffer_1 (n_PAx, out_latch_valout);
endmodule

module PAMUX (
  input  PCLK,
  input  PARR,
  input  DB_PAR,
  input  PAH,
  input  PAL,
  input  F_AT,
  input  [13:0] AT_ADR,
  input  [13:0] NT_ADR,
  input  [13:0] PAT_ADR,
  input  [7:0] DB_in,
  output [13:0] n_PAx
);

  PamuxLowBit pamuxlowbit_1 (
    .PCLK(PCLK), .PARR(PARR), .DB_PAR(DB_PAR), .PAL(PAL), .F_AT(F_AT), .AT_ADR(AT_ADR[0]),
    .NT_ADR(NT_ADR[0]), .PAT_ADR(PAT_ADR[0]), .DBx(DB_in[0]), .n_PAx(n_PAx[0]));
  PamuxLowBit pamuxlowbit_2 (
    .PCLK(PCLK), .PARR(PARR), .DB_PAR(DB_PAR), .PAL(PAL), .F_AT(F_AT), .AT_ADR(AT_ADR[1]),
    .NT_ADR(NT_ADR[1]), .PAT_ADR(PAT_ADR[1]), .DBx(DB_in[1]), .n_PAx(n_PAx[1]));
  PamuxLowBit pamuxlowbit_3 (
    .PCLK(PCLK), .PARR(PARR), .DB_PAR(DB_PAR), .PAL(PAL), .F_AT(F_AT), .AT_ADR(AT_ADR[2]),
    .NT_ADR(NT_ADR[2]), .PAT_ADR(PAT_ADR[3]), .DBx(DB_in[2]), .n_PAx(n_PAx[2]));
  PamuxLowBit pamuxlowbit_4 (
    .PCLK(PCLK), .PARR(PARR), .DB_PAR(DB_PAR), .PAL(PAL), .F_AT(F_AT), .AT_ADR(AT_ADR[3]),
    .NT_ADR(NT_ADR[3]), .PAT_ADR(PAT_ADR[2]), .DBx(DB_in[3]), .n_PAx(n_PAx[3]));
  PamuxLowBit pamuxlowbit_5 (
    .PCLK(PCLK), .PARR(PARR), .DB_PAR(DB_PAR), .PAL(PAL), .F_AT(F_AT), .AT_ADR(AT_ADR[4]),
    .NT_ADR(NT_ADR[4]), .PAT_ADR(PAT_ADR[4]), .DBx(DB_in[4]), .n_PAx(n_PAx[4]));
  PamuxLowBit pamuxlowbit_6 (
    .PCLK(PCLK), .PARR(PARR), .DB_PAR(DB_PAR), .PAL(PAL), .F_AT(F_AT), .AT_ADR(AT_ADR[5]),
    .NT_ADR(NT_ADR[5]), .PAT_ADR(PAT_ADR[5]), .DBx(DB_in[5]), .n_PAx(n_PAx[5]));
  PamuxLowBit pamuxlowbit_7 (
    .PCLK(PCLK), .PARR(PARR), .DB_PAR(DB_PAR), .PAL(PAL), .F_AT(F_AT), .AT_ADR(AT_ADR[6]),
    .NT_ADR(NT_ADR[6]), .PAT_ADR(PAT_ADR[6]), .DBx(DB_in[6]), .n_PAx(n_PAx[6]));
  PamuxLowBit pamuxlowbit_8 (
    .PCLK(PCLK), .PARR(PARR), .DB_PAR(DB_PAR), .PAL(PAL), .F_AT(F_AT), .AT_ADR(AT_ADR[7]),
    .NT_ADR(NT_ADR[7]), .PAT_ADR(PAT_ADR[7]), .DBx(DB_in[7]), .n_PAx(n_PAx[7]));
  PamuxHighBit pamuxhighbit_1 (
    .PCLK(PCLK), .PARR(PARR), .PAH(PAH), .F_AT(F_AT), .AT_ADR(AT_ADR[8]), .NT_ADR(NT_ADR[8]),
    .PAT_ADR(PAT_ADR[8]), .n_PAx(n_PAx[8]));
  PamuxHighBit pamuxhighbit_2 (
    .PCLK(PCLK), .PARR(PARR), .PAH(PAH), .F_AT(F_AT), .AT_ADR(AT_ADR[9]), .NT_ADR(NT_ADR[9]),
    .PAT_ADR(PAT_ADR[9]), .n_PAx(n_PAx[9]));
  PamuxHighBit pamuxhighbit_3 (
    .PCLK(PCLK), .PARR(PARR), .PAH(PAH), .F_AT(F_AT), .AT_ADR(AT_ADR[10]), .NT_ADR(NT_ADR[10]),
    .PAT_ADR(PAT_ADR[10]), .n_PAx(n_PAx[10]));
  PamuxHighBit pamuxhighbit_4 (
    .PCLK(PCLK), .PARR(PARR), .PAH(PAH), .F_AT(F_AT), .AT_ADR(AT_ADR[11]), .NT_ADR(NT_ADR[11]),
    .PAT_ADR(PAT_ADR[11]), .n_PAx(n_PAx[11]));
  PamuxHighBit pamuxhighbit_5 (
    .PCLK(PCLK), .PARR(PARR), .PAH(PAH), .F_AT(F_AT), .AT_ADR(AT_ADR[12]), .NT_ADR(NT_ADR[12]),
    .PAT_ADR(PAT_ADR[12]), .n_PAx(n_PAx[12]));
  PamuxHighBit pamuxhighbit_6 (
    .PCLK(PCLK), .PARR(PARR), .PAH(PAH), .F_AT(F_AT), .AT_ADR(AT_ADR[13]), .NT_ADR(NT_ADR[13]),
    .PAT_ADR(PAT_ADR[13]), .n_PAx(n_PAx[13]));

  // Other names for the same wires on the sheet: DB0 = DB_in[0]; DB1 = DB_in[1]; DB2 = DB_in[2]; DB3 = DB_in[3];
  //   DB4 = DB_in[4]; DB5 = DB_in[5]; DB6 = DB_in[6]; DB7 = DB_in[7]
endmodule

module PAMUX_All (
  input  PCLK,
  input  n_H2_D,
  input  BLNK,
  input  F_AT,
  input  DB_PAR,
  input  [13:0] AT_ADR,
  input  [13:0] NT_ADR,
  input  [13:0] PAT_ADR,
  input  [7:0] DB_in,
  output [13:0] n_PAx
);

  wire pamux_ctrl_pah, pamux_ctrl_pal, pamux_ctrl_parr;

  PamuxControl pamux_ctrl (
    .n_H2_D(n_H2_D), .BLNK(BLNK), .F_AT(F_AT), .DB_PAR(DB_PAR), .PARR(pamux_ctrl_parr), .PAH(pamux_ctrl_pah),
    .PAL(pamux_ctrl_pal));
  PAMUX pamux_out (
    .PCLK(PCLK), .PARR(pamux_ctrl_parr), .DB_PAR(DB_PAR), .PAH(pamux_ctrl_pah), .PAL(pamux_ctrl_pal),
    .F_AT(F_AT), .AT_ADR(AT_ADR), .NT_ADR(NT_ADR), .PAT_ADR(PAT_ADR), .DB_in(DB_in), .n_PAx(n_PAx));
endmodule

module TileCounters_All (
  input  n_PCLK,
  input  PCLK,
  input  W62_EN,
  input  SC_CNT,
  input  RESCL,
  input  E_EV,
  input  TSTEP,
  input  F_TB,
  input  H0_DD,
  input  BLNK,
  input  I1_32,
  input  [2:0] FVx,
  input  NTH,
  input  NTV,
  input  [4:0] TVx,
  input  [4:0] THx,
  output [2:0] n_FVO,
  output [4:0] THO,
  output [4:0] TVO,
  output [13:0] AT_ADR,
  output [13:0] NT_ADR
);

  wire nor_1_out, not_1_out, tile_nt_counters_1_ntho, tile_nt_counters_1_ntvo, tilecounterscontrol2_1_fvin,
       tilecounterscontrol2_1_nthin, tilecounterscontrol2_1_ntvin, tilecounterscontrol2_1_thin,
       tilecounterscontrol2_1_tvin, tilecounterscontrol2_1_z_tv, tilecounterscontrol_1_thload,
       tilecounterscontrol_1_thstep, tilecounterscontrol_1_tvload, tilecounterscontrol_1_tvstep;
  wire [2:0] tile_fv_counter_1_fvo;
  wire [4:0] tile_th_counter_1_n_tho, tile_tv_counter_1_n_tvo;

  TileCountersControl tilecounterscontrol_1 (
    .n_PCLK(n_PCLK), .PCLK(PCLK), .W6_2_Enable(W62_EN), .SC_CNT(SC_CNT), .RESCL(RESCL), .E_EV(E_EV),
    .TSTEP(TSTEP), .F_TB(F_TB), .H0_DD(H0_DD), .TVLOAD(tilecounterscontrol_1_tvload),
    .THLOAD(tilecounterscontrol_1_thload), .THSTEP(tilecounterscontrol_1_thstep),
    .TVSTEP(tilecounterscontrol_1_tvstep));
  TileCountersControl2 tilecounterscontrol2_1 (
    .n_PCLK(n_PCLK), .PCLK(PCLK), .BLNK(BLNK), .n_THO(tile_th_counter_1_n_tho),
    .n_TVO(tile_tv_counter_1_n_tvo), .NTHO(tile_nt_counters_1_ntho), .NTVO(tile_nt_counters_1_ntvo),
    .n_FVO(n_FVO), .I1_32(I1_32), .TVSTEP(tilecounterscontrol_1_tvstep),
    .NTHIN(tilecounterscontrol2_1_nthin), .NTVIN(tilecounterscontrol2_1_ntvin),
    .FVIN(tilecounterscontrol2_1_fvin), .TVIN(tilecounterscontrol2_1_tvin),
    .THIN(tilecounterscontrol2_1_thin), .Z_TV(tilecounterscontrol2_1_z_tv));
  Tile_FV_Counter tile_fv_counter_1 (
    .PCLK(PCLK), .TVLOAD(tilecounterscontrol_1_tvload), .TVSTEP(tilecounterscontrol_1_tvstep),
    .FVIN(tilecounterscontrol2_1_fvin), .FVx(FVx), .n_FVO(n_FVO), .FVO(tile_fv_counter_1_fvo));
  Tile_NT_Counters tile_nt_counters_1 (
    .PCLK(PCLK), .THLOAD(tilecounterscontrol_1_thload), .THSTEP(tilecounterscontrol_1_thstep),
    .NTHIN(tilecounterscontrol2_1_nthin), .NTH(NTH), .TVLOAD(tilecounterscontrol_1_tvload),
    .TVSTEP(tilecounterscontrol_1_tvstep), .NTVIN(tilecounterscontrol2_1_ntvin), .NTV(NTV),
    .NTHOut(AT_ADR[10]), .NTHO(tile_nt_counters_1_ntho), .NTVOut(AT_ADR[11]), .NTVO(tile_nt_counters_1_ntvo));
  Tile_TV_Counter tile_tv_counter_1 (
    .PCLK(PCLK), .TVLOAD(tilecounterscontrol_1_tvload), .TVSTEP(tilecounterscontrol_1_tvstep),
    .TVIN(tilecounterscontrol2_1_tvin), .TVx(TVx), .Z_TV(tilecounterscontrol2_1_z_tv),
    .n_TVO(tile_tv_counter_1_n_tvo), .TVO({AT_ADR[5:3], NT_ADR[6:5]}));
  Tile_TH_Counter tile_th_counter_1 (
    .PCLK(PCLK), .THLOAD(tilecounterscontrol_1_thload), .THSTEP(tilecounterscontrol_1_thstep),
    .THIN(tilecounterscontrol2_1_thin), .THx(THx), .n_THO(tile_th_counter_1_n_tho),
    .THO({AT_ADR[2:0], NT_ADR[1:0]}));
  not not_1 (not_1_out, BLNK);
  not not_2 (AT_ADR[13], nor_1_out);
  nor nor_1 (nor_1_out, tile_fv_counter_1_fvo[1], not_1_out);
  nor nor_2 (AT_ADR[12], n_FVO[0], not_1_out);

  assign AT_ADR[9:6] = 4'b1111;
  assign {NT_ADR[13:7], NT_ADR[4:2]} = {AT_ADR[13:10], AT_ADR[5:0]};
  assign THO = {AT_ADR[2:0], NT_ADR[1:0]};
  assign TVO = {AT_ADR[5:3], NT_ADR[6:5]};

  // Notes on the sheet:
  //   bit13
  //   bit10
  //   bit11
  //   bit12
endmodule

module BGC_Control (
  input  PCLK,
  input  n_PCLK,
  input  H0_DD,
  input  F_TA,
  input  F_TB,
  input  n_FO,
  input  F_AT,
  input  [4:0] THO,
  output PD_SR,
  output SRLOAD,
  output STEP,
  output STEP2,
  output PD_SEL,
  output NEXTS,
  output H01
);

  wire fat_latch_valout, nor_3_out, not_1_out, not_2_out, not_3_out, not_4_out, not_5_out,
       tho1_latch_n_valout;

  not not_1 (not_1_out, H0_DD);
  not not_2 (not_2_out, F_TA);
  not not_3 (not_3_out, F_TB);
  not not_4 (not_4_out, n_FO);
  DLatch fat_latch (.Enable(PCLK), .Value(not_5_out), .ValOut(fat_latch_valout));  // open: n_ValOut
  not not_5 (not_5_out, F_AT);
  nor nor_1 (PD_SR, not_2_out, not_1_out, PCLK);
  nor nor_2 (SRLOAD, not_3_out, not_1_out, PCLK);
  nor nor_3 (nor_3_out, not_3_out, not_1_out);
  nor nor_4 (STEP, PCLK, nor_3_out, not_4_out);
  nor nor_5 (STEP2, PCLK, not_4_out);
  nor nor_6 (PD_SEL, fat_latch_valout, PCLK, not_1_out);
  nor nor_7 (NEXTS, STEP, STEP2, n_PCLK);
  DLatch tho1_latch (.Enable(PCLK), .Value(THO[1]), .n_ValOut(tho1_latch_n_valout));  // open: ValOut
  not not_6 (H01, tho1_latch_n_valout);

  // Notes on the sheet:
  //   /H0''
  //   aka NEXT
endmodule

module BGC_SRBit (
  input  shift_in,
  input  val_in,
  input  LOAD,
  input  STEP,
  input  NEXTS,
  output shift_out
);

  wire controlled_buffer_1_out, in_latch_qn;

  assign controlled_buffer_1_out = LOAD ? val_in : 1'bz;  // Controlled_Buffer controlled_buffer_1
  assign controlled_buffer_1_out = STEP ? shift_in : 1'bz;  // Controlled_Buffer controlled_buffer_2
  D_Flip_Flop #(.trigger("high")) in_latch (
    .D(controlled_buffer_1_out), .clk(1'b1), .Qn(in_latch_qn));  // open: Q, preset, reset
  DLatch out_latch (.Enable(NEXTS), .Value(in_latch_qn), .n_ValOut(shift_out));  // open: ValOut
endmodule

module BGC_SR8 (
  input  sin,
  input  Load,
  input  Step,
  input  Nexts,
  input  [7:0] val,
  output [7:0] sout
);

  BGC_SRBit bit_7 (.shift_in(sin), .val_in(val[7]), .LOAD(Load), .STEP(Step), .NEXTS(Nexts), .shift_out(sout[7]));
  BGC_SRBit bit_3 (.shift_in(sout[4]), .val_in(val[3]), .LOAD(Load), .STEP(Step), .NEXTS(Nexts), .shift_out(sout[3]));
  BGC_SRBit bit_6 (.shift_in(sout[7]), .val_in(val[6]), .LOAD(Load), .STEP(Step), .NEXTS(Nexts), .shift_out(sout[6]));
  BGC_SRBit bit_2 (.shift_in(sout[3]), .val_in(val[2]), .LOAD(Load), .STEP(Step), .NEXTS(Nexts), .shift_out(sout[2]));
  BGC_SRBit bit_5 (.shift_in(sout[6]), .val_in(val[5]), .LOAD(Load), .STEP(Step), .NEXTS(Nexts), .shift_out(sout[5]));
  BGC_SRBit bit_1 (.shift_in(sout[2]), .val_in(val[1]), .LOAD(Load), .STEP(Step), .NEXTS(Nexts), .shift_out(sout[1]));
  BGC_SRBit bit_4 (.shift_in(sout[5]), .val_in(val[4]), .LOAD(Load), .STEP(Step), .NEXTS(Nexts), .shift_out(sout[4]));
  BGC_SRBit bit_0 (.shift_in(sout[1]), .val_in(val[0]), .LOAD(Load), .STEP(Step), .NEXTS(Nexts), .shift_out(sout[0]));
endmodule

module BGC_0 (
  input  PD_SR,
  input  [7:0] PD,
  input  SRLOAD,
  input  STEP,
  input  STEP2,
  input  NEXTS,
  input  [2:0] FH,
  output n_BGC0_Out
);

  wire [7:0] bgc_sr8_1_sout, bgc_sr8_2_sout, dlatch_x8_1_n_val_out, undriven;

  DLatch_x8 dlatch_x8_1 (.enable(PD_SR), .val(PD), .n_val_out(dlatch_x8_1_n_val_out));  // open: val_out
  BGC_SR8 bgc_sr8_1 (
    .sin(1'b1), .Load(SRLOAD), .Step(STEP), .Nexts(NEXTS),
    .val({dlatch_x8_1_n_val_out[0], dlatch_x8_1_n_val_out[1], dlatch_x8_1_n_val_out[2], dlatch_x8_1_n_val_out[3], dlatch_x8_1_n_val_out[4], dlatch_x8_1_n_val_out[5], dlatch_x8_1_n_val_out[6], dlatch_x8_1_n_val_out[7]}),
    .sout(bgc_sr8_1_sout));
  // NoConnect on undriven
  BGC_SR8 bgc_sr8_2 (
    .sin(bgc_sr8_1_sout[0]), .Load(1'b0), .Step(STEP2), .Nexts(NEXTS), .val(undriven), .sout(bgc_sr8_2_sout));
  Multiplexer #(.select(3)) multiplexer_1 (
    .in0(bgc_sr8_2_sout[0]), .in1(bgc_sr8_2_sout[1]), .in2(bgc_sr8_2_sout[2]), .in3(bgc_sr8_2_sout[3]),
    .in4(bgc_sr8_2_sout[4]), .in5(bgc_sr8_2_sout[5]), .in6(bgc_sr8_2_sout[6]), .in7(bgc_sr8_2_sout[7]),
    .out(n_BGC0_Out), .sel(FH));

  // Notes on the sheet:
  //   The PD is loaded into the SR in reverse order according to the pixel output order.
endmodule

module BGC_1 (
  input  [7:0] PD,
  input  SRLOAD,
  input  STEP,
  input  STEP2,
  input  NEXTS,
  input  [2:0] FH,
  output BGC1_Out
);

  wire [7:0] bgc_sr8_1_sout, bgc_sr8_2_sout, undriven;

  BGC_SR8 bgc_sr8_1 (
    .sin(1'b1), .Load(SRLOAD), .Step(STEP), .Nexts(NEXTS),
    .val({PD[0], PD[1], PD[2], PD[3], PD[4], PD[5], PD[6], PD[7]}), .sout(bgc_sr8_1_sout));
  // NoConnect on undriven
  BGC_SR8 bgc_sr8_2 (
    .sin(bgc_sr8_1_sout[0]), .Load(1'b0), .Step(STEP2), .Nexts(NEXTS), .val(undriven), .sout(bgc_sr8_2_sout));
  Multiplexer #(.select(3)) multiplexer_1 (
    .in0(bgc_sr8_2_sout[0]), .in1(bgc_sr8_2_sout[1]), .in2(bgc_sr8_2_sout[2]), .in3(bgc_sr8_2_sout[3]),
    .in4(bgc_sr8_2_sout[4]), .in5(bgc_sr8_2_sout[5]), .in6(bgc_sr8_2_sout[6]), .in7(bgc_sr8_2_sout[7]),
    .out(BGC1_Out), .sel(FH));
endmodule

module BGC_2 (
  input  [4:0] TVO,
  input  H01,
  input  PD_SEL,
  input  [7:0] PD,
  input  SRLOAD,
  input  STEP2,
  input  NEXTS,
  input  [2:0] FH,
  output n_BGC2_Out
);

  wire bgc_srbit_1_shift_out, multiplexer_1_out, pd0_latch_n_valout, pd2_latch_n_valout, pd4_latch_n_valout,
       pd6_latch_n_valout, undriven;
  wire [7:0] bgc_sr8_1_sout, undriven_2;

  DLatch pd0_latch (.Enable(PD_SEL), .Value(PD[0]), .n_ValOut(pd0_latch_n_valout));  // open: ValOut
  DLatch pd2_latch (.Enable(PD_SEL), .Value(PD[2]), .n_ValOut(pd2_latch_n_valout));  // open: ValOut
  DLatch pd4_latch (.Enable(PD_SEL), .Value(PD[4]), .n_ValOut(pd4_latch_n_valout));  // open: ValOut
  DLatch pd6_latch (.Enable(PD_SEL), .Value(PD[6]), .n_ValOut(pd6_latch_n_valout));  // open: ValOut
  // NoConnect on undriven
  Multiplexer #(.select(2)) multiplexer_1 (
    .in0(pd0_latch_n_valout), .in1(pd2_latch_n_valout), .in2(pd4_latch_n_valout), .in3(pd6_latch_n_valout),
    .out(multiplexer_1_out), .sel({TVO[1], H01}));
  BGC_SRBit bgc_srbit_1 (
    .shift_in(undriven), .val_in(multiplexer_1_out), .LOAD(SRLOAD), .STEP(1'b0), .NEXTS(NEXTS),
    .shift_out(bgc_srbit_1_shift_out));
  // NoConnect on undriven_2
  BGC_SR8 bgc_sr8_1 (
    .sin(bgc_srbit_1_shift_out), .Load(1'b0), .Step(STEP2), .Nexts(NEXTS), .val(undriven_2),
    .sout(bgc_sr8_1_sout));
  Multiplexer #(.select(3)) multiplexer_2 (
    .in0(bgc_sr8_1_sout[0]), .in1(bgc_sr8_1_sout[1]), .in2(bgc_sr8_1_sout[2]), .in3(bgc_sr8_1_sout[3]),
    .in4(bgc_sr8_1_sout[4]), .in5(bgc_sr8_1_sout[5]), .in6(bgc_sr8_1_sout[6]), .in7(bgc_sr8_1_sout[7]),
    .out(n_BGC2_Out), .sel(FH));
endmodule

module BGC_3 (
  input  [4:0] TVO,
  input  H01,
  input  PD_SEL,
  input  [7:0] PD,
  input  SRLOAD,
  input  STEP2,
  input  NEXTS,
  input  [2:0] FH,
  output n_BGC3_Out
);

  wire bgc_srbit_1_shift_out, multiplexer_1_out, pd1_latch_n_valout, pd3_latch_n_valout, pd5_latch_n_valout,
       pd7_latch_n_valout, undriven;
  wire [7:0] bgc_sr8_1_sout, undriven_2;

  DLatch pd1_latch (.Enable(PD_SEL), .Value(PD[1]), .n_ValOut(pd1_latch_n_valout));  // open: ValOut
  DLatch pd3_latch (.Enable(PD_SEL), .Value(PD[3]), .n_ValOut(pd3_latch_n_valout));  // open: ValOut
  DLatch pd5_latch (.Enable(PD_SEL), .Value(PD[5]), .n_ValOut(pd5_latch_n_valout));  // open: ValOut
  DLatch pd7_latch (.Enable(PD_SEL), .Value(PD[7]), .n_ValOut(pd7_latch_n_valout));  // open: ValOut
  // NoConnect on undriven
  Multiplexer #(.select(2)) multiplexer_1 (
    .in0(pd1_latch_n_valout), .in1(pd3_latch_n_valout), .in2(pd5_latch_n_valout), .in3(pd7_latch_n_valout),
    .out(multiplexer_1_out), .sel({TVO[1], H01}));
  BGC_SRBit bgc_srbit_1 (
    .shift_in(undriven), .val_in(multiplexer_1_out), .LOAD(SRLOAD), .STEP(1'b0), .NEXTS(NEXTS),
    .shift_out(bgc_srbit_1_shift_out));
  // NoConnect on undriven_2
  BGC_SR8 bgc_sr8_1 (
    .sin(bgc_srbit_1_shift_out), .Load(1'b0), .Step(STEP2), .Nexts(NEXTS), .val(undriven_2),
    .sout(bgc_sr8_1_sout));
  Multiplexer #(.select(3)) multiplexer_2 (
    .in0(bgc_sr8_1_sout[0]), .in1(bgc_sr8_1_sout[1]), .in2(bgc_sr8_1_sout[2]), .in3(bgc_sr8_1_sout[3]),
    .in4(bgc_sr8_1_sout[4]), .in5(bgc_sr8_1_sout[5]), .in6(bgc_sr8_1_sout[6]), .in7(bgc_sr8_1_sout[7]),
    .out(n_BGC3_Out), .sel(FH));

  // Notes on the sheet:
  //   Repeats the BGC2 circuit, but uses odd bits instead of even PD bits.
endmodule

module BGC_Out (
  input  PCLK,
  input  n_PCLK,
  input  n_CLPB,
  input  n_BGC0_Out,
  input  BGC1_Out,
  input  n_BGC2_Out,
  input  n_BGC3_Out,
  output [3:0] BGC
);

  wire bgc0_latch1_n_valout, bgc0_latch2_valout, bgc1_latch1_n_valout, bgc1_latch2_valout,
       bgc2_latch1_n_valout, bgc2_latch2_valout, bgc3_latch1_n_valout, bgc3_latch2_valout,
       clpb_latch_n_valout, not_1_out, not_2_out, not_3_out;

  DLatch bgc0_latch1 (.Enable(n_PCLK), .Value(not_1_out), .n_ValOut(bgc0_latch1_n_valout));  // open: ValOut
  not not_1 (not_1_out, n_BGC0_Out);
  DLatch bgc1_latch1 (.Enable(n_PCLK), .Value(BGC1_Out), .n_ValOut(bgc1_latch1_n_valout));  // open: ValOut
  DLatch bgc2_latch1 (.Enable(n_PCLK), .Value(not_2_out), .n_ValOut(bgc2_latch1_n_valout));  // open: ValOut
  not not_2 (not_2_out, n_BGC2_Out);
  DLatch bgc3_latch1 (.Enable(n_PCLK), .Value(not_3_out), .n_ValOut(bgc3_latch1_n_valout));  // open: ValOut
  not not_3 (not_3_out, n_BGC3_Out);
  DLatch clpb_latch (.Enable(PCLK), .Value(n_CLPB), .n_ValOut(clpb_latch_n_valout));  // open: ValOut
  DLatch bgc0_latch2 (.Enable(PCLK), .Value(bgc0_latch1_n_valout), .ValOut(bgc0_latch2_valout));  // open: n_ValOut
  DLatch bgc1_latch2 (.Enable(PCLK), .Value(bgc1_latch1_n_valout), .ValOut(bgc1_latch2_valout));  // open: n_ValOut
  DLatch bgc2_latch2 (.Enable(PCLK), .Value(bgc2_latch1_n_valout), .ValOut(bgc2_latch2_valout));  // open: n_ValOut
  DLatch bgc3_latch2 (.Enable(PCLK), .Value(bgc3_latch1_n_valout), .ValOut(bgc3_latch2_valout));  // open: n_ValOut
  nor nor_1 (BGC[0], bgc0_latch2_valout, clpb_latch_n_valout);
  nor nor_2 (BGC[1], bgc1_latch2_valout, clpb_latch_n_valout);
  nor nor_3 (BGC[2], bgc2_latch2_valout, clpb_latch_n_valout);
  nor nor_4 (BGC[3], bgc3_latch2_valout, clpb_latch_n_valout);
endmodule

module BGC_All (
  input  PCLK,
  input  n_PCLK,
  input  H0_DD,
  input  F_TA,
  input  F_TB,
  input  n_FO,
  input  F_AT,
  input  [4:0] THO,
  input  [4:0] TVO,
  input  [2:0] FH,
  input  [7:0] PD,
  input  n_CLPB,
  output [3:0] BGC
);

  wire bgc_0_1_n_bgc0_out, bgc_1_1_bgc1_out, bgc_2_1_n_bgc2_out, bgc_3_1_n_bgc3_out, bgc_control_1_h01,
       bgc_control_1_nexts, bgc_control_1_pd_sel, bgc_control_1_pd_sr, bgc_control_1_srload,
       bgc_control_1_step, bgc_control_1_step2;

  BGC_Control bgc_control_1 (
    .PCLK(PCLK), .n_PCLK(n_PCLK), .H0_DD(H0_DD), .F_TA(F_TA), .F_TB(F_TB), .n_FO(n_FO), .F_AT(F_AT),
    .THO(THO), .PD_SR(bgc_control_1_pd_sr), .SRLOAD(bgc_control_1_srload), .STEP(bgc_control_1_step),
    .STEP2(bgc_control_1_step2), .PD_SEL(bgc_control_1_pd_sel), .NEXTS(bgc_control_1_nexts),
    .H01(bgc_control_1_h01));
  BGC_0 bgc_0_1 (
    .PD_SR(bgc_control_1_pd_sr), .PD(PD), .SRLOAD(bgc_control_1_srload), .STEP(bgc_control_1_step),
    .STEP2(bgc_control_1_step2), .NEXTS(bgc_control_1_nexts), .FH(FH), .n_BGC0_Out(bgc_0_1_n_bgc0_out));
  BGC_1 bgc_1_1 (
    .PD(PD), .SRLOAD(bgc_control_1_srload), .STEP(bgc_control_1_step), .STEP2(bgc_control_1_step2),
    .NEXTS(bgc_control_1_nexts), .FH(FH), .BGC1_Out(bgc_1_1_bgc1_out));
  BGC_2 bgc_2_1 (
    .TVO(TVO), .H01(bgc_control_1_h01), .PD_SEL(bgc_control_1_pd_sel), .PD(PD),
    .SRLOAD(bgc_control_1_srload), .STEP2(bgc_control_1_step2), .NEXTS(bgc_control_1_nexts), .FH(FH),
    .n_BGC2_Out(bgc_2_1_n_bgc2_out));
  BGC_3 bgc_3_1 (
    .TVO(TVO), .H01(bgc_control_1_h01), .PD_SEL(bgc_control_1_pd_sel), .PD(PD),
    .SRLOAD(bgc_control_1_srload), .STEP2(bgc_control_1_step2), .NEXTS(bgc_control_1_nexts), .FH(FH),
    .n_BGC3_Out(bgc_3_1_n_bgc3_out));
  BGC_Out bgc_out_1 (
    .PCLK(PCLK), .n_PCLK(n_PCLK), .n_CLPB(n_CLPB), .n_BGC0_Out(bgc_0_1_n_bgc0_out),
    .BGC1_Out(bgc_1_1_bgc1_out), .n_BGC2_Out(bgc_2_1_n_bgc2_out), .n_BGC3_Out(bgc_3_1_n_bgc3_out), .BGC(BGC));
endmodule

module ReadBuffer (
  input  XRB,
  input  RC,
  input  PD_RB,
  input  [7:0] PD_in,
  output [7:0] DB_out
);
endmodule

module CRAM_All (
  input  PCLK,
  input  n_PCLK,
  input  n_R7,
  input  n_DBE,
  input  TH_MUX,
  input  DB_PAR,
  input  n_PICTURE,
  input  BnW,
  input  [4:0] CGA,
  input  [7:0] DB_in,
  output [3:0] n_CC,
  output [1:0] n_LL,
  output [7:0] DB_out
);

  wire cb_ctrl_n_bw, cb_ctrl_n_cb_db, cb_ctrl_n_db_cb, cram_dec_col0, cram_dec_col1, cram_dec_col2,
       cram_dec_col3, cram_dec_row0_4, cram_dec_row1, cram_dec_row2, cram_dec_row3, cram_dec_row5,
       cram_dec_row6, cram_dec_row7;
  wire [1:0] cc0_bl_out, cram_mem_bl_out;

  CB_Control cb_ctrl (
    .PCLK(PCLK), .n_R7(n_R7), .n_DBE(n_DBE), .TH_MUX(TH_MUX), .DB_PAR(DB_PAR), .n_PICTURE(n_PICTURE),
    .BnW(BnW), .n_CB_DB(cb_ctrl_n_cb_db), .n_BW(cb_ctrl_n_bw), .n_DB_CB(cb_ctrl_n_db_cb));
  CRAM_Decoder cram_dec (
    .CGA(CGA), .PCLK(PCLK), .COL0(cram_dec_col0), .COL1(cram_dec_col1), .COL2(cram_dec_col2),
    .COL3(cram_dec_col3), .ROW0_4(cram_dec_row0_4), .ROW1(cram_dec_row1), .ROW2(cram_dec_row2),
    .ROW3(cram_dec_row3), .ROW5(cram_dec_row5), .ROW6(cram_dec_row6), .ROW7(cram_dec_row7));
  CB_Bit cc0 (
    .PCLK(PCLK), .n_PCLK(n_PCLK), .DB_In(DB_in[0]), .n_DB_CB(cb_ctrl_n_db_cb), .n_CB_DB(cb_ctrl_n_cb_db),
    .BL_in(cram_mem_bl_out[0]), .n_BL_in(cram_mem_bl_out[1]), .n_OE(cb_ctrl_n_bw), .BL_out(cc0_bl_out[0]),
    .n_BL_out(cc0_bl_out[1]), .DB_Out(DB_out[0]), .CB_Out(n_CC[0]));
  CB_Bit cc1 (
    .PCLK(PCLK), .n_PCLK(n_PCLK), .DB_In(DB_in[1]), .n_DB_CB(cb_ctrl_n_db_cb), .n_CB_DB(cb_ctrl_n_cb_db),
    .BL_in(cram_mem_bl_out[0]), .n_BL_in(cram_mem_bl_out[1]), .n_OE(cb_ctrl_n_bw), .BL_out(cc0_bl_out[0]),
    .n_BL_out(cc0_bl_out[1]), .DB_Out(DB_out[1]), .CB_Out(n_CC[1]));
  CB_Bit cc2 (
    .PCLK(PCLK), .n_PCLK(n_PCLK), .DB_In(DB_in[2]), .n_DB_CB(cb_ctrl_n_db_cb), .n_CB_DB(cb_ctrl_n_cb_db),
    .BL_in(cram_mem_bl_out[0]), .n_BL_in(cram_mem_bl_out[1]), .n_OE(cb_ctrl_n_bw), .BL_out(cc0_bl_out[0]),
    .n_BL_out(cc0_bl_out[1]), .DB_Out(DB_out[2]), .CB_Out(n_CC[2]));
  CB_Bit cc3 (
    .PCLK(PCLK), .n_PCLK(n_PCLK), .DB_In(DB_in[3]), .n_DB_CB(cb_ctrl_n_db_cb), .n_CB_DB(cb_ctrl_n_cb_db),
    .BL_in(cram_mem_bl_out[0]), .n_BL_in(cram_mem_bl_out[1]), .n_OE(cb_ctrl_n_bw), .BL_out(cc0_bl_out[0]),
    .n_BL_out(cc0_bl_out[1]), .DB_Out(DB_out[3]), .CB_Out(n_CC[3]));
  CRAM cram_mem (
    .PCLK(PCLK), .COL0(cram_dec_col0), .COL1(cram_dec_col1), .COL2(cram_dec_col2), .COL3(cram_dec_col3),
    .ROW0_4(cram_dec_row0_4), .ROW1(cram_dec_row1), .ROW2(cram_dec_row2), .ROW3(cram_dec_row3),
    .ROW5(cram_dec_row5), .ROW6(cram_dec_row6), .ROW7(cram_dec_row7), .BL_in(cc0_bl_out[0]),
    .n_BL_in(cc0_bl_out[1]), .BL_out(cram_mem_bl_out[0]), .n_BL_out(cram_mem_bl_out[1]));
  CB_Bit ll0 (
    .PCLK(PCLK), .n_PCLK(n_PCLK), .DB_In(DB_in[4]), .n_DB_CB(cb_ctrl_n_db_cb), .n_CB_DB(cb_ctrl_n_cb_db),
    .BL_in(cram_mem_bl_out[0]), .n_BL_in(cram_mem_bl_out[1]), .n_OE(1'b1), .BL_out(cc0_bl_out[0]),
    .n_BL_out(cc0_bl_out[1]), .DB_Out(DB_out[4]), .CB_Out(n_LL[0]));
  CB_Bit ll1 (
    .PCLK(PCLK), .n_PCLK(n_PCLK), .DB_In(DB_in[5]), .n_DB_CB(cb_ctrl_n_db_cb), .n_CB_DB(cb_ctrl_n_cb_db),
    .BL_in(cram_mem_bl_out[0]), .n_BL_in(cram_mem_bl_out[1]), .n_OE(1'b1), .BL_out(cc0_bl_out[0]),
    .n_BL_out(cc0_bl_out[1]), .DB_Out(DB_out[5]), .CB_Out(n_LL[1]));
endmodule

module CRAM (
  input  PCLK,
  input  COL0,
  input  COL1,
  input  COL2,
  input  COL3,
  input  ROW0_4,
  input  ROW1,
  input  ROW2,
  input  ROW3,
  input  ROW5,
  input  ROW6,
  input  ROW7,
  input  BL_in,
  input  n_BL_in,
  output BL_out,
  output n_BL_out
);


  assign BL_out = 1'b0;
  assign n_BL_out = 1'b1;
endmodule

module ResetPad (
  input  n_RES,
  input  RESCL,
  output RES,
  output RC
);

  wire nor_1_out, nor_2_out, not_1_out, not_2_out;

  not not_1 (not_1_out, n_RES);
  buf buffer_1 (RES, not_1_out);
  nor nor_1 (nor_1_out, RES, nor_2_out);
  not not_2 (not_2_out, nor_1_out);
  nor nor_2 (nor_2_out, nor_1_out, RESCL);
  buf buffer_2 (RC, not_2_out);

  // Notes on the sheet:
  //   S
  //   Reset_FF
  //   R
endmodule

module EXTPads (
  input  [3:0] EXT_Pad_In,
  input  n_SLAVE,
  input  n_PCLK,
  input  [3:0] n_EXT_OUT,
  output [3:0] EXT_IN,
  output [3:0] EXT_Pad_Out
);

  wire not_3_out, not_4_out;
  wire [3:0] bit_extender_1_out, bit_extender_2_out, dlatch_x4_1_n_val_out, dlatch_x4_2_val_out, nor_1_out,
       nor_2_out, not_1_out, not_2_out;

  DLatch_x4 dlatch_x4_1 (.enable(1'b1), .val(EXT_Pad_In), .n_val_out(dlatch_x4_1_n_val_out));  // open: val_out
  DLatch_x4 dlatch_x4_2 (.enable(n_PCLK), .val(n_EXT_OUT), .val_out(dlatch_x4_2_val_out));  // open: n_val_out
  assign not_1_out = ~dlatch_x4_1_n_val_out;  // NOT_Gate not_1, 4 bits wide
  assign not_2_out = ~not_1_out;  // NOT_Gate not_2, 4 bits wide
  not not_3 (not_3_out, n_SLAVE);
  assign bit_extender_1_out = {{3{n_SLAVE}}, n_SLAVE};  // Bit_Extender bit_extender_1
  assign bit_extender_2_out = {{3{not_3_out}}, not_3_out};  // Bit_Extender bit_extender_2
  assign nor_1_out = ~(not_2_out | bit_extender_1_out);  // NOR_Gate nor_1, 4 bits wide
  not not_4 (not_4_out, not_3_out);
  assign nor_2_out = ~(bit_extender_2_out | dlatch_x4_2_val_out);  // NOR_Gate nor_2, 4 bits wide
  assign EXT_IN = nor_1_out;  // Buffer buffer_1, 4 bits wide
  assign EXT_Pad_Out = not_4_out ? nor_2_out : 4'bz;  // Controlled_Buffer controlled_buffer_1

  // Notes on the sheet:
  //   from pads
  //   from mux
  //   transparent DLatch
  //   to mux
  //   to pads
endmodule

module HV_Counters (
  input  PCLK,
  input  n_PCLK,
  input  RES,
  input  HC,
  input  VC,
  input  V_IN,
  output [8:0] H,
  output [8:0] V
);

  wire hvcounterbit_1_cout, hvcounterbit_1_n_val, hvcounterbit_2_cout, hvcounterbit_2_n_val,
       hvcounterbit_3_cout, hvcounterbit_3_n_val, hvcounterbit_4_cout, hvcounterbit_4_n_val,
       hvcounterbit_5_cout, hvcounterbit_5_n_val, hvcounterbit_6_cout, hvcounterbit_7_cout,
       hvcounterbit_8_cout, hvcounterbit_9_cout, hvcounterbit_10_cout, hvcounterbit_10_n_val,
       hvcounterbit_11_cout, hvcounterbit_11_n_val, hvcounterbit_12_cout, hvcounterbit_12_n_val,
       hvcounterbit_13_cout, hvcounterbit_13_n_val, hvcounterbit_14_cout, hvcounterbit_14_n_val,
       hvcounterbit_15_cout, hvcounterbit_16_cout, hvcounterbit_17_cout, hvcounterbit_18_cout, nor_1_out,
       nor_2_out, not_1_out;

  HVCounterBit hvcounterbit_1 (
    .PCLK(PCLK), .n_PCLK(n_PCLK), .CLR(HC), .RES(RES), .cin(1'b1), .val(H[0]), .n_val(hvcounterbit_1_n_val),
    .cout(hvcounterbit_1_cout));
  HVCounterBit hvcounterbit_2 (
    .PCLK(PCLK), .n_PCLK(n_PCLK), .CLR(HC), .RES(RES), .cin(hvcounterbit_1_cout), .val(H[1]),
    .n_val(hvcounterbit_2_n_val), .cout(hvcounterbit_2_cout));
  HVCounterBit hvcounterbit_3 (
    .PCLK(PCLK), .n_PCLK(n_PCLK), .CLR(HC), .RES(RES), .cin(hvcounterbit_2_cout), .val(H[2]),
    .n_val(hvcounterbit_3_n_val), .cout(hvcounterbit_3_cout));
  HVCounterBit hvcounterbit_4 (
    .PCLK(PCLK), .n_PCLK(n_PCLK), .CLR(HC), .RES(RES), .cin(hvcounterbit_3_cout), .val(H[3]),
    .n_val(hvcounterbit_4_n_val), .cout(hvcounterbit_4_cout));
  HVCounterBit hvcounterbit_5 (
    .PCLK(PCLK), .n_PCLK(n_PCLK), .CLR(HC), .RES(RES), .cin(hvcounterbit_4_cout), .val(H[4]),
    .n_val(hvcounterbit_5_n_val), .cout(hvcounterbit_5_cout));
  // NoConnect on hvcounterbit_5_cout
  HVCounterBit hvcounterbit_6 (
    .PCLK(PCLK), .n_PCLK(n_PCLK), .CLR(HC), .RES(RES), .cin(nor_1_out), .val(H[5]), .cout(hvcounterbit_6_cout));  // open: n_val
  HVCounterBit hvcounterbit_7 (
    .PCLK(PCLK), .n_PCLK(n_PCLK), .CLR(HC), .RES(RES), .cin(hvcounterbit_6_cout), .val(H[6]),
    .cout(hvcounterbit_7_cout));  // open: n_val
  HVCounterBit hvcounterbit_8 (
    .PCLK(PCLK), .n_PCLK(n_PCLK), .CLR(HC), .RES(RES), .cin(hvcounterbit_7_cout), .val(H[7]),
    .cout(hvcounterbit_8_cout));  // open: n_val
  HVCounterBit hvcounterbit_9 (
    .PCLK(PCLK), .n_PCLK(n_PCLK), .CLR(HC), .RES(RES), .cin(hvcounterbit_8_cout), .val(H[8]),
    .cout(hvcounterbit_9_cout));  // open: n_val
  // NoConnect on hvcounterbit_9_cout
  nor nor_1 (nor_1_out, hvcounterbit_1_n_val, hvcounterbit_2_n_val, hvcounterbit_3_n_val, hvcounterbit_4_n_val, hvcounterbit_5_n_val);
  HVCounterBit hvcounterbit_10 (
    .PCLK(PCLK), .n_PCLK(n_PCLK), .CLR(VC), .RES(RES), .cin(V_IN), .val(V[0]), .n_val(hvcounterbit_10_n_val),
    .cout(hvcounterbit_10_cout));
  HVCounterBit hvcounterbit_11 (
    .PCLK(PCLK), .n_PCLK(n_PCLK), .CLR(VC), .RES(RES), .cin(hvcounterbit_10_cout), .val(V[1]),
    .n_val(hvcounterbit_11_n_val), .cout(hvcounterbit_11_cout));
  HVCounterBit hvcounterbit_12 (
    .PCLK(PCLK), .n_PCLK(n_PCLK), .CLR(VC), .RES(RES), .cin(hvcounterbit_11_cout), .val(V[2]),
    .n_val(hvcounterbit_12_n_val), .cout(hvcounterbit_12_cout));
  HVCounterBit hvcounterbit_13 (
    .PCLK(PCLK), .n_PCLK(n_PCLK), .CLR(VC), .RES(RES), .cin(hvcounterbit_12_cout), .val(V[3]),
    .n_val(hvcounterbit_13_n_val), .cout(hvcounterbit_13_cout));
  HVCounterBit hvcounterbit_14 (
    .PCLK(PCLK), .n_PCLK(n_PCLK), .CLR(VC), .RES(RES), .cin(hvcounterbit_13_cout), .val(V[4]),
    .n_val(hvcounterbit_14_n_val), .cout(hvcounterbit_14_cout));
  // NoConnect on hvcounterbit_14_cout
  HVCounterBit hvcounterbit_15 (
    .PCLK(PCLK), .n_PCLK(n_PCLK), .CLR(VC), .RES(RES), .cin(nor_2_out), .val(V[5]),
    .cout(hvcounterbit_15_cout));  // open: n_val
  HVCounterBit hvcounterbit_16 (
    .PCLK(PCLK), .n_PCLK(n_PCLK), .CLR(VC), .RES(RES), .cin(hvcounterbit_15_cout), .val(V[6]),
    .cout(hvcounterbit_16_cout));  // open: n_val
  HVCounterBit hvcounterbit_17 (
    .PCLK(PCLK), .n_PCLK(n_PCLK), .CLR(VC), .RES(RES), .cin(hvcounterbit_16_cout), .val(V[7]),
    .cout(hvcounterbit_17_cout));  // open: n_val
  HVCounterBit hvcounterbit_18 (
    .PCLK(PCLK), .n_PCLK(n_PCLK), .CLR(VC), .RES(RES), .cin(hvcounterbit_17_cout), .val(V[8]),
    .cout(hvcounterbit_18_cout));  // open: n_val
  // NoConnect on hvcounterbit_18_cout
  not not_1 (not_1_out, V_IN);
  nor nor_2 (nor_2_out, not_1_out, hvcounterbit_10_n_val, hvcounterbit_11_n_val, hvcounterbit_12_n_val, hvcounterbit_13_n_val, hvcounterbit_14_n_val);
endmodule

module HVCounterBit (
  input  PCLK,
  input  n_PCLK,
  input  CLR,
  input  RES,
  input  cin,
  output val,
  output n_val,
  output cout
);

  wire keep_latch_valout, multiplexer_1_out, multiplexer_2_out, nor_1_out, not_1_out;

  Multiplexer multiplexer_1 (.in0(n_val), .in1(val), .out(multiplexer_1_out), .sel(cin));
  DLatch keep_latch (.Enable(n_PCLK), .Value(multiplexer_1_out), .ValOut(keep_latch_valout));  // open: n_ValOut
  nor nor_1 (nor_1_out, keep_latch_valout, CLR);
  DLatch out_latch (.Enable(1'b1), .Value(multiplexer_2_out), .n_ValOut(n_val));  // open: ValOut
  Multiplexer multiplexer_2 (.in0(val), .in1(nor_1_out), .out(multiplexer_2_out), .sel(PCLK));
  nor nor_2 (val, n_val, RES);
  not not_1 (not_1_out, cin);
  nor nor_3 (cout, n_val, not_1_out);
endmodule

module HV_Decoders (
  input  [8:0] H,
  input  [8:0] V,
  input  VB,
  input  BLNK,
  output [23:0] HPLA_out,
  output [8:0] VPLA_out
);

  H_Decoder hpla (.H(H), .VB(VB), .BLNK(BLNK), .HPLA_out(HPLA_out));
  V_Decoder vpla (.V(V), .VPLA_out(VPLA_out));
endmodule

module H_Decoder (
  input  [8:0] H,
  input  VB,
  input  BLNK,
  output [23:0] HPLA_out
);

  wire [8:0] not_1_out;

  assign not_1_out = ~H;  // NOT_Gate not_1, 9 bits wide
  nor nor_1 (HPLA_out[12], not_1_out[1], not_1_out[2]);
  nor nor_2 (HPLA_out[13], H[1], not_1_out[2]);
  nor nor_3 (HPLA_out[0], not_1_out[0], not_1_out[1], not_1_out[2], H[3], not_1_out[4], H[5], H[6], H[7], not_1_out[8]);
  nor nor_4 (HPLA_out[1], H[0], H[1], H[2], H[3], H[4], H[5], H[6], H[7], not_1_out[8]);
  nor nor_5 (HPLA_out[2], not_1_out[0], H[1], H[2], H[3], H[4], H[5], not_1_out[6], H[7], H[8], BLNK);
  nor nor_6 (HPLA_out[3], H[3], H[4], H[5], H[6], H[7]);
  nor nor_7 (HPLA_out[4], H[8], VB);
  nor nor_8 (HPLA_out[5], not_1_out[0], not_1_out[1], H[2], H[3], not_1_out[4], H[5], not_1_out[6], H[7], not_1_out[8], BLNK);
  nor nor_9 (HPLA_out[6], not_1_out[0], not_1_out[1], not_1_out[2], not_1_out[3], not_1_out[4], not_1_out[5], H[6], H[7], H[8], BLNK);
  nor nor_10 (HPLA_out[7], not_1_out[0], not_1_out[1], not_1_out[2], not_1_out[3], not_1_out[4], not_1_out[5], not_1_out[6], not_1_out[7], BLNK);
  nor nor_11 (HPLA_out[8], H[6], H[7], H[8], BLNK);
  nor nor_12 (HPLA_out[9], H[6], H[7], not_1_out[8], BLNK);
  nor nor_13 (HPLA_out[10], H[8], VB, BLNK);
  nor nor_14 (HPLA_out[11], H[1], H[2], BLNK);
  nor nor_15 (HPLA_out[14], H[4], H[5], not_1_out[6], not_1_out[8], BLNK);
  nor nor_16 (HPLA_out[15], H[8], BLNK);
  nor nor_17 (HPLA_out[16], not_1_out[1], H[2]);
  nor nor_18 (HPLA_out[17], H[0], not_1_out[1], not_1_out[2], not_1_out[3], H[4], H[5], H[6], H[7], not_1_out[8]);
  nor nor_19 (HPLA_out[18], H[0], H[1], H[2], not_1_out[3], H[4], H[5], not_1_out[6], H[7], not_1_out[8]);
  nor nor_20 (HPLA_out[19], not_1_out[0], not_1_out[1], not_1_out[2], H[3], not_1_out[4], H[5], H[6], H[7], not_1_out[8]);
  nor nor_21 (HPLA_out[20], H[0], H[1], H[2], H[3], not_1_out[4], not_1_out[5], H[6], H[7], not_1_out[8]);
  nor nor_22 (HPLA_out[21], not_1_out[0], not_1_out[1], H[2], H[3], H[4], H[5], not_1_out[6], H[6], not_1_out[8]);
  nor nor_23 (HPLA_out[22], H[0], H[1], not_1_out[2], H[3], not_1_out[4], not_1_out[5], H[6], H[7], not_1_out[8]);
  nor nor_24 (HPLA_out[23], H[0], H[1], not_1_out[2], H[3], not_1_out[4], H[5], not_1_out[6], H[7], not_1_out[8]);
endmodule

module V_Decoder (
  input  [8:0] V,
  output [8:0] VPLA_out
);

  wire [8:0] not_1_out;

  assign not_1_out = ~V;  // NOT_Gate not_1, 9 bits wide
  nor nor_1 (VPLA_out[0], not_1_out[0], not_1_out[1], not_1_out[2], V[3], not_1_out[4], not_1_out[5], not_1_out[6], not_1_out[7]);
  nor nor_2 (VPLA_out[1], V[0], V[1], not_1_out[2], V[3], not_1_out[4], not_1_out[5], not_1_out[6], not_1_out[7]);
  nor nor_3 (VPLA_out[2], not_1_out[0], V[1], not_1_out[2], V[3], V[4], V[5], V[6], V[7], not_1_out[8]);
  nor nor_4 (VPLA_out[3], not_1_out[0], V[1], V[2], V[3], not_1_out[4], not_1_out[5], not_1_out[6], not_1_out[7]);
  nor nor_5 (VPLA_out[4], not_1_out[0], V[1], V[2], V[3], not_1_out[4], not_1_out[5], not_1_out[6], not_1_out[7]);
  nor nor_6 (VPLA_out[5], V[0], V[1], V[2], V[3], V[4], V[5], V[6], V[7], V[8]);
  nor nor_7 (VPLA_out[6], V[0], V[1], V[2], V[3], not_1_out[4], not_1_out[5], not_1_out[6], not_1_out[7]);
  nor nor_8 (VPLA_out[7], not_1_out[0], V[1], not_1_out[2], V[3], V[4], V[5], V[6], V[7], not_1_out[8]);
  nor nor_9 (VPLA_out[8], not_1_out[0], V[1], not_1_out[2], V[3], V[4], V[5], V[6], V[7], not_1_out[8]);
endmodule
